// Logisim project 8.0.circ as structural Verilog
module main (
  input  in_1
);

  wire button_1_out, button_2_out, button_3_out, clock_1_out, cpuc_1_write, xor_1_out;
  wire [23:0] bit_extender_1_out, bit_extender_2_out, bit_extender_3_out, bit_extender_4_out;
  wire [31:0] cpuc_1_data_out_0, cpuc_1_data_out_1, cpuc_1_main_stream_address_0,
       cpuc_1_second_stream_address_0, ram_1_data, ram_2_data, ram_3_data, ram_4_data;

  Clock clock_1 (.out(clock_1_out));
  xor xor_1 (xor_1_out, clock_1_out, in_1);
  Bit_Extender #(.in_width(32), .out_width(24)) bit_extender_1 (
    .in(cpuc_1_main_stream_address_0), .out(bit_extender_1_out));
  Bit_Extender #(.in_width(32), .out_width(24)) bit_extender_2 (
    .in(cpuc_1_main_stream_address_0), .out(bit_extender_2_out));
  Bit_Extender #(.in_width(32), .out_width(24)) bit_extender_3 (
    .in(cpuc_1_second_stream_address_0), .out(bit_extender_3_out));
  Bit_Extender #(.in_width(32), .out_width(24)) bit_extender_4 (
    .in(cpuc_1_second_stream_address_0), .out(bit_extender_4_out));
  RAM #(.addrWidth(24), .dataWidth(32), .bus("separate")) ram_1 (
    .addr(bit_extender_1_out), .din(cpuc_1_data_out_0), .data(ram_1_data), .str(1'b0), .clk(xor_1_out),
    .ld(1'b1), .clr(button_2_out));  // open: sel
  RAM #(.addrWidth(24), .dataWidth(32), .bus("separate")) ram_2 (
    .addr(bit_extender_2_out), .din(cpuc_1_data_out_1), .data(ram_2_data), .str(1'b0), .clk(xor_1_out),
    .ld(1'b1), .clr(button_2_out));  // open: sel
  RAM #(.addrWidth(24), .dataWidth(32), .bus("separate")) ram_3 (
    .addr(bit_extender_3_out), .din(cpuc_1_data_out_0), .data(ram_3_data), .str(cpuc_1_write),
    .clk(xor_1_out), .ld(1'b1), .clr(button_3_out));  // open: sel
  RAM #(.addrWidth(24), .dataWidth(32), .bus("separate")) ram_4 (
    .addr(bit_extender_4_out), .din(cpuc_1_data_out_1), .data(ram_4_data), .str(cpuc_1_write),
    .clk(xor_1_out), .ld(1'b1), .clr(button_3_out));  // open: sel
  Button button_1 (.out(button_1_out));
  Button button_2 (.out(button_2_out));
  Button button_3 (.out(button_3_out));
  CPUC cpuc_1 (
    .Main_Stream_0(ram_1_data), .Second_Steram_0(ram_3_data), .write(cpuc_1_write),
    .Main_Stream_Address_0(cpuc_1_main_stream_address_0), .Data_Out_0(cpuc_1_data_out_0),
    .Main_Stream_1(ram_2_data), .clock(xor_1_out), .Second_Steram_1(ram_4_data),
    .Data_Out_1(cpuc_1_data_out_1), .Second_Stream_Address_0(cpuc_1_second_stream_address_0),
    .kill(button_1_out));  // open: External_Access_Data_1, External_Access_Data_0, use_main_or_second_for_in, Main_Stream_Address_1, Second_Stream_Address_1
endmodule

module CPUC (
  input  clock,
  input  [31:0] Main_Stream_0,
  input  [31:0] Main_Stream_1,
  input  [31:0] Second_Steram_0,
  input  [31:0] Second_Steram_1,
  input  kill,
  output use_main_or_second_for_in,
  output write,
  output [31:0] External_Access_Data_0,
  output [31:0] External_Access_Data_1,
  output [31:0] Main_Stream_Address_0,
  output [31:0] Main_Stream_Address_1,
  output [31:0] Data_Out_0,
  output [31:0] Data_Out_1,
  output [31:0] Second_Stream_Address_0,
  output [31:0] Second_Stream_Address_1
);

  wire alu_1_boolean, or_1_out;
  wire [1:0] priority_encoder_1_p1;
  wire [3:0] cpuccu_1_alu_control;
  wire [3:1] cpuccu_1_data_control_0;
  wire [12:4] cpuccu_1_alu_control_2;
  wire [13:0] cpuccu_1_data_control_1, cpuccu_1_data_control_1_2;
  wire [14:0] cpuccu_1_data_control_0_2;
  wire [31:0] alu_1_result_0, alu_1_result_1, cpuccu_1_pc0, cpuccu_1_pc1, cpucm_65536b_1_operand_b,
       cpucm_65536b_2_operand_b, multiplexer_1_out, multiplexer_2_out;

  CPUCM_65536b cpucm_65536b_1 (
    .External_Access_Data_2(External_Access_Data_0), .Operand_B(cpucm_65536b_1_operand_b),
    .Operand_A(Data_Out_0), .operation(cpuccu_1_data_control_0_2), .get_A(cpuccu_1_data_control_1),
    .get_B(cpuccu_1_data_control_1_2), .External_access_Data({14{1'b0}}), .Data_IN(multiplexer_1_out),
    .clock(clock), .clear(or_1_out));
  CPUCM_65536b cpucm_65536b_2 (
    .External_Access_Data_2(External_Access_Data_1), .Operand_B(cpucm_65536b_2_operand_b),
    .Operand_A(Data_Out_1), .operation(cpuccu_1_data_control_0_2), .get_A(cpuccu_1_data_control_1),
    .get_B(cpuccu_1_data_control_1_2), .External_access_Data({14{1'b0}}), .Data_IN(multiplexer_2_out),
    .clock(clock), .clear(or_1_out));
  Multiplexer #(.select(2), .width(32), .disabled(0), .enable("false")) multiplexer_1 (
    .in0(Second_Steram_0), .in1(cpuccu_1_pc1), .in2(alu_1_result_0), .in3(Main_Stream_0),
    .out(multiplexer_1_out), .sel(priority_encoder_1_p1));
  or or_1 (or_1_out, cpuccu_1_data_control_0[3], kill);
  Multiplexer #(.select(2), .width(32), .disabled(0), .enable("false")) multiplexer_2 (
    .in0(Second_Steram_1), .in1(cpuccu_1_pc0), .in2(alu_1_result_1), .in3(Main_Stream_1),
    .out(multiplexer_2_out), .sel(priority_encoder_1_p1));
  CPUCCU cpuccu_1 (
    .loadingmain_stream_data(use_main_or_second_for_in), .Main_stream_0(Main_Stream_0),
    .Main_stream_1(Main_Stream_1), .\bool (alu_1_boolean), .Operand_B_0(cpucm_65536b_1_operand_b),
    .Operand_B_1(cpucm_65536b_2_operand_b), .Main_sream_address_0(Main_Stream_Address_0),
    .Main_sream_address_1(Main_Stream_Address_1), .Second_sream_address_0(Second_Stream_Address_0),
    .Second_sream_address_1(Second_Stream_Address_1), .clock(clock),
    .ALU_control({cpuccu_1_alu_control_2, cpuccu_1_alu_control}),
    .Data_control_0({cpuccu_1_data_control_0_2[10:0], cpuccu_1_data_control_0, write}),
    .Data_control_1({cpuccu_1_data_control_1_2, cpuccu_1_data_control_1, cpuccu_1_data_control_0_2[14:11]}),
    .PC0(cpuccu_1_pc0), .PC1(cpuccu_1_pc1), .kill(kill));
  ALU alu_1 (
    .operation_control(cpuccu_1_alu_control), .operand_A_0(Data_Out_0), .boolean(alu_1_boolean),
    .bool_control(cpuccu_1_alu_control_2), .result_0(alu_1_result_0), .operand_A_1(Data_Out_1),
    .operand_B_0(cpucm_65536b_1_operand_b), .operand_B_1(cpucm_65536b_2_operand_b), .result_1(alu_1_result_1));
  // Priority_Encoder #(.select(2), .disabled(0)) priority_encoder_1: pin names not known; wires that end beside it: priority_encoder_1_p1, 1'b1, cpuccu_1_data_control_0[2], cpuccu_1_data_control_0[1], use_main_or_second_for_in
endmodule

module CPUCCU (
  input  [31:0] Main_stream_0,
  input  [31:0] Main_stream_1,
  input  \bool ,
  input  clock,
  input  [31:0] Operand_B_0,
  input  [31:0] Operand_B_1,
  input  kill,
  output loadingmain_stream_data,
  output [12:0] ALU_control,
  output [14:0] Data_control_0,
  output [31:0] Data_control_1,
  output [31:0] Main_sream_address_0,
  output [31:0] Main_sream_address_1,
  output [31:0] Second_sream_address_0,
  output [31:0] PC0,
  output [31:0] Second_sream_address_1,
  output [31:0] PC1
);

  wire adder_1_cout, adder_3_cout, and_1_out, and_2_out, and_3_out, counter_1_carry, demultiplexer_1_out0,
       demultiplexer_1_out1, demultiplexer_1_out2, demultiplexer_1_out3, execute_load_qn, nand_1_out,
       nor_1_out, nor_2_out, or_1_out, or_2_out, or_3_out, register_3_q, total_or_1_out_2, total_or_2_out_2,
       total_or_3_out_2, total_or_4_out_2;
  wire [1:0] controlled_buffer_1_out, controlled_buffer_1_out_2;
  wire [31:0] multiplexer_1_out, multiplexer_2_out, register_1_q, register_2_q, register_4_q, register_5_q;

  Demultiplexer #(.select(2), .disabled(0)) demultiplexer_1 (
    .out0(demultiplexer_1_out0), .out1(demultiplexer_1_out1), .out2(demultiplexer_1_out2),
    .out3(demultiplexer_1_out3), .in(\bool ), .sel(controlled_buffer_1_out_2), .en(controlled_buffer_1_out[1]));
  Register #(.width(32)) register_1 (
    .D(multiplexer_1_out), .en(execute_load_qn), .Q(register_1_q), .clk(clock), .clr(kill));
  Multiplexer #(.width(32), .disabled(0), .enable("false")) multiplexer_1 (
    .in0(Main_stream_0), .in1(Operand_B_0), .out(multiplexer_1_out), .sel(demultiplexer_1_out2));
  Register #(.width(32)) register_2 (
    .D(multiplexer_2_out), .en(execute_load_qn), .Q(register_2_q), .clk(clock), .clr(kill));
  Multiplexer #(.width(32), .disabled(0), .enable("false")) multiplexer_2 (
    .in0(Main_stream_1), .in1(Operand_B_1), .out(multiplexer_2_out), .sel(demultiplexer_1_out2));
  nor nor_1 (nor_1_out, demultiplexer_1_out0, and_1_out);
  and and_1 (and_1_out, execute_load_qn, register_3_q);
  Register #(.width(1)) register_3 (
    .D(demultiplexer_1_out2), .Q(register_3_q), .clk(clock), .clr(and_2_out));  // open: en
  total_OR total_or_1 (.in_1(register_2_q), .out_2(total_or_1_out_2));
  total_OR total_or_2 (.in_1(register_1_q), .out_2(total_or_2_out_2));
  assign {Data_control_0, ALU_control, controlled_buffer_1_out_2, controlled_buffer_1_out} = nand_1_out ? register_1_q : 32'bz;  // Controlled_Buffer controlled_buffer_1
  Pull_Resistor pull_resistor_1 (.node({Data_control_0, ALU_control, controlled_buffer_1_out_2, controlled_buffer_1_out}));
  nand nand_1 (nand_1_out, register_1_q[0], execute_load_qn);
  Pull_Resistor pull_resistor_2 (.node(Data_control_1));
  assign Data_control_1 = nand_1_out ? register_2_q : 32'bz;  // Controlled_Buffer controlled_buffer_2
  and and_2 (and_2_out, ~clock, or_2_out, or_3_out);  // AND_Gate
  Counter #(.width(32), .max('hffffffff), .trigger("falling")) counter_1 (
    .load(demultiplexer_1_out0), .D(Operand_B_0), .count(nor_1_out), .Q(PC0), .carry(counter_1_carry),
    .clk(clock), .clr(or_1_out));
  total_OR total_or_3 (.in_1(PC0), .out_2(total_or_3_out_2));
  total_OR total_or_4 (.in_1(PC1), .out_2(total_or_4_out_2));
  Counter #(.width(32), .max('hffffffff), .trigger("falling")) counter_2 (
    .load(demultiplexer_1_out0), .D(Operand_B_1), .count(nor_1_out), .Q(PC1), .clk(counter_1_carry),
    .clr(or_1_out));  // open: carry
  and and_3 (and_3_out, or_3_out, demultiplexer_1_out1);
  or or_1 (or_1_out, and_3_out, and_2_out);
  Register #(.width(32), .trigger("falling")) register_4 (
    .D(Operand_B_0), .en(demultiplexer_1_out1), .Q(register_4_q), .clk(clock), .clr(and_2_out));
  Register #(.width(32), .trigger("falling")) register_5 (
    .D(Operand_B_1), .en(demultiplexer_1_out1), .Q(register_5_q), .clk(clock), .clr(and_2_out));
  or or_2 (or_2_out, demultiplexer_1_out3, nor_2_out);
  nor nor_2 (nor_2_out, total_or_1_out_2, total_or_2_out_2);
  T_Flip_Flop #(.trigger("falling")) execute_load (
    .clk(clock), .T(register_1_q[0]), .Q(loadingmain_stream_data), .Qn(execute_load_qn), .preset(1'b0),
    .reset(and_2_out), .en(1'b1));
  or or_3 (or_3_out, total_or_3_out_2, total_or_4_out_2);
  Adder #(.width(32)) adder_1 (
    .a(PC0), .b(register_4_q), .out(Main_sream_address_0), .cout(adder_1_cout));  // open: cin
  Adder #(.width(32)) adder_2 (
    .a(PC1), .b(register_5_q), .out(Main_sream_address_1), .cin(adder_1_cout));  // open: cout
  Adder #(.width(32)) adder_3 (
    .a(register_4_q), .b(Operand_B_0), .out(Second_sream_address_0), .cout(adder_3_cout));  // open: cin
  Adder #(.width(32)) adder_4 (
    .a(register_5_q), .b(Operand_B_1), .out(Second_sream_address_1), .cin(adder_3_cout));  // open: cout

  // Notes on the sheet:
  //   PC
  //   Program shift
endmodule

module CPUCM_128b (
  input  [4:0] get_A,
  input  [4:0] get_B,
  input  [4:0] External_access_Address,
  input  clear,
  input  clock,
  input  write,
  input  [4:0] get_reg,
  input  [31:0] Data_IN,
  output [31:0] Operand_A,
  output [31:0] Operand_B,
  output [31:0] External_Access_Data
);

  wire decoder_1_out0, decoder_1_out1, decoder_1_out2, decoder_1_out3, decoder_1_out4, decoder_1_out5,
       decoder_1_out6, decoder_1_out7, decoder_1_out8, decoder_1_out9, decoder_1_out10, decoder_1_out11,
       decoder_1_out12, decoder_1_out13, decoder_1_out14, decoder_1_out15, decoder_1_out16, decoder_1_out17,
       decoder_1_out18, decoder_1_out19, decoder_1_out20, decoder_1_out21, decoder_1_out22, decoder_1_out23,
       decoder_1_out24, decoder_1_out25, decoder_1_out26, decoder_1_out27, decoder_1_out28, decoder_1_out29,
       decoder_1_out30, decoder_1_out31;
  wire [31:0] register_1_q, register_2_q, register_3_q, register_4_q, register_5_q, register_6_q,
       register_7_q, register_8_q, register_9_q, register_10_q, register_11_q, register_12_q, register_13_q,
       register_14_q, register_15_q, register_16_q, register_17_q, register_18_q, register_19_q,
       register_20_q, register_21_q, register_22_q, register_23_q, register_24_q, register_25_q,
       register_26_q, register_27_q, register_28_q, register_29_q, register_30_q, register_31_q,
       register_32_q;

  Decoder #(.select(5), .disabled(0)) decoder_1 (
    .out0(decoder_1_out0), .out1(decoder_1_out1), .out2(decoder_1_out2), .out3(decoder_1_out3),
    .out4(decoder_1_out4), .out5(decoder_1_out5), .out6(decoder_1_out6), .out7(decoder_1_out7),
    .out8(decoder_1_out8), .out9(decoder_1_out9), .out10(decoder_1_out10), .out11(decoder_1_out11),
    .out12(decoder_1_out12), .out13(decoder_1_out13), .out14(decoder_1_out14), .out15(decoder_1_out15),
    .out16(decoder_1_out16), .out17(decoder_1_out17), .out18(decoder_1_out18), .out19(decoder_1_out19),
    .out20(decoder_1_out20), .out21(decoder_1_out21), .out22(decoder_1_out22), .out23(decoder_1_out23),
    .out24(decoder_1_out24), .out25(decoder_1_out25), .out26(decoder_1_out26), .out27(decoder_1_out27),
    .out28(decoder_1_out28), .out29(decoder_1_out29), .out30(decoder_1_out30), .out31(decoder_1_out31),
    .sel(get_reg), .en(write));
  Register #(.width(32)) register_1 (.D(Data_IN), .en(decoder_1_out0), .Q(register_1_q), .clk(clock), .clr(clear));
  Register #(.width(32)) register_2 (.D(Data_IN), .en(decoder_1_out1), .Q(register_2_q), .clk(clock), .clr(clear));
  Register #(.width(32)) register_3 (.D(Data_IN), .en(decoder_1_out2), .Q(register_3_q), .clk(clock), .clr(clear));
  Register #(.width(32)) register_4 (.D(Data_IN), .en(decoder_1_out3), .Q(register_4_q), .clk(clock), .clr(clear));
  Register #(.width(32)) register_5 (.D(Data_IN), .en(decoder_1_out4), .Q(register_5_q), .clk(clock), .clr(clear));
  Register #(.width(32)) register_6 (.D(Data_IN), .en(decoder_1_out5), .Q(register_6_q), .clk(clock), .clr(clear));
  Register #(.width(32)) register_7 (.D(Data_IN), .en(decoder_1_out6), .Q(register_7_q), .clk(clock), .clr(clear));
  Register #(.width(32)) register_8 (.D(Data_IN), .en(decoder_1_out7), .Q(register_8_q), .clk(clock), .clr(clear));
  Register #(.width(32)) register_9 (.D(Data_IN), .en(decoder_1_out8), .Q(register_9_q), .clk(clock), .clr(clear));
  Register #(.width(32)) register_10 (.D(Data_IN), .en(decoder_1_out9), .Q(register_10_q), .clk(clock), .clr(clear));
  Register #(.width(32)) register_11 (.D(Data_IN), .en(decoder_1_out10), .Q(register_11_q), .clk(clock), .clr(clear));
  Register #(.width(32)) register_12 (.D(Data_IN), .en(decoder_1_out11), .Q(register_12_q), .clk(clock), .clr(clear));
  Register #(.width(32)) register_13 (.D(Data_IN), .en(decoder_1_out12), .Q(register_13_q), .clk(clock), .clr(clear));
  Register #(.width(32)) register_14 (.D(Data_IN), .en(decoder_1_out13), .Q(register_14_q), .clk(clock), .clr(clear));
  Register #(.width(32)) register_15 (.D(Data_IN), .en(decoder_1_out14), .Q(register_15_q), .clk(clock), .clr(clear));
  Register #(.width(32)) register_16 (.D(Data_IN), .en(decoder_1_out15), .Q(register_16_q), .clk(clock), .clr(clear));
  Register #(.width(32)) register_17 (.D(Data_IN), .en(decoder_1_out16), .Q(register_17_q), .clk(clock), .clr(clear));
  Register #(.width(32)) register_18 (.D(Data_IN), .en(decoder_1_out17), .Q(register_18_q), .clk(clock), .clr(clear));
  Register #(.width(32)) register_19 (.D(Data_IN), .en(decoder_1_out18), .Q(register_19_q), .clk(clock), .clr(clear));
  Register #(.width(32)) register_20 (.D(Data_IN), .en(decoder_1_out19), .Q(register_20_q), .clk(clock), .clr(clear));
  Register #(.width(32)) register_21 (.D(Data_IN), .en(decoder_1_out20), .Q(register_21_q), .clk(clock), .clr(clear));
  Register #(.width(32)) register_22 (.D(Data_IN), .en(decoder_1_out21), .Q(register_22_q), .clk(clock), .clr(clear));
  Register #(.width(32)) register_23 (.D(Data_IN), .en(decoder_1_out22), .Q(register_23_q), .clk(clock), .clr(clear));
  Register #(.width(32)) register_24 (.D(Data_IN), .en(decoder_1_out23), .Q(register_24_q), .clk(clock), .clr(clear));
  Register #(.width(32)) register_25 (.D(Data_IN), .en(decoder_1_out24), .Q(register_25_q), .clk(clock), .clr(clear));
  Register #(.width(32)) register_26 (.D(Data_IN), .en(decoder_1_out25), .Q(register_26_q), .clk(clock), .clr(clear));
  Register #(.width(32)) register_27 (.D(Data_IN), .en(decoder_1_out26), .Q(register_27_q), .clk(clock), .clr(clear));
  Register #(.width(32)) register_28 (.D(Data_IN), .en(decoder_1_out27), .Q(register_28_q), .clk(clock), .clr(clear));
  Register #(.width(32)) register_29 (.D(Data_IN), .en(decoder_1_out28), .Q(register_29_q), .clk(clock), .clr(clear));
  Register #(.width(32)) register_30 (.D(Data_IN), .en(decoder_1_out29), .Q(register_30_q), .clk(clock), .clr(clear));
  Register #(.width(32)) register_31 (.D(Data_IN), .en(decoder_1_out30), .Q(register_31_q), .clk(clock), .clr(clear));
  Register #(.width(32)) register_32 (.D(Data_IN), .en(decoder_1_out31), .Q(register_32_q), .clk(clock), .clr(clear));
  Multiplexer #(.select(5), .width(32), .disabled(0), .enable("false")) multiplexer_1 (
    .in0(register_1_q), .in1(register_2_q), .in2(register_3_q), .in3(register_4_q), .in4(register_5_q),
    .in5(register_6_q), .in6(register_7_q), .in7(register_8_q), .in8(register_9_q), .in9(register_10_q),
    .in10(register_11_q), .in11(register_12_q), .in12(register_13_q), .in13(register_14_q),
    .in14(register_15_q), .in15(register_16_q), .in16(register_17_q), .in17(register_18_q),
    .in18(register_19_q), .in19(register_20_q), .in20(register_21_q), .in21(register_22_q),
    .in22(register_23_q), .in23(register_24_q), .in24(register_25_q), .in25(register_26_q),
    .in26(register_27_q), .in27(register_28_q), .in28(register_29_q), .in29(register_30_q),
    .in30(register_31_q), .in31(register_32_q), .out(Operand_A), .sel(get_A));
  Multiplexer #(.select(5), .width(32), .disabled(0), .enable("false")) multiplexer_2 (
    .in0(register_1_q), .in1(register_2_q), .in2(register_3_q), .in3(register_4_q), .in4(register_5_q),
    .in5(register_6_q), .in6(register_7_q), .in7(register_8_q), .in8(register_9_q), .in9(register_10_q),
    .in10(register_11_q), .in11(register_12_q), .in12(register_13_q), .in13(register_14_q),
    .in14(register_15_q), .in15(register_16_q), .in16(register_17_q), .in17(register_18_q),
    .in18(register_19_q), .in19(register_20_q), .in20(register_21_q), .in21(register_22_q),
    .in22(register_23_q), .in23(register_24_q), .in24(register_25_q), .in25(register_26_q),
    .in26(register_27_q), .in27(register_28_q), .in28(register_29_q), .in29(register_30_q),
    .in30(register_31_q), .in31(register_32_q), .out(Operand_B), .sel(get_B));
  Multiplexer #(.select(5), .width(32), .disabled(0), .enable("false")) multiplexer_3 (
    .in0(register_1_q), .in1(register_2_q), .in2(register_3_q), .in3(register_4_q), .in4(register_5_q),
    .in5(register_6_q), .in6(register_7_q), .in7(register_8_q), .in8(register_9_q), .in9(register_10_q),
    .in10(register_11_q), .in11(register_12_q), .in12(register_13_q), .in13(register_14_q),
    .in14(register_15_q), .in15(register_16_q), .in16(register_17_q), .in17(register_18_q),
    .in18(register_19_q), .in19(register_20_q), .in20(register_21_q), .in21(register_22_q),
    .in22(register_23_q), .in23(register_24_q), .in24(register_25_q), .in25(register_26_q),
    .in26(register_27_q), .in27(register_28_q), .in28(register_29_q), .in29(register_30_q),
    .in30(register_31_q), .in31(register_32_q), .out(External_Access_Data), .sel(External_access_Address));
endmodule
module CPUCM_16384b (
  input  [31:0] Data_IN,
  input  [11:0] External_access_address,
  input  [11:0] get_B,
  input  [11:0] get_A,
  input  clock,
  input  [12:0] operation,
  input  clear,
  output [31:0] External_Access_Data,
  output [31:0] Operand_B,
  output [31:0] Operand_A
);

  wire [0:0] demultiplexer_2_out0, demultiplexer_2_out2, demultiplexer_2_out4, demultiplexer_2_out5,
       demultiplexer_2_out6, demultiplexer_2_out8, demultiplexer_2_out10, demultiplexer_2_out11,
       demultiplexer_2_out12, demultiplexer_2_out14, demultiplexer_2_out16, demultiplexer_2_out17,
       demultiplexer_2_out18, demultiplexer_2_out20, demultiplexer_2_out23, demultiplexer_2_out24,
       demultiplexer_2_out26, demultiplexer_2_out29, demultiplexer_2_out30, demultiplexer_3_out0,
       demultiplexer_3_out1, demultiplexer_3_out3, demultiplexer_3_out5, demultiplexer_3_out11,
       demultiplexer_3_out13, demultiplexer_3_out15, demultiplexer_3_out17, demultiplexer_3_out19,
       demultiplexer_3_out21, demultiplexer_3_out23, demultiplexer_3_out25, demultiplexer_3_out27,
       demultiplexer_4_out0, demultiplexer_4_out2, demultiplexer_4_out4, demultiplexer_4_out5,
       demultiplexer_4_out6, demultiplexer_4_out7, demultiplexer_4_out8, demultiplexer_4_out10,
       demultiplexer_4_out11, demultiplexer_4_out12, demultiplexer_4_out13, demultiplexer_4_out14,
       demultiplexer_4_out16, demultiplexer_4_out17, demultiplexer_4_out19, demultiplexer_4_out23,
       demultiplexer_4_out25, demultiplexer_4_out29, demultiplexer_4_out31, demultiplexer_5_out0,
       demultiplexer_5_out1, demultiplexer_5_out3, demultiplexer_5_out4, demultiplexer_5_out5,
       demultiplexer_5_out10, demultiplexer_5_out16, demultiplexer_5_out17, demultiplexer_5_out20,
       demultiplexer_5_out22, demultiplexer_5_out23, demultiplexer_5_out26, demultiplexer_5_out28,
       demultiplexer_5_out29, demultiplexer_5_out30;
  wire [4:0] demultiplexer_2_out0_2, demultiplexer_2_out2_2, demultiplexer_2_out4_2, demultiplexer_2_out5_2,
       demultiplexer_2_out6_2, demultiplexer_2_out8_2, demultiplexer_2_out10_2, demultiplexer_2_out11_2,
       demultiplexer_2_out12_2, demultiplexer_2_out14_2, demultiplexer_2_out16_2, demultiplexer_2_out17_2,
       demultiplexer_2_out18_2, demultiplexer_2_out20_2, demultiplexer_2_out23_2, demultiplexer_2_out24_2,
       demultiplexer_2_out26_2, demultiplexer_2_out29_2, demultiplexer_2_out30_2, demultiplexer_3_out0_2,
       demultiplexer_3_out1_2, demultiplexer_3_out3_2, demultiplexer_3_out5_2, demultiplexer_3_out11_2,
       demultiplexer_3_out13_2, demultiplexer_3_out15_2, demultiplexer_3_out17_2, demultiplexer_3_out19_2,
       demultiplexer_3_out21_2, demultiplexer_3_out23_2, demultiplexer_3_out25_2, demultiplexer_3_out27_2,
       demultiplexer_4_out0_2, demultiplexer_4_out2_2, demultiplexer_4_out4_2, demultiplexer_4_out5_2,
       demultiplexer_4_out6_2, demultiplexer_4_out7_2, demultiplexer_4_out8_2, demultiplexer_4_out10_2,
       demultiplexer_4_out11_2, demultiplexer_4_out12_2, demultiplexer_4_out13_2, demultiplexer_4_out14_2,
       demultiplexer_4_out16_2, demultiplexer_4_out17_2, demultiplexer_4_out19_2, demultiplexer_4_out23_2,
       demultiplexer_4_out25_2, demultiplexer_4_out29_2, demultiplexer_4_out31_2, demultiplexer_5_out0_2,
       demultiplexer_5_out1_2, demultiplexer_5_out3_2, demultiplexer_5_out4_2, demultiplexer_5_out5_2,
       demultiplexer_5_out10_2, demultiplexer_5_out16_2, demultiplexer_5_out17_2, demultiplexer_5_out20_2,
       demultiplexer_5_out22_2, demultiplexer_5_out23_2, demultiplexer_5_out26_2, demultiplexer_5_out28_2,
       demultiplexer_5_out29_2, demultiplexer_5_out30_2;
  wire [5:0] demultiplexer_1_out0, demultiplexer_1_out1, demultiplexer_1_out2, demultiplexer_1_out3,
       demultiplexer_2_out1, demultiplexer_2_out3, demultiplexer_2_out7, demultiplexer_2_out9,
       demultiplexer_2_out13, demultiplexer_2_out15, demultiplexer_2_out19, demultiplexer_2_out21,
       demultiplexer_2_out22, demultiplexer_2_out25, demultiplexer_2_out27, demultiplexer_2_out28,
       demultiplexer_2_out31, demultiplexer_3_out2, demultiplexer_3_out4, demultiplexer_3_out6,
       demultiplexer_3_out7, demultiplexer_3_out8, demultiplexer_3_out9, demultiplexer_3_out10,
       demultiplexer_3_out12, demultiplexer_3_out14, demultiplexer_3_out16, demultiplexer_3_out18,
       demultiplexer_3_out20, demultiplexer_3_out22, demultiplexer_3_out24, demultiplexer_3_out26,
       demultiplexer_3_out28, demultiplexer_3_out29, demultiplexer_3_out30, demultiplexer_3_out31,
       demultiplexer_4_out1, demultiplexer_4_out3, demultiplexer_4_out9, demultiplexer_4_out15,
       demultiplexer_4_out18, demultiplexer_4_out20, demultiplexer_4_out21, demultiplexer_4_out22,
       demultiplexer_4_out24, demultiplexer_4_out26, demultiplexer_4_out27, demultiplexer_4_out28,
       demultiplexer_4_out30, demultiplexer_5_out2, demultiplexer_5_out6, demultiplexer_5_out7,
       demultiplexer_5_out8, demultiplexer_5_out9, demultiplexer_5_out11, demultiplexer_5_out12,
       demultiplexer_5_out13, demultiplexer_5_out14, demultiplexer_5_out15, demultiplexer_5_out18,
       demultiplexer_5_out19, demultiplexer_5_out21, demultiplexer_5_out24, demultiplexer_5_out25,
       demultiplexer_5_out27, demultiplexer_5_out31;
  wire [31:0] cpucm_128b_1_external_access_data, cpucm_128b_1_operand_a, cpucm_128b_1_operand_b,
       cpucm_128b_2_external_access_data, cpucm_128b_2_operand_a, cpucm_128b_2_operand_b,
       cpucm_128b_3_external_access_data, cpucm_128b_3_operand_a, cpucm_128b_3_operand_b,
       cpucm_128b_4_external_access_data, cpucm_128b_4_operand_a, cpucm_128b_4_operand_b,
       cpucm_128b_5_external_access_data, cpucm_128b_5_operand_a, cpucm_128b_5_operand_b,
       cpucm_128b_6_external_access_data, cpucm_128b_6_operand_a, cpucm_128b_6_operand_b,
       cpucm_128b_7_external_access_data, cpucm_128b_7_operand_a, cpucm_128b_7_operand_b,
       cpucm_128b_8_external_access_data, cpucm_128b_8_operand_a, cpucm_128b_8_operand_b,
       cpucm_128b_9_external_access_data, cpucm_128b_9_operand_a, cpucm_128b_9_operand_b,
       cpucm_128b_10_external_access_data, cpucm_128b_10_operand_a, cpucm_128b_10_operand_b,
       cpucm_128b_11_external_access_data, cpucm_128b_11_operand_a, cpucm_128b_11_operand_b,
       cpucm_128b_12_external_access_data, cpucm_128b_12_operand_a, cpucm_128b_12_operand_b,
       cpucm_128b_13_external_access_data, cpucm_128b_13_operand_a, cpucm_128b_13_operand_b,
       cpucm_128b_14_external_access_data, cpucm_128b_14_operand_a, cpucm_128b_14_operand_b,
       cpucm_128b_15_external_access_data, cpucm_128b_15_operand_a, cpucm_128b_15_operand_b,
       cpucm_128b_16_external_access_data, cpucm_128b_16_operand_a, cpucm_128b_16_operand_b,
       cpucm_128b_17_external_access_data, cpucm_128b_17_operand_a, cpucm_128b_17_operand_b,
       cpucm_128b_18_external_access_data, cpucm_128b_18_operand_a, cpucm_128b_18_operand_b,
       cpucm_128b_19_external_access_data, cpucm_128b_19_operand_a, cpucm_128b_19_operand_b,
       cpucm_128b_20_external_access_data, cpucm_128b_20_operand_a, cpucm_128b_20_operand_b,
       cpucm_128b_21_external_access_data, cpucm_128b_21_operand_a, cpucm_128b_21_operand_b,
       cpucm_128b_22_external_access_data, cpucm_128b_22_operand_a, cpucm_128b_22_operand_b,
       cpucm_128b_23_external_access_data, cpucm_128b_23_operand_a, cpucm_128b_23_operand_b,
       cpucm_128b_24_external_access_data, cpucm_128b_24_operand_a, cpucm_128b_24_operand_b,
       cpucm_128b_25_external_access_data, cpucm_128b_25_operand_a, cpucm_128b_25_operand_b,
       cpucm_128b_26_external_access_data, cpucm_128b_26_operand_a, cpucm_128b_26_operand_b,
       cpucm_128b_27_external_access_data, cpucm_128b_27_operand_a, cpucm_128b_27_operand_b,
       cpucm_128b_28_external_access_data, cpucm_128b_28_operand_a, cpucm_128b_28_operand_b,
       cpucm_128b_29_external_access_data, cpucm_128b_29_operand_a, cpucm_128b_29_operand_b,
       cpucm_128b_30_external_access_data, cpucm_128b_30_operand_a, cpucm_128b_30_operand_b,
       cpucm_128b_31_external_access_data, cpucm_128b_31_operand_a, cpucm_128b_31_operand_b,
       cpucm_128b_32_external_access_data, cpucm_128b_32_operand_a, cpucm_128b_32_operand_b,
       cpucm_128b_33_external_access_data, cpucm_128b_33_operand_a, cpucm_128b_33_operand_b,
       cpucm_128b_34_external_access_data, cpucm_128b_34_operand_a, cpucm_128b_34_operand_b,
       cpucm_128b_35_external_access_data, cpucm_128b_35_operand_a, cpucm_128b_35_operand_b,
       cpucm_128b_36_external_access_data, cpucm_128b_36_operand_a, cpucm_128b_36_operand_b,
       cpucm_128b_37_external_access_data, cpucm_128b_37_operand_a, cpucm_128b_37_operand_b,
       cpucm_128b_38_external_access_data, cpucm_128b_38_operand_a, cpucm_128b_38_operand_b,
       cpucm_128b_39_external_access_data, cpucm_128b_39_operand_a, cpucm_128b_39_operand_b,
       cpucm_128b_40_external_access_data, cpucm_128b_40_operand_a, cpucm_128b_40_operand_b,
       cpucm_128b_41_external_access_data, cpucm_128b_41_operand_a, cpucm_128b_41_operand_b,
       cpucm_128b_42_external_access_data, cpucm_128b_42_operand_a, cpucm_128b_42_operand_b,
       cpucm_128b_43_external_access_data, cpucm_128b_43_operand_a, cpucm_128b_43_operand_b,
       cpucm_128b_44_external_access_data, cpucm_128b_44_operand_a, cpucm_128b_44_operand_b,
       cpucm_128b_45_external_access_data, cpucm_128b_45_operand_a, cpucm_128b_45_operand_b,
       cpucm_128b_46_external_access_data, cpucm_128b_46_operand_a, cpucm_128b_46_operand_b,
       cpucm_128b_47_external_access_data, cpucm_128b_47_operand_a, cpucm_128b_47_operand_b,
       cpucm_128b_48_external_access_data, cpucm_128b_48_operand_a, cpucm_128b_48_operand_b,
       cpucm_128b_49_external_access_data, cpucm_128b_49_operand_a, cpucm_128b_49_operand_b,
       cpucm_128b_50_external_access_data, cpucm_128b_50_operand_a, cpucm_128b_50_operand_b,
       cpucm_128b_51_external_access_data, cpucm_128b_51_operand_a, cpucm_128b_51_operand_b,
       cpucm_128b_52_external_access_data, cpucm_128b_52_operand_a, cpucm_128b_52_operand_b,
       cpucm_128b_53_external_access_data, cpucm_128b_53_operand_a, cpucm_128b_53_operand_b,
       cpucm_128b_54_external_access_data, cpucm_128b_54_operand_a, cpucm_128b_54_operand_b,
       cpucm_128b_55_external_access_data, cpucm_128b_55_operand_a, cpucm_128b_55_operand_b,
       cpucm_128b_56_external_access_data, cpucm_128b_56_operand_a, cpucm_128b_56_operand_b,
       cpucm_128b_57_external_access_data, cpucm_128b_57_operand_a, cpucm_128b_57_operand_b,
       cpucm_128b_58_external_access_data, cpucm_128b_58_operand_a, cpucm_128b_58_operand_b,
       cpucm_128b_59_external_access_data, cpucm_128b_59_operand_a, cpucm_128b_59_operand_b,
       cpucm_128b_60_external_access_data, cpucm_128b_60_operand_a, cpucm_128b_60_operand_b,
       cpucm_128b_61_external_access_data, cpucm_128b_61_operand_a, cpucm_128b_61_operand_b,
       cpucm_128b_62_external_access_data, cpucm_128b_62_operand_a, cpucm_128b_62_operand_b,
       cpucm_128b_63_external_access_data, cpucm_128b_63_operand_a, cpucm_128b_63_operand_b,
       cpucm_128b_64_external_access_data, cpucm_128b_64_operand_a, cpucm_128b_64_operand_b,
       cpucm_128b_65_external_access_data, cpucm_128b_65_operand_a, cpucm_128b_65_operand_b,
       cpucm_128b_66_external_access_data, cpucm_128b_66_operand_a, cpucm_128b_66_operand_b,
       cpucm_128b_67_external_access_data, cpucm_128b_67_operand_a, cpucm_128b_67_operand_b,
       cpucm_128b_68_external_access_data, cpucm_128b_68_operand_a, cpucm_128b_68_operand_b,
       cpucm_128b_69_external_access_data, cpucm_128b_69_operand_a, cpucm_128b_69_operand_b,
       cpucm_128b_70_external_access_data, cpucm_128b_70_operand_a, cpucm_128b_70_operand_b,
       cpucm_128b_71_external_access_data, cpucm_128b_71_operand_a, cpucm_128b_71_operand_b,
       cpucm_128b_72_external_access_data, cpucm_128b_72_operand_a, cpucm_128b_72_operand_b,
       cpucm_128b_73_external_access_data, cpucm_128b_73_operand_a, cpucm_128b_73_operand_b,
       cpucm_128b_74_external_access_data, cpucm_128b_74_operand_a, cpucm_128b_74_operand_b,
       cpucm_128b_75_external_access_data, cpucm_128b_75_operand_a, cpucm_128b_75_operand_b,
       cpucm_128b_76_external_access_data, cpucm_128b_76_operand_a, cpucm_128b_76_operand_b,
       cpucm_128b_77_external_access_data, cpucm_128b_77_operand_a, cpucm_128b_77_operand_b,
       cpucm_128b_78_external_access_data, cpucm_128b_78_operand_a, cpucm_128b_78_operand_b,
       cpucm_128b_79_external_access_data, cpucm_128b_79_operand_a, cpucm_128b_79_operand_b,
       cpucm_128b_80_external_access_data, cpucm_128b_80_operand_a, cpucm_128b_80_operand_b,
       cpucm_128b_81_external_access_data, cpucm_128b_81_operand_a, cpucm_128b_81_operand_b,
       cpucm_128b_82_external_access_data, cpucm_128b_82_operand_a, cpucm_128b_82_operand_b,
       cpucm_128b_83_external_access_data, cpucm_128b_83_operand_a, cpucm_128b_83_operand_b,
       cpucm_128b_84_external_access_data, cpucm_128b_84_operand_a, cpucm_128b_84_operand_b,
       cpucm_128b_85_external_access_data, cpucm_128b_85_operand_a, cpucm_128b_85_operand_b,
       cpucm_128b_86_external_access_data, cpucm_128b_86_operand_a, cpucm_128b_86_operand_b,
       cpucm_128b_87_external_access_data, cpucm_128b_87_operand_a, cpucm_128b_87_operand_b,
       cpucm_128b_88_external_access_data, cpucm_128b_88_operand_a, cpucm_128b_88_operand_b,
       cpucm_128b_89_external_access_data, cpucm_128b_89_operand_a, cpucm_128b_89_operand_b,
       cpucm_128b_90_external_access_data, cpucm_128b_90_operand_a, cpucm_128b_90_operand_b,
       cpucm_128b_91_external_access_data, cpucm_128b_91_operand_a, cpucm_128b_91_operand_b,
       cpucm_128b_92_external_access_data, cpucm_128b_92_operand_a, cpucm_128b_92_operand_b,
       cpucm_128b_93_external_access_data, cpucm_128b_93_operand_a, cpucm_128b_93_operand_b,
       cpucm_128b_94_external_access_data, cpucm_128b_94_operand_a, cpucm_128b_94_operand_b,
       cpucm_128b_95_external_access_data, cpucm_128b_95_operand_a, cpucm_128b_95_operand_b,
       cpucm_128b_96_external_access_data, cpucm_128b_96_operand_a, cpucm_128b_96_operand_b,
       cpucm_128b_97_external_access_data, cpucm_128b_97_operand_a, cpucm_128b_97_operand_b,
       cpucm_128b_98_external_access_data, cpucm_128b_98_operand_a, cpucm_128b_98_operand_b,
       cpucm_128b_99_external_access_data, cpucm_128b_99_operand_a, cpucm_128b_99_operand_b,
       cpucm_128b_100_external_access_data, cpucm_128b_100_operand_a, cpucm_128b_100_operand_b,
       cpucm_128b_101_external_access_data, cpucm_128b_101_operand_a, cpucm_128b_101_operand_b,
       cpucm_128b_102_external_access_data, cpucm_128b_102_operand_a, cpucm_128b_102_operand_b,
       cpucm_128b_103_external_access_data, cpucm_128b_103_operand_a, cpucm_128b_103_operand_b,
       cpucm_128b_104_external_access_data, cpucm_128b_104_operand_a, cpucm_128b_104_operand_b,
       cpucm_128b_105_external_access_data, cpucm_128b_105_operand_a, cpucm_128b_105_operand_b,
       cpucm_128b_106_external_access_data, cpucm_128b_106_operand_a, cpucm_128b_106_operand_b,
       cpucm_128b_107_external_access_data, cpucm_128b_107_operand_a, cpucm_128b_107_operand_b,
       cpucm_128b_108_external_access_data, cpucm_128b_108_operand_a, cpucm_128b_108_operand_b,
       cpucm_128b_109_external_access_data, cpucm_128b_109_operand_a, cpucm_128b_109_operand_b,
       cpucm_128b_110_external_access_data, cpucm_128b_110_operand_a, cpucm_128b_110_operand_b,
       cpucm_128b_111_external_access_data, cpucm_128b_111_operand_a, cpucm_128b_111_operand_b,
       cpucm_128b_112_external_access_data, cpucm_128b_112_operand_a, cpucm_128b_112_operand_b,
       cpucm_128b_113_external_access_data, cpucm_128b_113_operand_a, cpucm_128b_113_operand_b,
       cpucm_128b_114_external_access_data, cpucm_128b_114_operand_a, cpucm_128b_114_operand_b,
       cpucm_128b_115_external_access_data, cpucm_128b_115_operand_a, cpucm_128b_115_operand_b,
       cpucm_128b_116_external_access_data, cpucm_128b_116_operand_a, cpucm_128b_116_operand_b,
       cpucm_128b_117_external_access_data, cpucm_128b_117_operand_a, cpucm_128b_117_operand_b,
       cpucm_128b_118_external_access_data, cpucm_128b_118_operand_a, cpucm_128b_118_operand_b,
       cpucm_128b_119_external_access_data, cpucm_128b_119_operand_a, cpucm_128b_119_operand_b,
       cpucm_128b_120_external_access_data, cpucm_128b_120_operand_a, cpucm_128b_120_operand_b,
       cpucm_128b_121_external_access_data, cpucm_128b_121_operand_a, cpucm_128b_121_operand_b,
       cpucm_128b_122_external_access_data, cpucm_128b_122_operand_a, cpucm_128b_122_operand_b,
       cpucm_128b_123_external_access_data, cpucm_128b_123_operand_a, cpucm_128b_123_operand_b,
       cpucm_128b_124_external_access_data, cpucm_128b_124_operand_a, cpucm_128b_124_operand_b,
       cpucm_128b_125_external_access_data, cpucm_128b_125_operand_a, cpucm_128b_125_operand_b,
       cpucm_128b_126_external_access_data, cpucm_128b_126_operand_a, cpucm_128b_126_operand_b,
       cpucm_128b_127_external_access_data, cpucm_128b_127_operand_a, cpucm_128b_127_operand_b,
       cpucm_128b_128_external_access_data, cpucm_128b_128_operand_a, cpucm_128b_128_operand_b,
       multiplexer_2_out, multiplexer_3_out, multiplexer_6_out, multiplexer_7_out, multiplexer_8_out,
       multiplexer_9_out, multiplexer_10_out, multiplexer_11_out, multiplexer_12_out, multiplexer_13_out,
       multiplexer_14_out, multiplexer_15_out;

  Demultiplexer #(.select(2), .width(6), .disabled(0), .enable("false")) demultiplexer_1 (
    .out0(demultiplexer_1_out0), .out1(demultiplexer_1_out1), .out2(demultiplexer_1_out2),
    .out3(demultiplexer_1_out3), .in(operation[5:0]), .sel(operation[12:11]));
  Demultiplexer #(.select(5), .width(6), .disabled(0), .enable("false")) demultiplexer_2 (
    .out0({demultiplexer_2_out0_2, demultiplexer_2_out0[0]}), .out1(demultiplexer_2_out1),
    .out2({demultiplexer_2_out2_2, demultiplexer_2_out2[0]}), .out3(demultiplexer_2_out3),
    .out4({demultiplexer_2_out4_2, demultiplexer_2_out4[0]}),
    .out5({demultiplexer_2_out5_2, demultiplexer_2_out5[0]}),
    .out6({demultiplexer_2_out6_2, demultiplexer_2_out6[0]}), .out7(demultiplexer_2_out7),
    .out8({demultiplexer_2_out8_2, demultiplexer_2_out8[0]}), .out9(demultiplexer_2_out9),
    .out10({demultiplexer_2_out10_2, demultiplexer_2_out10[0]}),
    .out11({demultiplexer_2_out11_2, demultiplexer_2_out11[0]}),
    .out12({demultiplexer_2_out12_2, demultiplexer_2_out12[0]}), .out13(demultiplexer_2_out13),
    .out14({demultiplexer_2_out14_2, demultiplexer_2_out14[0]}), .out15(demultiplexer_2_out15),
    .out16({demultiplexer_2_out16_2, demultiplexer_2_out16[0]}),
    .out17({demultiplexer_2_out17_2, demultiplexer_2_out17[0]}),
    .out18({demultiplexer_2_out18_2, demultiplexer_2_out18[0]}), .out19(demultiplexer_2_out19),
    .out20({demultiplexer_2_out20_2, demultiplexer_2_out20[0]}), .out21(demultiplexer_2_out21),
    .out22(demultiplexer_2_out22), .out23({demultiplexer_2_out23_2, demultiplexer_2_out23[0]}),
    .out24({demultiplexer_2_out24_2, demultiplexer_2_out24[0]}), .out25(demultiplexer_2_out25),
    .out26({demultiplexer_2_out26_2, demultiplexer_2_out26[0]}), .out27(demultiplexer_2_out27),
    .out28(demultiplexer_2_out28), .out29({demultiplexer_2_out29_2, demultiplexer_2_out29[0]}),
    .out30({demultiplexer_2_out30_2, demultiplexer_2_out30[0]}), .out31(demultiplexer_2_out31),
    .in(demultiplexer_1_out0), .sel(operation[10:6]));
  CPUCM_128b cpucm_128b_1 (
    .get_A(get_A[4:0]), .get_B(get_B[4:0]), .External_access_Address(External_access_address[4:0]),
    .clear(clear), .clock(clock), .Operand_A(cpucm_128b_1_operand_a), .Operand_B(cpucm_128b_1_operand_b),
    .External_Access_Data(cpucm_128b_1_external_access_data), .write(demultiplexer_2_out0[0]),
    .get_reg(demultiplexer_2_out0_2), .Data_IN(Data_IN));
  CPUCM_128b cpucm_128b_2 (
    .get_A(get_A[4:0]), .get_B(get_B[4:0]), .External_access_Address(External_access_address[4:0]),
    .clear(clear), .clock(clock), .Operand_A(cpucm_128b_2_operand_a), .Operand_B(cpucm_128b_2_operand_b),
    .External_Access_Data(cpucm_128b_2_external_access_data), .write(demultiplexer_2_out1[0]),
    .get_reg(demultiplexer_2_out1[5:1]), .Data_IN(Data_IN));
  CPUCM_128b cpucm_128b_3 (
    .get_A(get_A[4:0]), .get_B(get_B[4:0]), .External_access_Address(External_access_address[4:0]),
    .clear(clear), .clock(clock), .Operand_A(cpucm_128b_3_operand_a), .Operand_B(cpucm_128b_3_operand_b),
    .External_Access_Data(cpucm_128b_3_external_access_data), .write(demultiplexer_2_out2[0]),
    .get_reg(demultiplexer_2_out2_2), .Data_IN(Data_IN));
  CPUCM_128b cpucm_128b_4 (
    .get_A(get_A[4:0]), .get_B(get_B[4:0]), .External_access_Address(External_access_address[4:0]),
    .clear(clear), .clock(clock), .Operand_A(cpucm_128b_4_operand_a), .Operand_B(cpucm_128b_4_operand_b),
    .External_Access_Data(cpucm_128b_4_external_access_data), .write(demultiplexer_2_out3[0]),
    .get_reg(demultiplexer_2_out3[5:1]), .Data_IN(Data_IN));
  CPUCM_128b cpucm_128b_5 (
    .get_A(get_A[4:0]), .get_B(get_B[4:0]), .External_access_Address(External_access_address[4:0]),
    .clear(clear), .clock(clock), .Operand_A(cpucm_128b_5_operand_a), .Operand_B(cpucm_128b_5_operand_b),
    .External_Access_Data(cpucm_128b_5_external_access_data), .write(demultiplexer_2_out4[0]),
    .get_reg(demultiplexer_2_out4_2), .Data_IN(Data_IN));
  CPUCM_128b cpucm_128b_6 (
    .get_A(get_A[4:0]), .get_B(get_B[4:0]), .External_access_Address(External_access_address[4:0]),
    .clear(clear), .clock(clock), .Operand_A(cpucm_128b_6_operand_a), .Operand_B(cpucm_128b_6_operand_b),
    .External_Access_Data(cpucm_128b_6_external_access_data), .write(demultiplexer_2_out5[0]),
    .get_reg(demultiplexer_2_out5_2), .Data_IN(Data_IN));
  CPUCM_128b cpucm_128b_7 (
    .get_A(get_A[4:0]), .get_B(get_B[4:0]), .External_access_Address(External_access_address[4:0]),
    .clear(clear), .clock(clock), .Operand_A(cpucm_128b_7_operand_a), .Operand_B(cpucm_128b_7_operand_b),
    .External_Access_Data(cpucm_128b_7_external_access_data), .write(demultiplexer_2_out6[0]),
    .get_reg(demultiplexer_2_out6_2), .Data_IN(Data_IN));
  CPUCM_128b cpucm_128b_8 (
    .get_A(get_A[4:0]), .get_B(get_B[4:0]), .External_access_Address(External_access_address[4:0]),
    .clear(clear), .clock(clock), .Operand_A(cpucm_128b_8_operand_a), .Operand_B(cpucm_128b_8_operand_b),
    .External_Access_Data(cpucm_128b_8_external_access_data), .write(demultiplexer_2_out7[0]),
    .get_reg(demultiplexer_2_out7[5:1]), .Data_IN(Data_IN));
  CPUCM_128b cpucm_128b_9 (
    .get_A(get_A[4:0]), .get_B(get_B[4:0]), .External_access_Address(External_access_address[4:0]),
    .clear(clear), .clock(clock), .Operand_A(cpucm_128b_9_operand_a), .Operand_B(cpucm_128b_9_operand_b),
    .External_Access_Data(cpucm_128b_9_external_access_data), .write(demultiplexer_2_out8[0]),
    .get_reg(demultiplexer_2_out8_2), .Data_IN(Data_IN));
  CPUCM_128b cpucm_128b_10 (
    .get_A(get_A[4:0]), .get_B(get_B[4:0]), .External_access_Address(External_access_address[4:0]),
    .clear(clear), .clock(clock), .Operand_A(cpucm_128b_10_operand_a), .Operand_B(cpucm_128b_10_operand_b),
    .External_Access_Data(cpucm_128b_10_external_access_data), .write(demultiplexer_2_out9[0]),
    .get_reg(demultiplexer_2_out9[5:1]), .Data_IN(Data_IN));
  CPUCM_128b cpucm_128b_11 (
    .get_A(get_A[4:0]), .get_B(get_B[4:0]), .External_access_Address(External_access_address[4:0]),
    .clear(clear), .clock(clock), .Operand_A(cpucm_128b_11_operand_a), .Operand_B(cpucm_128b_11_operand_b),
    .External_Access_Data(cpucm_128b_11_external_access_data), .write(demultiplexer_2_out10[0]),
    .get_reg(demultiplexer_2_out10_2), .Data_IN(Data_IN));
  CPUCM_128b cpucm_128b_12 (
    .get_A(get_A[4:0]), .get_B(get_B[4:0]), .External_access_Address(External_access_address[4:0]),
    .clear(clear), .clock(clock), .Operand_A(cpucm_128b_12_operand_a), .Operand_B(cpucm_128b_12_operand_b),
    .External_Access_Data(cpucm_128b_12_external_access_data), .write(demultiplexer_2_out11[0]),
    .get_reg(demultiplexer_2_out11_2), .Data_IN(Data_IN));
  CPUCM_128b cpucm_128b_13 (
    .get_A(get_A[4:0]), .get_B(get_B[4:0]), .External_access_Address(External_access_address[4:0]),
    .clear(clear), .clock(clock), .Operand_A(cpucm_128b_13_operand_a), .Operand_B(cpucm_128b_13_operand_b),
    .External_Access_Data(cpucm_128b_13_external_access_data), .write(demultiplexer_2_out12[0]),
    .get_reg(demultiplexer_2_out12_2), .Data_IN(Data_IN));
  CPUCM_128b cpucm_128b_14 (
    .get_A(get_A[4:0]), .get_B(get_B[4:0]), .External_access_Address(External_access_address[4:0]),
    .clear(clear), .clock(clock), .Operand_A(cpucm_128b_14_operand_a), .Operand_B(cpucm_128b_14_operand_b),
    .External_Access_Data(cpucm_128b_14_external_access_data), .write(demultiplexer_2_out13[0]),
    .get_reg(demultiplexer_2_out13[5:1]), .Data_IN(Data_IN));
  CPUCM_128b cpucm_128b_15 (
    .get_A(get_A[4:0]), .get_B(get_B[4:0]), .External_access_Address(External_access_address[4:0]),
    .clear(clear), .clock(clock), .Operand_A(cpucm_128b_15_operand_a), .Operand_B(cpucm_128b_15_operand_b),
    .External_Access_Data(cpucm_128b_15_external_access_data), .write(demultiplexer_2_out14[0]),
    .get_reg(demultiplexer_2_out14_2), .Data_IN(Data_IN));
  CPUCM_128b cpucm_128b_16 (
    .get_A(get_A[4:0]), .get_B(get_B[4:0]), .External_access_Address(External_access_address[4:0]),
    .clear(clear), .clock(clock), .Operand_A(cpucm_128b_16_operand_a), .Operand_B(cpucm_128b_16_operand_b),
    .External_Access_Data(cpucm_128b_16_external_access_data), .write(demultiplexer_2_out15[0]),
    .get_reg(demultiplexer_2_out15[5:1]), .Data_IN(Data_IN));
  CPUCM_128b cpucm_128b_17 (
    .get_A(get_A[4:0]), .get_B(get_B[4:0]), .External_access_Address(External_access_address[4:0]),
    .clear(clear), .clock(clock), .Operand_A(cpucm_128b_17_operand_a), .Operand_B(cpucm_128b_17_operand_b),
    .External_Access_Data(cpucm_128b_17_external_access_data), .write(demultiplexer_2_out16[0]),
    .get_reg(demultiplexer_2_out16_2), .Data_IN(Data_IN));
  CPUCM_128b cpucm_128b_18 (
    .get_A(get_A[4:0]), .get_B(get_B[4:0]), .External_access_Address(External_access_address[4:0]),
    .clear(clear), .clock(clock), .Operand_A(cpucm_128b_18_operand_a), .Operand_B(cpucm_128b_18_operand_b),
    .External_Access_Data(cpucm_128b_18_external_access_data), .write(demultiplexer_2_out17[0]),
    .get_reg(demultiplexer_2_out17_2), .Data_IN(Data_IN));
  CPUCM_128b cpucm_128b_19 (
    .get_A(get_A[4:0]), .get_B(get_B[4:0]), .External_access_Address(External_access_address[4:0]),
    .clear(clear), .clock(clock), .Operand_A(cpucm_128b_19_operand_a), .Operand_B(cpucm_128b_19_operand_b),
    .External_Access_Data(cpucm_128b_19_external_access_data), .write(demultiplexer_2_out18[0]),
    .get_reg(demultiplexer_2_out18_2), .Data_IN(Data_IN));
  CPUCM_128b cpucm_128b_20 (
    .get_A(get_A[4:0]), .get_B(get_B[4:0]), .External_access_Address(External_access_address[4:0]),
    .clear(clear), .clock(clock), .Operand_A(cpucm_128b_20_operand_a), .Operand_B(cpucm_128b_20_operand_b),
    .External_Access_Data(cpucm_128b_20_external_access_data), .write(demultiplexer_2_out19[0]),
    .get_reg(demultiplexer_2_out19[5:1]), .Data_IN(Data_IN));
  CPUCM_128b cpucm_128b_21 (
    .get_A(get_A[4:0]), .get_B(get_B[4:0]), .External_access_Address(External_access_address[4:0]),
    .clear(clear), .clock(clock), .Operand_A(cpucm_128b_21_operand_a), .Operand_B(cpucm_128b_21_operand_b),
    .External_Access_Data(cpucm_128b_21_external_access_data), .write(demultiplexer_2_out20[0]),
    .get_reg(demultiplexer_2_out20_2), .Data_IN(Data_IN));
  CPUCM_128b cpucm_128b_22 (
    .get_A(get_A[4:0]), .get_B(get_B[4:0]), .External_access_Address(External_access_address[4:0]),
    .clear(clear), .clock(clock), .Operand_A(cpucm_128b_22_operand_a), .Operand_B(cpucm_128b_22_operand_b),
    .External_Access_Data(cpucm_128b_22_external_access_data), .write(demultiplexer_2_out21[0]),
    .get_reg(demultiplexer_2_out21[5:1]), .Data_IN(Data_IN));
  CPUCM_128b cpucm_128b_23 (
    .get_A(get_A[4:0]), .get_B(get_B[4:0]), .External_access_Address(External_access_address[4:0]),
    .clear(clear), .clock(clock), .Operand_A(cpucm_128b_23_operand_a), .Operand_B(cpucm_128b_23_operand_b),
    .External_Access_Data(cpucm_128b_23_external_access_data), .write(demultiplexer_2_out22[0]),
    .get_reg(demultiplexer_2_out22[5:1]), .Data_IN(Data_IN));
  CPUCM_128b cpucm_128b_24 (
    .get_A(get_A[4:0]), .get_B(get_B[4:0]), .External_access_Address(External_access_address[4:0]),
    .clear(clear), .clock(clock), .Operand_A(cpucm_128b_24_operand_a), .Operand_B(cpucm_128b_24_operand_b),
    .External_Access_Data(cpucm_128b_24_external_access_data), .write(demultiplexer_2_out23[0]),
    .get_reg(demultiplexer_2_out23_2), .Data_IN(Data_IN));
  CPUCM_128b cpucm_128b_25 (
    .get_A(get_A[4:0]), .get_B(get_B[4:0]), .External_access_Address(External_access_address[4:0]),
    .clear(clear), .clock(clock), .Operand_A(cpucm_128b_25_operand_a), .Operand_B(cpucm_128b_25_operand_b),
    .External_Access_Data(cpucm_128b_25_external_access_data), .write(demultiplexer_2_out24[0]),
    .get_reg(demultiplexer_2_out24_2), .Data_IN(Data_IN));
  CPUCM_128b cpucm_128b_26 (
    .get_A(get_A[4:0]), .get_B(get_B[4:0]), .External_access_Address(External_access_address[4:0]),
    .clear(clear), .clock(clock), .Operand_A(cpucm_128b_26_operand_a), .Operand_B(cpucm_128b_26_operand_b),
    .External_Access_Data(cpucm_128b_26_external_access_data), .write(demultiplexer_2_out25[0]),
    .get_reg(demultiplexer_2_out25[5:1]), .Data_IN(Data_IN));
  CPUCM_128b cpucm_128b_27 (
    .get_A(get_A[4:0]), .get_B(get_B[4:0]), .External_access_Address(External_access_address[4:0]),
    .clear(clear), .clock(clock), .Operand_A(cpucm_128b_27_operand_a), .Operand_B(cpucm_128b_27_operand_b),
    .External_Access_Data(cpucm_128b_27_external_access_data), .write(demultiplexer_2_out26[0]),
    .get_reg(demultiplexer_2_out26_2), .Data_IN(Data_IN));
  CPUCM_128b cpucm_128b_28 (
    .get_A(get_A[4:0]), .get_B(get_B[4:0]), .External_access_Address(External_access_address[4:0]),
    .clear(clear), .clock(clock), .Operand_A(cpucm_128b_28_operand_a), .Operand_B(cpucm_128b_28_operand_b),
    .External_Access_Data(cpucm_128b_28_external_access_data), .write(demultiplexer_2_out27[0]),
    .get_reg(demultiplexer_2_out27[5:1]), .Data_IN(Data_IN));
  CPUCM_128b cpucm_128b_29 (
    .get_A(get_A[4:0]), .get_B(get_B[4:0]), .External_access_Address(External_access_address[4:0]),
    .clear(clear), .clock(clock), .Operand_A(cpucm_128b_29_operand_a), .Operand_B(cpucm_128b_29_operand_b),
    .External_Access_Data(cpucm_128b_29_external_access_data), .write(demultiplexer_2_out28[0]),
    .get_reg(demultiplexer_2_out28[5:1]), .Data_IN(Data_IN));
  CPUCM_128b cpucm_128b_30 (
    .get_A(get_A[4:0]), .get_B(get_B[4:0]), .External_access_Address(External_access_address[4:0]),
    .clear(clear), .clock(clock), .Operand_A(cpucm_128b_30_operand_a), .Operand_B(cpucm_128b_30_operand_b),
    .External_Access_Data(cpucm_128b_30_external_access_data), .write(demultiplexer_2_out29[0]),
    .get_reg(demultiplexer_2_out29_2), .Data_IN(Data_IN));
  CPUCM_128b cpucm_128b_31 (
    .get_A(get_A[4:0]), .get_B(get_B[4:0]), .External_access_Address(External_access_address[4:0]),
    .clear(clear), .clock(clock), .Operand_A(cpucm_128b_31_operand_a), .Operand_B(cpucm_128b_31_operand_b),
    .External_Access_Data(cpucm_128b_31_external_access_data), .write(demultiplexer_2_out30[0]),
    .get_reg(demultiplexer_2_out30_2), .Data_IN(Data_IN));
  CPUCM_128b cpucm_128b_32 (
    .get_A(get_A[4:0]), .get_B(get_B[4:0]), .External_access_Address(External_access_address[4:0]),
    .clear(clear), .clock(clock), .Operand_A(cpucm_128b_32_operand_a), .Operand_B(cpucm_128b_32_operand_b),
    .External_Access_Data(cpucm_128b_32_external_access_data), .write(demultiplexer_2_out31[0]),
    .get_reg(demultiplexer_2_out31[5:1]), .Data_IN(Data_IN));
  Multiplexer #(.select(2), .width(32), .disabled(0), .enable("false")) multiplexer_1 (
    .in0(multiplexer_2_out), .in1(multiplexer_7_out), .in2(multiplexer_10_out), .in3(multiplexer_13_out),
    .out(Operand_A), .sel(get_A[11:10]));
  Multiplexer #(.select(5), .width(32), .disabled(0), .enable("false")) multiplexer_2 (
    .in0(cpucm_128b_1_operand_a), .in1(cpucm_128b_2_operand_a), .in2(cpucm_128b_3_operand_a),
    .in3(cpucm_128b_4_operand_a), .in4(cpucm_128b_5_operand_a), .in5(cpucm_128b_6_operand_a),
    .in6(cpucm_128b_7_operand_a), .in7(cpucm_128b_8_operand_a), .in8(cpucm_128b_9_operand_a),
    .in9(cpucm_128b_10_operand_a), .in10(cpucm_128b_11_operand_a), .in11(cpucm_128b_12_operand_a),
    .in12(cpucm_128b_13_operand_a), .in13(cpucm_128b_14_operand_a), .in14(cpucm_128b_15_operand_a),
    .in15(cpucm_128b_16_operand_a), .in16(cpucm_128b_17_operand_a), .in17(cpucm_128b_18_operand_a),
    .in18(cpucm_128b_19_operand_a), .in19(cpucm_128b_20_operand_a), .in20(cpucm_128b_21_operand_a),
    .in21(cpucm_128b_22_operand_a), .in22(cpucm_128b_23_operand_a), .in23(cpucm_128b_24_operand_a),
    .in24(cpucm_128b_25_operand_a), .in25(cpucm_128b_26_operand_a), .in26(cpucm_128b_27_operand_a),
    .in27(cpucm_128b_28_operand_a), .in28(cpucm_128b_29_operand_a), .in29(cpucm_128b_30_operand_a),
    .in30(cpucm_128b_31_operand_a), .in31(cpucm_128b_32_operand_a), .out(multiplexer_2_out), .sel(get_A[9:5]));
  Multiplexer #(.select(5), .width(32), .disabled(0), .enable("false")) multiplexer_3 (
    .in0(cpucm_128b_1_operand_b), .in1(cpucm_128b_2_operand_b), .in2(cpucm_128b_3_operand_b),
    .in3(cpucm_128b_4_operand_b), .in4(cpucm_128b_5_operand_b), .in5(cpucm_128b_6_operand_b),
    .in6(cpucm_128b_7_operand_b), .in7(cpucm_128b_8_operand_b), .in8(cpucm_128b_9_operand_b),
    .in9(cpucm_128b_10_operand_b), .in10(cpucm_128b_11_operand_b), .in11(cpucm_128b_12_operand_b),
    .in12(cpucm_128b_13_operand_b), .in13(cpucm_128b_14_operand_b), .in14(cpucm_128b_15_operand_b),
    .in15(cpucm_128b_16_operand_b), .in16(cpucm_128b_17_operand_b), .in17(cpucm_128b_18_operand_b),
    .in18(cpucm_128b_19_operand_b), .in19(cpucm_128b_20_operand_b), .in20(cpucm_128b_21_operand_b),
    .in21(cpucm_128b_22_operand_b), .in22(cpucm_128b_23_operand_b), .in23(cpucm_128b_24_operand_b),
    .in24(cpucm_128b_25_operand_b), .in25(cpucm_128b_26_operand_b), .in26(cpucm_128b_27_operand_b),
    .in27(cpucm_128b_28_operand_b), .in28(cpucm_128b_29_operand_b), .in29(cpucm_128b_30_operand_b),
    .in30(cpucm_128b_31_operand_b), .in31(cpucm_128b_32_operand_b), .out(multiplexer_3_out), .sel(get_B[9:5]));
  Multiplexer #(.select(2), .width(32), .disabled(0), .enable("false")) multiplexer_4 (
    .in0(multiplexer_3_out), .in1(multiplexer_8_out), .in2(multiplexer_11_out), .in3(multiplexer_14_out),
    .out(Operand_B), .sel(get_B[11:10]));
  Multiplexer #(.select(2), .width(32), .disabled(0), .enable("false")) multiplexer_5 (
    .in0(multiplexer_6_out), .in1(multiplexer_9_out), .in2(multiplexer_12_out), .in3(multiplexer_15_out),
    .out(External_Access_Data), .sel(External_access_address[11:10]));
  Multiplexer #(.select(5), .width(32), .disabled(0), .enable("false")) multiplexer_6 (
    .in0(cpucm_128b_1_external_access_data), .in1(cpucm_128b_2_external_access_data),
    .in2(cpucm_128b_3_external_access_data), .in3(cpucm_128b_4_external_access_data),
    .in4(cpucm_128b_5_external_access_data), .in5(cpucm_128b_6_external_access_data),
    .in6(cpucm_128b_7_external_access_data), .in7(cpucm_128b_8_external_access_data),
    .in8(cpucm_128b_9_external_access_data), .in9(cpucm_128b_10_external_access_data),
    .in10(cpucm_128b_11_external_access_data), .in11(cpucm_128b_12_external_access_data),
    .in12(cpucm_128b_13_external_access_data), .in13(cpucm_128b_14_external_access_data),
    .in14(cpucm_128b_15_external_access_data), .in15(cpucm_128b_16_external_access_data),
    .in16(cpucm_128b_17_external_access_data), .in17(cpucm_128b_18_external_access_data),
    .in18(cpucm_128b_19_external_access_data), .in19(cpucm_128b_20_external_access_data),
    .in20(cpucm_128b_21_external_access_data), .in21(cpucm_128b_22_external_access_data),
    .in22(cpucm_128b_23_external_access_data), .in23(cpucm_128b_24_external_access_data),
    .in24(cpucm_128b_25_external_access_data), .in25(cpucm_128b_26_external_access_data),
    .in26(cpucm_128b_27_external_access_data), .in27(cpucm_128b_28_external_access_data),
    .in28(cpucm_128b_29_external_access_data), .in29(cpucm_128b_30_external_access_data),
    .in30(cpucm_128b_31_external_access_data), .in31(cpucm_128b_32_external_access_data),
    .out(multiplexer_6_out), .sel(External_access_address[9:5]));
  Demultiplexer #(.select(5), .width(6), .disabled(0), .enable("false")) demultiplexer_3 (
    .out0({demultiplexer_3_out0_2, demultiplexer_3_out0[0]}),
    .out1({demultiplexer_3_out1_2, demultiplexer_3_out1[0]}), .out2(demultiplexer_3_out2),
    .out3({demultiplexer_3_out3_2, demultiplexer_3_out3[0]}), .out4(demultiplexer_3_out4),
    .out5({demultiplexer_3_out5_2, demultiplexer_3_out5[0]}), .out6(demultiplexer_3_out6),
    .out7(demultiplexer_3_out7), .out8(demultiplexer_3_out8), .out9(demultiplexer_3_out9),
    .out10(demultiplexer_3_out10), .out11({demultiplexer_3_out11_2, demultiplexer_3_out11[0]}),
    .out12(demultiplexer_3_out12), .out13({demultiplexer_3_out13_2, demultiplexer_3_out13[0]}),
    .out14(demultiplexer_3_out14), .out15({demultiplexer_3_out15_2, demultiplexer_3_out15[0]}),
    .out16(demultiplexer_3_out16), .out17({demultiplexer_3_out17_2, demultiplexer_3_out17[0]}),
    .out18(demultiplexer_3_out18), .out19({demultiplexer_3_out19_2, demultiplexer_3_out19[0]}),
    .out20(demultiplexer_3_out20), .out21({demultiplexer_3_out21_2, demultiplexer_3_out21[0]}),
    .out22(demultiplexer_3_out22), .out23({demultiplexer_3_out23_2, demultiplexer_3_out23[0]}),
    .out24(demultiplexer_3_out24), .out25({demultiplexer_3_out25_2, demultiplexer_3_out25[0]}),
    .out26(demultiplexer_3_out26), .out27({demultiplexer_3_out27_2, demultiplexer_3_out27[0]}),
    .out28(demultiplexer_3_out28), .out29(demultiplexer_3_out29), .out30(demultiplexer_3_out30),
    .out31(demultiplexer_3_out31), .in(demultiplexer_1_out1), .sel(operation[10:6]));
  CPUCM_128b cpucm_128b_33 (
    .get_A(get_A[4:0]), .get_B(get_B[4:0]), .External_access_Address(External_access_address[4:0]),
    .clear(clear), .clock(clock), .Operand_A(cpucm_128b_33_operand_a), .Operand_B(cpucm_128b_33_operand_b),
    .External_Access_Data(cpucm_128b_33_external_access_data), .write(demultiplexer_3_out0[0]),
    .get_reg(demultiplexer_3_out0_2), .Data_IN(Data_IN));
  CPUCM_128b cpucm_128b_34 (
    .get_A(get_A[4:0]), .get_B(get_B[4:0]), .External_access_Address(External_access_address[4:0]),
    .clear(clear), .clock(clock), .Operand_A(cpucm_128b_34_operand_a), .Operand_B(cpucm_128b_34_operand_b),
    .External_Access_Data(cpucm_128b_34_external_access_data), .write(demultiplexer_3_out1[0]),
    .get_reg(demultiplexer_3_out1_2), .Data_IN(Data_IN));
  CPUCM_128b cpucm_128b_35 (
    .get_A(get_A[4:0]), .get_B(get_B[4:0]), .External_access_Address(External_access_address[4:0]),
    .clear(clear), .clock(clock), .Operand_A(cpucm_128b_35_operand_a), .Operand_B(cpucm_128b_35_operand_b),
    .External_Access_Data(cpucm_128b_35_external_access_data), .write(demultiplexer_3_out2[0]),
    .get_reg(demultiplexer_3_out2[5:1]), .Data_IN(Data_IN));
  CPUCM_128b cpucm_128b_36 (
    .get_A(get_A[4:0]), .get_B(get_B[4:0]), .External_access_Address(External_access_address[4:0]),
    .clear(clear), .clock(clock), .Operand_A(cpucm_128b_36_operand_a), .Operand_B(cpucm_128b_36_operand_b),
    .External_Access_Data(cpucm_128b_36_external_access_data), .write(demultiplexer_3_out3[0]),
    .get_reg(demultiplexer_3_out3_2), .Data_IN(Data_IN));
  CPUCM_128b cpucm_128b_37 (
    .get_A(get_A[4:0]), .get_B(get_B[4:0]), .External_access_Address(External_access_address[4:0]),
    .clear(clear), .clock(clock), .Operand_A(cpucm_128b_37_operand_a), .Operand_B(cpucm_128b_37_operand_b),
    .External_Access_Data(cpucm_128b_37_external_access_data), .write(demultiplexer_3_out4[0]),
    .get_reg(demultiplexer_3_out4[5:1]), .Data_IN(Data_IN));
  CPUCM_128b cpucm_128b_38 (
    .get_A(get_A[4:0]), .get_B(get_B[4:0]), .External_access_Address(External_access_address[4:0]),
    .clear(clear), .clock(clock), .Operand_A(cpucm_128b_38_operand_a), .Operand_B(cpucm_128b_38_operand_b),
    .External_Access_Data(cpucm_128b_38_external_access_data), .write(demultiplexer_3_out5[0]),
    .get_reg(demultiplexer_3_out5_2), .Data_IN(Data_IN));
  CPUCM_128b cpucm_128b_39 (
    .get_A(get_A[4:0]), .get_B(get_B[4:0]), .External_access_Address(External_access_address[4:0]),
    .clear(clear), .clock(clock), .Operand_A(cpucm_128b_39_operand_a), .Operand_B(cpucm_128b_39_operand_b),
    .External_Access_Data(cpucm_128b_39_external_access_data), .write(demultiplexer_3_out6[0]),
    .get_reg(demultiplexer_3_out6[5:1]), .Data_IN(Data_IN));
  CPUCM_128b cpucm_128b_40 (
    .get_A(get_A[4:0]), .get_B(get_B[4:0]), .External_access_Address(External_access_address[4:0]),
    .clear(clear), .clock(clock), .Operand_A(cpucm_128b_40_operand_a), .Operand_B(cpucm_128b_40_operand_b),
    .External_Access_Data(cpucm_128b_40_external_access_data), .write(demultiplexer_3_out7[0]),
    .get_reg(demultiplexer_3_out7[5:1]), .Data_IN(Data_IN));
  CPUCM_128b cpucm_128b_41 (
    .get_A(get_A[4:0]), .get_B(get_B[4:0]), .External_access_Address(External_access_address[4:0]),
    .clear(clear), .clock(clock), .Operand_A(cpucm_128b_41_operand_a), .Operand_B(cpucm_128b_41_operand_b),
    .External_Access_Data(cpucm_128b_41_external_access_data), .write(demultiplexer_3_out8[0]),
    .get_reg(demultiplexer_3_out8[5:1]), .Data_IN(Data_IN));
  CPUCM_128b cpucm_128b_42 (
    .get_A(get_A[4:0]), .get_B(get_B[4:0]), .External_access_Address(External_access_address[4:0]),
    .clear(clear), .clock(clock), .Operand_A(cpucm_128b_42_operand_a), .Operand_B(cpucm_128b_42_operand_b),
    .External_Access_Data(cpucm_128b_42_external_access_data), .write(demultiplexer_3_out9[0]),
    .get_reg(demultiplexer_3_out9[5:1]), .Data_IN(Data_IN));
  CPUCM_128b cpucm_128b_43 (
    .get_A(get_A[4:0]), .get_B(get_B[4:0]), .External_access_Address(External_access_address[4:0]),
    .clear(clear), .clock(clock), .Operand_A(cpucm_128b_43_operand_a), .Operand_B(cpucm_128b_43_operand_b),
    .External_Access_Data(cpucm_128b_43_external_access_data), .write(demultiplexer_3_out10[0]),
    .get_reg(demultiplexer_3_out10[5:1]), .Data_IN(Data_IN));
  CPUCM_128b cpucm_128b_44 (
    .get_A(get_A[4:0]), .get_B(get_B[4:0]), .External_access_Address(External_access_address[4:0]),
    .clear(clear), .clock(clock), .Operand_A(cpucm_128b_44_operand_a), .Operand_B(cpucm_128b_44_operand_b),
    .External_Access_Data(cpucm_128b_44_external_access_data), .write(demultiplexer_3_out11[0]),
    .get_reg(demultiplexer_3_out11_2), .Data_IN(Data_IN));
  CPUCM_128b cpucm_128b_45 (
    .get_A(get_A[4:0]), .get_B(get_B[4:0]), .External_access_Address(External_access_address[4:0]),
    .clear(clear), .clock(clock), .Operand_A(cpucm_128b_45_operand_a), .Operand_B(cpucm_128b_45_operand_b),
    .External_Access_Data(cpucm_128b_45_external_access_data), .write(demultiplexer_3_out12[0]),
    .get_reg(demultiplexer_3_out12[5:1]), .Data_IN(Data_IN));
  CPUCM_128b cpucm_128b_46 (
    .get_A(get_A[4:0]), .get_B(get_B[4:0]), .External_access_Address(External_access_address[4:0]),
    .clear(clear), .clock(clock), .Operand_A(cpucm_128b_46_operand_a), .Operand_B(cpucm_128b_46_operand_b),
    .External_Access_Data(cpucm_128b_46_external_access_data), .write(demultiplexer_3_out13[0]),
    .get_reg(demultiplexer_3_out13_2), .Data_IN(Data_IN));
  CPUCM_128b cpucm_128b_47 (
    .get_A(get_A[4:0]), .get_B(get_B[4:0]), .External_access_Address(External_access_address[4:0]),
    .clear(clear), .clock(clock), .Operand_A(cpucm_128b_47_operand_a), .Operand_B(cpucm_128b_47_operand_b),
    .External_Access_Data(cpucm_128b_47_external_access_data), .write(demultiplexer_3_out14[0]),
    .get_reg(demultiplexer_3_out14[5:1]), .Data_IN(Data_IN));
  CPUCM_128b cpucm_128b_48 (
    .get_A(get_A[4:0]), .get_B(get_B[4:0]), .External_access_Address(External_access_address[4:0]),
    .clear(clear), .clock(clock), .Operand_A(cpucm_128b_48_operand_a), .Operand_B(cpucm_128b_48_operand_b),
    .External_Access_Data(cpucm_128b_48_external_access_data), .write(demultiplexer_3_out15[0]),
    .get_reg(demultiplexer_3_out15_2), .Data_IN(Data_IN));
  CPUCM_128b cpucm_128b_49 (
    .get_A(get_A[4:0]), .get_B(get_B[4:0]), .External_access_Address(External_access_address[4:0]),
    .clear(clear), .clock(clock), .Operand_A(cpucm_128b_49_operand_a), .Operand_B(cpucm_128b_49_operand_b),
    .External_Access_Data(cpucm_128b_49_external_access_data), .write(demultiplexer_3_out16[0]),
    .get_reg(demultiplexer_3_out16[5:1]), .Data_IN(Data_IN));
  CPUCM_128b cpucm_128b_50 (
    .get_A(get_A[4:0]), .get_B(get_B[4:0]), .External_access_Address(External_access_address[4:0]),
    .clear(clear), .clock(clock), .Operand_A(cpucm_128b_50_operand_a), .Operand_B(cpucm_128b_50_operand_b),
    .External_Access_Data(cpucm_128b_50_external_access_data), .write(demultiplexer_3_out17[0]),
    .get_reg(demultiplexer_3_out17_2), .Data_IN(Data_IN));
  CPUCM_128b cpucm_128b_51 (
    .get_A(get_A[4:0]), .get_B(get_B[4:0]), .External_access_Address(External_access_address[4:0]),
    .clear(clear), .clock(clock), .Operand_A(cpucm_128b_51_operand_a), .Operand_B(cpucm_128b_51_operand_b),
    .External_Access_Data(cpucm_128b_51_external_access_data), .write(demultiplexer_3_out18[0]),
    .get_reg(demultiplexer_3_out18[5:1]), .Data_IN(Data_IN));
  CPUCM_128b cpucm_128b_52 (
    .get_A(get_A[4:0]), .get_B(get_B[4:0]), .External_access_Address(External_access_address[4:0]),
    .clear(clear), .clock(clock), .Operand_A(cpucm_128b_52_operand_a), .Operand_B(cpucm_128b_52_operand_b),
    .External_Access_Data(cpucm_128b_52_external_access_data), .write(demultiplexer_3_out19[0]),
    .get_reg(demultiplexer_3_out19_2), .Data_IN(Data_IN));
  CPUCM_128b cpucm_128b_53 (
    .get_A(get_A[4:0]), .get_B(get_B[4:0]), .External_access_Address(External_access_address[4:0]),
    .clear(clear), .clock(clock), .Operand_A(cpucm_128b_53_operand_a), .Operand_B(cpucm_128b_53_operand_b),
    .External_Access_Data(cpucm_128b_53_external_access_data), .write(demultiplexer_3_out20[0]),
    .get_reg(demultiplexer_3_out20[5:1]), .Data_IN(Data_IN));
  CPUCM_128b cpucm_128b_54 (
    .get_A(get_A[4:0]), .get_B(get_B[4:0]), .External_access_Address(External_access_address[4:0]),
    .clear(clear), .clock(clock), .Operand_A(cpucm_128b_54_operand_a), .Operand_B(cpucm_128b_54_operand_b),
    .External_Access_Data(cpucm_128b_54_external_access_data), .write(demultiplexer_3_out21[0]),
    .get_reg(demultiplexer_3_out21_2), .Data_IN(Data_IN));
  CPUCM_128b cpucm_128b_55 (
    .get_A(get_A[4:0]), .get_B(get_B[4:0]), .External_access_Address(External_access_address[4:0]),
    .clear(clear), .clock(clock), .Operand_A(cpucm_128b_55_operand_a), .Operand_B(cpucm_128b_55_operand_b),
    .External_Access_Data(cpucm_128b_55_external_access_data), .write(demultiplexer_3_out22[0]),
    .get_reg(demultiplexer_3_out22[5:1]), .Data_IN(Data_IN));
  CPUCM_128b cpucm_128b_56 (
    .get_A(get_A[4:0]), .get_B(get_B[4:0]), .External_access_Address(External_access_address[4:0]),
    .clear(clear), .clock(clock), .Operand_A(cpucm_128b_56_operand_a), .Operand_B(cpucm_128b_56_operand_b),
    .External_Access_Data(cpucm_128b_56_external_access_data), .write(demultiplexer_3_out23[0]),
    .get_reg(demultiplexer_3_out23_2), .Data_IN(Data_IN));
  CPUCM_128b cpucm_128b_57 (
    .get_A(get_A[4:0]), .get_B(get_B[4:0]), .External_access_Address(External_access_address[4:0]),
    .clear(clear), .clock(clock), .Operand_A(cpucm_128b_57_operand_a), .Operand_B(cpucm_128b_57_operand_b),
    .External_Access_Data(cpucm_128b_57_external_access_data), .write(demultiplexer_3_out24[0]),
    .get_reg(demultiplexer_3_out24[5:1]), .Data_IN(Data_IN));
  CPUCM_128b cpucm_128b_58 (
    .get_A(get_A[4:0]), .get_B(get_B[4:0]), .External_access_Address(External_access_address[4:0]),
    .clear(clear), .clock(clock), .Operand_A(cpucm_128b_58_operand_a), .Operand_B(cpucm_128b_58_operand_b),
    .External_Access_Data(cpucm_128b_58_external_access_data), .write(demultiplexer_3_out25[0]),
    .get_reg(demultiplexer_3_out25_2), .Data_IN(Data_IN));
  CPUCM_128b cpucm_128b_59 (
    .get_A(get_A[4:0]), .get_B(get_B[4:0]), .External_access_Address(External_access_address[4:0]),
    .clear(clear), .clock(clock), .Operand_A(cpucm_128b_59_operand_a), .Operand_B(cpucm_128b_59_operand_b),
    .External_Access_Data(cpucm_128b_59_external_access_data), .write(demultiplexer_3_out26[0]),
    .get_reg(demultiplexer_3_out26[5:1]), .Data_IN(Data_IN));
  CPUCM_128b cpucm_128b_60 (
    .get_A(get_A[4:0]), .get_B(get_B[4:0]), .External_access_Address(External_access_address[4:0]),
    .clear(clear), .clock(clock), .Operand_A(cpucm_128b_60_operand_a), .Operand_B(cpucm_128b_60_operand_b),
    .External_Access_Data(cpucm_128b_60_external_access_data), .write(demultiplexer_3_out27[0]),
    .get_reg(demultiplexer_3_out27_2), .Data_IN(Data_IN));
  CPUCM_128b cpucm_128b_61 (
    .get_A(get_A[4:0]), .get_B(get_B[4:0]), .External_access_Address(External_access_address[4:0]),
    .clear(clear), .clock(clock), .Operand_A(cpucm_128b_61_operand_a), .Operand_B(cpucm_128b_61_operand_b),
    .External_Access_Data(cpucm_128b_61_external_access_data), .write(demultiplexer_3_out28[0]),
    .get_reg(demultiplexer_3_out28[5:1]), .Data_IN(Data_IN));
  CPUCM_128b cpucm_128b_62 (
    .get_A(get_A[4:0]), .get_B(get_B[4:0]), .External_access_Address(External_access_address[4:0]),
    .clear(clear), .clock(clock), .Operand_A(cpucm_128b_62_operand_a), .Operand_B(cpucm_128b_62_operand_b),
    .External_Access_Data(cpucm_128b_62_external_access_data), .write(demultiplexer_3_out29[0]),
    .get_reg(demultiplexer_3_out29[5:1]), .Data_IN(Data_IN));
  CPUCM_128b cpucm_128b_63 (
    .get_A(get_A[4:0]), .get_B(get_B[4:0]), .External_access_Address(External_access_address[4:0]),
    .clear(clear), .clock(clock), .Operand_A(cpucm_128b_63_operand_a), .Operand_B(cpucm_128b_63_operand_b),
    .External_Access_Data(cpucm_128b_63_external_access_data), .write(demultiplexer_3_out30[0]),
    .get_reg(demultiplexer_3_out30[5:1]), .Data_IN(Data_IN));
  CPUCM_128b cpucm_128b_64 (
    .get_A(get_A[4:0]), .get_B(get_B[4:0]), .External_access_Address(External_access_address[4:0]),
    .clear(clear), .clock(clock), .Operand_A(cpucm_128b_64_operand_a), .Operand_B(cpucm_128b_64_operand_b),
    .External_Access_Data(cpucm_128b_64_external_access_data), .write(demultiplexer_3_out31[0]),
    .get_reg(demultiplexer_3_out31[5:1]), .Data_IN(Data_IN));
  Multiplexer #(.select(5), .width(32), .disabled(0), .enable("false")) multiplexer_7 (
    .in0(cpucm_128b_33_operand_a), .in1(cpucm_128b_34_operand_a), .in2(cpucm_128b_35_operand_a),
    .in3(cpucm_128b_36_operand_a), .in4(cpucm_128b_37_operand_a), .in5(cpucm_128b_38_operand_a),
    .in6(cpucm_128b_39_operand_a), .in7(cpucm_128b_40_operand_a), .in8(cpucm_128b_41_operand_a),
    .in9(cpucm_128b_42_operand_a), .in10(cpucm_128b_43_operand_a), .in11(cpucm_128b_44_operand_a),
    .in12(cpucm_128b_45_operand_a), .in13(cpucm_128b_46_operand_a), .in14(cpucm_128b_47_operand_a),
    .in15(cpucm_128b_48_operand_a), .in16(cpucm_128b_49_operand_a), .in17(cpucm_128b_50_operand_a),
    .in18(cpucm_128b_51_operand_a), .in19(cpucm_128b_52_operand_a), .in20(cpucm_128b_53_operand_a),
    .in21(cpucm_128b_54_operand_a), .in22(cpucm_128b_55_operand_a), .in23(cpucm_128b_56_operand_a),
    .in24(cpucm_128b_57_operand_a), .in25(cpucm_128b_58_operand_a), .in26(cpucm_128b_59_operand_a),
    .in27(cpucm_128b_60_operand_a), .in28(cpucm_128b_61_operand_a), .in29(cpucm_128b_62_operand_a),
    .in30(cpucm_128b_63_operand_a), .in31(cpucm_128b_64_operand_a), .out(multiplexer_7_out), .sel(get_A[9:5]));
  Multiplexer #(.select(5), .width(32), .disabled(0), .enable("false")) multiplexer_8 (
    .in0(cpucm_128b_33_operand_b), .in1(cpucm_128b_34_operand_b), .in2(cpucm_128b_35_operand_b),
    .in3(cpucm_128b_36_operand_b), .in4(cpucm_128b_37_operand_b), .in5(cpucm_128b_38_operand_b),
    .in6(cpucm_128b_39_operand_b), .in7(cpucm_128b_40_operand_b), .in8(cpucm_128b_41_operand_b),
    .in9(cpucm_128b_42_operand_b), .in10(cpucm_128b_43_operand_b), .in11(cpucm_128b_44_operand_b),
    .in12(cpucm_128b_45_operand_b), .in13(cpucm_128b_46_operand_b), .in14(cpucm_128b_47_operand_b),
    .in15(cpucm_128b_48_operand_b), .in16(cpucm_128b_49_operand_b), .in17(cpucm_128b_50_operand_b),
    .in18(cpucm_128b_51_operand_b), .in19(cpucm_128b_52_operand_b), .in20(cpucm_128b_53_operand_b),
    .in21(cpucm_128b_54_operand_b), .in22(cpucm_128b_55_operand_b), .in23(cpucm_128b_56_operand_b),
    .in24(cpucm_128b_57_operand_b), .in25(cpucm_128b_58_operand_b), .in26(cpucm_128b_59_operand_b),
    .in27(cpucm_128b_60_operand_b), .in28(cpucm_128b_61_operand_b), .in29(cpucm_128b_62_operand_b),
    .in30(cpucm_128b_63_operand_b), .in31(cpucm_128b_64_operand_b), .out(multiplexer_8_out), .sel(get_B[9:5]));
  Multiplexer #(.select(5), .width(32), .disabled(0), .enable("false")) multiplexer_9 (
    .in0(cpucm_128b_33_external_access_data), .in1(cpucm_128b_34_external_access_data),
    .in2(cpucm_128b_35_external_access_data), .in3(cpucm_128b_36_external_access_data),
    .in4(cpucm_128b_37_external_access_data), .in5(cpucm_128b_38_external_access_data),
    .in6(cpucm_128b_39_external_access_data), .in7(cpucm_128b_40_external_access_data),
    .in8(cpucm_128b_41_external_access_data), .in9(cpucm_128b_42_external_access_data),
    .in10(cpucm_128b_43_external_access_data), .in11(cpucm_128b_44_external_access_data),
    .in12(cpucm_128b_45_external_access_data), .in13(cpucm_128b_46_external_access_data),
    .in14(cpucm_128b_47_external_access_data), .in15(cpucm_128b_48_external_access_data),
    .in16(cpucm_128b_49_external_access_data), .in17(cpucm_128b_50_external_access_data),
    .in18(cpucm_128b_51_external_access_data), .in19(cpucm_128b_52_external_access_data),
    .in20(cpucm_128b_53_external_access_data), .in21(cpucm_128b_54_external_access_data),
    .in22(cpucm_128b_55_external_access_data), .in23(cpucm_128b_56_external_access_data),
    .in24(cpucm_128b_57_external_access_data), .in25(cpucm_128b_58_external_access_data),
    .in26(cpucm_128b_59_external_access_data), .in27(cpucm_128b_60_external_access_data),
    .in28(cpucm_128b_61_external_access_data), .in29(cpucm_128b_62_external_access_data),
    .in30(cpucm_128b_63_external_access_data), .in31(cpucm_128b_64_external_access_data),
    .out(multiplexer_9_out), .sel(External_access_address[9:5]));
  Demultiplexer #(.select(5), .width(6), .disabled(0), .enable("false")) demultiplexer_4 (
    .out0({demultiplexer_4_out0_2, demultiplexer_4_out0[0]}), .out1(demultiplexer_4_out1),
    .out2({demultiplexer_4_out2_2, demultiplexer_4_out2[0]}), .out3(demultiplexer_4_out3),
    .out4({demultiplexer_4_out4_2, demultiplexer_4_out4[0]}),
    .out5({demultiplexer_4_out5_2, demultiplexer_4_out5[0]}),
    .out6({demultiplexer_4_out6_2, demultiplexer_4_out6[0]}),
    .out7({demultiplexer_4_out7_2, demultiplexer_4_out7[0]}),
    .out8({demultiplexer_4_out8_2, demultiplexer_4_out8[0]}), .out9(demultiplexer_4_out9),
    .out10({demultiplexer_4_out10_2, demultiplexer_4_out10[0]}),
    .out11({demultiplexer_4_out11_2, demultiplexer_4_out11[0]}),
    .out12({demultiplexer_4_out12_2, demultiplexer_4_out12[0]}),
    .out13({demultiplexer_4_out13_2, demultiplexer_4_out13[0]}),
    .out14({demultiplexer_4_out14_2, demultiplexer_4_out14[0]}), .out15(demultiplexer_4_out15),
    .out16({demultiplexer_4_out16_2, demultiplexer_4_out16[0]}),
    .out17({demultiplexer_4_out17_2, demultiplexer_4_out17[0]}), .out18(demultiplexer_4_out18),
    .out19({demultiplexer_4_out19_2, demultiplexer_4_out19[0]}), .out20(demultiplexer_4_out20),
    .out21(demultiplexer_4_out21), .out22(demultiplexer_4_out22),
    .out23({demultiplexer_4_out23_2, demultiplexer_4_out23[0]}), .out24(demultiplexer_4_out24),
    .out25({demultiplexer_4_out25_2, demultiplexer_4_out25[0]}), .out26(demultiplexer_4_out26),
    .out27(demultiplexer_4_out27), .out28(demultiplexer_4_out28),
    .out29({demultiplexer_4_out29_2, demultiplexer_4_out29[0]}), .out30(demultiplexer_4_out30),
    .out31({demultiplexer_4_out31_2, demultiplexer_4_out31[0]}), .in(demultiplexer_1_out2),
    .sel(operation[10:6]));
  CPUCM_128b cpucm_128b_65 (
    .get_A(get_A[4:0]), .get_B(get_B[4:0]), .External_access_Address(External_access_address[4:0]),
    .clear(clear), .clock(clock), .Operand_A(cpucm_128b_65_operand_a), .Operand_B(cpucm_128b_65_operand_b),
    .External_Access_Data(cpucm_128b_65_external_access_data), .write(demultiplexer_4_out0[0]),
    .get_reg(demultiplexer_4_out0_2), .Data_IN(Data_IN));
  CPUCM_128b cpucm_128b_66 (
    .get_A(get_A[4:0]), .get_B(get_B[4:0]), .External_access_Address(External_access_address[4:0]),
    .clear(clear), .clock(clock), .Operand_A(cpucm_128b_66_operand_a), .Operand_B(cpucm_128b_66_operand_b),
    .External_Access_Data(cpucm_128b_66_external_access_data), .write(demultiplexer_4_out1[0]),
    .get_reg(demultiplexer_4_out1[5:1]), .Data_IN(Data_IN));
  CPUCM_128b cpucm_128b_67 (
    .get_A(get_A[4:0]), .get_B(get_B[4:0]), .External_access_Address(External_access_address[4:0]),
    .clear(clear), .clock(clock), .Operand_A(cpucm_128b_67_operand_a), .Operand_B(cpucm_128b_67_operand_b),
    .External_Access_Data(cpucm_128b_67_external_access_data), .write(demultiplexer_4_out2[0]),
    .get_reg(demultiplexer_4_out2_2), .Data_IN(Data_IN));
  CPUCM_128b cpucm_128b_68 (
    .get_A(get_A[4:0]), .get_B(get_B[4:0]), .External_access_Address(External_access_address[4:0]),
    .clear(clear), .clock(clock), .Operand_A(cpucm_128b_68_operand_a), .Operand_B(cpucm_128b_68_operand_b),
    .External_Access_Data(cpucm_128b_68_external_access_data), .write(demultiplexer_4_out3[0]),
    .get_reg(demultiplexer_4_out3[5:1]), .Data_IN(Data_IN));
  CPUCM_128b cpucm_128b_69 (
    .get_A(get_A[4:0]), .get_B(get_B[4:0]), .External_access_Address(External_access_address[4:0]),
    .clear(clear), .clock(clock), .Operand_A(cpucm_128b_69_operand_a), .Operand_B(cpucm_128b_69_operand_b),
    .External_Access_Data(cpucm_128b_69_external_access_data), .write(demultiplexer_4_out4[0]),
    .get_reg(demultiplexer_4_out4_2), .Data_IN(Data_IN));
  CPUCM_128b cpucm_128b_70 (
    .get_A(get_A[4:0]), .get_B(get_B[4:0]), .External_access_Address(External_access_address[4:0]),
    .clear(clear), .clock(clock), .Operand_A(cpucm_128b_70_operand_a), .Operand_B(cpucm_128b_70_operand_b),
    .External_Access_Data(cpucm_128b_70_external_access_data), .write(demultiplexer_4_out5[0]),
    .get_reg(demultiplexer_4_out5_2), .Data_IN(Data_IN));
  CPUCM_128b cpucm_128b_71 (
    .get_A(get_A[4:0]), .get_B(get_B[4:0]), .External_access_Address(External_access_address[4:0]),
    .clear(clear), .clock(clock), .Operand_A(cpucm_128b_71_operand_a), .Operand_B(cpucm_128b_71_operand_b),
    .External_Access_Data(cpucm_128b_71_external_access_data), .write(demultiplexer_4_out6[0]),
    .get_reg(demultiplexer_4_out6_2), .Data_IN(Data_IN));
  CPUCM_128b cpucm_128b_72 (
    .get_A(get_A[4:0]), .get_B(get_B[4:0]), .External_access_Address(External_access_address[4:0]),
    .clear(clear), .clock(clock), .Operand_A(cpucm_128b_72_operand_a), .Operand_B(cpucm_128b_72_operand_b),
    .External_Access_Data(cpucm_128b_72_external_access_data), .write(demultiplexer_4_out7[0]),
    .get_reg(demultiplexer_4_out7_2), .Data_IN(Data_IN));
  CPUCM_128b cpucm_128b_73 (
    .get_A(get_A[4:0]), .get_B(get_B[4:0]), .External_access_Address(External_access_address[4:0]),
    .clear(clear), .clock(clock), .Operand_A(cpucm_128b_73_operand_a), .Operand_B(cpucm_128b_73_operand_b),
    .External_Access_Data(cpucm_128b_73_external_access_data), .write(demultiplexer_4_out8[0]),
    .get_reg(demultiplexer_4_out8_2), .Data_IN(Data_IN));
  CPUCM_128b cpucm_128b_74 (
    .get_A(get_A[4:0]), .get_B(get_B[4:0]), .External_access_Address(External_access_address[4:0]),
    .clear(clear), .clock(clock), .Operand_A(cpucm_128b_74_operand_a), .Operand_B(cpucm_128b_74_operand_b),
    .External_Access_Data(cpucm_128b_74_external_access_data), .write(demultiplexer_4_out9[0]),
    .get_reg(demultiplexer_4_out9[5:1]), .Data_IN(Data_IN));
  CPUCM_128b cpucm_128b_75 (
    .get_A(get_A[4:0]), .get_B(get_B[4:0]), .External_access_Address(External_access_address[4:0]),
    .clear(clear), .clock(clock), .Operand_A(cpucm_128b_75_operand_a), .Operand_B(cpucm_128b_75_operand_b),
    .External_Access_Data(cpucm_128b_75_external_access_data), .write(demultiplexer_4_out10[0]),
    .get_reg(demultiplexer_4_out10_2), .Data_IN(Data_IN));
  CPUCM_128b cpucm_128b_76 (
    .get_A(get_A[4:0]), .get_B(get_B[4:0]), .External_access_Address(External_access_address[4:0]),
    .clear(clear), .clock(clock), .Operand_A(cpucm_128b_76_operand_a), .Operand_B(cpucm_128b_76_operand_b),
    .External_Access_Data(cpucm_128b_76_external_access_data), .write(demultiplexer_4_out11[0]),
    .get_reg(demultiplexer_4_out11_2), .Data_IN(Data_IN));
  CPUCM_128b cpucm_128b_77 (
    .get_A(get_A[4:0]), .get_B(get_B[4:0]), .External_access_Address(External_access_address[4:0]),
    .clear(clear), .clock(clock), .Operand_A(cpucm_128b_77_operand_a), .Operand_B(cpucm_128b_77_operand_b),
    .External_Access_Data(cpucm_128b_77_external_access_data), .write(demultiplexer_4_out12[0]),
    .get_reg(demultiplexer_4_out12_2), .Data_IN(Data_IN));
  CPUCM_128b cpucm_128b_78 (
    .get_A(get_A[4:0]), .get_B(get_B[4:0]), .External_access_Address(External_access_address[4:0]),
    .clear(clear), .clock(clock), .Operand_A(cpucm_128b_78_operand_a), .Operand_B(cpucm_128b_78_operand_b),
    .External_Access_Data(cpucm_128b_78_external_access_data), .write(demultiplexer_4_out13[0]),
    .get_reg(demultiplexer_4_out13_2), .Data_IN(Data_IN));
  CPUCM_128b cpucm_128b_79 (
    .get_A(get_A[4:0]), .get_B(get_B[4:0]), .External_access_Address(External_access_address[4:0]),
    .clear(clear), .clock(clock), .Operand_A(cpucm_128b_79_operand_a), .Operand_B(cpucm_128b_79_operand_b),
    .External_Access_Data(cpucm_128b_79_external_access_data), .write(demultiplexer_4_out14[0]),
    .get_reg(demultiplexer_4_out14_2), .Data_IN(Data_IN));
  CPUCM_128b cpucm_128b_80 (
    .get_A(get_A[4:0]), .get_B(get_B[4:0]), .External_access_Address(External_access_address[4:0]),
    .clear(clear), .clock(clock), .Operand_A(cpucm_128b_80_operand_a), .Operand_B(cpucm_128b_80_operand_b),
    .External_Access_Data(cpucm_128b_80_external_access_data), .write(demultiplexer_4_out15[0]),
    .get_reg(demultiplexer_4_out15[5:1]), .Data_IN(Data_IN));
  CPUCM_128b cpucm_128b_81 (
    .get_A(get_A[4:0]), .get_B(get_B[4:0]), .External_access_Address(External_access_address[4:0]),
    .clear(clear), .clock(clock), .Operand_A(cpucm_128b_81_operand_a), .Operand_B(cpucm_128b_81_operand_b),
    .External_Access_Data(cpucm_128b_81_external_access_data), .write(demultiplexer_4_out16[0]),
    .get_reg(demultiplexer_4_out16_2), .Data_IN(Data_IN));
  CPUCM_128b cpucm_128b_82 (
    .get_A(get_A[4:0]), .get_B(get_B[4:0]), .External_access_Address(External_access_address[4:0]),
    .clear(clear), .clock(clock), .Operand_A(cpucm_128b_82_operand_a), .Operand_B(cpucm_128b_82_operand_b),
    .External_Access_Data(cpucm_128b_82_external_access_data), .write(demultiplexer_4_out17[0]),
    .get_reg(demultiplexer_4_out17_2), .Data_IN(Data_IN));
  CPUCM_128b cpucm_128b_83 (
    .get_A(get_A[4:0]), .get_B(get_B[4:0]), .External_access_Address(External_access_address[4:0]),
    .clear(clear), .clock(clock), .Operand_A(cpucm_128b_83_operand_a), .Operand_B(cpucm_128b_83_operand_b),
    .External_Access_Data(cpucm_128b_83_external_access_data), .write(demultiplexer_4_out18[0]),
    .get_reg(demultiplexer_4_out18[5:1]), .Data_IN(Data_IN));
  CPUCM_128b cpucm_128b_84 (
    .get_A(get_A[4:0]), .get_B(get_B[4:0]), .External_access_Address(External_access_address[4:0]),
    .clear(clear), .clock(clock), .Operand_A(cpucm_128b_84_operand_a), .Operand_B(cpucm_128b_84_operand_b),
    .External_Access_Data(cpucm_128b_84_external_access_data), .write(demultiplexer_4_out19[0]),
    .get_reg(demultiplexer_4_out19_2), .Data_IN(Data_IN));
  CPUCM_128b cpucm_128b_85 (
    .get_A(get_A[4:0]), .get_B(get_B[4:0]), .External_access_Address(External_access_address[4:0]),
    .clear(clear), .clock(clock), .Operand_A(cpucm_128b_85_operand_a), .Operand_B(cpucm_128b_85_operand_b),
    .External_Access_Data(cpucm_128b_85_external_access_data), .write(demultiplexer_4_out20[0]),
    .get_reg(demultiplexer_4_out20[5:1]), .Data_IN(Data_IN));
  CPUCM_128b cpucm_128b_86 (
    .get_A(get_A[4:0]), .get_B(get_B[4:0]), .External_access_Address(External_access_address[4:0]),
    .clear(clear), .clock(clock), .Operand_A(cpucm_128b_86_operand_a), .Operand_B(cpucm_128b_86_operand_b),
    .External_Access_Data(cpucm_128b_86_external_access_data), .write(demultiplexer_4_out21[0]),
    .get_reg(demultiplexer_4_out21[5:1]), .Data_IN(Data_IN));
  CPUCM_128b cpucm_128b_87 (
    .get_A(get_A[4:0]), .get_B(get_B[4:0]), .External_access_Address(External_access_address[4:0]),
    .clear(clear), .clock(clock), .Operand_A(cpucm_128b_87_operand_a), .Operand_B(cpucm_128b_87_operand_b),
    .External_Access_Data(cpucm_128b_87_external_access_data), .write(demultiplexer_4_out22[0]),
    .get_reg(demultiplexer_4_out22[5:1]), .Data_IN(Data_IN));
  CPUCM_128b cpucm_128b_88 (
    .get_A(get_A[4:0]), .get_B(get_B[4:0]), .External_access_Address(External_access_address[4:0]),
    .clear(clear), .clock(clock), .Operand_A(cpucm_128b_88_operand_a), .Operand_B(cpucm_128b_88_operand_b),
    .External_Access_Data(cpucm_128b_88_external_access_data), .write(demultiplexer_4_out23[0]),
    .get_reg(demultiplexer_4_out23_2), .Data_IN(Data_IN));
  CPUCM_128b cpucm_128b_89 (
    .get_A(get_A[4:0]), .get_B(get_B[4:0]), .External_access_Address(External_access_address[4:0]),
    .clear(clear), .clock(clock), .Operand_A(cpucm_128b_89_operand_a), .Operand_B(cpucm_128b_89_operand_b),
    .External_Access_Data(cpucm_128b_89_external_access_data), .write(demultiplexer_4_out24[0]),
    .get_reg(demultiplexer_4_out24[5:1]), .Data_IN(Data_IN));
  CPUCM_128b cpucm_128b_90 (
    .get_A(get_A[4:0]), .get_B(get_B[4:0]), .External_access_Address(External_access_address[4:0]),
    .clear(clear), .clock(clock), .Operand_A(cpucm_128b_90_operand_a), .Operand_B(cpucm_128b_90_operand_b),
    .External_Access_Data(cpucm_128b_90_external_access_data), .write(demultiplexer_4_out25[0]),
    .get_reg(demultiplexer_4_out25_2), .Data_IN(Data_IN));
  CPUCM_128b cpucm_128b_91 (
    .get_A(get_A[4:0]), .get_B(get_B[4:0]), .External_access_Address(External_access_address[4:0]),
    .clear(clear), .clock(clock), .Operand_A(cpucm_128b_91_operand_a), .Operand_B(cpucm_128b_91_operand_b),
    .External_Access_Data(cpucm_128b_91_external_access_data), .write(demultiplexer_4_out26[0]),
    .get_reg(demultiplexer_4_out26[5:1]), .Data_IN(Data_IN));
  CPUCM_128b cpucm_128b_92 (
    .get_A(get_A[4:0]), .get_B(get_B[4:0]), .External_access_Address(External_access_address[4:0]),
    .clear(clear), .clock(clock), .Operand_A(cpucm_128b_92_operand_a), .Operand_B(cpucm_128b_92_operand_b),
    .External_Access_Data(cpucm_128b_92_external_access_data), .write(demultiplexer_4_out27[0]),
    .get_reg(demultiplexer_4_out27[5:1]), .Data_IN(Data_IN));
  CPUCM_128b cpucm_128b_93 (
    .get_A(get_A[4:0]), .get_B(get_B[4:0]), .External_access_Address(External_access_address[4:0]),
    .clear(clear), .clock(clock), .Operand_A(cpucm_128b_93_operand_a), .Operand_B(cpucm_128b_93_operand_b),
    .External_Access_Data(cpucm_128b_93_external_access_data), .write(demultiplexer_4_out28[0]),
    .get_reg(demultiplexer_4_out28[5:1]), .Data_IN(Data_IN));
  CPUCM_128b cpucm_128b_94 (
    .get_A(get_A[4:0]), .get_B(get_B[4:0]), .External_access_Address(External_access_address[4:0]),
    .clear(clear), .clock(clock), .Operand_A(cpucm_128b_94_operand_a), .Operand_B(cpucm_128b_94_operand_b),
    .External_Access_Data(cpucm_128b_94_external_access_data), .write(demultiplexer_4_out29[0]),
    .get_reg(demultiplexer_4_out29_2), .Data_IN(Data_IN));
  CPUCM_128b cpucm_128b_95 (
    .get_A(get_A[4:0]), .get_B(get_B[4:0]), .External_access_Address(External_access_address[4:0]),
    .clear(clear), .clock(clock), .Operand_A(cpucm_128b_95_operand_a), .Operand_B(cpucm_128b_95_operand_b),
    .External_Access_Data(cpucm_128b_95_external_access_data), .write(demultiplexer_4_out30[0]),
    .get_reg(demultiplexer_4_out30[5:1]), .Data_IN(Data_IN));
  CPUCM_128b cpucm_128b_96 (
    .get_A(get_A[4:0]), .get_B(get_B[4:0]), .External_access_Address(External_access_address[4:0]),
    .clear(clear), .clock(clock), .Operand_A(cpucm_128b_96_operand_a), .Operand_B(cpucm_128b_96_operand_b),
    .External_Access_Data(cpucm_128b_96_external_access_data), .write(demultiplexer_4_out31[0]),
    .get_reg(demultiplexer_4_out31_2), .Data_IN(Data_IN));
  Multiplexer #(.select(5), .width(32), .disabled(0), .enable("false")) multiplexer_10 (
    .in0(cpucm_128b_65_operand_a), .in1(cpucm_128b_66_operand_a), .in2(cpucm_128b_67_operand_a),
    .in3(cpucm_128b_68_operand_a), .in4(cpucm_128b_69_operand_a), .in5(cpucm_128b_70_operand_a),
    .in6(cpucm_128b_71_operand_a), .in7(cpucm_128b_72_operand_a), .in8(cpucm_128b_73_operand_a),
    .in9(cpucm_128b_74_operand_a), .in10(cpucm_128b_75_operand_a), .in11(cpucm_128b_76_operand_a),
    .in12(cpucm_128b_77_operand_a), .in13(cpucm_128b_78_operand_a), .in14(cpucm_128b_79_operand_a),
    .in15(cpucm_128b_80_operand_a), .in16(cpucm_128b_81_operand_a), .in17(cpucm_128b_82_operand_a),
    .in18(cpucm_128b_83_operand_a), .in19(cpucm_128b_84_operand_a), .in20(cpucm_128b_85_operand_a),
    .in21(cpucm_128b_86_operand_a), .in22(cpucm_128b_87_operand_a), .in23(cpucm_128b_88_operand_a),
    .in24(cpucm_128b_89_operand_a), .in25(cpucm_128b_90_operand_a), .in26(cpucm_128b_91_operand_a),
    .in27(cpucm_128b_92_operand_a), .in28(cpucm_128b_93_operand_a), .in29(cpucm_128b_94_operand_a),
    .in30(cpucm_128b_95_operand_a), .in31(cpucm_128b_96_operand_a), .out(multiplexer_10_out), .sel(get_A[9:5]));
  Multiplexer #(.select(5), .width(32), .disabled(0), .enable("false")) multiplexer_11 (
    .in0(cpucm_128b_65_operand_b), .in1(cpucm_128b_66_operand_b), .in2(cpucm_128b_67_operand_b),
    .in3(cpucm_128b_68_operand_b), .in4(cpucm_128b_69_operand_b), .in5(cpucm_128b_70_operand_b),
    .in6(cpucm_128b_71_operand_b), .in7(cpucm_128b_72_operand_b), .in8(cpucm_128b_73_operand_b),
    .in9(cpucm_128b_74_operand_b), .in10(cpucm_128b_75_operand_b), .in11(cpucm_128b_76_operand_b),
    .in12(cpucm_128b_77_operand_b), .in13(cpucm_128b_78_operand_b), .in14(cpucm_128b_79_operand_b),
    .in15(cpucm_128b_80_operand_b), .in16(cpucm_128b_81_operand_b), .in17(cpucm_128b_82_operand_b),
    .in18(cpucm_128b_83_operand_b), .in19(cpucm_128b_84_operand_b), .in20(cpucm_128b_85_operand_b),
    .in21(cpucm_128b_86_operand_b), .in22(cpucm_128b_87_operand_b), .in23(cpucm_128b_88_operand_b),
    .in24(cpucm_128b_89_operand_b), .in25(cpucm_128b_90_operand_b), .in26(cpucm_128b_91_operand_b),
    .in27(cpucm_128b_92_operand_b), .in28(cpucm_128b_93_operand_b), .in29(cpucm_128b_94_operand_b),
    .in30(cpucm_128b_95_operand_b), .in31(cpucm_128b_96_operand_b), .out(multiplexer_11_out), .sel(get_B[9:5]));
  Multiplexer #(.select(5), .width(32), .disabled(0), .enable("false")) multiplexer_12 (
    .in0(cpucm_128b_65_external_access_data), .in1(cpucm_128b_66_external_access_data),
    .in2(cpucm_128b_67_external_access_data), .in3(cpucm_128b_68_external_access_data),
    .in4(cpucm_128b_69_external_access_data), .in5(cpucm_128b_70_external_access_data),
    .in6(cpucm_128b_71_external_access_data), .in7(cpucm_128b_72_external_access_data),
    .in8(cpucm_128b_73_external_access_data), .in9(cpucm_128b_74_external_access_data),
    .in10(cpucm_128b_75_external_access_data), .in11(cpucm_128b_76_external_access_data),
    .in12(cpucm_128b_77_external_access_data), .in13(cpucm_128b_78_external_access_data),
    .in14(cpucm_128b_79_external_access_data), .in15(cpucm_128b_80_external_access_data),
    .in16(cpucm_128b_81_external_access_data), .in17(cpucm_128b_82_external_access_data),
    .in18(cpucm_128b_83_external_access_data), .in19(cpucm_128b_84_external_access_data),
    .in20(cpucm_128b_85_external_access_data), .in21(cpucm_128b_86_external_access_data),
    .in22(cpucm_128b_87_external_access_data), .in23(cpucm_128b_88_external_access_data),
    .in24(cpucm_128b_89_external_access_data), .in25(cpucm_128b_90_external_access_data),
    .in26(cpucm_128b_91_external_access_data), .in27(cpucm_128b_92_external_access_data),
    .in28(cpucm_128b_93_external_access_data), .in29(cpucm_128b_94_external_access_data),
    .in30(cpucm_128b_95_external_access_data), .in31(cpucm_128b_96_external_access_data),
    .out(multiplexer_12_out), .sel(External_access_address[9:5]));
  Demultiplexer #(.select(5), .width(6), .disabled(0), .enable("false")) demultiplexer_5 (
    .out0({demultiplexer_5_out0_2, demultiplexer_5_out0[0]}),
    .out1({demultiplexer_5_out1_2, demultiplexer_5_out1[0]}), .out2(demultiplexer_5_out2),
    .out3({demultiplexer_5_out3_2, demultiplexer_5_out3[0]}),
    .out4({demultiplexer_5_out4_2, demultiplexer_5_out4[0]}),
    .out5({demultiplexer_5_out5_2, demultiplexer_5_out5[0]}), .out6(demultiplexer_5_out6),
    .out7(demultiplexer_5_out7), .out8(demultiplexer_5_out8), .out9(demultiplexer_5_out9),
    .out10({demultiplexer_5_out10_2, demultiplexer_5_out10[0]}), .out11(demultiplexer_5_out11),
    .out12(demultiplexer_5_out12), .out13(demultiplexer_5_out13), .out14(demultiplexer_5_out14),
    .out15(demultiplexer_5_out15), .out16({demultiplexer_5_out16_2, demultiplexer_5_out16[0]}),
    .out17({demultiplexer_5_out17_2, demultiplexer_5_out17[0]}), .out18(demultiplexer_5_out18),
    .out19(demultiplexer_5_out19), .out20({demultiplexer_5_out20_2, demultiplexer_5_out20[0]}),
    .out21(demultiplexer_5_out21), .out22({demultiplexer_5_out22_2, demultiplexer_5_out22[0]}),
    .out23({demultiplexer_5_out23_2, demultiplexer_5_out23[0]}), .out24(demultiplexer_5_out24),
    .out25(demultiplexer_5_out25), .out26({demultiplexer_5_out26_2, demultiplexer_5_out26[0]}),
    .out27(demultiplexer_5_out27), .out28({demultiplexer_5_out28_2, demultiplexer_5_out28[0]}),
    .out29({demultiplexer_5_out29_2, demultiplexer_5_out29[0]}),
    .out30({demultiplexer_5_out30_2, demultiplexer_5_out30[0]}), .out31(demultiplexer_5_out31),
    .in(demultiplexer_1_out3), .sel(operation[10:6]));
  CPUCM_128b cpucm_128b_97 (
    .get_A(get_A[4:0]), .get_B(get_B[4:0]), .External_access_Address(External_access_address[4:0]),
    .clear(clear), .clock(clock), .Operand_A(cpucm_128b_97_operand_a), .Operand_B(cpucm_128b_97_operand_b),
    .External_Access_Data(cpucm_128b_97_external_access_data), .write(demultiplexer_5_out0[0]),
    .get_reg(demultiplexer_5_out0_2), .Data_IN(Data_IN));
  CPUCM_128b cpucm_128b_98 (
    .get_A(get_A[4:0]), .get_B(get_B[4:0]), .External_access_Address(External_access_address[4:0]),
    .clear(clear), .clock(clock), .Operand_A(cpucm_128b_98_operand_a), .Operand_B(cpucm_128b_98_operand_b),
    .External_Access_Data(cpucm_128b_98_external_access_data), .write(demultiplexer_5_out1[0]),
    .get_reg(demultiplexer_5_out1_2), .Data_IN(Data_IN));
  CPUCM_128b cpucm_128b_99 (
    .get_A(get_A[4:0]), .get_B(get_B[4:0]), .External_access_Address(External_access_address[4:0]),
    .clear(clear), .clock(clock), .Operand_A(cpucm_128b_99_operand_a), .Operand_B(cpucm_128b_99_operand_b),
    .External_Access_Data(cpucm_128b_99_external_access_data), .write(demultiplexer_5_out2[0]),
    .get_reg(demultiplexer_5_out2[5:1]), .Data_IN(Data_IN));
  CPUCM_128b cpucm_128b_100 (
    .get_A(get_A[4:0]), .get_B(get_B[4:0]), .External_access_Address(External_access_address[4:0]),
    .clear(clear), .clock(clock), .Operand_A(cpucm_128b_100_operand_a), .Operand_B(cpucm_128b_100_operand_b),
    .External_Access_Data(cpucm_128b_100_external_access_data), .write(demultiplexer_5_out3[0]),
    .get_reg(demultiplexer_5_out3_2), .Data_IN(Data_IN));
  CPUCM_128b cpucm_128b_101 (
    .get_A(get_A[4:0]), .get_B(get_B[4:0]), .External_access_Address(External_access_address[4:0]),
    .clear(clear), .clock(clock), .Operand_A(cpucm_128b_101_operand_a), .Operand_B(cpucm_128b_101_operand_b),
    .External_Access_Data(cpucm_128b_101_external_access_data), .write(demultiplexer_5_out4[0]),
    .get_reg(demultiplexer_5_out4_2), .Data_IN(Data_IN));
  CPUCM_128b cpucm_128b_102 (
    .get_A(get_A[4:0]), .get_B(get_B[4:0]), .External_access_Address(External_access_address[4:0]),
    .clear(clear), .clock(clock), .Operand_A(cpucm_128b_102_operand_a), .Operand_B(cpucm_128b_102_operand_b),
    .External_Access_Data(cpucm_128b_102_external_access_data), .write(demultiplexer_5_out5[0]),
    .get_reg(demultiplexer_5_out5_2), .Data_IN(Data_IN));
  CPUCM_128b cpucm_128b_103 (
    .get_A(get_A[4:0]), .get_B(get_B[4:0]), .External_access_Address(External_access_address[4:0]),
    .clear(clear), .clock(clock), .Operand_A(cpucm_128b_103_operand_a), .Operand_B(cpucm_128b_103_operand_b),
    .External_Access_Data(cpucm_128b_103_external_access_data), .write(demultiplexer_5_out6[0]),
    .get_reg(demultiplexer_5_out6[5:1]), .Data_IN(Data_IN));
  CPUCM_128b cpucm_128b_104 (
    .get_A(get_A[4:0]), .get_B(get_B[4:0]), .External_access_Address(External_access_address[4:0]),
    .clear(clear), .clock(clock), .Operand_A(cpucm_128b_104_operand_a), .Operand_B(cpucm_128b_104_operand_b),
    .External_Access_Data(cpucm_128b_104_external_access_data), .write(demultiplexer_5_out7[0]),
    .get_reg(demultiplexer_5_out7[5:1]), .Data_IN(Data_IN));
  CPUCM_128b cpucm_128b_105 (
    .get_A(get_A[4:0]), .get_B(get_B[4:0]), .External_access_Address(External_access_address[4:0]),
    .clear(clear), .clock(clock), .Operand_A(cpucm_128b_105_operand_a), .Operand_B(cpucm_128b_105_operand_b),
    .External_Access_Data(cpucm_128b_105_external_access_data), .write(demultiplexer_5_out8[0]),
    .get_reg(demultiplexer_5_out8[5:1]), .Data_IN(Data_IN));
  CPUCM_128b cpucm_128b_106 (
    .get_A(get_A[4:0]), .get_B(get_B[4:0]), .External_access_Address(External_access_address[4:0]),
    .clear(clear), .clock(clock), .Operand_A(cpucm_128b_106_operand_a), .Operand_B(cpucm_128b_106_operand_b),
    .External_Access_Data(cpucm_128b_106_external_access_data), .write(demultiplexer_5_out9[0]),
    .get_reg(demultiplexer_5_out9[5:1]), .Data_IN(Data_IN));
  CPUCM_128b cpucm_128b_107 (
    .get_A(get_A[4:0]), .get_B(get_B[4:0]), .External_access_Address(External_access_address[4:0]),
    .clear(clear), .clock(clock), .Operand_A(cpucm_128b_107_operand_a), .Operand_B(cpucm_128b_107_operand_b),
    .External_Access_Data(cpucm_128b_107_external_access_data), .write(demultiplexer_5_out10[0]),
    .get_reg(demultiplexer_5_out10_2), .Data_IN(Data_IN));
  CPUCM_128b cpucm_128b_108 (
    .get_A(get_A[4:0]), .get_B(get_B[4:0]), .External_access_Address(External_access_address[4:0]),
    .clear(clear), .clock(clock), .Operand_A(cpucm_128b_108_operand_a), .Operand_B(cpucm_128b_108_operand_b),
    .External_Access_Data(cpucm_128b_108_external_access_data), .write(demultiplexer_5_out11[0]),
    .get_reg(demultiplexer_5_out11[5:1]), .Data_IN(Data_IN));
  CPUCM_128b cpucm_128b_109 (
    .get_A(get_A[4:0]), .get_B(get_B[4:0]), .External_access_Address(External_access_address[4:0]),
    .clear(clear), .clock(clock), .Operand_A(cpucm_128b_109_operand_a), .Operand_B(cpucm_128b_109_operand_b),
    .External_Access_Data(cpucm_128b_109_external_access_data), .write(demultiplexer_5_out12[0]),
    .get_reg(demultiplexer_5_out12[5:1]), .Data_IN(Data_IN));
  CPUCM_128b cpucm_128b_110 (
    .get_A(get_A[4:0]), .get_B(get_B[4:0]), .External_access_Address(External_access_address[4:0]),
    .clear(clear), .clock(clock), .Operand_A(cpucm_128b_110_operand_a), .Operand_B(cpucm_128b_110_operand_b),
    .External_Access_Data(cpucm_128b_110_external_access_data), .write(demultiplexer_5_out13[0]),
    .get_reg(demultiplexer_5_out13[5:1]), .Data_IN(Data_IN));
  CPUCM_128b cpucm_128b_111 (
    .get_A(get_A[4:0]), .get_B(get_B[4:0]), .External_access_Address(External_access_address[4:0]),
    .clear(clear), .clock(clock), .Operand_A(cpucm_128b_111_operand_a), .Operand_B(cpucm_128b_111_operand_b),
    .External_Access_Data(cpucm_128b_111_external_access_data), .write(demultiplexer_5_out14[0]),
    .get_reg(demultiplexer_5_out14[5:1]), .Data_IN(Data_IN));
  CPUCM_128b cpucm_128b_112 (
    .get_A(get_A[4:0]), .get_B(get_B[4:0]), .External_access_Address(External_access_address[4:0]),
    .clear(clear), .clock(clock), .Operand_A(cpucm_128b_112_operand_a), .Operand_B(cpucm_128b_112_operand_b),
    .External_Access_Data(cpucm_128b_112_external_access_data), .write(demultiplexer_5_out15[0]),
    .get_reg(demultiplexer_5_out15[5:1]), .Data_IN(Data_IN));
  CPUCM_128b cpucm_128b_113 (
    .get_A(get_A[4:0]), .get_B(get_B[4:0]), .External_access_Address(External_access_address[4:0]),
    .clear(clear), .clock(clock), .Operand_A(cpucm_128b_113_operand_a), .Operand_B(cpucm_128b_113_operand_b),
    .External_Access_Data(cpucm_128b_113_external_access_data), .write(demultiplexer_5_out16[0]),
    .get_reg(demultiplexer_5_out16_2), .Data_IN(Data_IN));
  CPUCM_128b cpucm_128b_114 (
    .get_A(get_A[4:0]), .get_B(get_B[4:0]), .External_access_Address(External_access_address[4:0]),
    .clear(clear), .clock(clock), .Operand_A(cpucm_128b_114_operand_a), .Operand_B(cpucm_128b_114_operand_b),
    .External_Access_Data(cpucm_128b_114_external_access_data), .write(demultiplexer_5_out17[0]),
    .get_reg(demultiplexer_5_out17_2), .Data_IN(Data_IN));
  CPUCM_128b cpucm_128b_115 (
    .get_A(get_A[4:0]), .get_B(get_B[4:0]), .External_access_Address(External_access_address[4:0]),
    .clear(clear), .clock(clock), .Operand_A(cpucm_128b_115_operand_a), .Operand_B(cpucm_128b_115_operand_b),
    .External_Access_Data(cpucm_128b_115_external_access_data), .write(demultiplexer_5_out18[0]),
    .get_reg(demultiplexer_5_out18[5:1]), .Data_IN(Data_IN));
  CPUCM_128b cpucm_128b_116 (
    .get_A(get_A[4:0]), .get_B(get_B[4:0]), .External_access_Address(External_access_address[4:0]),
    .clear(clear), .clock(clock), .Operand_A(cpucm_128b_116_operand_a), .Operand_B(cpucm_128b_116_operand_b),
    .External_Access_Data(cpucm_128b_116_external_access_data), .write(demultiplexer_5_out19[0]),
    .get_reg(demultiplexer_5_out19[5:1]), .Data_IN(Data_IN));
  CPUCM_128b cpucm_128b_117 (
    .get_A(get_A[4:0]), .get_B(get_B[4:0]), .External_access_Address(External_access_address[4:0]),
    .clear(clear), .clock(clock), .Operand_A(cpucm_128b_117_operand_a), .Operand_B(cpucm_128b_117_operand_b),
    .External_Access_Data(cpucm_128b_117_external_access_data), .write(demultiplexer_5_out20[0]),
    .get_reg(demultiplexer_5_out20_2), .Data_IN(Data_IN));
  CPUCM_128b cpucm_128b_118 (
    .get_A(get_A[4:0]), .get_B(get_B[4:0]), .External_access_Address(External_access_address[4:0]),
    .clear(clear), .clock(clock), .Operand_A(cpucm_128b_118_operand_a), .Operand_B(cpucm_128b_118_operand_b),
    .External_Access_Data(cpucm_128b_118_external_access_data), .write(demultiplexer_5_out21[0]),
    .get_reg(demultiplexer_5_out21[5:1]), .Data_IN(Data_IN));
  CPUCM_128b cpucm_128b_119 (
    .get_A(get_A[4:0]), .get_B(get_B[4:0]), .External_access_Address(External_access_address[4:0]),
    .clear(clear), .clock(clock), .Operand_A(cpucm_128b_119_operand_a), .Operand_B(cpucm_128b_119_operand_b),
    .External_Access_Data(cpucm_128b_119_external_access_data), .write(demultiplexer_5_out22[0]),
    .get_reg(demultiplexer_5_out22_2), .Data_IN(Data_IN));
  CPUCM_128b cpucm_128b_120 (
    .get_A(get_A[4:0]), .get_B(get_B[4:0]), .External_access_Address(External_access_address[4:0]),
    .clear(clear), .clock(clock), .Operand_A(cpucm_128b_120_operand_a), .Operand_B(cpucm_128b_120_operand_b),
    .External_Access_Data(cpucm_128b_120_external_access_data), .write(demultiplexer_5_out23[0]),
    .get_reg(demultiplexer_5_out23_2), .Data_IN(Data_IN));
  CPUCM_128b cpucm_128b_121 (
    .get_A(get_A[4:0]), .get_B(get_B[4:0]), .External_access_Address(External_access_address[4:0]),
    .clear(clear), .clock(clock), .Operand_A(cpucm_128b_121_operand_a), .Operand_B(cpucm_128b_121_operand_b),
    .External_Access_Data(cpucm_128b_121_external_access_data), .write(demultiplexer_5_out24[0]),
    .get_reg(demultiplexer_5_out24[5:1]), .Data_IN(Data_IN));
  CPUCM_128b cpucm_128b_122 (
    .get_A(get_A[4:0]), .get_B(get_B[4:0]), .External_access_Address(External_access_address[4:0]),
    .clear(clear), .clock(clock), .Operand_A(cpucm_128b_122_operand_a), .Operand_B(cpucm_128b_122_operand_b),
    .External_Access_Data(cpucm_128b_122_external_access_data), .write(demultiplexer_5_out25[0]),
    .get_reg(demultiplexer_5_out25[5:1]), .Data_IN(Data_IN));
  CPUCM_128b cpucm_128b_123 (
    .get_A(get_A[4:0]), .get_B(get_B[4:0]), .External_access_Address(External_access_address[4:0]),
    .clear(clear), .clock(clock), .Operand_A(cpucm_128b_123_operand_a), .Operand_B(cpucm_128b_123_operand_b),
    .External_Access_Data(cpucm_128b_123_external_access_data), .write(demultiplexer_5_out26[0]),
    .get_reg(demultiplexer_5_out26_2), .Data_IN(Data_IN));
  CPUCM_128b cpucm_128b_124 (
    .get_A(get_A[4:0]), .get_B(get_B[4:0]), .External_access_Address(External_access_address[4:0]),
    .clear(clear), .clock(clock), .Operand_A(cpucm_128b_124_operand_a), .Operand_B(cpucm_128b_124_operand_b),
    .External_Access_Data(cpucm_128b_124_external_access_data), .write(demultiplexer_5_out27[0]),
    .get_reg(demultiplexer_5_out27[5:1]), .Data_IN(Data_IN));
  CPUCM_128b cpucm_128b_125 (
    .get_A(get_A[4:0]), .get_B(get_B[4:0]), .External_access_Address(External_access_address[4:0]),
    .clear(clear), .clock(clock), .Operand_A(cpucm_128b_125_operand_a), .Operand_B(cpucm_128b_125_operand_b),
    .External_Access_Data(cpucm_128b_125_external_access_data), .write(demultiplexer_5_out28[0]),
    .get_reg(demultiplexer_5_out28_2), .Data_IN(Data_IN));
  CPUCM_128b cpucm_128b_126 (
    .get_A(get_A[4:0]), .get_B(get_B[4:0]), .External_access_Address(External_access_address[4:0]),
    .clear(clear), .clock(clock), .Operand_A(cpucm_128b_126_operand_a), .Operand_B(cpucm_128b_126_operand_b),
    .External_Access_Data(cpucm_128b_126_external_access_data), .write(demultiplexer_5_out29[0]),
    .get_reg(demultiplexer_5_out29_2), .Data_IN(Data_IN));
  CPUCM_128b cpucm_128b_127 (
    .get_A(get_A[4:0]), .get_B(get_B[4:0]), .External_access_Address(External_access_address[4:0]),
    .clear(clear), .clock(clock), .Operand_A(cpucm_128b_127_operand_a), .Operand_B(cpucm_128b_127_operand_b),
    .External_Access_Data(cpucm_128b_127_external_access_data), .write(demultiplexer_5_out30[0]),
    .get_reg(demultiplexer_5_out30_2), .Data_IN(Data_IN));
  CPUCM_128b cpucm_128b_128 (
    .get_A(get_A[4:0]), .get_B(get_B[4:0]), .External_access_Address(External_access_address[4:0]),
    .clear(clear), .clock(clock), .Operand_A(cpucm_128b_128_operand_a), .Operand_B(cpucm_128b_128_operand_b),
    .External_Access_Data(cpucm_128b_128_external_access_data), .write(demultiplexer_5_out31[0]),
    .get_reg(demultiplexer_5_out31[5:1]), .Data_IN(Data_IN));
  Multiplexer #(.select(5), .width(32), .disabled(0), .enable("false")) multiplexer_13 (
    .in0(cpucm_128b_97_operand_a), .in1(cpucm_128b_98_operand_a), .in2(cpucm_128b_99_operand_a),
    .in3(cpucm_128b_100_operand_a), .in4(cpucm_128b_101_operand_a), .in5(cpucm_128b_102_operand_a),
    .in6(cpucm_128b_103_operand_a), .in7(cpucm_128b_104_operand_a), .in8(cpucm_128b_105_operand_a),
    .in9(cpucm_128b_106_operand_a), .in10(cpucm_128b_107_operand_a), .in11(cpucm_128b_108_operand_a),
    .in12(cpucm_128b_109_operand_a), .in13(cpucm_128b_110_operand_a), .in14(cpucm_128b_111_operand_a),
    .in15(cpucm_128b_112_operand_a), .in16(cpucm_128b_113_operand_a), .in17(cpucm_128b_114_operand_a),
    .in18(cpucm_128b_115_operand_a), .in19(cpucm_128b_116_operand_a), .in20(cpucm_128b_117_operand_a),
    .in21(cpucm_128b_118_operand_a), .in22(cpucm_128b_119_operand_a), .in23(cpucm_128b_120_operand_a),
    .in24(cpucm_128b_121_operand_a), .in25(cpucm_128b_122_operand_a), .in26(cpucm_128b_123_operand_a),
    .in27(cpucm_128b_124_operand_a), .in28(cpucm_128b_125_operand_a), .in29(cpucm_128b_126_operand_a),
    .in30(cpucm_128b_127_operand_a), .in31(cpucm_128b_128_operand_a), .out(multiplexer_13_out),
    .sel(get_A[9:5]));
  Multiplexer #(.select(5), .width(32), .disabled(0), .enable("false")) multiplexer_14 (
    .in0(cpucm_128b_97_operand_b), .in1(cpucm_128b_98_operand_b), .in2(cpucm_128b_99_operand_b),
    .in3(cpucm_128b_100_operand_b), .in4(cpucm_128b_101_operand_b), .in5(cpucm_128b_102_operand_b),
    .in6(cpucm_128b_103_operand_b), .in7(cpucm_128b_104_operand_b), .in8(cpucm_128b_105_operand_b),
    .in9(cpucm_128b_106_operand_b), .in10(cpucm_128b_107_operand_b), .in11(cpucm_128b_108_operand_b),
    .in12(cpucm_128b_109_operand_b), .in13(cpucm_128b_110_operand_b), .in14(cpucm_128b_111_operand_b),
    .in15(cpucm_128b_112_operand_b), .in16(cpucm_128b_113_operand_b), .in17(cpucm_128b_114_operand_b),
    .in18(cpucm_128b_115_operand_b), .in19(cpucm_128b_116_operand_b), .in20(cpucm_128b_117_operand_b),
    .in21(cpucm_128b_118_operand_b), .in22(cpucm_128b_119_operand_b), .in23(cpucm_128b_120_operand_b),
    .in24(cpucm_128b_121_operand_b), .in25(cpucm_128b_122_operand_b), .in26(cpucm_128b_123_operand_b),
    .in27(cpucm_128b_124_operand_b), .in28(cpucm_128b_125_operand_b), .in29(cpucm_128b_126_operand_b),
    .in30(cpucm_128b_127_operand_b), .in31(cpucm_128b_128_operand_b), .out(multiplexer_14_out),
    .sel(get_B[9:5]));
  Multiplexer #(.select(5), .width(32), .disabled(0), .enable("false")) multiplexer_15 (
    .in0(cpucm_128b_97_external_access_data), .in1(cpucm_128b_98_external_access_data),
    .in2(cpucm_128b_99_external_access_data), .in3(cpucm_128b_100_external_access_data),
    .in4(cpucm_128b_101_external_access_data), .in5(cpucm_128b_102_external_access_data),
    .in6(cpucm_128b_103_external_access_data), .in7(cpucm_128b_104_external_access_data),
    .in8(cpucm_128b_105_external_access_data), .in9(cpucm_128b_106_external_access_data),
    .in10(cpucm_128b_107_external_access_data), .in11(cpucm_128b_108_external_access_data),
    .in12(cpucm_128b_109_external_access_data), .in13(cpucm_128b_110_external_access_data),
    .in14(cpucm_128b_111_external_access_data), .in15(cpucm_128b_112_external_access_data),
    .in16(cpucm_128b_113_external_access_data), .in17(cpucm_128b_114_external_access_data),
    .in18(cpucm_128b_115_external_access_data), .in19(cpucm_128b_116_external_access_data),
    .in20(cpucm_128b_117_external_access_data), .in21(cpucm_128b_118_external_access_data),
    .in22(cpucm_128b_119_external_access_data), .in23(cpucm_128b_120_external_access_data),
    .in24(cpucm_128b_121_external_access_data), .in25(cpucm_128b_122_external_access_data),
    .in26(cpucm_128b_123_external_access_data), .in27(cpucm_128b_124_external_access_data),
    .in28(cpucm_128b_125_external_access_data), .in29(cpucm_128b_126_external_access_data),
    .in30(cpucm_128b_127_external_access_data), .in31(cpucm_128b_128_external_access_data),
    .out(multiplexer_15_out), .sel(External_access_address[9:5]));
endmodule

module CPUCM_65536b (
  input  clear,
  input  [14:0] operation,
  input  clock,
  input  [13:0] get_A,
  input  [13:0] get_B,
  input  [13:0] External_access_Data,
  input  [31:0] Data_IN,
  output [31:0] External_Access_Data_2,
  output [31:0] Operand_B,
  output [31:0] Operand_A
);

  wire [12:0] demultiplexer_1_out0, demultiplexer_1_out1, demultiplexer_1_out2, demultiplexer_1_out3;
  wire [31:0] cpucm_16384b_1_external_access_data, cpucm_16384b_1_operand_a, cpucm_16384b_1_operand_b,
       cpucm_16384b_2_external_access_data, cpucm_16384b_2_operand_a, cpucm_16384b_2_operand_b,
       cpucm_16384b_3_external_access_data, cpucm_16384b_3_operand_a, cpucm_16384b_3_operand_b,
       cpucm_16384b_4_external_access_data, cpucm_16384b_4_operand_a, cpucm_16384b_4_operand_b;

  Demultiplexer #(.select(2), .width(13), .disabled(0), .enable("false")) demultiplexer_1 (
    .out0(demultiplexer_1_out0), .out1(demultiplexer_1_out1), .out2(demultiplexer_1_out2),
    .out3(demultiplexer_1_out3), .in(operation[12:0]), .sel(operation[14:13]));
  Multiplexer #(.select(2), .width(32), .disabled(0), .enable("false")) multiplexer_1 (
    .in0(cpucm_16384b_1_external_access_data), .in1(cpucm_16384b_2_external_access_data),
    .in2(cpucm_16384b_3_external_access_data), .in3(cpucm_16384b_4_external_access_data),
    .out(External_Access_Data_2), .sel(External_access_Data[13:12]));
  Multiplexer #(.select(2), .width(32), .disabled(0), .enable("false")) multiplexer_2 (
    .in0(cpucm_16384b_1_operand_b), .in1(cpucm_16384b_2_operand_b), .in2(cpucm_16384b_3_operand_b),
    .in3(cpucm_16384b_4_operand_b), .out(Operand_B), .sel(get_B[13:12]));
  Multiplexer #(.select(2), .width(32), .disabled(0), .enable("false")) multiplexer_3 (
    .in0(cpucm_16384b_1_operand_a), .in1(cpucm_16384b_2_operand_a), .in2(cpucm_16384b_3_operand_a),
    .in3(cpucm_16384b_4_operand_a), .out(Operand_A), .sel(get_A[13:12]));
  CPUCM_16384b cpucm_16384b_1 (
    .Data_IN(Data_IN), .External_access_address(External_access_Data[11:0]), .get_B(get_B[11:0]),
    .get_A(get_A[11:0]), .clock(clock), .operation(demultiplexer_1_out0),
    .External_Access_Data(cpucm_16384b_1_external_access_data), .Operand_B(cpucm_16384b_1_operand_b),
    .Operand_A(cpucm_16384b_1_operand_a), .clear(clear));
  CPUCM_16384b cpucm_16384b_2 (
    .Data_IN(Data_IN), .External_access_address(External_access_Data[11:0]), .get_B(get_B[11:0]),
    .get_A(get_A[11:0]), .clock(clock), .operation(demultiplexer_1_out1),
    .External_Access_Data(cpucm_16384b_2_external_access_data), .Operand_B(cpucm_16384b_2_operand_b),
    .Operand_A(cpucm_16384b_2_operand_a), .clear(clear));
  CPUCM_16384b cpucm_16384b_3 (
    .Data_IN(Data_IN), .External_access_address(External_access_Data[11:0]), .get_B(get_B[11:0]),
    .get_A(get_A[11:0]), .clock(clock), .operation(demultiplexer_1_out2),
    .External_Access_Data(cpucm_16384b_3_external_access_data), .Operand_B(cpucm_16384b_3_operand_b),
    .Operand_A(cpucm_16384b_3_operand_a), .clear(clear));
  CPUCM_16384b cpucm_16384b_4 (
    .Data_IN(Data_IN), .External_access_address(External_access_Data[11:0]), .get_B(get_B[11:0]),
    .get_A(get_A[11:0]), .clock(clock), .operation(demultiplexer_1_out3),
    .External_Access_Data(cpucm_16384b_4_external_access_data), .Operand_B(cpucm_16384b_4_operand_b),
    .Operand_A(cpucm_16384b_4_operand_a), .clear(clear));
endmodule

module total_OR (
  input  [31:0] in_1,
  output out_2
);

  or or_1 (out_2, in_1[0], in_1[1], in_1[2], in_1[3], in_1[4], in_1[5], in_1[6], in_1[7], in_1[8], in_1[9], in_1[10], in_1[11], in_1[12], in_1[13], in_1[14], in_1[15], in_1[17], in_1[18], in_1[19], in_1[20], in_1[21], in_1[22], in_1[23], in_1[24], in_1[25], in_1[26], in_1[27], in_1[28], in_1[29], in_1[30], in_1[31], in_1[16]);
endmodule
module ALU (
  input  [8:0] bool_control,
  input  [31:0] operand_A_0,
  input  [31:0] operand_A_1,
  input  [3:0] operation_control,
  input  [31:0] operand_B_0,
  input  [31:0] operand_B_1,
  output boolean,
  output [31:0] result_0,
  output [31:0] result_1
);

  wire adder_1_cout, adder_2_cout, bitselector_1_out, bitselector_2_out, or_1_out, subtractor_1_bout,
       subtractor_2_bout, total_or_1_out_2, total_or_2_out_2, \компаратор_64х_беззнаковый_1_out_5 ,
       \компаратор_64х_беззнаковый_1_out_6 , \компаратор_64х_беззнаковый_1_out_7 ;
  wire [5:0] adder_3_out, bitadder_1_out, bitadder_2_out;
  wire [6:6] adder_3_cout;
  wire [31:0] adder_1_out, adder_2_out, and_1_out, and_2_out, bit_extender_1_out, bit_extender_2_out,
       not_1_out, not_2_out, or_2_out, or_3_out, subtractor_1_out, subtractor_2_out, undriven, undriven_2,
       undriven_3, undriven_4, undriven_5, undriven_6, undriven_7, undriven_8, xor_1_out, xor_2_out,
       \сдвигатель_64х_левый_логический_1_r0 , \сдвигатель_64х_левый_логический_1_r1 ,
       \сдвигатель_64х_левый_циклический_1_r0 , \сдвигатель_64х_левый_циклический_1_r1 ,
       \сдвигатель_64х_правый_логический_1_r0 , \сдвигатель_64х_правый_логический_1_r1 ,
       \сдвигатель_64х_правый_циклический_1_r0 , \сдвигатель_64х_правый_циклический_1_r1 ;

  \множитель_64х  \u_множитель_64х_1  ();  // open: B_0, B_1, A_0, A_1, R_0, R_1, C_out_0, C_out_1
  \делитель_64х  \u_делитель_64х_1  ();  // open: A0, A1, B0, B1, Remainder_0, Remainder_1, R1, R0
  BitSelector #(.width(32)) bitselector_1 (.in(operand_A_0), .out(bitselector_1_out), .sel(bool_control[4:0]));
  BitSelector #(.width(32)) bitselector_2 (.in(operand_A_1), .out(bitselector_2_out), .sel(bool_control[4:0]));
  \компаратор_64х_беззнаковый  \u_компаратор_64х_беззнаковый_1  (
    .A0(operand_A_0), .B0(operand_B_0), .A1(operand_A_1), .B1(operand_B_1),
    .out_5(\компаратор_64х_беззнаковый_1_out_5 ), .out_6(\компаратор_64х_беззнаковый_1_out_6 ),
    .out_7(\компаратор_64х_беззнаковый_1_out_7 ));
  total_OR total_or_1 (.in_1(operand_A_0), .out_2(total_or_1_out_2));
  total_OR total_or_2 (.in_1(operand_A_1), .out_2(total_or_2_out_2));
  \сдвигатель_64х_левый_логический  \u_сдвигатель_64х_левый_логический_1  (
    .R0(\сдвигатель_64х_левый_логический_1_r0 ), .A0(operand_A_0), .A1(operand_A_1), .in_3(operand_B_0[5:0]),
    .R1(\сдвигатель_64х_левый_логический_1_r1 ));
  \сдвигатель_64х_левый_циклический  \u_сдвигатель_64х_левый_циклический_1  (
    .R0(\сдвигатель_64х_левый_циклический_1_r0 ), .A0(operand_A_0), .A1(operand_A_1),
    .in_3(operand_B_0[5:0]), .R1(\сдвигатель_64х_левый_циклический_1_r1 ));
  \сдвигатель_64х_правый_логический  \u_сдвигатель_64х_правый_логический_1  (
    .R0(\сдвигатель_64х_правый_логический_1_r0 ), .A0(operand_A_0), .A1(operand_A_1),
    .in_3(operand_B_0[5:0]), .R1(\сдвигатель_64х_правый_логический_1_r1 ));
  \сдвигатель_64х_правый_циклический  \u_сдвигатель_64х_правый_циклический_1  (
    .R0(\сдвигатель_64х_правый_циклический_1_r0 ), .A0(operand_A_0), .A1(operand_A_1),
    .in_3(operand_B_0[5:0]), .R1(\сдвигатель_64х_правый_циклический_1_r1 ));
  or or_1 (or_1_out, total_or_1_out_2, total_or_2_out_2);
  Adder #(.width(32)) adder_1 (.a(operand_A_0), .b(operand_B_0), .out(adder_1_out), .cin(1'b0), .cout(adder_1_cout));
  Adder #(.width(32)) adder_2 (
    .a(operand_A_1), .b(operand_B_1), .out(adder_2_out), .cin(adder_1_cout), .cout(adder_2_cout));
  Subtractor #(.width(32)) subtractor_1 (
    .a(operand_A_0), .b(operand_B_0), .out(subtractor_1_out), .bin(1'b0), .bout(subtractor_1_bout));
  Subtractor #(.width(32)) subtractor_2 (
    .a(operand_A_1), .b(operand_B_1), .out(subtractor_2_out), .bin(subtractor_1_bout),
    .bout(subtractor_2_bout));
  assign not_1_out = ~operand_A_0;  // NOT_Gate not_1, 32 bits wide
  assign not_2_out = ~operand_A_1;  // NOT_Gate not_2, 32 bits wide
  assign and_1_out = operand_A_0 & operand_B_0;  // AND_Gate and_1, 32 bits wide
  assign and_2_out = operand_A_1 & operand_B_1;  // AND_Gate and_2, 32 bits wide
  assign or_2_out = operand_A_0 | operand_B_0;  // OR_Gate or_2, 32 bits wide
  assign or_3_out = operand_A_1 | operand_B_1;  // OR_Gate or_3, 32 bits wide
  assign xor_1_out = operand_A_0 ^ operand_B_0;  // XOR_Gate xor_1, 32 bits wide
  assign xor_2_out = operand_A_1 ^ operand_B_1;  // XOR_Gate xor_2, 32 bits wide
  BitAdder #(.width(32)) bitadder_1 (.in0(operand_A_0), .out(bitadder_1_out));
  BitAdder #(.width(32)) bitadder_2 (.in0(operand_A_1), .out(bitadder_2_out));
  Adder #(.width(6)) adder_3 (
    .a(bitadder_1_out), .b(bitadder_2_out), .out(adder_3_out), .cout(adder_3_cout[6]));  // open: cin
  assign bit_extender_1_out = {{25{1'b0}}, {adder_3_cout[6], adder_3_out}};  // Bit_Extender bit_extender_1
  Multiplexer #(.select(4), .disabled(0), .enable("false")) multiplexer_1 (
    .in0(1'b0), .in1(1'b1), .in2(bitselector_1_out), .in3(bitselector_2_out),
    .in4(\компаратор_64х_беззнаковый_1_out_5 ), .in5(\компаратор_64х_беззнаковый_1_out_6 ),
    .in6(\компаратор_64х_беззнаковый_1_out_7 ), .in7(adder_2_cout), .in8(subtractor_2_bout), .in9(or_1_out),
    .out(boolean), .sel(bool_control[8:5]));  // open: in10, in11, in12, in13, in14, in15
  assign bit_extender_2_out = {{31{1'b0}}, boolean};  // Bit_Extender bit_extender_2
  Multiplexer #(.select(4), .width(32), .disabled(0), .enable("false")) multiplexer_2 (
    .in0(operand_A_0), .in1(adder_1_out), .in2(subtractor_1_out), .in3(undriven_6), .in4(undriven_2),
    .in5(undriven_4), .in6(undriven_7), .in7(not_1_out), .in8(and_1_out), .in9(or_2_out), .in10(xor_1_out),
    .in11(\сдвигатель_64х_левый_логический_1_r0 ), .in12(\сдвигатель_64х_левый_циклический_1_r0 ),
    .in13(\сдвигатель_64х_правый_логический_1_r0 ), .in14(\сдвигатель_64х_правый_циклический_1_r0 ),
    .in15(bit_extender_2_out), .out(result_0), .sel(operation_control));
  Multiplexer #(.select(4), .width(32), .disabled(0), .enable("false")) multiplexer_3 (
    .in0(operand_A_1), .in1(adder_2_out), .in2(subtractor_2_out), .in3(undriven), .in4(undriven_3),
    .in5(undriven_5), .in6(undriven_8), .in7(not_2_out), .in8(and_2_out), .in9(or_3_out), .in10(xor_2_out),
    .in11(\сдвигатель_64х_левый_логический_1_r1 ), .in12(\сдвигатель_64х_левый_циклический_1_r1 ),
    .in13(\сдвигатель_64х_правый_логический_1_r1 ), .in14(\сдвигатель_64х_правый_циклический_1_r1 ),
    .in15(bit_extender_1_out), .out(result_1), .sel(operation_control));
endmodule

module \делитель_64х  (
  input  [31:0] A0,
  input  [31:0] A1,
  input  [31:0] B0,
  input  [31:0] B1,
  output [31:0] R1,
  output [31:0] R0,
  output [31:0] Remainder_0,
  output [31:0] Remainder_1
);

  wire [30:0] \ступень_делителя_1_out_0 , \ступень_делителя_2_out_0 , \ступень_делителя_3_out_0 ,
       \ступень_делителя_4_out_0 , \ступень_делителя_5_out_0 , \ступень_делителя_6_out_0 ,
       \ступень_делителя_7_out_0 , \ступень_делителя_8_out_0 , \ступень_делителя_9_out_0 ,
       \ступень_делителя_10_out_0 , \ступень_делителя_11_out_0 , \ступень_делителя_12_out_0 ,
       \ступень_делителя_13_out_0 , \ступень_делителя_14_out_0 , \ступень_делителя_15_out_0 ,
       \ступень_делителя_16_out_0 , \ступень_делителя_17_out_0 , \ступень_делителя_18_out_0 ,
       \ступень_делителя_19_out_0 , \ступень_делителя_20_out_0 , \ступень_делителя_21_out_0 ,
       \ступень_делителя_22_out_0 , \ступень_делителя_23_out_0 , \ступень_делителя_24_out_0 ,
       \ступень_делителя_25_out_0 , \ступень_делителя_26_out_0 , \ступень_делителя_27_out_0 ,
       \ступень_делителя_28_out_0 , \ступень_делителя_29_out_0 , \ступень_делителя_30_out_0 ,
       \ступень_делителя_31_out_0 , \ступень_делителя_32_out_0 , \ступень_делителя_33_out_0 ,
       \ступень_делителя_34_out_0 , \ступень_делителя_35_out_0 , \ступень_делителя_36_out_0 ,
       \ступень_делителя_37_out_0 , \ступень_делителя_38_out_0 , \ступень_делителя_39_out_0 ,
       \ступень_делителя_40_out_0 , \ступень_делителя_41_out_0 , \ступень_делителя_42_out_0 ,
       \ступень_делителя_43_out_0 , \ступень_делителя_44_out_0 , \ступень_делителя_45_out_0 ,
       \ступень_делителя_46_out_0 , \ступень_делителя_47_out_0 , \ступень_делителя_48_out_0 ,
       \ступень_делителя_49_out_0 , \ступень_делителя_50_out_0 , \ступень_делителя_51_out_0 ,
       \ступень_делителя_52_out_0 , \ступень_делителя_53_out_0 , \ступень_делителя_54_out_0 ,
       \ступень_делителя_55_out_0 , \ступень_делителя_56_out_0 , \ступень_делителя_57_out_0 ,
       \ступень_делителя_58_out_0 , \ступень_делителя_59_out_0 , \ступень_делителя_60_out_0 ,
       \ступень_делителя_61_out_0 , \ступень_делителя_62_out_0 , \ступень_делителя_63_out_0 ,
       \ступень_делителя_64_out_0 ;
  wire [31:0] \ступень_делителя_1_out_1 , \ступень_делителя_2_out_1 , \ступень_делителя_2_q ,
       \ступень_делителя_3_out_1 , \ступень_делителя_4_out_1 , \ступень_делителя_5_out_1 ,
       \ступень_делителя_6_out_1 , \ступень_делителя_7_out_1 , \ступень_делителя_8_out_1 ,
       \ступень_делителя_9_out_1 , \ступень_делителя_10_out_1 , \ступень_делителя_11_out_1 ,
       \ступень_делителя_12_out_1 , \ступень_делителя_13_out_1 , \ступень_делителя_14_out_1 ,
       \ступень_делителя_15_out_1 , \ступень_делителя_16_out_1 , \ступень_делителя_17_out_1 ,
       \ступень_делителя_18_out_1 , \ступень_делителя_19_out_1 , \ступень_делителя_20_out_1 ,
       \ступень_делителя_21_out_1 , \ступень_делителя_22_out_1 , \ступень_делителя_23_out_1 ,
       \ступень_делителя_24_out_1 , \ступень_делителя_25_out_1 , \ступень_делителя_26_out_1 ,
       \ступень_делителя_27_out_1 , \ступень_делителя_28_out_1 , \ступень_делителя_29_out_1 ,
       \ступень_делителя_30_out_1 , \ступень_делителя_31_out_1 , \ступень_делителя_32_out_1 ,
       \ступень_делителя_33_out_1 , \ступень_делителя_33_q , \ступень_делителя_34_out_1 ,
       \ступень_делителя_35_out_1 , \ступень_делителя_36_out_1 , \ступень_делителя_37_out_1 ,
       \ступень_делителя_38_out_1 , \ступень_делителя_39_out_1 , \ступень_делителя_40_out_1 ,
       \ступень_делителя_41_out_1 , \ступень_делителя_42_out_1 , \ступень_делителя_43_out_1 ,
       \ступень_делителя_44_out_1 , \ступень_делителя_45_out_1 , \ступень_делителя_46_out_1 ,
       \ступень_делителя_47_out_1 , \ступень_делителя_48_out_1 , \ступень_делителя_49_out_1 ,
       \ступень_делителя_50_out_1 , \ступень_делителя_51_out_1 , \ступень_делителя_52_out_1 ,
       \ступень_делителя_53_out_1 , \ступень_делителя_54_out_1 , \ступень_делителя_55_out_1 ,
       \ступень_делителя_56_out_1 , \ступень_делителя_57_out_1 , \ступень_делителя_58_out_1 ,
       \ступень_делителя_59_out_1 , \ступень_делителя_60_out_1 , \ступень_делителя_61_out_1 ,
       \ступень_делителя_62_out_1 , \ступень_делителя_63_out_1 ;

  \ступень_делителя  \u_ступень_делителя_1  (
    .i(A1[30]), .IN0(\ступень_делителя_2_out_0 ), .IN1(\ступень_делителя_2_out_1 ), .D0(B0), .D1(B1),
    .OUT_0(\ступень_делителя_1_out_0 ), .OUT_1(\ступень_делителя_1_out_1 ), .Q(\ступень_делителя_2_q [1]));
  \ступень_делителя  \u_ступень_делителя_2  (
    .i(A1[31]), .IN0({31{1'b0}}), .IN1({32{1'b0}}), .D0(B0), .D1(B1), .OUT_0(\ступень_делителя_2_out_0 ),
    .OUT_1(\ступень_делителя_2_out_1 ), .Q(\ступень_делителя_2_q [0]));
  \ступень_делителя  \u_ступень_делителя_3  (
    .i(A1[28]), .IN0(\ступень_делителя_4_out_0 ), .IN1(\ступень_делителя_4_out_1 ), .D0(B0), .D1(B1),
    .OUT_0(\ступень_делителя_3_out_0 ), .OUT_1(\ступень_делителя_3_out_1 ), .Q(\ступень_делителя_2_q [3]));
  \ступень_делителя  \u_ступень_делителя_4  (
    .i(A1[29]), .IN0(\ступень_делителя_1_out_0 ), .IN1(\ступень_делителя_1_out_1 ), .D0(B0), .D1(B1),
    .OUT_0(\ступень_делителя_4_out_0 ), .OUT_1(\ступень_делителя_4_out_1 ), .Q(\ступень_делителя_2_q [2]));
  \ступень_делителя  \u_ступень_делителя_5  (
    .i(A1[26]), .IN0(\ступень_делителя_7_out_0 ), .IN1(\ступень_делителя_7_out_1 ), .D0(B0), .D1(B1),
    .OUT_0(\ступень_делителя_5_out_0 ), .OUT_1(\ступень_делителя_5_out_1 ), .Q(\ступень_делителя_2_q [5]));
  \ступень_делителя  \u_ступень_делителя_6  (
    .i(A1[25]), .IN0(\ступень_делителя_5_out_0 ), .IN1(\ступень_делителя_5_out_1 ), .D0(B0), .D1(B1),
    .OUT_0(\ступень_делителя_6_out_0 ), .OUT_1(\ступень_делителя_6_out_1 ), .Q(\ступень_делителя_2_q [6]));
  \ступень_делителя  \u_ступень_делителя_7  (
    .i(A1[27]), .IN0(\ступень_делителя_3_out_0 ), .IN1(\ступень_делителя_3_out_1 ), .D0(B0), .D1(B1),
    .OUT_0(\ступень_делителя_7_out_0 ), .OUT_1(\ступень_делителя_7_out_1 ), .Q(\ступень_делителя_2_q [4]));
  \ступень_делителя  \u_ступень_делителя_8  (
    .i(A1[24]), .IN0(\ступень_делителя_6_out_0 ), .IN1(\ступень_делителя_6_out_1 ), .D0(B0), .D1(B1),
    .OUT_0(\ступень_делителя_8_out_0 ), .OUT_1(\ступень_делителя_8_out_1 ), .Q(\ступень_делителя_2_q [7]));
  \ступень_делителя  \u_ступень_делителя_9  (
    .i(A1[22]), .IN0(\ступень_делителя_10_out_0 ), .IN1(\ступень_делителя_10_out_1 ), .D0(B0), .D1(B1),
    .OUT_0(\ступень_делителя_9_out_0 ), .OUT_1(\ступень_делителя_9_out_1 ), .Q(\ступень_делителя_2_q [9]));
  \ступень_делителя  \u_ступень_делителя_10  (
    .i(A1[23]), .IN0(\ступень_делителя_8_out_0 ), .IN1(\ступень_делителя_8_out_1 ), .D0(B0), .D1(B1),
    .OUT_0(\ступень_делителя_10_out_0 ), .OUT_1(\ступень_делителя_10_out_1 ), .Q(\ступень_делителя_2_q [8]));
  \ступень_делителя  \u_ступень_делителя_11  (
    .i(A1[20]), .IN0(\ступень_делителя_12_out_0 ), .IN1(\ступень_делителя_12_out_1 ), .D0(B0), .D1(B1),
    .OUT_0(\ступень_делителя_11_out_0 ), .OUT_1(\ступень_делителя_11_out_1 ), .Q(\ступень_делителя_2_q [11]));
  \ступень_делителя  \u_ступень_делителя_12  (
    .i(A1[21]), .IN0(\ступень_делителя_9_out_0 ), .IN1(\ступень_делителя_9_out_1 ), .D0(B0), .D1(B1),
    .OUT_0(\ступень_делителя_12_out_0 ), .OUT_1(\ступень_делителя_12_out_1 ), .Q(\ступень_делителя_2_q [10]));
  \ступень_делителя  \u_ступень_делителя_13  (
    .i(A1[19]), .IN0(\ступень_делителя_11_out_0 ), .IN1(\ступень_делителя_11_out_1 ), .D0(B0), .D1(B1),
    .OUT_0(\ступень_делителя_13_out_0 ), .OUT_1(\ступень_делителя_13_out_1 ), .Q(\ступень_делителя_2_q [12]));
  \ступень_делителя  \u_ступень_делителя_14  (
    .i(A1[17]), .IN0(\ступень_делителя_15_out_0 ), .IN1(\ступень_делителя_15_out_1 ), .D0(B0), .D1(B1),
    .OUT_0(\ступень_делителя_14_out_0 ), .OUT_1(\ступень_делителя_14_out_1 ), .Q(\ступень_делителя_2_q [14]));
  \ступень_делителя  \u_ступень_делителя_15  (
    .i(A1[18]), .IN0(\ступень_делителя_13_out_0 ), .IN1(\ступень_делителя_13_out_1 ), .D0(B0), .D1(B1),
    .OUT_0(\ступень_делителя_15_out_0 ), .OUT_1(\ступень_делителя_15_out_1 ), .Q(\ступень_делителя_2_q [13]));
  \ступень_делителя  \u_ступень_делителя_16  (
    .i(A1[15]), .IN0(\ступень_делителя_18_out_0 ), .IN1(\ступень_делителя_18_out_1 ), .D0(B0), .D1(B1),
    .OUT_0(\ступень_делителя_16_out_0 ), .OUT_1(\ступень_делителя_16_out_1 ), .Q(\ступень_делителя_2_q [16]));
  \ступень_делителя  \u_ступень_делителя_17  (
    .i(A1[14]), .IN0(\ступень_делителя_16_out_0 ), .IN1(\ступень_делителя_16_out_1 ), .D0(B0), .D1(B1),
    .OUT_0(\ступень_делителя_17_out_0 ), .OUT_1(\ступень_делителя_17_out_1 ), .Q(\ступень_делителя_2_q [17]));
  \ступень_делителя  \u_ступень_делителя_18  (
    .i(A1[16]), .IN0(\ступень_делителя_14_out_0 ), .IN1(\ступень_делителя_14_out_1 ), .D0(B0), .D1(B1),
    .OUT_0(\ступень_делителя_18_out_0 ), .OUT_1(\ступень_делителя_18_out_1 ), .Q(\ступень_делителя_2_q [15]));
  \ступень_делителя  \u_ступень_делителя_19  (
    .i(A1[12]), .IN0(\ступень_делителя_20_out_0 ), .IN1(\ступень_делителя_20_out_1 ), .D0(B0), .D1(B1),
    .OUT_0(\ступень_делителя_19_out_0 ), .OUT_1(\ступень_делителя_19_out_1 ), .Q(\ступень_делителя_2_q [19]));
  \ступень_делителя  \u_ступень_делителя_20  (
    .i(A1[13]), .IN0(\ступень_делителя_17_out_0 ), .IN1(\ступень_делителя_17_out_1 ), .D0(B0), .D1(B1),
    .OUT_0(\ступень_делителя_20_out_0 ), .OUT_1(\ступень_делителя_20_out_1 ), .Q(\ступень_делителя_2_q [18]));
  \ступень_делителя  \u_ступень_делителя_21  (
    .i(A1[10]), .IN0(\ступень_делителя_23_out_0 ), .IN1(\ступень_делителя_23_out_1 ), .D0(B0), .D1(B1),
    .OUT_0(\ступень_делителя_21_out_0 ), .OUT_1(\ступень_делителя_21_out_1 ), .Q(\ступень_делителя_2_q [21]));
  \ступень_делителя  \u_ступень_делителя_22  (
    .i(A1[9]), .IN0(\ступень_делителя_21_out_0 ), .IN1(\ступень_делителя_21_out_1 ), .D0(B0), .D1(B1),
    .OUT_0(\ступень_делителя_22_out_0 ), .OUT_1(\ступень_делителя_22_out_1 ), .Q(\ступень_делителя_2_q [22]));
  \ступень_делителя  \u_ступень_делителя_23  (
    .i(A1[11]), .IN0(\ступень_делителя_19_out_0 ), .IN1(\ступень_делителя_19_out_1 ), .D0(B0), .D1(B1),
    .OUT_0(\ступень_делителя_23_out_0 ), .OUT_1(\ступень_делителя_23_out_1 ), .Q(\ступень_делителя_2_q [20]));
  \ступень_делителя  \u_ступень_делителя_24  (
    .i(A1[7]), .IN0(\ступень_делителя_25_out_0 ), .IN1(\ступень_делителя_25_out_1 ), .D0(B0), .D1(B1),
    .OUT_0(\ступень_делителя_24_out_0 ), .OUT_1(\ступень_делителя_24_out_1 ), .Q(\ступень_делителя_2_q [24]));
  \ступень_делителя  \u_ступень_делителя_25  (
    .i(A1[8]), .IN0(\ступень_делителя_22_out_0 ), .IN1(\ступень_делителя_22_out_1 ), .D0(B0), .D1(B1),
    .OUT_0(\ступень_делителя_25_out_0 ), .OUT_1(\ступень_делителя_25_out_1 ), .Q(\ступень_делителя_2_q [23]));
  \ступень_делителя  \u_ступень_делителя_26  (
    .i(A1[6]), .IN0(\ступень_делителя_24_out_0 ), .IN1(\ступень_делителя_24_out_1 ), .D0(B0), .D1(B1),
    .OUT_0(\ступень_делителя_26_out_0 ), .OUT_1(\ступень_делителя_26_out_1 ), .Q(\ступень_делителя_2_q [25]));
  \ступень_делителя  \u_ступень_делителя_27  (
    .i(A1[4]), .IN0(\ступень_делителя_28_out_0 ), .IN1(\ступень_делителя_28_out_1 ), .D0(B0), .D1(B1),
    .OUT_0(\ступень_делителя_27_out_0 ), .OUT_1(\ступень_делителя_27_out_1 ), .Q(\ступень_делителя_2_q [27]));
  \ступень_делителя  \u_ступень_делителя_28  (
    .i(A1[5]), .IN0(\ступень_делителя_26_out_0 ), .IN1(\ступень_делителя_26_out_1 ), .D0(B0), .D1(B1),
    .OUT_0(\ступень_делителя_28_out_0 ), .OUT_1(\ступень_делителя_28_out_1 ), .Q(\ступень_делителя_2_q [26]));
  \ступень_делителя  \u_ступень_делителя_29  (
    .i(A1[3]), .IN0(\ступень_делителя_27_out_0 ), .IN1(\ступень_делителя_27_out_1 ), .D0(B0), .D1(B1),
    .OUT_0(\ступень_делителя_29_out_0 ), .OUT_1(\ступень_делителя_29_out_1 ), .Q(\ступень_делителя_2_q [28]));
  \ступень_делителя  \u_ступень_делителя_30  (
    .i(A1[1]), .IN0(\ступень_делителя_31_out_0 ), .IN1(\ступень_делителя_31_out_1 ), .D0(B0), .D1(B1),
    .OUT_0(\ступень_делителя_30_out_0 ), .OUT_1(\ступень_делителя_30_out_1 ), .Q(\ступень_делителя_2_q [30]));
  \ступень_делителя  \u_ступень_делителя_31  (
    .i(A1[2]), .IN0(\ступень_делителя_29_out_0 ), .IN1(\ступень_делителя_29_out_1 ), .D0(B0), .D1(B1),
    .OUT_0(\ступень_делителя_31_out_0 ), .OUT_1(\ступень_делителя_31_out_1 ), .Q(\ступень_делителя_2_q [29]));
  assign R1 = ~\ступень_делителя_2_q ;  // NOT_Gate not_1, 32 bits wide
  \ступень_делителя  \u_ступень_делителя_32  (
    .i(A1[0]), .IN0(\ступень_делителя_30_out_0 ), .IN1(\ступень_делителя_30_out_1 ), .D0(B0), .D1(B1),
    .OUT_0(\ступень_делителя_32_out_0 ), .OUT_1(\ступень_делителя_32_out_1 ), .Q(\ступень_делителя_2_q [31]));
  \ступень_делителя  \u_ступень_делителя_33  (
    .i(A0[31]), .IN0(\ступень_делителя_32_out_0 ), .IN1(\ступень_делителя_32_out_1 ), .D0(B0), .D1(B1),
    .OUT_0(\ступень_делителя_33_out_0 ), .OUT_1(\ступень_делителя_33_out_1 ), .Q(\ступень_делителя_33_q [0]));
  \ступень_делителя  \u_ступень_делителя_34  (
    .i(A0[30]), .IN0(\ступень_делителя_33_out_0 ), .IN1(\ступень_делителя_33_out_1 ), .D0(B0), .D1(B1),
    .OUT_0(\ступень_делителя_34_out_0 ), .OUT_1(\ступень_делителя_34_out_1 ), .Q(\ступень_делителя_33_q [1]));
  \ступень_делителя  \u_ступень_делителя_35  (
    .i(A0[29]), .IN0(\ступень_делителя_34_out_0 ), .IN1(\ступень_делителя_34_out_1 ), .D0(B0), .D1(B1),
    .OUT_0(\ступень_делителя_35_out_0 ), .OUT_1(\ступень_делителя_35_out_1 ), .Q(\ступень_делителя_33_q [2]));
  \ступень_делителя  \u_ступень_делителя_36  (
    .i(A0[28]), .IN0(\ступень_делителя_35_out_0 ), .IN1(\ступень_делителя_35_out_1 ), .D0(B0), .D1(B1),
    .OUT_0(\ступень_делителя_36_out_0 ), .OUT_1(\ступень_делителя_36_out_1 ), .Q(\ступень_делителя_33_q [3]));
  \ступень_делителя  \u_ступень_делителя_37  (
    .i(A0[26]), .IN0(\ступень_делителя_38_out_0 ), .IN1(\ступень_делителя_38_out_1 ), .D0(B0), .D1(B1),
    .OUT_0(\ступень_делителя_37_out_0 ), .OUT_1(\ступень_делителя_37_out_1 ), .Q(\ступень_делителя_33_q [5]));
  \ступень_делителя  \u_ступень_делителя_38  (
    .i(A0[27]), .IN0(\ступень_делителя_36_out_0 ), .IN1(\ступень_делителя_36_out_1 ), .D0(B0), .D1(B1),
    .OUT_0(\ступень_делителя_38_out_0 ), .OUT_1(\ступень_делителя_38_out_1 ), .Q(\ступень_делителя_33_q [4]));
  \ступень_делителя  \u_ступень_делителя_39  (
    .i(A0[25]), .IN0(\ступень_делителя_37_out_0 ), .IN1(\ступень_делителя_37_out_1 ), .D0(B0), .D1(B1),
    .OUT_0(\ступень_делителя_39_out_0 ), .OUT_1(\ступень_делителя_39_out_1 ), .Q(\ступень_делителя_33_q [6]));
  \ступень_делителя  \u_ступень_делителя_40  (
    .i(A0[24]), .IN0(\ступень_делителя_39_out_0 ), .IN1(\ступень_делителя_39_out_1 ), .D0(B0), .D1(B1),
    .OUT_0(\ступень_делителя_40_out_0 ), .OUT_1(\ступень_делителя_40_out_1 ), .Q(\ступень_делителя_33_q [7]));
  \ступень_делителя  \u_ступень_делителя_41  (
    .i(A0[23]), .IN0(\ступень_делителя_40_out_0 ), .IN1(\ступень_делителя_40_out_1 ), .D0(B0), .D1(B1),
    .OUT_0(\ступень_делителя_41_out_0 ), .OUT_1(\ступень_делителя_41_out_1 ), .Q(\ступень_делителя_33_q [8]));
  \ступень_делителя  \u_ступень_делителя_42  (
    .i(A0[22]), .IN0(\ступень_делителя_41_out_0 ), .IN1(\ступень_делителя_41_out_1 ), .D0(B0), .D1(B1),
    .OUT_0(\ступень_делителя_42_out_0 ), .OUT_1(\ступень_делителя_42_out_1 ), .Q(\ступень_делителя_33_q [9]));
  \ступень_делителя  \u_ступень_делителя_43  (
    .i(A0[21]), .IN0(\ступень_делителя_42_out_0 ), .IN1(\ступень_делителя_42_out_1 ), .D0(B0), .D1(B1),
    .OUT_0(\ступень_делителя_43_out_0 ), .OUT_1(\ступень_делителя_43_out_1 ), .Q(\ступень_делителя_33_q [10]));
  \ступень_делителя  \u_ступень_делителя_44  (
    .i(A0[20]), .IN0(\ступень_делителя_43_out_0 ), .IN1(\ступень_делителя_43_out_1 ), .D0(B0), .D1(B1),
    .OUT_0(\ступень_делителя_44_out_0 ), .OUT_1(\ступень_делителя_44_out_1 ), .Q(\ступень_делителя_33_q [11]));
  \ступень_делителя  \u_ступень_делителя_45  (
    .i(A0[19]), .IN0(\ступень_делителя_44_out_0 ), .IN1(\ступень_делителя_44_out_1 ), .D0(B0), .D1(B1),
    .OUT_0(\ступень_делителя_45_out_0 ), .OUT_1(\ступень_делителя_45_out_1 ), .Q(\ступень_делителя_33_q [12]));
  \ступень_делителя  \u_ступень_делителя_46  (
    .i(A0[18]), .IN0(\ступень_делителя_45_out_0 ), .IN1(\ступень_делителя_45_out_1 ), .D0(B0), .D1(B1),
    .OUT_0(\ступень_делителя_46_out_0 ), .OUT_1(\ступень_делителя_46_out_1 ), .Q(\ступень_делителя_33_q [13]));
  \ступень_делителя  \u_ступень_делителя_47  (
    .i(A0[17]), .IN0(\ступень_делителя_46_out_0 ), .IN1(\ступень_делителя_46_out_1 ), .D0(B0), .D1(B1),
    .OUT_0(\ступень_делителя_47_out_0 ), .OUT_1(\ступень_делителя_47_out_1 ), .Q(\ступень_делителя_33_q [14]));
  \ступень_делителя  \u_ступень_делителя_48  (
    .i(A0[14]), .IN0(\ступень_делителя_49_out_0 ), .IN1(\ступень_делителя_49_out_1 ), .D0(B0), .D1(B1),
    .OUT_0(\ступень_делителя_48_out_0 ), .OUT_1(\ступень_делителя_48_out_1 ), .Q(\ступень_делителя_33_q [17]));
  \ступень_делителя  \u_ступень_делителя_49  (
    .i(A0[15]), .IN0(\ступень_делителя_50_out_0 ), .IN1(\ступень_делителя_50_out_1 ), .D0(B0), .D1(B1),
    .OUT_0(\ступень_делителя_49_out_0 ), .OUT_1(\ступень_делителя_49_out_1 ), .Q(\ступень_делителя_33_q [16]));
  \ступень_делителя  \u_ступень_делителя_50  (
    .i(A0[16]), .IN0(\ступень_делителя_47_out_0 ), .IN1(\ступень_делителя_47_out_1 ), .D0(B0), .D1(B1),
    .OUT_0(\ступень_делителя_50_out_0 ), .OUT_1(\ступень_делителя_50_out_1 ), .Q(\ступень_делителя_33_q [15]));
  \ступень_делителя  \u_ступень_делителя_51  (
    .i(A0[13]), .IN0(\ступень_делителя_48_out_0 ), .IN1(\ступень_делителя_48_out_1 ), .D0(B0), .D1(B1),
    .OUT_0(\ступень_делителя_51_out_0 ), .OUT_1(\ступень_делителя_51_out_1 ), .Q(\ступень_делителя_33_q [18]));
  \ступень_делителя  \u_ступень_делителя_52  (
    .i(A0[12]), .IN0(\ступень_делителя_51_out_0 ), .IN1(\ступень_делителя_51_out_1 ), .D0(B0), .D1(B1),
    .OUT_0(\ступень_делителя_52_out_0 ), .OUT_1(\ступень_делителя_52_out_1 ), .Q(\ступень_делителя_33_q [19]));
  \ступень_делителя  \u_ступень_делителя_53  (
    .i(A0[11]), .IN0(\ступень_делителя_52_out_0 ), .IN1(\ступень_делителя_52_out_1 ), .D0(B0), .D1(B1),
    .OUT_0(\ступень_делителя_53_out_0 ), .OUT_1(\ступень_делителя_53_out_1 ), .Q(\ступень_делителя_33_q [20]));
  \ступень_делителя  \u_ступень_делителя_54  (
    .i(A0[9]), .IN0(\ступень_делителя_55_out_0 ), .IN1(\ступень_делителя_55_out_1 ), .D0(B0), .D1(B1),
    .OUT_0(\ступень_делителя_54_out_0 ), .OUT_1(\ступень_делителя_54_out_1 ), .Q(\ступень_делителя_33_q [22]));
  \ступень_делителя  \u_ступень_делителя_55  (
    .i(A0[10]), .IN0(\ступень_делителя_53_out_0 ), .IN1(\ступень_делителя_53_out_1 ), .D0(B0), .D1(B1),
    .OUT_0(\ступень_делителя_55_out_0 ), .OUT_1(\ступень_делителя_55_out_1 ), .Q(\ступень_делителя_33_q [21]));
  \ступень_делителя  \u_ступень_делителя_56  (
    .i(A0[8]), .IN0(\ступень_делителя_54_out_0 ), .IN1(\ступень_делителя_54_out_1 ), .D0(B0), .D1(B1),
    .OUT_0(\ступень_делителя_56_out_0 ), .OUT_1(\ступень_делителя_56_out_1 ), .Q(\ступень_делителя_33_q [23]));
  \ступень_делителя  \u_ступень_делителя_57  (
    .i(A0[6]), .IN0(\ступень_делителя_58_out_0 ), .IN1(\ступень_делителя_58_out_1 ), .D0(B0), .D1(B1),
    .OUT_0(\ступень_делителя_57_out_0 ), .OUT_1(\ступень_делителя_57_out_1 ), .Q(\ступень_делителя_33_q [25]));
  \ступень_делителя  \u_ступень_делителя_58  (
    .i(A0[7]), .IN0(\ступень_делителя_56_out_0 ), .IN1(\ступень_делителя_56_out_1 ), .D0(B0), .D1(B1),
    .OUT_0(\ступень_делителя_58_out_0 ), .OUT_1(\ступень_делителя_58_out_1 ), .Q(\ступень_делителя_33_q [24]));
  \ступень_делителя  \u_ступень_делителя_59  (
    .i(A0[5]), .IN0(\ступень_делителя_57_out_0 ), .IN1(\ступень_делителя_57_out_1 ), .D0(B0), .D1(B1),
    .OUT_0(\ступень_делителя_59_out_0 ), .OUT_1(\ступень_делителя_59_out_1 ), .Q(\ступень_делителя_33_q [26]));
  \ступень_делителя  \u_ступень_делителя_60  (
    .i(A0[4]), .IN0(\ступень_делителя_59_out_0 ), .IN1(\ступень_делителя_59_out_1 ), .D0(B0), .D1(B1),
    .OUT_0(\ступень_делителя_60_out_0 ), .OUT_1(\ступень_делителя_60_out_1 ), .Q(\ступень_делителя_33_q [27]));
  \ступень_делителя  \u_ступень_делителя_61  (
    .i(A0[1]), .IN0(\ступень_делителя_62_out_0 ), .IN1(\ступень_делителя_62_out_1 ), .D0(B0), .D1(B1),
    .OUT_0(\ступень_делителя_61_out_0 ), .OUT_1(\ступень_делителя_61_out_1 ), .Q(\ступень_делителя_33_q [30]));
  \ступень_делителя  \u_ступень_делителя_62  (
    .i(A0[2]), .IN0(\ступень_делителя_63_out_0 ), .IN1(\ступень_делителя_63_out_1 ), .D0(B0), .D1(B1),
    .OUT_0(\ступень_делителя_62_out_0 ), .OUT_1(\ступень_делителя_62_out_1 ), .Q(\ступень_делителя_33_q [29]));
  \ступень_делителя  \u_ступень_делителя_63  (
    .i(A0[3]), .IN0(\ступень_делителя_60_out_0 ), .IN1(\ступень_делителя_60_out_1 ), .D0(B0), .D1(B1),
    .OUT_0(\ступень_делителя_63_out_0 ), .OUT_1(\ступень_делителя_63_out_1 ), .Q(\ступень_делителя_33_q [28]));
  assign R0 = ~\ступень_делителя_33_q ;  // NOT_Gate not_2, 32 bits wide
  \ступень_делителя  \u_ступень_делителя_64  (
    .i(A0[0]), .IN0(\ступень_делителя_61_out_0 ), .IN1(\ступень_делителя_61_out_1 ), .D0(B0), .D1(B1),
    .OUT_0(\ступень_делителя_64_out_0 ), .OUT_1(Remainder_1), .Q(\ступень_делителя_33_q [31]));
  assign Remainder_0 = {{1{1'b0}}, \ступень_делителя_64_out_0 };  // Bit_Extender bit_extender_1
endmodule

module \ступень_делителя  (
  input  i,
  input  [30:0] IN0,
  input  [31:0] IN1,
  input  [31:0] D0,
  input  [31:0] D1,
  output [30:0] OUT_0,
  output [31:0] OUT_1,
  output Q
);

  wire subtractor_1_bout;
  wire [31:0] subtractor_1_out, subtractor_2_out;
  wire [31:31] multiplexer_2_out;

  Subtractor #(.width(32)) subtractor_1 (
    .a({IN0, i}), .b(D0), .out(subtractor_1_out), .bin(1'b0), .bout(subtractor_1_bout));
  Subtractor #(.width(32)) subtractor_2 (.a(IN1), .b(D1), .out(subtractor_2_out), .bin(subtractor_1_bout), .bout(Q));
  Multiplexer #(.width(32), .disabled(0), .enable("false")) multiplexer_1 (
    .in0(subtractor_1_out), .in1({IN0, i}), .out({OUT_1[0], OUT_0}), .sel(Q));
  Multiplexer #(.width(32), .disabled(0), .enable("false")) multiplexer_2 (
    .in0(subtractor_2_out), .in1(IN1), .out({multiplexer_2_out[31], OUT_1[31:1]}), .sel(Q));
endmodule

module \множитель_64х  (
  input  [31:0] B_0,
  input  [31:0] B_1,
  input  [31:0] A_0,
  input  [31:0] A_1,
  output [31:0] R_0,
  output [31:0] R_1,
  output [31:0] C_out_0,
  output [31:0] C_out_1
);

  wire [31:0] \ступень_множителя_1_c_out_0 , \ступень_множителя_1_c_out_1 , \ступень_множителя_2_c_out_0 ,
       \ступень_множителя_2_c_out_1 , \ступень_множителя_3_c_out_0 , \ступень_множителя_3_c_out_1 ,
       \ступень_множителя_4_c_out_0 , \ступень_множителя_4_c_out_1 , \ступень_множителя_5_c_out_0 ,
       \ступень_множителя_5_c_out_1 , \ступень_множителя_6_c_out_0 , \ступень_множителя_6_c_out_1 ,
       \ступень_множителя_7_c_out_0 , \ступень_множителя_7_c_out_1 , \ступень_множителя_8_c_out_0 ,
       \ступень_множителя_8_c_out_1 , \ступень_множителя_9_c_out_0 , \ступень_множителя_9_c_out_1 ,
       \ступень_множителя_10_c_out_0 , \ступень_множителя_10_c_out_1 , \ступень_множителя_11_c_out_0 ,
       \ступень_множителя_11_c_out_1 , \ступень_множителя_12_c_out_0 , \ступень_множителя_12_c_out_1 ,
       \ступень_множителя_13_c_out_0 , \ступень_множителя_13_c_out_1 , \ступень_множителя_14_c_out_0 ,
       \ступень_множителя_14_c_out_1 , \ступень_множителя_15_c_out_0 , \ступень_множителя_15_c_out_1 ,
       \ступень_множителя_16_c_out_0 , \ступень_множителя_16_c_out_1 , \ступень_множителя_17_c_out_0 ,
       \ступень_множителя_17_c_out_1 , \ступень_множителя_18_c_out_0 , \ступень_множителя_18_c_out_1 ,
       \ступень_множителя_19_c_out_0 , \ступень_множителя_19_c_out_1 , \ступень_множителя_20_c_out_0 ,
       \ступень_множителя_20_c_out_1 , \ступень_множителя_21_c_out_0 , \ступень_множителя_21_c_out_1 ,
       \ступень_множителя_22_c_out_0 , \ступень_множителя_22_c_out_1 , \ступень_множителя_23_c_out_0 ,
       \ступень_множителя_23_c_out_1 , \ступень_множителя_24_c_out_0 , \ступень_множителя_24_c_out_1 ,
       \ступень_множителя_25_c_out_0 , \ступень_множителя_25_c_out_1 , \ступень_множителя_26_c_out_0 ,
       \ступень_множителя_26_c_out_1 , \ступень_множителя_27_c_out_0 , \ступень_множителя_27_c_out_1 ,
       \ступень_множителя_28_c_out_0 , \ступень_множителя_28_c_out_1 , \ступень_множителя_29_c_out_0 ,
       \ступень_множителя_29_c_out_1 , \ступень_множителя_30_c_out_0 , \ступень_множителя_30_c_out_1 ,
       \ступень_множителя_31_c_out_0 , \ступень_множителя_31_c_out_1 , \ступень_множителя_32_c_out_0 ,
       \ступень_множителя_32_c_out_1 , \ступень_множителя_33_c_out_0 , \ступень_множителя_33_c_out_1 ,
       \ступень_множителя_34_c_out_0 , \ступень_множителя_34_c_out_1 , \ступень_множителя_35_c_out_0 ,
       \ступень_множителя_35_c_out_1 , \ступень_множителя_36_c_out_0 , \ступень_множителя_36_c_out_1 ,
       \ступень_множителя_37_c_out_0 , \ступень_множителя_37_c_out_1 , \ступень_множителя_38_c_out_0 ,
       \ступень_множителя_38_c_out_1 , \ступень_множителя_39_c_out_0 , \ступень_множителя_39_c_out_1 ,
       \ступень_множителя_40_c_out_0 , \ступень_множителя_40_c_out_1 , \ступень_множителя_41_c_out_0 ,
       \ступень_множителя_41_c_out_1 , \ступень_множителя_42_c_out_0 , \ступень_множителя_42_c_out_1 ,
       \ступень_множителя_43_c_out_0 , \ступень_множителя_43_c_out_1 , \ступень_множителя_44_c_out_0 ,
       \ступень_множителя_44_c_out_1 , \ступень_множителя_45_c_out_0 , \ступень_множителя_45_c_out_1 ,
       \ступень_множителя_46_c_out_0 , \ступень_множителя_46_c_out_1 , \ступень_множителя_47_c_out_0 ,
       \ступень_множителя_47_c_out_1 , \ступень_множителя_48_c_out_0 , \ступень_множителя_48_c_out_1 ,
       \ступень_множителя_49_c_out_0 , \ступень_множителя_49_c_out_1 , \ступень_множителя_50_c_out_0 ,
       \ступень_множителя_50_c_out_1 , \ступень_множителя_51_c_out_0 , \ступень_множителя_51_c_out_1 ,
       \ступень_множителя_52_c_out_0 , \ступень_множителя_52_c_out_1 , \ступень_множителя_53_c_out_0 ,
       \ступень_множителя_53_c_out_1 , \ступень_множителя_54_c_out_0 , \ступень_множителя_54_c_out_1 ,
       \ступень_множителя_55_c_out_0 , \ступень_множителя_55_c_out_1 , \ступень_множителя_56_c_out_0 ,
       \ступень_множителя_56_c_out_1 , \ступень_множителя_57_c_out_0 , \ступень_множителя_57_c_out_1 ,
       \ступень_множителя_58_c_out_0 , \ступень_множителя_58_c_out_1 , \ступень_множителя_59_c_out_0 ,
       \ступень_множителя_59_c_out_1 , \ступень_множителя_60_c_out_0 , \ступень_множителя_60_c_out_1 ,
       \ступень_множителя_61_c_out_0 , \ступень_множителя_61_c_out_1 , \ступень_множителя_62_c_out_0 ,
       \ступень_множителя_62_c_out_1 , \ступень_множителя_63_c_out_0 , \ступень_множителя_63_c_out_1 ;

  \ступень_множителя  \u_ступень_множителя_1  (
    .in__B(B_0[1]), .in_0__A(A_0), .in_1__A(A_1), .C_in_0(\ступень_множителя_2_c_out_0 ),
    .C_in_1(\ступень_множителя_2_c_out_1 ), .out(R_0[1]), .C_out_0(\ступень_множителя_1_c_out_0 ),
    .C_out_1(\ступень_множителя_1_c_out_1 ));
  \ступень_множителя  \u_ступень_множителя_2  (
    .in__B(B_0[0]), .in_0__A(A_0), .in_1__A(A_1), .C_in_0({32{1'b0}}), .C_in_1({32{1'b0}}), .out(R_0[0]),
    .C_out_0(\ступень_множителя_2_c_out_0 ), .C_out_1(\ступень_множителя_2_c_out_1 ));
  \ступень_множителя  \u_ступень_множителя_3  (
    .in__B(B_0[2]), .in_0__A(A_0), .in_1__A(A_1), .C_in_0(\ступень_множителя_1_c_out_0 ),
    .C_in_1(\ступень_множителя_1_c_out_1 ), .out(R_0[2]), .C_out_0(\ступень_множителя_3_c_out_0 ),
    .C_out_1(\ступень_множителя_3_c_out_1 ));
  \ступень_множителя  \u_ступень_множителя_4  (
    .in__B(B_0[3]), .in_0__A(A_0), .in_1__A(A_1), .C_in_0(\ступень_множителя_3_c_out_0 ),
    .C_in_1(\ступень_множителя_3_c_out_1 ), .out(R_0[3]), .C_out_0(\ступень_множителя_4_c_out_0 ),
    .C_out_1(\ступень_множителя_4_c_out_1 ));
  \ступень_множителя  \u_ступень_множителя_5  (
    .in__B(B_0[4]), .in_0__A(A_0), .in_1__A(A_1), .C_in_0(\ступень_множителя_4_c_out_0 ),
    .C_in_1(\ступень_множителя_4_c_out_1 ), .out(R_0[4]), .C_out_0(\ступень_множителя_5_c_out_0 ),
    .C_out_1(\ступень_множителя_5_c_out_1 ));
  \ступень_множителя  \u_ступень_множителя_6  (
    .in__B(B_0[6]), .in_0__A(A_0), .in_1__A(A_1), .C_in_0(\ступень_множителя_7_c_out_0 ),
    .C_in_1(\ступень_множителя_7_c_out_1 ), .out(R_0[6]), .C_out_0(\ступень_множителя_6_c_out_0 ),
    .C_out_1(\ступень_множителя_6_c_out_1 ));
  \ступень_множителя  \u_ступень_множителя_7  (
    .in__B(B_0[5]), .in_0__A(A_0), .in_1__A(A_1), .C_in_0(\ступень_множителя_5_c_out_0 ),
    .C_in_1(\ступень_множителя_5_c_out_1 ), .out(R_0[5]), .C_out_0(\ступень_множителя_7_c_out_0 ),
    .C_out_1(\ступень_множителя_7_c_out_1 ));
  \ступень_множителя  \u_ступень_множителя_8  (
    .in__B(B_0[8]), .in_0__A(A_0), .in_1__A(A_1), .C_in_0(\ступень_множителя_10_c_out_0 ),
    .C_in_1(\ступень_множителя_10_c_out_1 ), .out(R_0[8]), .C_out_0(\ступень_множителя_8_c_out_0 ),
    .C_out_1(\ступень_множителя_8_c_out_1 ));
  \ступень_множителя  \u_ступень_множителя_9  (
    .in__B(B_0[9]), .in_0__A(A_0), .in_1__A(A_1), .C_in_0(\ступень_множителя_8_c_out_0 ),
    .C_in_1(\ступень_множителя_8_c_out_1 ), .out(R_0[9]), .C_out_0(\ступень_множителя_9_c_out_0 ),
    .C_out_1(\ступень_множителя_9_c_out_1 ));
  \ступень_множителя  \u_ступень_множителя_10  (
    .in__B(B_0[7]), .in_0__A(A_0), .in_1__A(A_1), .C_in_0(\ступень_множителя_6_c_out_0 ),
    .C_in_1(\ступень_множителя_6_c_out_1 ), .out(R_0[7]), .C_out_0(\ступень_множителя_10_c_out_0 ),
    .C_out_1(\ступень_множителя_10_c_out_1 ));
  \ступень_множителя  \u_ступень_множителя_11  (
    .in__B(B_0[10]), .in_0__A(A_0), .in_1__A(A_1), .C_in_0(\ступень_множителя_9_c_out_0 ),
    .C_in_1(\ступень_множителя_9_c_out_1 ), .out(R_0[10]), .C_out_0(\ступень_множителя_11_c_out_0 ),
    .C_out_1(\ступень_множителя_11_c_out_1 ));
  \ступень_множителя  \u_ступень_множителя_12  (
    .in__B(B_0[12]), .in_0__A(A_0), .in_1__A(A_1), .C_in_0(\ступень_множителя_13_c_out_0 ),
    .C_in_1(\ступень_множителя_13_c_out_1 ), .out(R_0[12]), .C_out_0(\ступень_множителя_12_c_out_0 ),
    .C_out_1(\ступень_множителя_12_c_out_1 ));
  \ступень_множителя  \u_ступень_множителя_13  (
    .in__B(B_0[11]), .in_0__A(A_0), .in_1__A(A_1), .C_in_0(\ступень_множителя_11_c_out_0 ),
    .C_in_1(\ступень_множителя_11_c_out_1 ), .out(R_0[11]), .C_out_0(\ступень_множителя_13_c_out_0 ),
    .C_out_1(\ступень_множителя_13_c_out_1 ));
  \ступень_множителя  \u_ступень_множителя_14  (
    .in__B(B_0[14]), .in_0__A(A_0), .in_1__A(A_1), .C_in_0(\ступень_множителя_15_c_out_0 ),
    .C_in_1(\ступень_множителя_15_c_out_1 ), .out(R_0[14]), .C_out_0(\ступень_множителя_14_c_out_0 ),
    .C_out_1(\ступень_множителя_14_c_out_1 ));
  \ступень_множителя  \u_ступень_множителя_15  (
    .in__B(B_0[13]), .in_0__A(A_0), .in_1__A(A_1), .C_in_0(\ступень_множителя_12_c_out_0 ),
    .C_in_1(\ступень_множителя_12_c_out_1 ), .out(R_0[13]), .C_out_0(\ступень_множителя_15_c_out_0 ),
    .C_out_1(\ступень_множителя_15_c_out_1 ));
  \ступень_множителя  \u_ступень_множителя_16  (
    .in__B(B_0[16]), .in_0__A(A_0), .in_1__A(A_1), .C_in_0(\ступень_множителя_18_c_out_0 ),
    .C_in_1(\ступень_множителя_18_c_out_1 ), .out(R_0[16]), .C_out_0(\ступень_множителя_16_c_out_0 ),
    .C_out_1(\ступень_множителя_16_c_out_1 ));
  \ступень_множителя  \u_ступень_множителя_17  (
    .in__B(B_0[17]), .in_0__A(A_0), .in_1__A(A_1), .C_in_0(\ступень_множителя_16_c_out_0 ),
    .C_in_1(\ступень_множителя_16_c_out_1 ), .out(R_0[17]), .C_out_0(\ступень_множителя_17_c_out_0 ),
    .C_out_1(\ступень_множителя_17_c_out_1 ));
  \ступень_множителя  \u_ступень_множителя_18  (
    .in__B(B_0[15]), .in_0__A(A_0), .in_1__A(A_1), .C_in_0(\ступень_множителя_14_c_out_0 ),
    .C_in_1(\ступень_множителя_14_c_out_1 ), .out(R_0[15]), .C_out_0(\ступень_множителя_18_c_out_0 ),
    .C_out_1(\ступень_множителя_18_c_out_1 ));
  \ступень_множителя  \u_ступень_множителя_19  (
    .in__B(B_0[19]), .in_0__A(A_0), .in_1__A(A_1), .C_in_0(\ступень_множителя_20_c_out_0 ),
    .C_in_1(\ступень_множителя_20_c_out_1 ), .out(R_0[19]), .C_out_0(\ступень_множителя_19_c_out_0 ),
    .C_out_1(\ступень_множителя_19_c_out_1 ));
  \ступень_множителя  \u_ступень_множителя_20  (
    .in__B(B_0[18]), .in_0__A(A_0), .in_1__A(A_1), .C_in_0(\ступень_множителя_17_c_out_0 ),
    .C_in_1(\ступень_множителя_17_c_out_1 ), .out(R_0[18]), .C_out_0(\ступень_множителя_20_c_out_0 ),
    .C_out_1(\ступень_множителя_20_c_out_1 ));
  \ступень_множителя  \u_ступень_множителя_21  (
    .in__B(B_0[20]), .in_0__A(A_0), .in_1__A(A_1), .C_in_0(\ступень_множителя_19_c_out_0 ),
    .C_in_1(\ступень_множителя_19_c_out_1 ), .out(R_0[20]), .C_out_0(\ступень_множителя_21_c_out_0 ),
    .C_out_1(\ступень_множителя_21_c_out_1 ));
  \ступень_множителя  \u_ступень_множителя_22  (
    .in__B(B_0[21]), .in_0__A(A_0), .in_1__A(A_1), .C_in_0(\ступень_множителя_21_c_out_0 ),
    .C_in_1(\ступень_множителя_21_c_out_1 ), .out(R_0[21]), .C_out_0(\ступень_множителя_22_c_out_0 ),
    .C_out_1(\ступень_множителя_22_c_out_1 ));
  \ступень_множителя  \u_ступень_множителя_23  (
    .in__B(B_0[22]), .in_0__A(A_0), .in_1__A(A_1), .C_in_0(\ступень_множителя_22_c_out_0 ),
    .C_in_1(\ступень_множителя_22_c_out_1 ), .out(R_0[22]), .C_out_0(\ступень_множителя_23_c_out_0 ),
    .C_out_1(\ступень_множителя_23_c_out_1 ));
  \ступень_множителя  \u_ступень_множителя_24  (
    .in__B(B_0[24]), .in_0__A(A_0), .in_1__A(A_1), .C_in_0(\ступень_множителя_25_c_out_0 ),
    .C_in_1(\ступень_множителя_25_c_out_1 ), .out(R_0[24]), .C_out_0(\ступень_множителя_24_c_out_0 ),
    .C_out_1(\ступень_множителя_24_c_out_1 ));
  \ступень_множителя  \u_ступень_множителя_25  (
    .in__B(B_0[23]), .in_0__A(A_0), .in_1__A(A_1), .C_in_0(\ступень_множителя_23_c_out_0 ),
    .C_in_1(\ступень_множителя_23_c_out_1 ), .out(R_0[23]), .C_out_0(\ступень_множителя_25_c_out_0 ),
    .C_out_1(\ступень_множителя_25_c_out_1 ));
  \ступень_множителя  \u_ступень_множителя_26  (
    .in__B(B_0[25]), .in_0__A(A_0), .in_1__A(A_1), .C_in_0(\ступень_множителя_24_c_out_0 ),
    .C_in_1(\ступень_множителя_24_c_out_1 ), .out(R_0[25]), .C_out_0(\ступень_множителя_26_c_out_0 ),
    .C_out_1(\ступень_множителя_26_c_out_1 ));
  \ступень_множителя  \u_ступень_множителя_27  (
    .in__B(B_0[26]), .in_0__A(A_0), .in_1__A(A_1), .C_in_0(\ступень_множителя_26_c_out_0 ),
    .C_in_1(\ступень_множителя_26_c_out_1 ), .out(R_0[26]), .C_out_0(\ступень_множителя_27_c_out_0 ),
    .C_out_1(\ступень_множителя_27_c_out_1 ));
  \ступень_множителя  \u_ступень_множителя_28  (
    .in__B(B_0[28]), .in_0__A(A_0), .in_1__A(A_1), .C_in_0(\ступень_множителя_29_c_out_0 ),
    .C_in_1(\ступень_множителя_29_c_out_1 ), .out(R_0[28]), .C_out_0(\ступень_множителя_28_c_out_0 ),
    .C_out_1(\ступень_множителя_28_c_out_1 ));
  \ступень_множителя  \u_ступень_множителя_29  (
    .in__B(B_0[27]), .in_0__A(A_0), .in_1__A(A_1), .C_in_0(\ступень_множителя_27_c_out_0 ),
    .C_in_1(\ступень_множителя_27_c_out_1 ), .out(R_0[27]), .C_out_0(\ступень_множителя_29_c_out_0 ),
    .C_out_1(\ступень_множителя_29_c_out_1 ));
  \ступень_множителя  \u_ступень_множителя_30  (
    .in__B(B_0[30]), .in_0__A(A_0), .in_1__A(A_1), .C_in_0(\ступень_множителя_31_c_out_0 ),
    .C_in_1(\ступень_множителя_31_c_out_1 ), .out(R_0[30]), .C_out_0(\ступень_множителя_30_c_out_0 ),
    .C_out_1(\ступень_множителя_30_c_out_1 ));
  \ступень_множителя  \u_ступень_множителя_31  (
    .in__B(B_0[29]), .in_0__A(A_0), .in_1__A(A_1), .C_in_0(\ступень_множителя_28_c_out_0 ),
    .C_in_1(\ступень_множителя_28_c_out_1 ), .out(R_0[29]), .C_out_0(\ступень_множителя_31_c_out_0 ),
    .C_out_1(\ступень_множителя_31_c_out_1 ));
  \ступень_множителя  \u_ступень_множителя_32  (
    .in__B(B_0[31]), .in_0__A(A_0), .in_1__A(A_1), .C_in_0(\ступень_множителя_30_c_out_0 ),
    .C_in_1(\ступень_множителя_30_c_out_1 ), .out(R_0[31]), .C_out_0(\ступень_множителя_32_c_out_0 ),
    .C_out_1(\ступень_множителя_32_c_out_1 ));
  \ступень_множителя  \u_ступень_множителя_33  (
    .in__B(B_1[2]), .in_0__A(A_0), .in_1__A(A_1), .C_in_0(\ступень_множителя_34_c_out_0 ),
    .C_in_1(\ступень_множителя_34_c_out_1 ), .out(R_1[2]), .C_out_0(\ступень_множителя_33_c_out_0 ),
    .C_out_1(\ступень_множителя_33_c_out_1 ));
  \ступень_множителя  \u_ступень_множителя_34  (
    .in__B(B_1[1]), .in_0__A(A_0), .in_1__A(A_1), .C_in_0(\ступень_множителя_35_c_out_0 ),
    .C_in_1(\ступень_множителя_35_c_out_1 ), .out(R_1[1]), .C_out_0(\ступень_множителя_34_c_out_0 ),
    .C_out_1(\ступень_множителя_34_c_out_1 ));
  \ступень_множителя  \u_ступень_множителя_35  (
    .in__B(B_1[0]), .in_0__A(A_0), .in_1__A(A_1), .C_in_0(\ступень_множителя_32_c_out_0 ),
    .C_in_1(\ступень_множителя_32_c_out_1 ), .out(R_1[0]), .C_out_0(\ступень_множителя_35_c_out_0 ),
    .C_out_1(\ступень_множителя_35_c_out_1 ));
  \ступень_множителя  \u_ступень_множителя_36  (
    .in__B(B_1[3]), .in_0__A(A_0), .in_1__A(A_1), .C_in_0(\ступень_множителя_33_c_out_0 ),
    .C_in_1(\ступень_множителя_33_c_out_1 ), .out(R_1[3]), .C_out_0(\ступень_множителя_36_c_out_0 ),
    .C_out_1(\ступень_множителя_36_c_out_1 ));
  \ступень_множителя  \u_ступень_множителя_37  (
    .in__B(B_1[4]), .in_0__A(A_0), .in_1__A(A_1), .C_in_0(\ступень_множителя_36_c_out_0 ),
    .C_in_1(\ступень_множителя_36_c_out_1 ), .out(R_1[4]), .C_out_0(\ступень_множителя_37_c_out_0 ),
    .C_out_1(\ступень_множителя_37_c_out_1 ));
  \ступень_множителя  \u_ступень_множителя_38  (
    .in__B(B_1[5]), .in_0__A(A_0), .in_1__A(A_1), .C_in_0(\ступень_множителя_37_c_out_0 ),
    .C_in_1(\ступень_множителя_37_c_out_1 ), .out(R_1[5]), .C_out_0(\ступень_множителя_38_c_out_0 ),
    .C_out_1(\ступень_множителя_38_c_out_1 ));
  \ступень_множителя  \u_ступень_множителя_39  (
    .in__B(B_1[7]), .in_0__A(A_0), .in_1__A(A_1), .C_in_0(\ступень_множителя_40_c_out_0 ),
    .C_in_1(\ступень_множителя_40_c_out_1 ), .out(R_1[7]), .C_out_0(\ступень_множителя_39_c_out_0 ),
    .C_out_1(\ступень_множителя_39_c_out_1 ));
  \ступень_множителя  \u_ступень_множителя_40  (
    .in__B(B_1[6]), .in_0__A(A_0), .in_1__A(A_1), .C_in_0(\ступень_множителя_38_c_out_0 ),
    .C_in_1(\ступень_множителя_38_c_out_1 ), .out(R_1[6]), .C_out_0(\ступень_множителя_40_c_out_0 ),
    .C_out_1(\ступень_множителя_40_c_out_1 ));
  \ступень_множителя  \u_ступень_множителя_41  (
    .in__B(B_1[9]), .in_0__A(A_0), .in_1__A(A_1), .C_in_0(\ступень_множителя_42_c_out_0 ),
    .C_in_1(\ступень_множителя_42_c_out_1 ), .out(R_1[9]), .C_out_0(\ступень_множителя_41_c_out_0 ),
    .C_out_1(\ступень_множителя_41_c_out_1 ));
  \ступень_множителя  \u_ступень_множителя_42  (
    .in__B(B_1[8]), .in_0__A(A_0), .in_1__A(A_1), .C_in_0(\ступень_множителя_39_c_out_0 ),
    .C_in_1(\ступень_множителя_39_c_out_1 ), .out(R_1[8]), .C_out_0(\ступень_множителя_42_c_out_0 ),
    .C_out_1(\ступень_множителя_42_c_out_1 ));
  \ступень_множителя  \u_ступень_множителя_43  (
    .in__B(B_1[10]), .in_0__A(A_0), .in_1__A(A_1), .C_in_0(\ступень_множителя_41_c_out_0 ),
    .C_in_1(\ступень_множителя_41_c_out_1 ), .out(R_1[10]), .C_out_0(\ступень_множителя_43_c_out_0 ),
    .C_out_1(\ступень_множителя_43_c_out_1 ));
  \ступень_множителя  \u_ступень_множителя_44  (
    .in__B(B_1[11]), .in_0__A(A_0), .in_1__A(A_1), .C_in_0(\ступень_множителя_43_c_out_0 ),
    .C_in_1(\ступень_множителя_43_c_out_1 ), .out(R_1[11]), .C_out_0(\ступень_множителя_44_c_out_0 ),
    .C_out_1(\ступень_множителя_44_c_out_1 ));
  \ступень_множителя  \u_ступень_множителя_45  (
    .in__B(B_1[12]), .in_0__A(A_0), .in_1__A(A_1), .C_in_0(\ступень_множителя_44_c_out_0 ),
    .C_in_1(\ступень_множителя_44_c_out_1 ), .out(R_1[12]), .C_out_0(\ступень_множителя_45_c_out_0 ),
    .C_out_1(\ступень_множителя_45_c_out_1 ));
  \ступень_множителя  \u_ступень_множителя_46  (
    .in__B(B_1[14]), .in_0__A(A_0), .in_1__A(A_1), .C_in_0(\ступень_множителя_47_c_out_0 ),
    .C_in_1(\ступень_множителя_47_c_out_1 ), .out(R_1[14]), .C_out_0(\ступень_множителя_46_c_out_0 ),
    .C_out_1(\ступень_множителя_46_c_out_1 ));
  \ступень_множителя  \u_ступень_множителя_47  (
    .in__B(B_1[13]), .in_0__A(A_0), .in_1__A(A_1), .C_in_0(\ступень_множителя_45_c_out_0 ),
    .C_in_1(\ступень_множителя_45_c_out_1 ), .out(R_1[13]), .C_out_0(\ступень_множителя_47_c_out_0 ),
    .C_out_1(\ступень_множителя_47_c_out_1 ));
  \ступень_множителя  \u_ступень_множителя_48  (
    .in__B(B_1[15]), .in_0__A(A_0), .in_1__A(A_1), .C_in_0(\ступень_множителя_46_c_out_0 ),
    .C_in_1(\ступень_множителя_46_c_out_1 ), .out(R_1[15]), .C_out_0(\ступень_множителя_48_c_out_0 ),
    .C_out_1(\ступень_множителя_48_c_out_1 ));
  \ступень_множителя  \u_ступень_множителя_49  (
    .in__B(B_1[17]), .in_0__A(A_0), .in_1__A(A_1), .C_in_0(\ступень_множителя_51_c_out_0 ),
    .C_in_1(\ступень_множителя_51_c_out_1 ), .out(R_1[17]), .C_out_0(\ступень_множителя_49_c_out_0 ),
    .C_out_1(\ступень_множителя_49_c_out_1 ));
  \ступень_множителя  \u_ступень_множителя_50  (
    .in__B(B_1[18]), .in_0__A(A_0), .in_1__A(A_1), .C_in_0(\ступень_множителя_49_c_out_0 ),
    .C_in_1(\ступень_множителя_49_c_out_1 ), .out(R_1[18]), .C_out_0(\ступень_множителя_50_c_out_0 ),
    .C_out_1(\ступень_множителя_50_c_out_1 ));
  \ступень_множителя  \u_ступень_множителя_51  (
    .in__B(B_1[16]), .in_0__A(A_0), .in_1__A(A_1), .C_in_0(\ступень_множителя_48_c_out_0 ),
    .C_in_1(\ступень_множителя_48_c_out_1 ), .out(R_1[16]), .C_out_0(\ступень_множителя_51_c_out_0 ),
    .C_out_1(\ступень_множителя_51_c_out_1 ));
  \ступень_множителя  \u_ступень_множителя_52  (
    .in__B(B_1[19]), .in_0__A(A_0), .in_1__A(A_1), .C_in_0(\ступень_множителя_50_c_out_0 ),
    .C_in_1(\ступень_множителя_50_c_out_1 ), .out(R_1[19]), .C_out_0(\ступень_множителя_52_c_out_0 ),
    .C_out_1(\ступень_множителя_52_c_out_1 ));
  \ступень_множителя  \u_ступень_множителя_53  (
    .in__B(B_1[20]), .in_0__A(A_0), .in_1__A(A_1), .C_in_0(\ступень_множителя_52_c_out_0 ),
    .C_in_1(\ступень_множителя_52_c_out_1 ), .out(R_1[20]), .C_out_0(\ступень_множителя_53_c_out_0 ),
    .C_out_1(\ступень_множителя_53_c_out_1 ));
  \ступень_множителя  \u_ступень_множителя_54  (
    .in__B(B_1[21]), .in_0__A(A_0), .in_1__A(A_1), .C_in_0(\ступень_множителя_53_c_out_0 ),
    .C_in_1(\ступень_множителя_53_c_out_1 ), .out(R_1[21]), .C_out_0(\ступень_множителя_54_c_out_0 ),
    .C_out_1(\ступень_множителя_54_c_out_1 ));
  \ступень_множителя  \u_ступень_множителя_55  (
    .in__B(B_1[22]), .in_0__A(A_0), .in_1__A(A_1), .C_in_0(\ступень_множителя_54_c_out_0 ),
    .C_in_1(\ступень_множителя_54_c_out_1 ), .out(R_1[22]), .C_out_0(\ступень_множителя_55_c_out_0 ),
    .C_out_1(\ступень_множителя_55_c_out_1 ));
  \ступень_множителя  \u_ступень_множителя_56  (
    .in__B(B_1[23]), .in_0__A(A_0), .in_1__A(A_1), .C_in_0(\ступень_множителя_55_c_out_0 ),
    .C_in_1(\ступень_множителя_55_c_out_1 ), .out(R_1[23]), .C_out_0(\ступень_множителя_56_c_out_0 ),
    .C_out_1(\ступень_множителя_56_c_out_1 ));
  \ступень_множителя  \u_ступень_множителя_57  (
    .in__B(B_1[26]), .in_0__A(A_0), .in_1__A(A_1), .C_in_0(\ступень_множителя_59_c_out_0 ),
    .C_in_1(\ступень_множителя_59_c_out_1 ), .out(R_1[26]), .C_out_0(\ступень_множителя_57_c_out_0 ),
    .C_out_1(\ступень_множителя_57_c_out_1 ));
  \ступень_множителя  \u_ступень_множителя_58  (
    .in__B(B_1[24]), .in_0__A(A_0), .in_1__A(A_1), .C_in_0(\ступень_множителя_56_c_out_0 ),
    .C_in_1(\ступень_множителя_56_c_out_1 ), .out(R_1[24]), .C_out_0(\ступень_множителя_58_c_out_0 ),
    .C_out_1(\ступень_множителя_58_c_out_1 ));
  \ступень_множителя  \u_ступень_множителя_59  (
    .in__B(B_1[25]), .in_0__A(A_0), .in_1__A(A_1), .C_in_0(\ступень_множителя_58_c_out_0 ),
    .C_in_1(\ступень_множителя_58_c_out_1 ), .out(R_1[25]), .C_out_0(\ступень_множителя_59_c_out_0 ),
    .C_out_1(\ступень_множителя_59_c_out_1 ));
  \ступень_множителя  \u_ступень_множителя_60  (
    .in__B(B_1[28]), .in_0__A(A_0), .in_1__A(A_1), .C_in_0(\ступень_множителя_61_c_out_0 ),
    .C_in_1(\ступень_множителя_61_c_out_1 ), .out(R_1[28]), .C_out_0(\ступень_множителя_60_c_out_0 ),
    .C_out_1(\ступень_множителя_60_c_out_1 ));
  \ступень_множителя  \u_ступень_множителя_61  (
    .in__B(B_1[27]), .in_0__A(A_0), .in_1__A(A_1), .C_in_0(\ступень_множителя_57_c_out_0 ),
    .C_in_1(\ступень_множителя_57_c_out_1 ), .out(R_1[27]), .C_out_0(\ступень_множителя_61_c_out_0 ),
    .C_out_1(\ступень_множителя_61_c_out_1 ));
  \ступень_множителя  \u_ступень_множителя_62  (
    .in__B(B_1[30]), .in_0__A(A_0), .in_1__A(A_1), .C_in_0(\ступень_множителя_63_c_out_0 ),
    .C_in_1(\ступень_множителя_63_c_out_1 ), .out(R_1[30]), .C_out_0(\ступень_множителя_62_c_out_0 ),
    .C_out_1(\ступень_множителя_62_c_out_1 ));
  \ступень_множителя  \u_ступень_множителя_63  (
    .in__B(B_1[29]), .in_0__A(A_0), .in_1__A(A_1), .C_in_0(\ступень_множителя_60_c_out_0 ),
    .C_in_1(\ступень_множителя_60_c_out_1 ), .out(R_1[29]), .C_out_0(\ступень_множителя_63_c_out_0 ),
    .C_out_1(\ступень_множителя_63_c_out_1 ));
  \ступень_множителя  \u_ступень_множителя_64  (
    .in__B(B_1[31]), .in_0__A(A_0), .in_1__A(A_1), .C_in_0(\ступень_множителя_62_c_out_0 ),
    .C_in_1(\ступень_множителя_62_c_out_1 ), .out(R_1[31]), .C_out_0(C_out_0), .C_out_1(C_out_1));
endmodule

module \ступень_множителя  (
  input  in__B,
  input  [31:0] in_0__A,
  input  [31:0] in_1__A,
  input  [31:0] C_in_0,
  input  [31:0] C_in_1,
  output out,
  output [31:0] C_out_0,
  output [31:0] C_out_1
);

  wire adder_1_cout;
  wire [31:0] controlled_buffer_1_out, controlled_buffer_2_out;

  assign controlled_buffer_1_out = in__B ? in_0__A : 32'bz;  // Controlled_Buffer controlled_buffer_1
  Pull_Resistor pull_resistor_1 (.node(controlled_buffer_1_out));
  assign controlled_buffer_2_out = in__B ? in_1__A : 32'bz;  // Controlled_Buffer controlled_buffer_2
  Pull_Resistor pull_resistor_2 (.node(controlled_buffer_2_out));
  Adder #(.width(32)) adder_1 (
    .a(controlled_buffer_1_out), .b(C_in_0), .out({C_out_0[30:0], out}), .cin(1'b0), .cout(adder_1_cout));
  Adder #(.width(32)) adder_2 (
    .a(controlled_buffer_2_out), .b(C_in_1), .out({C_out_1[30:0], C_out_0[31]}), .cin(adder_1_cout),
    .cout(C_out_1[31]));
endmodule

module \компаратор_64х_беззнаковый  (
  input  [31:0] A0,
  input  [31:0] B0,
  input  [31:0] A1,
  input  [31:0] B1,
  output out_5,
  output out_6,
  output out_7
);

  wire and_2_out, and_3_out, comparator_1_eq, comparator_1_gt, comparator_1_lt, comparator_2_eq,
       comparator_2_gt, comparator_2_lt;

  Comparator #(.width(32)) comparator_1 (
    .a(A0), .b(B0), .gt(comparator_1_gt), .eq(comparator_1_eq), .lt(comparator_1_lt));
  Comparator #(.width(32)) comparator_2 (
    .a(A1), .b(B1), .gt(comparator_2_gt), .eq(comparator_2_eq), .lt(comparator_2_lt));
  and and_1 (out_5, comparator_1_eq, comparator_2_eq);
  and and_2 (and_2_out, comparator_1_gt, comparator_2_eq);
  and and_3 (and_3_out, comparator_2_eq, comparator_1_lt);
  or or_1 (out_6, and_2_out, comparator_2_gt);
  or or_2 (out_7, comparator_2_lt, and_3_out);
endmodule

module \ступень_сдвигателя_64х_левого_логического  (
  input  [31:0] \А0 ,
  input  [31:0] \А1 ,
  output [31:0] R0,
  output [31:0] R1
);


  assign R0 = {\А0 [30:0], 1'b0};
  assign R1 = {\А1 [30:0], \А0 [31]};
endmodule

module \ступень_сдвигателя_64х_левого_циклического  (
  input  [31:0] \А0 ,
  input  [31:0] \А1 ,
  output [31:0] R0,
  output [31:0] R1
);


  assign R0 = {\А0 [30:0], \А1 [31]};
  assign R1 = {\А1 [30:0], \А0 [31]};
endmodule

module \ступень_сдвигателя_64х_правого_логического  (
  input  [31:0] \А0 ,
  input  [31:0] \А1 ,
  output [31:0] R0,
  output [31:0] R1
);


  assign R0 = {\А1 [0], \А0 [31:1]};
  assign R1 = {1'b0, \А1 [31:1]};
endmodule

module \ступень_сдвигателя_64х_правого_циклического  (
  input  [31:0] \А0 ,
  input  [31:0] \А1 ,
  output [31:0] R0,
  output [31:0] R1
);


  assign R0 = {\А1 [0], \А0 [31:1]};
  assign R1 = {\А0 [0], \А1 [31:1]};
endmodule

module \сдвигатель_64х_левый_логический  (
  input  [31:0] A0,
  input  [31:0] A1,
  input  [5:0] in_3,
  output [31:0] R0,
  output [31:0] R1
);

  wire [31:0] multiplexer_3_out, multiplexer_4_out, multiplexer_5_out, multiplexer_6_out,
       \ступень_сдвигателя_64х_левого_логического_1_r0 , \ступень_сдвигателя_64х_левого_логического_1_r1 ,
       \ступень_сдвигателя_64х_левого_логического_2_r0 , \ступень_сдвигателя_64х_левого_логического_2_r1 ,
       \ступень_сдвигателя_64х_левого_логического_3_r0 , \ступень_сдвигателя_64х_левого_логического_3_r1 ,
       \ступень_сдвигателя_64х_левого_логического_4_r0 , \ступень_сдвигателя_64х_левого_логического_4_r1 ,
       \ступень_сдвигателя_64х_левого_логического_5_r0 , \ступень_сдвигателя_64х_левого_логического_5_r1 ,
       \ступень_сдвигателя_64х_левого_логического_6_r0 , \ступень_сдвигателя_64х_левого_логического_6_r1 ,
       \ступень_сдвигателя_64х_левого_логического_7_r0 , \ступень_сдвигателя_64х_левого_логического_7_r1 ,
       \ступень_сдвигателя_64х_левого_логического_8_r0 , \ступень_сдвигателя_64х_левого_логического_8_r1 ,
       \ступень_сдвигателя_64х_левого_логического_9_r0 , \ступень_сдвигателя_64х_левого_логического_9_r1 ,
       \ступень_сдвигателя_64х_левого_логического_10_r0 , \ступень_сдвигателя_64х_левого_логического_10_r1 ,
       \ступень_сдвигателя_64х_левого_логического_11_r0 , \ступень_сдвигателя_64х_левого_логического_11_r1 ,
       \ступень_сдвигателя_64х_левого_логического_12_r0 , \ступень_сдвигателя_64х_левого_логического_12_r1 ,
       \ступень_сдвигателя_64х_левого_логического_13_r0 , \ступень_сдвигателя_64х_левого_логического_13_r1 ,
       \ступень_сдвигателя_64х_левого_логического_14_r0 , \ступень_сдвигателя_64х_левого_логического_14_r1 ,
       \ступень_сдвигателя_64х_левого_логического_15_r0 , \ступень_сдвигателя_64х_левого_логического_15_r1 ,
       \ступень_сдвигателя_64х_левого_логического_16_r0 , \ступень_сдвигателя_64х_левого_логического_16_r1 ,
       \ступень_сдвигателя_64х_левого_логического_17_r0 , \ступень_сдвигателя_64х_левого_логического_17_r1 ,
       \ступень_сдвигателя_64х_левого_логического_18_r0 , \ступень_сдвигателя_64х_левого_логического_18_r1 ,
       \ступень_сдвигателя_64х_левого_логического_19_r0 , \ступень_сдвигателя_64х_левого_логического_19_r1 ,
       \ступень_сдвигателя_64х_левого_логического_20_r0 , \ступень_сдвигателя_64х_левого_логического_20_r1 ,
       \ступень_сдвигателя_64х_левого_логического_21_r0 , \ступень_сдвигателя_64х_левого_логического_21_r1 ,
       \ступень_сдвигателя_64х_левого_логического_22_r0 , \ступень_сдвигателя_64х_левого_логического_22_r1 ,
       \ступень_сдвигателя_64х_левого_логического_23_r0 , \ступень_сдвигателя_64х_левого_логического_23_r1 ,
       \ступень_сдвигателя_64х_левого_логического_24_r0 , \ступень_сдвигателя_64х_левого_логического_24_r1 ,
       \ступень_сдвигателя_64х_левого_логического_25_r0 , \ступень_сдвигателя_64х_левого_логического_25_r1 ,
       \ступень_сдвигателя_64х_левого_логического_26_r0 , \ступень_сдвигателя_64х_левого_логического_26_r1 ,
       \ступень_сдвигателя_64х_левого_логического_27_r0 , \ступень_сдвигателя_64х_левого_логического_27_r1 ,
       \ступень_сдвигателя_64х_левого_логического_28_r0 , \ступень_сдвигателя_64х_левого_логического_28_r1 ,
       \ступень_сдвигателя_64х_левого_логического_29_r0 , \ступень_сдвигателя_64х_левого_логического_29_r1 ,
       \ступень_сдвигателя_64х_левого_логического_30_r0 , \ступень_сдвигателя_64х_левого_логического_30_r1 ,
       \ступень_сдвигателя_64х_левого_логического_31_r0 , \ступень_сдвигателя_64х_левого_логического_31_r1 ,
       \ступень_сдвигателя_64х_левого_логического_32_r0 , \ступень_сдвигателя_64х_левого_логического_32_r1 ,
       \ступень_сдвигателя_64х_левого_логического_33_r0 , \ступень_сдвигателя_64х_левого_логического_33_r1 ,
       \ступень_сдвигателя_64х_левого_логического_34_r0 , \ступень_сдвигателя_64х_левого_логического_34_r1 ,
       \ступень_сдвигателя_64х_левого_логического_35_r0 , \ступень_сдвигателя_64х_левого_логического_35_r1 ,
       \ступень_сдвигателя_64х_левого_логического_36_r0 , \ступень_сдвигателя_64х_левого_логического_36_r1 ,
       \ступень_сдвигателя_64х_левого_логического_37_r0 , \ступень_сдвигателя_64х_левого_логического_37_r1 ,
       \ступень_сдвигателя_64х_левого_логического_38_r0 , \ступень_сдвигателя_64х_левого_логического_38_r1 ,
       \ступень_сдвигателя_64х_левого_логического_39_r0 , \ступень_сдвигателя_64х_левого_логического_39_r1 ,
       \ступень_сдвигателя_64х_левого_логического_40_r0 , \ступень_сдвигателя_64х_левого_логического_40_r1 ,
       \ступень_сдвигателя_64х_левого_логического_41_r0 , \ступень_сдвигателя_64х_левого_логического_41_r1 ,
       \ступень_сдвигателя_64х_левого_логического_42_r0 , \ступень_сдвигателя_64х_левого_логического_42_r1 ,
       \ступень_сдвигателя_64х_левого_логического_43_r0 , \ступень_сдвигателя_64х_левого_логического_43_r1 ,
       \ступень_сдвигателя_64х_левого_логического_44_r0 , \ступень_сдвигателя_64х_левого_логического_44_r1 ,
       \ступень_сдвигателя_64х_левого_логического_45_r0 , \ступень_сдвигателя_64х_левого_логического_45_r1 ,
       \ступень_сдвигателя_64х_левого_логического_46_r0 , \ступень_сдвигателя_64х_левого_логического_46_r1 ,
       \ступень_сдвигателя_64х_левого_логического_47_r0 , \ступень_сдвигателя_64х_левого_логического_47_r1 ,
       \ступень_сдвигателя_64х_левого_логического_48_r0 , \ступень_сдвигателя_64х_левого_логического_48_r1 ,
       \ступень_сдвигателя_64х_левого_логического_49_r0 , \ступень_сдвигателя_64х_левого_логического_49_r1 ,
       \ступень_сдвигателя_64х_левого_логического_50_r0 , \ступень_сдвигателя_64х_левого_логического_50_r1 ,
       \ступень_сдвигателя_64х_левого_логического_51_r0 , \ступень_сдвигателя_64х_левого_логического_51_r1 ,
       \ступень_сдвигателя_64х_левого_логического_52_r0 , \ступень_сдвигателя_64х_левого_логического_52_r1 ,
       \ступень_сдвигателя_64х_левого_логического_53_r0 , \ступень_сдвигателя_64х_левого_логического_53_r1 ,
       \ступень_сдвигателя_64х_левого_логического_54_r0 , \ступень_сдвигателя_64х_левого_логического_54_r1 ,
       \ступень_сдвигателя_64х_левого_логического_55_r0 , \ступень_сдвигателя_64х_левого_логического_55_r1 ,
       \ступень_сдвигателя_64х_левого_логического_56_r0 , \ступень_сдвигателя_64х_левого_логического_56_r1 ,
       \ступень_сдвигателя_64х_левого_логического_57_r0 , \ступень_сдвигателя_64х_левого_логического_57_r1 ,
       \ступень_сдвигателя_64х_левого_логического_58_r0 , \ступень_сдвигателя_64х_левого_логического_58_r1 ,
       \ступень_сдвигателя_64х_левого_логического_59_r0 , \ступень_сдвигателя_64х_левого_логического_59_r1 ,
       \ступень_сдвигателя_64х_левого_логического_60_r0 , \ступень_сдвигателя_64х_левого_логического_60_r1 ,
       \ступень_сдвигателя_64х_левого_логического_61_r0 , \ступень_сдвигателя_64х_левого_логического_61_r1 ,
       \ступень_сдвигателя_64х_левого_логического_62_r0 , \ступень_сдвигателя_64х_левого_логического_62_r1 ,
       \ступень_сдвигателя_64х_левого_логического_63_r0 , \ступень_сдвигателя_64х_левого_логического_63_r1 ;

  Multiplexer #(.width(32), .disabled(0), .enable("false")) multiplexer_1 (
    .in0(multiplexer_3_out), .in1(multiplexer_5_out), .out(R0), .sel(in_3[5]));
  Multiplexer #(.width(32), .disabled(0), .enable("false")) multiplexer_2 (
    .in0(multiplexer_4_out), .in1(multiplexer_6_out), .out(R1), .sel(in_3[5]));
  \ступень_сдвигателя_64х_левого_логического  \u_ступень_сдвигателя_64х_левого_логического_1  (
    .\А0 (A0), .\А1 (A1), .R0(\ступень_сдвигателя_64х_левого_логического_1_r0 ),
    .R1(\ступень_сдвигателя_64х_левого_логического_1_r1 ));
  \ступень_сдвигателя_64х_левого_логического  \u_ступень_сдвигателя_64х_левого_логического_2  (
    .\А0 (\ступень_сдвигателя_64х_левого_логического_1_r0 ),
    .\А1 (\ступень_сдвигателя_64х_левого_логического_1_r1 ),
    .R0(\ступень_сдвигателя_64х_левого_логического_2_r0 ),
    .R1(\ступень_сдвигателя_64х_левого_логического_2_r1 ));
  \ступень_сдвигателя_64х_левого_логического  \u_ступень_сдвигателя_64х_левого_логического_3  (
    .\А0 (\ступень_сдвигателя_64х_левого_логического_2_r0 ),
    .\А1 (\ступень_сдвигателя_64х_левого_логического_2_r1 ),
    .R0(\ступень_сдвигателя_64х_левого_логического_3_r0 ),
    .R1(\ступень_сдвигателя_64х_левого_логического_3_r1 ));
  Multiplexer #(.select(5), .width(32), .disabled(0), .enable("false")) multiplexer_3 (
    .in0(A0), .in1(\ступень_сдвигателя_64х_левого_логического_1_r0 ),
    .in2(\ступень_сдвигателя_64х_левого_логического_2_r0 ),
    .in3(\ступень_сдвигателя_64х_левого_логического_3_r0 ),
    .in4(\ступень_сдвигателя_64х_левого_логического_4_r0 ),
    .in5(\ступень_сдвигателя_64х_левого_логического_5_r0 ),
    .in6(\ступень_сдвигателя_64х_левого_логического_6_r0 ),
    .in7(\ступень_сдвигателя_64х_левого_логического_8_r0 ),
    .in8(\ступень_сдвигателя_64х_левого_логического_7_r0 ),
    .in9(\ступень_сдвигателя_64х_левого_логического_9_r0 ),
    .in10(\ступень_сдвигателя_64х_левого_логического_11_r0 ),
    .in11(\ступень_сдвигателя_64х_левого_логического_10_r0 ),
    .in12(\ступень_сдвигателя_64х_левого_логического_12_r0 ),
    .in13(\ступень_сдвигателя_64х_левого_логического_14_r0 ),
    .in14(\ступень_сдвигателя_64х_левого_логического_13_r0 ),
    .in15(\ступень_сдвигателя_64х_левого_логического_15_r0 ),
    .in16(\ступень_сдвигателя_64х_левого_логического_16_r0 ),
    .in17(\ступень_сдвигателя_64х_левого_логического_17_r0 ),
    .in18(\ступень_сдвигателя_64х_левого_логического_18_r0 ),
    .in19(\ступень_сдвигателя_64х_левого_логического_19_r0 ),
    .in20(\ступень_сдвигателя_64х_левого_логического_20_r0 ),
    .in21(\ступень_сдвигателя_64х_левого_логического_22_r0 ),
    .in22(\ступень_сдвигателя_64х_левого_логического_21_r0 ),
    .in23(\ступень_сдвигателя_64х_левого_логического_23_r0 ),
    .in24(\ступень_сдвигателя_64х_левого_логического_24_r0 ),
    .in25(\ступень_сдвигателя_64х_левого_логического_25_r0 ),
    .in26(\ступень_сдвигателя_64х_левого_логического_26_r0 ),
    .in27(\ступень_сдвигателя_64х_левого_логического_27_r0 ),
    .in28(\ступень_сдвигателя_64х_левого_логического_28_r0 ),
    .in29(\ступень_сдвигателя_64х_левого_логического_30_r0 ),
    .in30(\ступень_сдвигателя_64х_левого_логического_29_r0 ),
    .in31(\ступень_сдвигателя_64х_левого_логического_31_r0 ), .out(multiplexer_3_out), .sel(in_3[4:0]));
  \ступень_сдвигателя_64х_левого_логического  \u_ступень_сдвигателя_64х_левого_логического_4  (
    .\А0 (\ступень_сдвигателя_64х_левого_логического_3_r0 ),
    .\А1 (\ступень_сдвигателя_64х_левого_логического_3_r1 ),
    .R0(\ступень_сдвигателя_64х_левого_логического_4_r0 ),
    .R1(\ступень_сдвигателя_64х_левого_логического_4_r1 ));
  Multiplexer #(.select(5), .width(32), .disabled(0), .enable("false")) multiplexer_4 (
    .in0(A1), .in1(\ступень_сдвигателя_64х_левого_логического_1_r1 ),
    .in2(\ступень_сдвигателя_64х_левого_логического_2_r1 ),
    .in3(\ступень_сдвигателя_64х_левого_логического_3_r1 ),
    .in4(\ступень_сдвигателя_64х_левого_логического_4_r1 ),
    .in5(\ступень_сдвигателя_64х_левого_логического_5_r1 ),
    .in6(\ступень_сдвигателя_64х_левого_логического_6_r1 ),
    .in7(\ступень_сдвигателя_64х_левого_логического_8_r1 ),
    .in8(\ступень_сдвигателя_64х_левого_логического_7_r1 ),
    .in9(\ступень_сдвигателя_64х_левого_логического_9_r1 ),
    .in10(\ступень_сдвигателя_64х_левого_логического_11_r1 ),
    .in11(\ступень_сдвигателя_64х_левого_логического_10_r1 ),
    .in12(\ступень_сдвигателя_64х_левого_логического_12_r1 ),
    .in13(\ступень_сдвигателя_64х_левого_логического_14_r1 ),
    .in14(\ступень_сдвигателя_64х_левого_логического_13_r1 ),
    .in15(\ступень_сдвигателя_64х_левого_логического_15_r1 ),
    .in16(\ступень_сдвигателя_64х_левого_логического_16_r1 ),
    .in17(\ступень_сдвигателя_64х_левого_логического_17_r1 ),
    .in18(\ступень_сдвигателя_64х_левого_логического_18_r1 ),
    .in19(\ступень_сдвигателя_64х_левого_логического_19_r1 ),
    .in20(\ступень_сдвигателя_64х_левого_логического_20_r1 ),
    .in21(\ступень_сдвигателя_64х_левого_логического_22_r1 ),
    .in22(\ступень_сдвигателя_64х_левого_логического_21_r1 ),
    .in23(\ступень_сдвигателя_64х_левого_логического_23_r1 ),
    .in24(\ступень_сдвигателя_64х_левого_логического_24_r1 ),
    .in25(\ступень_сдвигателя_64х_левого_логического_25_r1 ),
    .in26(\ступень_сдвигателя_64х_левого_логического_26_r1 ),
    .in27(\ступень_сдвигателя_64х_левого_логического_27_r1 ),
    .in28(\ступень_сдвигателя_64х_левого_логического_28_r1 ),
    .in29(\ступень_сдвигателя_64х_левого_логического_30_r1 ),
    .in30(\ступень_сдвигателя_64х_левого_логического_29_r1 ),
    .in31(\ступень_сдвигателя_64х_левого_логического_31_r1 ), .out(multiplexer_4_out), .sel(in_3[4:0]));
  \ступень_сдвигателя_64х_левого_логического  \u_ступень_сдвигателя_64х_левого_логического_5  (
    .\А0 (\ступень_сдвигателя_64х_левого_логического_4_r0 ),
    .\А1 (\ступень_сдвигателя_64х_левого_логического_4_r1 ),
    .R0(\ступень_сдвигателя_64х_левого_логического_5_r0 ),
    .R1(\ступень_сдвигателя_64х_левого_логического_5_r1 ));
  \ступень_сдвигателя_64х_левого_логического  \u_ступень_сдвигателя_64х_левого_логического_6  (
    .\А0 (\ступень_сдвигателя_64х_левого_логического_5_r0 ),
    .\А1 (\ступень_сдвигателя_64х_левого_логического_5_r1 ),
    .R0(\ступень_сдвигателя_64х_левого_логического_6_r0 ),
    .R1(\ступень_сдвигателя_64х_левого_логического_6_r1 ));
  \ступень_сдвигателя_64х_левого_логического  \u_ступень_сдвигателя_64х_левого_логического_7  (
    .\А0 (\ступень_сдвигателя_64х_левого_логического_8_r0 ),
    .\А1 (\ступень_сдвигателя_64х_левого_логического_8_r1 ),
    .R0(\ступень_сдвигателя_64х_левого_логического_7_r0 ),
    .R1(\ступень_сдвигателя_64х_левого_логического_7_r1 ));
  \ступень_сдвигателя_64х_левого_логического  \u_ступень_сдвигателя_64х_левого_логического_8  (
    .\А0 (\ступень_сдвигателя_64х_левого_логического_6_r0 ),
    .\А1 (\ступень_сдвигателя_64х_левого_логического_6_r1 ),
    .R0(\ступень_сдвигателя_64х_левого_логического_8_r0 ),
    .R1(\ступень_сдвигателя_64х_левого_логического_8_r1 ));
  \ступень_сдвигателя_64х_левого_логического  \u_ступень_сдвигателя_64х_левого_логического_9  (
    .\А0 (\ступень_сдвигателя_64х_левого_логического_7_r0 ),
    .\А1 (\ступень_сдвигателя_64х_левого_логического_7_r1 ),
    .R0(\ступень_сдвигателя_64х_левого_логического_9_r0 ),
    .R1(\ступень_сдвигателя_64х_левого_логического_9_r1 ));
  \ступень_сдвигателя_64х_левого_логического  \u_ступень_сдвигателя_64х_левого_логического_10  (
    .\А0 (\ступень_сдвигателя_64х_левого_логического_11_r0 ),
    .\А1 (\ступень_сдвигателя_64х_левого_логического_11_r1 ),
    .R0(\ступень_сдвигателя_64х_левого_логического_10_r0 ),
    .R1(\ступень_сдвигателя_64х_левого_логического_10_r1 ));
  \ступень_сдвигателя_64х_левого_логического  \u_ступень_сдвигателя_64х_левого_логического_11  (
    .\А0 (\ступень_сдвигателя_64х_левого_логического_9_r0 ),
    .\А1 (\ступень_сдвигателя_64х_левого_логического_9_r1 ),
    .R0(\ступень_сдвигателя_64х_левого_логического_11_r0 ),
    .R1(\ступень_сдвигателя_64х_левого_логического_11_r1 ));
  \ступень_сдвигателя_64х_левого_логического  \u_ступень_сдвигателя_64х_левого_логического_12  (
    .\А0 (\ступень_сдвигателя_64х_левого_логического_10_r0 ),
    .\А1 (\ступень_сдвигателя_64х_левого_логического_10_r1 ),
    .R0(\ступень_сдвигателя_64х_левого_логического_12_r0 ),
    .R1(\ступень_сдвигателя_64х_левого_логического_12_r1 ));
  \ступень_сдвигателя_64х_левого_логического  \u_ступень_сдвигателя_64х_левого_логического_13  (
    .\А0 (\ступень_сдвигателя_64х_левого_логического_14_r0 ),
    .\А1 (\ступень_сдвигателя_64х_левого_логического_14_r1 ),
    .R0(\ступень_сдвигателя_64х_левого_логического_13_r0 ),
    .R1(\ступень_сдвигателя_64х_левого_логического_13_r1 ));
  \ступень_сдвигателя_64х_левого_логического  \u_ступень_сдвигателя_64х_левого_логического_14  (
    .\А0 (\ступень_сдвигателя_64х_левого_логического_12_r0 ),
    .\А1 (\ступень_сдвигателя_64х_левого_логического_12_r1 ),
    .R0(\ступень_сдвигателя_64х_левого_логического_14_r0 ),
    .R1(\ступень_сдвигателя_64х_левого_логического_14_r1 ));
  \ступень_сдвигателя_64х_левого_логического  \u_ступень_сдвигателя_64х_левого_логического_15  (
    .\А0 (\ступень_сдвигателя_64х_левого_логического_13_r0 ),
    .\А1 (\ступень_сдвигателя_64х_левого_логического_13_r1 ),
    .R0(\ступень_сдвигателя_64х_левого_логического_15_r0 ),
    .R1(\ступень_сдвигателя_64х_левого_логического_15_r1 ));
  \ступень_сдвигателя_64х_левого_логического  \u_ступень_сдвигателя_64х_левого_логического_16  (
    .\А0 (\ступень_сдвигателя_64х_левого_логического_15_r0 ),
    .\А1 (\ступень_сдвигателя_64х_левого_логического_15_r1 ),
    .R0(\ступень_сдвигателя_64х_левого_логического_16_r0 ),
    .R1(\ступень_сдвигателя_64х_левого_логического_16_r1 ));
  \ступень_сдвигателя_64х_левого_логического  \u_ступень_сдвигателя_64х_левого_логического_17  (
    .\А0 (\ступень_сдвигателя_64х_левого_логического_16_r0 ),
    .\А1 (\ступень_сдвигателя_64х_левого_логического_16_r1 ),
    .R0(\ступень_сдвигателя_64х_левого_логического_17_r0 ),
    .R1(\ступень_сдвигателя_64х_левого_логического_17_r1 ));
  \ступень_сдвигателя_64х_левого_логического  \u_ступень_сдвигателя_64х_левого_логического_18  (
    .\А0 (\ступень_сдвигателя_64х_левого_логического_17_r0 ),
    .\А1 (\ступень_сдвигателя_64х_левого_логического_17_r1 ),
    .R0(\ступень_сдвигателя_64х_левого_логического_18_r0 ),
    .R1(\ступень_сдвигателя_64х_левого_логического_18_r1 ));
  \ступень_сдвигателя_64х_левого_логического  \u_ступень_сдвигателя_64х_левого_логического_19  (
    .\А0 (\ступень_сдвигателя_64х_левого_логического_18_r0 ),
    .\А1 (\ступень_сдвигателя_64х_левого_логического_18_r1 ),
    .R0(\ступень_сдвигателя_64х_левого_логического_19_r0 ),
    .R1(\ступень_сдвигателя_64х_левого_логического_19_r1 ));
  \ступень_сдвигателя_64х_левого_логического  \u_ступень_сдвигателя_64х_левого_логического_20  (
    .\А0 (\ступень_сдвигателя_64х_левого_логического_19_r0 ),
    .\А1 (\ступень_сдвигателя_64х_левого_логического_19_r1 ),
    .R0(\ступень_сдвигателя_64х_левого_логического_20_r0 ),
    .R1(\ступень_сдвигателя_64х_левого_логического_20_r1 ));
  \ступень_сдвигателя_64х_левого_логического  \u_ступень_сдвигателя_64х_левого_логического_21  (
    .\А0 (\ступень_сдвигателя_64х_левого_логического_22_r0 ),
    .\А1 (\ступень_сдвигателя_64х_левого_логического_22_r1 ),
    .R0(\ступень_сдвигателя_64х_левого_логического_21_r0 ),
    .R1(\ступень_сдвигателя_64х_левого_логического_21_r1 ));
  \ступень_сдвигателя_64х_левого_логического  \u_ступень_сдвигателя_64х_левого_логического_22  (
    .\А0 (\ступень_сдвигателя_64х_левого_логического_20_r0 ),
    .\А1 (\ступень_сдвигателя_64х_левого_логического_20_r1 ),
    .R0(\ступень_сдвигателя_64х_левого_логического_22_r0 ),
    .R1(\ступень_сдвигателя_64х_левого_логического_22_r1 ));
  \ступень_сдвигателя_64х_левого_логического  \u_ступень_сдвигателя_64х_левого_логического_23  (
    .\А0 (\ступень_сдвигателя_64х_левого_логического_21_r0 ),
    .\А1 (\ступень_сдвигателя_64х_левого_логического_21_r1 ),
    .R0(\ступень_сдвигателя_64х_левого_логического_23_r0 ),
    .R1(\ступень_сдвигателя_64х_левого_логического_23_r1 ));
  \ступень_сдвигателя_64х_левого_логического  \u_ступень_сдвигателя_64х_левого_логического_24  (
    .\А0 (\ступень_сдвигателя_64х_левого_логического_23_r0 ),
    .\А1 (\ступень_сдвигателя_64х_левого_логического_23_r1 ),
    .R0(\ступень_сдвигателя_64х_левого_логического_24_r0 ),
    .R1(\ступень_сдвигателя_64х_левого_логического_24_r1 ));
  \ступень_сдвигателя_64х_левого_логического  \u_ступень_сдвигателя_64х_левого_логического_25  (
    .\А0 (\ступень_сдвигателя_64х_левого_логического_24_r0 ),
    .\А1 (\ступень_сдвигателя_64х_левого_логического_24_r1 ),
    .R0(\ступень_сдвигателя_64х_левого_логического_25_r0 ),
    .R1(\ступень_сдвигателя_64х_левого_логического_25_r1 ));
  \ступень_сдвигателя_64х_левого_логического  \u_ступень_сдвигателя_64х_левого_логического_26  (
    .\А0 (\ступень_сдвигателя_64х_левого_логического_25_r0 ),
    .\А1 (\ступень_сдвигателя_64х_левого_логического_25_r1 ),
    .R0(\ступень_сдвигателя_64х_левого_логического_26_r0 ),
    .R1(\ступень_сдвигателя_64х_левого_логического_26_r1 ));
  \ступень_сдвигателя_64х_левого_логического  \u_ступень_сдвигателя_64х_левого_логического_27  (
    .\А0 (\ступень_сдвигателя_64х_левого_логического_26_r0 ),
    .\А1 (\ступень_сдвигателя_64х_левого_логического_26_r1 ),
    .R0(\ступень_сдвигателя_64х_левого_логического_27_r0 ),
    .R1(\ступень_сдвигателя_64х_левого_логического_27_r1 ));
  \ступень_сдвигателя_64х_левого_логического  \u_ступень_сдвигателя_64х_левого_логического_28  (
    .\А0 (\ступень_сдвигателя_64х_левого_логического_27_r0 ),
    .\А1 (\ступень_сдвигателя_64х_левого_логического_27_r1 ),
    .R0(\ступень_сдвигателя_64х_левого_логического_28_r0 ),
    .R1(\ступень_сдвигателя_64х_левого_логического_28_r1 ));
  \ступень_сдвигателя_64х_левого_логического  \u_ступень_сдвигателя_64х_левого_логического_29  (
    .\А0 (\ступень_сдвигателя_64х_левого_логического_30_r0 ),
    .\А1 (\ступень_сдвигателя_64х_левого_логического_30_r1 ),
    .R0(\ступень_сдвигателя_64х_левого_логического_29_r0 ),
    .R1(\ступень_сдвигателя_64х_левого_логического_29_r1 ));
  \ступень_сдвигателя_64х_левого_логического  \u_ступень_сдвигателя_64х_левого_логического_30  (
    .\А0 (\ступень_сдвигателя_64х_левого_логического_28_r0 ),
    .\А1 (\ступень_сдвигателя_64х_левого_логического_28_r1 ),
    .R0(\ступень_сдвигателя_64х_левого_логического_30_r0 ),
    .R1(\ступень_сдвигателя_64х_левого_логического_30_r1 ));
  \ступень_сдвигателя_64х_левого_логического  \u_ступень_сдвигателя_64х_левого_логического_31  (
    .\А0 (\ступень_сдвигателя_64х_левого_логического_29_r0 ),
    .\А1 (\ступень_сдвигателя_64х_левого_логического_29_r1 ),
    .R0(\ступень_сдвигателя_64х_левого_логического_31_r0 ),
    .R1(\ступень_сдвигателя_64х_левого_логического_31_r1 ));
  \ступень_сдвигателя_64х_левого_логического  \u_ступень_сдвигателя_64х_левого_логического_32  (
    .\А0 (\ступень_сдвигателя_64х_левого_логического_31_r0 ),
    .\А1 (\ступень_сдвигателя_64х_левого_логического_31_r1 ),
    .R0(\ступень_сдвигателя_64х_левого_логического_32_r0 ),
    .R1(\ступень_сдвигателя_64х_левого_логического_32_r1 ));
  \ступень_сдвигателя_64х_левого_логического  \u_ступень_сдвигателя_64х_левого_логического_33  (
    .\А0 (\ступень_сдвигателя_64х_левого_логического_32_r0 ),
    .\А1 (\ступень_сдвигателя_64х_левого_логического_32_r1 ),
    .R0(\ступень_сдвигателя_64х_левого_логического_33_r0 ),
    .R1(\ступень_сдвигателя_64х_левого_логического_33_r1 ));
  \ступень_сдвигателя_64х_левого_логического  \u_ступень_сдвигателя_64х_левого_логического_34  (
    .\А0 (\ступень_сдвигателя_64х_левого_логического_35_r0 ),
    .\А1 (\ступень_сдвигателя_64х_левого_логического_35_r1 ),
    .R0(\ступень_сдвигателя_64х_левого_логического_34_r0 ),
    .R1(\ступень_сдвигателя_64х_левого_логического_34_r1 ));
  \ступень_сдвигателя_64х_левого_логического  \u_ступень_сдвигателя_64х_левого_логического_35  (
    .\А0 (\ступень_сдвигателя_64х_левого_логического_33_r0 ),
    .\А1 (\ступень_сдвигателя_64х_левого_логического_33_r1 ),
    .R0(\ступень_сдвигателя_64х_левого_логического_35_r0 ),
    .R1(\ступень_сдвигателя_64х_левого_логического_35_r1 ));
  Multiplexer #(.select(5), .width(32), .disabled(0), .enable("false")) multiplexer_5 (
    .in0(\ступень_сдвигателя_64х_левого_логического_32_r0 ),
    .in1(\ступень_сдвигателя_64х_левого_логического_33_r0 ),
    .in2(\ступень_сдвигателя_64х_левого_логического_35_r0 ),
    .in3(\ступень_сдвигателя_64х_левого_логического_34_r0 ),
    .in4(\ступень_сдвигателя_64х_левого_логического_36_r0 ),
    .in5(\ступень_сдвигателя_64х_левого_логического_38_r0 ),
    .in6(\ступень_сдвигателя_64х_левого_логического_37_r0 ),
    .in7(\ступень_сдвигателя_64х_левого_логического_40_r0 ),
    .in8(\ступень_сдвигателя_64х_левого_логического_39_r0 ),
    .in9(\ступень_сдвигателя_64х_левого_логического_41_r0 ),
    .in10(\ступень_сдвигателя_64х_левого_логического_42_r0 ),
    .in11(\ступень_сдвигателя_64х_левого_логического_43_r0 ),
    .in12(\ступень_сдвигателя_64х_левого_логического_44_r0 ),
    .in13(\ступень_сдвигателя_64х_левого_логического_45_r0 ),
    .in14(\ступень_сдвигателя_64х_левого_логического_46_r0 ),
    .in15(\ступень_сдвигателя_64х_левого_логического_47_r0 ),
    .in16(\ступень_сдвигателя_64х_левого_логического_48_r0 ),
    .in17(\ступень_сдвигателя_64х_левого_логического_49_r0 ),
    .in18(\ступень_сдвигателя_64х_левого_логического_50_r0 ),
    .in19(\ступень_сдвигателя_64х_левого_логического_51_r0 ),
    .in20(\ступень_сдвигателя_64х_левого_логического_52_r0 ),
    .in21(\ступень_сдвигателя_64х_левого_логического_54_r0 ),
    .in22(\ступень_сдвигателя_64х_левого_логического_53_r0 ),
    .in23(\ступень_сдвигателя_64х_левого_логического_55_r0 ),
    .in24(\ступень_сдвигателя_64х_левого_логического_56_r0 ),
    .in25(\ступень_сдвигателя_64х_левого_логического_57_r0 ),
    .in26(\ступень_сдвигателя_64х_левого_логического_58_r0 ),
    .in27(\ступень_сдвигателя_64х_левого_логического_59_r0 ),
    .in28(\ступень_сдвигателя_64х_левого_логического_60_r0 ),
    .in29(\ступень_сдвигателя_64х_левого_логического_62_r0 ),
    .in30(\ступень_сдвигателя_64х_левого_логического_61_r0 ),
    .in31(\ступень_сдвигателя_64х_левого_логического_63_r0 ), .out(multiplexer_5_out), .sel(in_3[4:0]));
  \ступень_сдвигателя_64х_левого_логического  \u_ступень_сдвигателя_64х_левого_логического_36  (
    .\А0 (\ступень_сдвигателя_64х_левого_логического_34_r0 ),
    .\А1 (\ступень_сдвигателя_64х_левого_логического_34_r1 ),
    .R0(\ступень_сдвигателя_64х_левого_логического_36_r0 ),
    .R1(\ступень_сдвигателя_64х_левого_логического_36_r1 ));
  Multiplexer #(.select(5), .width(32), .disabled(0), .enable("false")) multiplexer_6 (
    .in0(\ступень_сдвигателя_64х_левого_логического_32_r1 ),
    .in1(\ступень_сдвигателя_64х_левого_логического_33_r1 ),
    .in2(\ступень_сдвигателя_64х_левого_логического_35_r1 ),
    .in3(\ступень_сдвигателя_64х_левого_логического_34_r1 ),
    .in4(\ступень_сдвигателя_64х_левого_логического_36_r1 ),
    .in5(\ступень_сдвигателя_64х_левого_логического_38_r1 ),
    .in6(\ступень_сдвигателя_64х_левого_логического_37_r1 ),
    .in7(\ступень_сдвигателя_64х_левого_логического_40_r1 ),
    .in8(\ступень_сдвигателя_64х_левого_логического_39_r1 ),
    .in9(\ступень_сдвигателя_64х_левого_логического_41_r1 ),
    .in10(\ступень_сдвигателя_64х_левого_логического_42_r1 ),
    .in11(\ступень_сдвигателя_64х_левого_логического_43_r1 ),
    .in12(\ступень_сдвигателя_64х_левого_логического_44_r1 ),
    .in13(\ступень_сдвигателя_64х_левого_логического_45_r1 ),
    .in14(\ступень_сдвигателя_64х_левого_логического_46_r1 ),
    .in15(\ступень_сдвигателя_64х_левого_логического_47_r1 ),
    .in16(\ступень_сдвигателя_64х_левого_логического_48_r1 ),
    .in17(\ступень_сдвигателя_64х_левого_логического_49_r1 ),
    .in18(\ступень_сдвигателя_64х_левого_логического_50_r1 ),
    .in19(\ступень_сдвигателя_64х_левого_логического_51_r1 ),
    .in20(\ступень_сдвигателя_64х_левого_логического_52_r1 ),
    .in21(\ступень_сдвигателя_64х_левого_логического_54_r1 ),
    .in22(\ступень_сдвигателя_64х_левого_логического_53_r1 ),
    .in23(\ступень_сдвигателя_64х_левого_логического_55_r1 ),
    .in24(\ступень_сдвигателя_64х_левого_логического_56_r1 ),
    .in25(\ступень_сдвигателя_64х_левого_логического_57_r1 ),
    .in26(\ступень_сдвигателя_64х_левого_логического_58_r1 ),
    .in27(\ступень_сдвигателя_64х_левого_логического_59_r1 ),
    .in28(\ступень_сдвигателя_64х_левого_логического_60_r1 ),
    .in29(\ступень_сдвигателя_64х_левого_логического_62_r1 ),
    .in30(\ступень_сдвигателя_64х_левого_логического_61_r1 ),
    .in31(\ступень_сдвигателя_64х_левого_логического_63_r1 ), .out(multiplexer_6_out), .sel(in_3[4:0]));
  \ступень_сдвигателя_64х_левого_логического  \u_ступень_сдвигателя_64х_левого_логического_37  (
    .\А0 (\ступень_сдвигателя_64х_левого_логического_38_r0 ),
    .\А1 (\ступень_сдвигателя_64х_левого_логического_38_r1 ),
    .R0(\ступень_сдвигателя_64х_левого_логического_37_r0 ),
    .R1(\ступень_сдвигателя_64х_левого_логического_37_r1 ));
  \ступень_сдвигателя_64х_левого_логического  \u_ступень_сдвигателя_64х_левого_логического_38  (
    .\А0 (\ступень_сдвигателя_64х_левого_логического_36_r0 ),
    .\А1 (\ступень_сдвигателя_64х_левого_логического_36_r1 ),
    .R0(\ступень_сдвигателя_64х_левого_логического_38_r0 ),
    .R1(\ступень_сдвигателя_64х_левого_логического_38_r1 ));
  \ступень_сдвигателя_64х_левого_логического  \u_ступень_сдвигателя_64х_левого_логического_39  (
    .\А0 (\ступень_сдвигателя_64х_левого_логического_40_r0 ),
    .\А1 (\ступень_сдвигателя_64х_левого_логического_40_r1 ),
    .R0(\ступень_сдвигателя_64х_левого_логического_39_r0 ),
    .R1(\ступень_сдвигателя_64х_левого_логического_39_r1 ));
  \ступень_сдвигателя_64х_левого_логического  \u_ступень_сдвигателя_64х_левого_логического_40  (
    .\А0 (\ступень_сдвигателя_64х_левого_логического_37_r0 ),
    .\А1 (\ступень_сдвигателя_64х_левого_логического_37_r1 ),
    .R0(\ступень_сдвигателя_64х_левого_логического_40_r0 ),
    .R1(\ступень_сдвигателя_64х_левого_логического_40_r1 ));
  \ступень_сдвигателя_64х_левого_логического  \u_ступень_сдвигателя_64х_левого_логического_41  (
    .\А0 (\ступень_сдвигателя_64х_левого_логического_39_r0 ),
    .\А1 (\ступень_сдвигателя_64х_левого_логического_39_r1 ),
    .R0(\ступень_сдвигателя_64х_левого_логического_41_r0 ),
    .R1(\ступень_сдвигателя_64х_левого_логического_41_r1 ));
  \ступень_сдвигателя_64х_левого_логического  \u_ступень_сдвигателя_64х_левого_логического_42  (
    .\А0 (\ступень_сдвигателя_64х_левого_логического_41_r0 ),
    .\А1 (\ступень_сдвигателя_64х_левого_логического_41_r1 ),
    .R0(\ступень_сдвигателя_64х_левого_логического_42_r0 ),
    .R1(\ступень_сдвигателя_64х_левого_логического_42_r1 ));
  \ступень_сдвигателя_64х_левого_логического  \u_ступень_сдвигателя_64х_левого_логического_43  (
    .\А0 (\ступень_сдвигателя_64х_левого_логического_42_r0 ),
    .\А1 (\ступень_сдвигателя_64х_левого_логического_42_r1 ),
    .R0(\ступень_сдвигателя_64х_левого_логического_43_r0 ),
    .R1(\ступень_сдвигателя_64х_левого_логического_43_r1 ));
  \ступень_сдвигателя_64х_левого_логического  \u_ступень_сдвигателя_64х_левого_логического_44  (
    .\А0 (\ступень_сдвигателя_64х_левого_логического_43_r0 ),
    .\А1 (\ступень_сдвигателя_64х_левого_логического_43_r1 ),
    .R0(\ступень_сдвигателя_64х_левого_логического_44_r0 ),
    .R1(\ступень_сдвигателя_64х_левого_логического_44_r1 ));
  \ступень_сдвигателя_64х_левого_логического  \u_ступень_сдвигателя_64х_левого_логического_45  (
    .\А0 (\ступень_сдвигателя_64х_левого_логического_44_r0 ),
    .\А1 (\ступень_сдвигателя_64х_левого_логического_44_r1 ),
    .R0(\ступень_сдвигателя_64х_левого_логического_45_r0 ),
    .R1(\ступень_сдвигателя_64х_левого_логического_45_r1 ));
  \ступень_сдвигателя_64х_левого_логического  \u_ступень_сдвигателя_64х_левого_логического_46  (
    .\А0 (\ступень_сдвигателя_64х_левого_логического_45_r0 ),
    .\А1 (\ступень_сдвигателя_64х_левого_логического_45_r1 ),
    .R0(\ступень_сдвигателя_64х_левого_логического_46_r0 ),
    .R1(\ступень_сдвигателя_64х_левого_логического_46_r1 ));
  \ступень_сдвигателя_64х_левого_логического  \u_ступень_сдвигателя_64х_левого_логического_47  (
    .\А0 (\ступень_сдвигателя_64х_левого_логического_46_r0 ),
    .\А1 (\ступень_сдвигателя_64х_левого_логического_46_r1 ),
    .R0(\ступень_сдвигателя_64х_левого_логического_47_r0 ),
    .R1(\ступень_сдвигателя_64х_левого_логического_47_r1 ));
  \ступень_сдвигателя_64х_левого_логического  \u_ступень_сдвигателя_64х_левого_логического_48  (
    .\А0 (\ступень_сдвигателя_64х_левого_логического_47_r0 ),
    .\А1 (\ступень_сдвигателя_64х_левого_логического_47_r1 ),
    .R0(\ступень_сдвигателя_64х_левого_логического_48_r0 ),
    .R1(\ступень_сдвигателя_64х_левого_логического_48_r1 ));
  \ступень_сдвигателя_64х_левого_логического  \u_ступень_сдвигателя_64х_левого_логического_49  (
    .\А0 (\ступень_сдвигателя_64х_левого_логического_48_r0 ),
    .\А1 (\ступень_сдвигателя_64х_левого_логического_48_r1 ),
    .R0(\ступень_сдвигателя_64х_левого_логического_49_r0 ),
    .R1(\ступень_сдвигателя_64х_левого_логического_49_r1 ));
  \ступень_сдвигателя_64х_левого_логического  \u_ступень_сдвигателя_64х_левого_логического_50  (
    .\А0 (\ступень_сдвигателя_64х_левого_логического_49_r0 ),
    .\А1 (\ступень_сдвигателя_64х_левого_логического_49_r1 ),
    .R0(\ступень_сдвигателя_64х_левого_логического_50_r0 ),
    .R1(\ступень_сдвигателя_64х_левого_логического_50_r1 ));
  \ступень_сдвигателя_64х_левого_логического  \u_ступень_сдвигателя_64х_левого_логического_51  (
    .\А0 (\ступень_сдвигателя_64х_левого_логического_50_r0 ),
    .\А1 (\ступень_сдвигателя_64х_левого_логического_50_r1 ),
    .R0(\ступень_сдвигателя_64х_левого_логического_51_r0 ),
    .R1(\ступень_сдвигателя_64х_левого_логического_51_r1 ));
  \ступень_сдвигателя_64х_левого_логического  \u_ступень_сдвигателя_64х_левого_логического_52  (
    .\А0 (\ступень_сдвигателя_64х_левого_логического_51_r0 ),
    .\А1 (\ступень_сдвигателя_64х_левого_логического_51_r1 ),
    .R0(\ступень_сдвигателя_64х_левого_логического_52_r0 ),
    .R1(\ступень_сдвигателя_64х_левого_логического_52_r1 ));
  \ступень_сдвигателя_64х_левого_логического  \u_ступень_сдвигателя_64х_левого_логического_53  (
    .\А0 (\ступень_сдвигателя_64х_левого_логического_54_r0 ),
    .\А1 (\ступень_сдвигателя_64х_левого_логического_54_r1 ),
    .R0(\ступень_сдвигателя_64х_левого_логического_53_r0 ),
    .R1(\ступень_сдвигателя_64х_левого_логического_53_r1 ));
  \ступень_сдвигателя_64х_левого_логического  \u_ступень_сдвигателя_64х_левого_логического_54  (
    .\А0 (\ступень_сдвигателя_64х_левого_логического_52_r0 ),
    .\А1 (\ступень_сдвигателя_64х_левого_логического_52_r1 ),
    .R0(\ступень_сдвигателя_64х_левого_логического_54_r0 ),
    .R1(\ступень_сдвигателя_64х_левого_логического_54_r1 ));
  \ступень_сдвигателя_64х_левого_логического  \u_ступень_сдвигателя_64х_левого_логического_55  (
    .\А0 (\ступень_сдвигателя_64х_левого_логического_53_r0 ),
    .\А1 (\ступень_сдвигателя_64х_левого_логического_53_r1 ),
    .R0(\ступень_сдвигателя_64х_левого_логического_55_r0 ),
    .R1(\ступень_сдвигателя_64х_левого_логического_55_r1 ));
  \ступень_сдвигателя_64х_левого_логического  \u_ступень_сдвигателя_64х_левого_логического_56  (
    .\А0 (\ступень_сдвигателя_64х_левого_логического_55_r0 ),
    .\А1 (\ступень_сдвигателя_64х_левого_логического_55_r1 ),
    .R0(\ступень_сдвигателя_64х_левого_логического_56_r0 ),
    .R1(\ступень_сдвигателя_64х_левого_логического_56_r1 ));
  \ступень_сдвигателя_64х_левого_логического  \u_ступень_сдвигателя_64х_левого_логического_57  (
    .\А0 (\ступень_сдвигателя_64х_левого_логического_56_r0 ),
    .\А1 (\ступень_сдвигателя_64х_левого_логического_56_r1 ),
    .R0(\ступень_сдвигателя_64х_левого_логического_57_r0 ),
    .R1(\ступень_сдвигателя_64х_левого_логического_57_r1 ));
  \ступень_сдвигателя_64х_левого_логического  \u_ступень_сдвигателя_64х_левого_логического_58  (
    .\А0 (\ступень_сдвигателя_64х_левого_логического_57_r0 ),
    .\А1 (\ступень_сдвигателя_64х_левого_логического_57_r1 ),
    .R0(\ступень_сдвигателя_64х_левого_логического_58_r0 ),
    .R1(\ступень_сдвигателя_64х_левого_логического_58_r1 ));
  \ступень_сдвигателя_64х_левого_логического  \u_ступень_сдвигателя_64х_левого_логического_59  (
    .\А0 (\ступень_сдвигателя_64х_левого_логического_58_r0 ),
    .\А1 (\ступень_сдвигателя_64х_левого_логического_58_r1 ),
    .R0(\ступень_сдвигателя_64х_левого_логического_59_r0 ),
    .R1(\ступень_сдвигателя_64х_левого_логического_59_r1 ));
  \ступень_сдвигателя_64х_левого_логического  \u_ступень_сдвигателя_64х_левого_логического_60  (
    .\А0 (\ступень_сдвигателя_64х_левого_логического_59_r0 ),
    .\А1 (\ступень_сдвигателя_64х_левого_логического_59_r1 ),
    .R0(\ступень_сдвигателя_64х_левого_логического_60_r0 ),
    .R1(\ступень_сдвигателя_64х_левого_логического_60_r1 ));
  \ступень_сдвигателя_64х_левого_логического  \u_ступень_сдвигателя_64х_левого_логического_61  (
    .\А0 (\ступень_сдвигателя_64х_левого_логического_62_r0 ),
    .\А1 (\ступень_сдвигателя_64х_левого_логического_62_r1 ),
    .R0(\ступень_сдвигателя_64х_левого_логического_61_r0 ),
    .R1(\ступень_сдвигателя_64х_левого_логического_61_r1 ));
  \ступень_сдвигателя_64х_левого_логического  \u_ступень_сдвигателя_64х_левого_логического_62  (
    .\А0 (\ступень_сдвигателя_64х_левого_логического_60_r0 ),
    .\А1 (\ступень_сдвигателя_64х_левого_логического_60_r1 ),
    .R0(\ступень_сдвигателя_64х_левого_логического_62_r0 ),
    .R1(\ступень_сдвигателя_64х_левого_логического_62_r1 ));
  \ступень_сдвигателя_64х_левого_логического  \u_ступень_сдвигателя_64х_левого_логического_63  (
    .\А0 (\ступень_сдвигателя_64х_левого_логического_61_r0 ),
    .\А1 (\ступень_сдвигателя_64х_левого_логического_61_r1 ),
    .R0(\ступень_сдвигателя_64х_левого_логического_63_r0 ),
    .R1(\ступень_сдвигателя_64х_левого_логического_63_r1 ));
endmodule
module \сдвигатель_64х_правый_логический  (
  input  [31:0] A0,
  input  [31:0] A1,
  input  [5:0] in_3,
  output [31:0] R0,
  output [31:0] R1
);

  wire [31:0] multiplexer_3_out, multiplexer_4_out, multiplexer_5_out, multiplexer_6_out,
       \ступень_сдвигателя_64х_правого_логического_1_r0 , \ступень_сдвигателя_64х_правого_логического_1_r1 ,
       \ступень_сдвигателя_64х_правого_логического_2_r0 , \ступень_сдвигателя_64х_правого_логического_2_r1 ,
       \ступень_сдвигателя_64х_правого_логического_3_r0 , \ступень_сдвигателя_64х_правого_логического_3_r1 ,
       \ступень_сдвигателя_64х_правого_логического_4_r0 , \ступень_сдвигателя_64х_правого_логического_4_r1 ,
       \ступень_сдвигателя_64х_правого_логического_5_r0 , \ступень_сдвигателя_64х_правого_логического_5_r1 ,
       \ступень_сдвигателя_64х_правого_логического_6_r0 , \ступень_сдвигателя_64х_правого_логического_6_r1 ,
       \ступень_сдвигателя_64х_правого_логического_7_r0 , \ступень_сдвигателя_64х_правого_логического_7_r1 ,
       \ступень_сдвигателя_64х_правого_логического_8_r0 , \ступень_сдвигателя_64х_правого_логического_8_r1 ,
       \ступень_сдвигателя_64х_правого_логического_9_r0 , \ступень_сдвигателя_64х_правого_логического_9_r1 ,
       \ступень_сдвигателя_64х_правого_логического_10_r0 ,
       \ступень_сдвигателя_64х_правого_логического_10_r1 ,
       \ступень_сдвигателя_64х_правого_логического_11_r0 ,
       \ступень_сдвигателя_64х_правого_логического_11_r1 ,
       \ступень_сдвигателя_64х_правого_логического_12_r0 ,
       \ступень_сдвигателя_64х_правого_логического_12_r1 ,
       \ступень_сдвигателя_64х_правого_логического_13_r0 ,
       \ступень_сдвигателя_64х_правого_логического_13_r1 ,
       \ступень_сдвигателя_64х_правого_логического_14_r0 ,
       \ступень_сдвигателя_64х_правого_логического_14_r1 ,
       \ступень_сдвигателя_64х_правого_логического_15_r0 ,
       \ступень_сдвигателя_64х_правого_логического_15_r1 ,
       \ступень_сдвигателя_64х_правого_логического_16_r0 ,
       \ступень_сдвигателя_64х_правого_логического_16_r1 ,
       \ступень_сдвигателя_64х_правого_логического_17_r0 ,
       \ступень_сдвигателя_64х_правого_логического_17_r1 ,
       \ступень_сдвигателя_64х_правого_логического_18_r0 ,
       \ступень_сдвигателя_64х_правого_логического_18_r1 ,
       \ступень_сдвигателя_64х_правого_логического_19_r0 ,
       \ступень_сдвигателя_64х_правого_логического_19_r1 ,
       \ступень_сдвигателя_64х_правого_логического_20_r0 ,
       \ступень_сдвигателя_64х_правого_логического_20_r1 ,
       \ступень_сдвигателя_64х_правого_логического_21_r0 ,
       \ступень_сдвигателя_64х_правого_логического_21_r1 ,
       \ступень_сдвигателя_64х_правого_логического_22_r0 ,
       \ступень_сдвигателя_64х_правого_логического_22_r1 ,
       \ступень_сдвигателя_64х_правого_логического_23_r0 ,
       \ступень_сдвигателя_64х_правого_логического_23_r1 ,
       \ступень_сдвигателя_64х_правого_логического_24_r0 ,
       \ступень_сдвигателя_64х_правого_логического_24_r1 ,
       \ступень_сдвигателя_64х_правого_логического_25_r0 ,
       \ступень_сдвигателя_64х_правого_логического_25_r1 ,
       \ступень_сдвигателя_64х_правого_логического_26_r0 ,
       \ступень_сдвигателя_64х_правого_логического_26_r1 ,
       \ступень_сдвигателя_64х_правого_логического_27_r0 ,
       \ступень_сдвигателя_64х_правого_логического_27_r1 ,
       \ступень_сдвигателя_64х_правого_логического_28_r0 ,
       \ступень_сдвигателя_64х_правого_логического_28_r1 ,
       \ступень_сдвигателя_64х_правого_логического_29_r0 ,
       \ступень_сдвигателя_64х_правого_логического_29_r1 ,
       \ступень_сдвигателя_64х_правого_логического_30_r0 ,
       \ступень_сдвигателя_64х_правого_логического_30_r1 ,
       \ступень_сдвигателя_64х_правого_логического_31_r0 ,
       \ступень_сдвигателя_64х_правого_логического_31_r1 ,
       \ступень_сдвигателя_64х_правого_логического_32_r0 ,
       \ступень_сдвигателя_64х_правого_логического_32_r1 ,
       \ступень_сдвигателя_64х_правого_логического_33_r0 ,
       \ступень_сдвигателя_64х_правого_логического_33_r1 ,
       \ступень_сдвигателя_64х_правого_логического_34_r0 ,
       \ступень_сдвигателя_64х_правого_логического_34_r1 ,
       \ступень_сдвигателя_64х_правого_логического_35_r0 ,
       \ступень_сдвигателя_64х_правого_логического_35_r1 ,
       \ступень_сдвигателя_64х_правого_логического_36_r0 ,
       \ступень_сдвигателя_64х_правого_логического_36_r1 ,
       \ступень_сдвигателя_64х_правого_логического_37_r0 ,
       \ступень_сдвигателя_64х_правого_логического_37_r1 ,
       \ступень_сдвигателя_64х_правого_логического_38_r0 ,
       \ступень_сдвигателя_64х_правого_логического_38_r1 ,
       \ступень_сдвигателя_64х_правого_логического_39_r0 ,
       \ступень_сдвигателя_64х_правого_логического_39_r1 ,
       \ступень_сдвигателя_64х_правого_логического_40_r0 ,
       \ступень_сдвигателя_64х_правого_логического_40_r1 ,
       \ступень_сдвигателя_64х_правого_логического_41_r0 ,
       \ступень_сдвигателя_64х_правого_логического_41_r1 ,
       \ступень_сдвигателя_64х_правого_логического_42_r0 ,
       \ступень_сдвигателя_64х_правого_логического_42_r1 ,
       \ступень_сдвигателя_64х_правого_логического_43_r0 ,
       \ступень_сдвигателя_64х_правого_логического_43_r1 ,
       \ступень_сдвигателя_64х_правого_логического_44_r0 ,
       \ступень_сдвигателя_64х_правого_логического_44_r1 ,
       \ступень_сдвигателя_64х_правого_логического_45_r0 ,
       \ступень_сдвигателя_64х_правого_логического_45_r1 ,
       \ступень_сдвигателя_64х_правого_логического_46_r0 ,
       \ступень_сдвигателя_64х_правого_логического_46_r1 ,
       \ступень_сдвигателя_64х_правого_логического_47_r0 ,
       \ступень_сдвигателя_64х_правого_логического_47_r1 ,
       \ступень_сдвигателя_64х_правого_логического_48_r0 ,
       \ступень_сдвигателя_64х_правого_логического_48_r1 ,
       \ступень_сдвигателя_64х_правого_логического_49_r0 ,
       \ступень_сдвигателя_64х_правого_логического_49_r1 ,
       \ступень_сдвигателя_64х_правого_логического_50_r0 ,
       \ступень_сдвигателя_64х_правого_логического_50_r1 ,
       \ступень_сдвигателя_64х_правого_логического_51_r0 ,
       \ступень_сдвигателя_64х_правого_логического_51_r1 ,
       \ступень_сдвигателя_64х_правого_логического_52_r0 ,
       \ступень_сдвигателя_64х_правого_логического_52_r1 ,
       \ступень_сдвигателя_64х_правого_логического_53_r0 ,
       \ступень_сдвигателя_64х_правого_логического_53_r1 ,
       \ступень_сдвигателя_64х_правого_логического_54_r0 ,
       \ступень_сдвигателя_64х_правого_логического_54_r1 ,
       \ступень_сдвигателя_64х_правого_логического_55_r0 ,
       \ступень_сдвигателя_64х_правого_логического_55_r1 ,
       \ступень_сдвигателя_64х_правого_логического_56_r0 ,
       \ступень_сдвигателя_64х_правого_логического_56_r1 ,
       \ступень_сдвигателя_64х_правого_логического_57_r0 ,
       \ступень_сдвигателя_64х_правого_логического_57_r1 ,
       \ступень_сдвигателя_64х_правого_логического_58_r0 ,
       \ступень_сдвигателя_64х_правого_логического_58_r1 ,
       \ступень_сдвигателя_64х_правого_логического_59_r0 ,
       \ступень_сдвигателя_64х_правого_логического_59_r1 ,
       \ступень_сдвигателя_64х_правого_логического_60_r0 ,
       \ступень_сдвигателя_64х_правого_логического_60_r1 ,
       \ступень_сдвигателя_64х_правого_логического_61_r0 ,
       \ступень_сдвигателя_64х_правого_логического_61_r1 ,
       \ступень_сдвигателя_64х_правого_логического_62_r0 ,
       \ступень_сдвигателя_64х_правого_логического_62_r1 ,
       \ступень_сдвигателя_64х_правого_логического_63_r0 , \ступень_сдвигателя_64х_правого_логического_63_r1 ;

  Multiplexer #(.width(32), .disabled(0), .enable("false")) multiplexer_1 (
    .in0(multiplexer_3_out), .in1(multiplexer_5_out), .out(R0), .sel(in_3[5]));
  Multiplexer #(.width(32), .disabled(0), .enable("false")) multiplexer_2 (
    .in0(multiplexer_4_out), .in1(multiplexer_6_out), .out(R1), .sel(in_3[5]));
  \ступень_сдвигателя_64х_правого_логического  \u_ступень_сдвигателя_64х_правого_логического_1  (
    .\А0 (A0), .\А1 (A1), .R0(\ступень_сдвигателя_64х_правого_логического_1_r0 ),
    .R1(\ступень_сдвигателя_64х_правого_логического_1_r1 ));
  \ступень_сдвигателя_64х_правого_логического  \u_ступень_сдвигателя_64х_правого_логического_2  (
    .\А0 (\ступень_сдвигателя_64х_правого_логического_1_r0 ),
    .\А1 (\ступень_сдвигателя_64х_правого_логического_1_r1 ),
    .R0(\ступень_сдвигателя_64х_правого_логического_2_r0 ),
    .R1(\ступень_сдвигателя_64х_правого_логического_2_r1 ));
  \ступень_сдвигателя_64х_правого_логического  \u_ступень_сдвигателя_64х_правого_логического_3  (
    .\А0 (\ступень_сдвигателя_64х_правого_логического_2_r0 ),
    .\А1 (\ступень_сдвигателя_64х_правого_логического_2_r1 ),
    .R0(\ступень_сдвигателя_64х_правого_логического_3_r0 ),
    .R1(\ступень_сдвигателя_64х_правого_логического_3_r1 ));
  Multiplexer #(.select(5), .width(32), .disabled(0), .enable("false")) multiplexer_3 (
    .in0(A0), .in1(\ступень_сдвигателя_64х_правого_логического_1_r0 ),
    .in2(\ступень_сдвигателя_64х_правого_логического_2_r0 ),
    .in3(\ступень_сдвигателя_64х_правого_логического_3_r0 ),
    .in4(\ступень_сдвигателя_64х_правого_логического_4_r0 ),
    .in5(\ступень_сдвигателя_64х_правого_логического_6_r0 ),
    .in6(\ступень_сдвигателя_64х_правого_логического_5_r0 ),
    .in7(\ступень_сдвигателя_64х_правого_логического_7_r0 ),
    .in8(\ступень_сдвигателя_64х_правого_логического_8_r0 ),
    .in9(\ступень_сдвигателя_64х_правого_логического_9_r0 ),
    .in10(\ступень_сдвигателя_64х_правого_логического_10_r0 ),
    .in11(\ступень_сдвигателя_64х_правого_логического_11_r0 ),
    .in12(\ступень_сдвигателя_64х_правого_логического_12_r0 ),
    .in13(\ступень_сдвигателя_64х_правого_логического_13_r0 ),
    .in14(\ступень_сдвигателя_64х_правого_логического_14_r0 ),
    .in15(\ступень_сдвигателя_64х_правого_логического_15_r0 ),
    .in16(\ступень_сдвигателя_64х_правого_логического_16_r0 ),
    .in17(\ступень_сдвигателя_64х_правого_логического_17_r0 ),
    .in18(\ступень_сдвигателя_64х_правого_логического_19_r0 ),
    .in19(\ступень_сдвигателя_64х_правого_логического_18_r0 ),
    .in20(\ступень_сдвигателя_64х_правого_логического_20_r0 ),
    .in21(\ступень_сдвигателя_64х_правого_логического_22_r0 ),
    .in22(\ступень_сдвигателя_64х_правого_логического_21_r0 ),
    .in23(\ступень_сдвигателя_64х_правого_логического_24_r0 ),
    .in24(\ступень_сдвигателя_64х_правого_логического_23_r0 ),
    .in25(\ступень_сдвигателя_64х_правого_логического_25_r0 ),
    .in26(\ступень_сдвигателя_64х_правого_логического_27_r0 ),
    .in27(\ступень_сдвигателя_64х_правого_логического_26_r0 ),
    .in28(\ступень_сдвигателя_64х_правого_логического_28_r0 ),
    .in29(\ступень_сдвигателя_64х_правого_логического_29_r0 ),
    .in30(\ступень_сдвигателя_64х_правого_логического_30_r0 ),
    .in31(\ступень_сдвигателя_64х_правого_логического_32_r0 ), .out(multiplexer_3_out), .sel(in_3[4:0]));
  \ступень_сдвигателя_64х_правого_логического  \u_ступень_сдвигателя_64х_правого_логического_4  (
    .\А0 (\ступень_сдвигателя_64х_правого_логического_3_r0 ),
    .\А1 (\ступень_сдвигателя_64х_правого_логического_3_r1 ),
    .R0(\ступень_сдвигателя_64х_правого_логического_4_r0 ),
    .R1(\ступень_сдвигателя_64х_правого_логического_4_r1 ));
  Multiplexer #(.select(5), .width(32), .disabled(0), .enable("false")) multiplexer_4 (
    .in0(A1), .in1(\ступень_сдвигателя_64х_правого_логического_1_r1 ),
    .in2(\ступень_сдвигателя_64х_правого_логического_2_r1 ),
    .in3(\ступень_сдвигателя_64х_правого_логического_3_r1 ),
    .in4(\ступень_сдвигателя_64х_правого_логического_4_r1 ),
    .in5(\ступень_сдвигателя_64х_правого_логического_6_r1 ),
    .in6(\ступень_сдвигателя_64х_правого_логического_5_r1 ),
    .in7(\ступень_сдвигателя_64х_правого_логического_7_r1 ),
    .in8(\ступень_сдвигателя_64х_правого_логического_8_r1 ),
    .in9(\ступень_сдвигателя_64х_правого_логического_9_r1 ),
    .in10(\ступень_сдвигателя_64х_правого_логического_10_r1 ),
    .in11(\ступень_сдвигателя_64х_правого_логического_11_r1 ),
    .in12(\ступень_сдвигателя_64х_правого_логического_12_r1 ),
    .in13(\ступень_сдвигателя_64х_правого_логического_13_r1 ),
    .in14(\ступень_сдвигателя_64х_правого_логического_14_r1 ),
    .in15(\ступень_сдвигателя_64х_правого_логического_15_r1 ),
    .in16(\ступень_сдвигателя_64х_правого_логического_16_r1 ),
    .in17(\ступень_сдвигателя_64х_правого_логического_17_r1 ),
    .in18(\ступень_сдвигателя_64х_правого_логического_19_r1 ),
    .in19(\ступень_сдвигателя_64х_правого_логического_18_r1 ),
    .in20(\ступень_сдвигателя_64х_правого_логического_20_r1 ),
    .in21(\ступень_сдвигателя_64х_правого_логического_22_r1 ),
    .in22(\ступень_сдвигателя_64х_правого_логического_21_r1 ),
    .in23(\ступень_сдвигателя_64х_правого_логического_24_r1 ),
    .in24(\ступень_сдвигателя_64х_правого_логического_23_r1 ),
    .in25(\ступень_сдвигателя_64х_правого_логического_25_r1 ),
    .in26(\ступень_сдвигателя_64х_правого_логического_27_r1 ),
    .in27(\ступень_сдвигателя_64х_правого_логического_26_r1 ),
    .in28(\ступень_сдвигателя_64х_правого_логического_28_r1 ),
    .in29(\ступень_сдвигателя_64х_правого_логического_29_r1 ),
    .in30(\ступень_сдвигателя_64х_правого_логического_30_r1 ),
    .in31(\ступень_сдвигателя_64х_правого_логического_32_r1 ), .out(multiplexer_4_out), .sel(in_3[4:0]));
  \ступень_сдвигателя_64х_правого_логического  \u_ступень_сдвигателя_64х_правого_логического_5  (
    .\А0 (\ступень_сдвигателя_64х_правого_логического_6_r0 ),
    .\А1 (\ступень_сдвигателя_64х_правого_логического_6_r1 ),
    .R0(\ступень_сдвигателя_64х_правого_логического_5_r0 ),
    .R1(\ступень_сдвигателя_64х_правого_логического_5_r1 ));
  \ступень_сдвигателя_64х_правого_логического  \u_ступень_сдвигателя_64х_правого_логического_6  (
    .\А0 (\ступень_сдвигателя_64х_правого_логического_4_r0 ),
    .\А1 (\ступень_сдвигателя_64х_правого_логического_4_r1 ),
    .R0(\ступень_сдвигателя_64х_правого_логического_6_r0 ),
    .R1(\ступень_сдвигателя_64х_правого_логического_6_r1 ));
  \ступень_сдвигателя_64х_правого_логического  \u_ступень_сдвигателя_64х_правого_логического_7  (
    .\А0 (\ступень_сдвигателя_64х_правого_логического_5_r0 ),
    .\А1 (\ступень_сдвигателя_64х_правого_логического_5_r1 ),
    .R0(\ступень_сдвигателя_64х_правого_логического_7_r0 ),
    .R1(\ступень_сдвигателя_64х_правого_логического_7_r1 ));
  \ступень_сдвигателя_64х_правого_логического  \u_ступень_сдвигателя_64х_правого_логического_8  (
    .\А0 (\ступень_сдвигателя_64х_правого_логического_7_r0 ),
    .\А1 (\ступень_сдвигателя_64х_правого_логического_7_r1 ),
    .R0(\ступень_сдвигателя_64х_правого_логического_8_r0 ),
    .R1(\ступень_сдвигателя_64х_правого_логического_8_r1 ));
  \ступень_сдвигателя_64х_правого_логического  \u_ступень_сдвигателя_64х_правого_логического_9  (
    .\А0 (\ступень_сдвигателя_64х_правого_логического_8_r0 ),
    .\А1 (\ступень_сдвигателя_64х_правого_логического_8_r1 ),
    .R0(\ступень_сдвигателя_64х_правого_логического_9_r0 ),
    .R1(\ступень_сдвигателя_64х_правого_логического_9_r1 ));
  \ступень_сдвигателя_64х_правого_логического  \u_ступень_сдвигателя_64х_правого_логического_10  (
    .\А0 (\ступень_сдвигателя_64х_правого_логического_9_r0 ),
    .\А1 (\ступень_сдвигателя_64х_правого_логического_9_r1 ),
    .R0(\ступень_сдвигателя_64х_правого_логического_10_r0 ),
    .R1(\ступень_сдвигателя_64х_правого_логического_10_r1 ));
  \ступень_сдвигателя_64х_правого_логического  \u_ступень_сдвигателя_64х_правого_логического_11  (
    .\А0 (\ступень_сдвигателя_64х_правого_логического_10_r0 ),
    .\А1 (\ступень_сдвигателя_64х_правого_логического_10_r1 ),
    .R0(\ступень_сдвигателя_64х_правого_логического_11_r0 ),
    .R1(\ступень_сдвигателя_64х_правого_логического_11_r1 ));
  \ступень_сдвигателя_64х_правого_логического  \u_ступень_сдвигателя_64х_правого_логического_12  (
    .\А0 (\ступень_сдвигателя_64х_правого_логического_11_r0 ),
    .\А1 (\ступень_сдвигателя_64х_правого_логического_11_r1 ),
    .R0(\ступень_сдвигателя_64х_правого_логического_12_r0 ),
    .R1(\ступень_сдвигателя_64х_правого_логического_12_r1 ));
  \ступень_сдвигателя_64х_правого_логического  \u_ступень_сдвигателя_64х_правого_логического_13  (
    .\А0 (\ступень_сдвигателя_64х_правого_логического_12_r0 ),
    .\А1 (\ступень_сдвигателя_64х_правого_логического_12_r1 ),
    .R0(\ступень_сдвигателя_64х_правого_логического_13_r0 ),
    .R1(\ступень_сдвигателя_64х_правого_логического_13_r1 ));
  \ступень_сдвигателя_64х_правого_логического  \u_ступень_сдвигателя_64х_правого_логического_14  (
    .\А0 (\ступень_сдвигателя_64х_правого_логического_13_r0 ),
    .\А1 (\ступень_сдвигателя_64х_правого_логического_13_r1 ),
    .R0(\ступень_сдвигателя_64х_правого_логического_14_r0 ),
    .R1(\ступень_сдвигателя_64х_правого_логического_14_r1 ));
  \ступень_сдвигателя_64х_правого_логического  \u_ступень_сдвигателя_64х_правого_логического_15  (
    .\А0 (\ступень_сдвигателя_64х_правого_логического_14_r0 ),
    .\А1 (\ступень_сдвигателя_64х_правого_логического_14_r1 ),
    .R0(\ступень_сдвигателя_64х_правого_логического_15_r0 ),
    .R1(\ступень_сдвигателя_64х_правого_логического_15_r1 ));
  \ступень_сдвигателя_64х_правого_логического  \u_ступень_сдвигателя_64х_правого_логического_16  (
    .\А0 (\ступень_сдвигателя_64х_правого_логического_15_r0 ),
    .\А1 (\ступень_сдвигателя_64х_правого_логического_15_r1 ),
    .R0(\ступень_сдвигателя_64х_правого_логического_16_r0 ),
    .R1(\ступень_сдвигателя_64х_правого_логического_16_r1 ));
  \ступень_сдвигателя_64х_правого_логического  \u_ступень_сдвигателя_64х_правого_логического_17  (
    .\А0 (\ступень_сдвигателя_64х_правого_логического_16_r0 ),
    .\А1 (\ступень_сдвигателя_64х_правого_логического_16_r1 ),
    .R0(\ступень_сдвигателя_64х_правого_логического_17_r0 ),
    .R1(\ступень_сдвигателя_64х_правого_логического_17_r1 ));
  \ступень_сдвигателя_64х_правого_логического  \u_ступень_сдвигателя_64х_правого_логического_18  (
    .\А0 (\ступень_сдвигателя_64х_правого_логического_19_r0 ),
    .\А1 (\ступень_сдвигателя_64х_правого_логического_19_r1 ),
    .R0(\ступень_сдвигателя_64х_правого_логического_18_r0 ),
    .R1(\ступень_сдвигателя_64х_правого_логического_18_r1 ));
  \ступень_сдвигателя_64х_правого_логического  \u_ступень_сдвигателя_64х_правого_логического_19  (
    .\А0 (\ступень_сдвигателя_64х_правого_логического_17_r0 ),
    .\А1 (\ступень_сдвигателя_64х_правого_логического_17_r1 ),
    .R0(\ступень_сдвигателя_64х_правого_логического_19_r0 ),
    .R1(\ступень_сдвигателя_64х_правого_логического_19_r1 ));
  \ступень_сдвигателя_64х_правого_логического  \u_ступень_сдвигателя_64х_правого_логического_20  (
    .\А0 (\ступень_сдвигателя_64х_правого_логического_18_r0 ),
    .\А1 (\ступень_сдвигателя_64х_правого_логического_18_r1 ),
    .R0(\ступень_сдвигателя_64х_правого_логического_20_r0 ),
    .R1(\ступень_сдвигателя_64х_правого_логического_20_r1 ));
  \ступень_сдвигателя_64х_правого_логического  \u_ступень_сдвигателя_64х_правого_логического_21  (
    .\А0 (\ступень_сдвигателя_64х_правого_логического_22_r0 ),
    .\А1 (\ступень_сдвигателя_64х_правого_логического_22_r1 ),
    .R0(\ступень_сдвигателя_64х_правого_логического_21_r0 ),
    .R1(\ступень_сдвигателя_64х_правого_логического_21_r1 ));
  \ступень_сдвигателя_64х_правого_логического  \u_ступень_сдвигателя_64х_правого_логического_22  (
    .\А0 (\ступень_сдвигателя_64х_правого_логического_20_r0 ),
    .\А1 (\ступень_сдвигателя_64х_правого_логического_20_r1 ),
    .R0(\ступень_сдвигателя_64х_правого_логического_22_r0 ),
    .R1(\ступень_сдвигателя_64х_правого_логического_22_r1 ));
  \ступень_сдвигателя_64х_правого_логического  \u_ступень_сдвигателя_64х_правого_логического_23  (
    .\А0 (\ступень_сдвигателя_64х_правого_логического_24_r0 ),
    .\А1 (\ступень_сдвигателя_64х_правого_логического_24_r1 ),
    .R0(\ступень_сдвигателя_64х_правого_логического_23_r0 ),
    .R1(\ступень_сдвигателя_64х_правого_логического_23_r1 ));
  \ступень_сдвигателя_64х_правого_логического  \u_ступень_сдвигателя_64х_правого_логического_24  (
    .\А0 (\ступень_сдвигателя_64х_правого_логического_21_r0 ),
    .\А1 (\ступень_сдвигателя_64х_правого_логического_21_r1 ),
    .R0(\ступень_сдвигателя_64х_правого_логического_24_r0 ),
    .R1(\ступень_сдвигателя_64х_правого_логического_24_r1 ));
  \ступень_сдвигателя_64х_правого_логического  \u_ступень_сдвигателя_64х_правого_логического_25  (
    .\А0 (\ступень_сдвигателя_64х_правого_логического_23_r0 ),
    .\А1 (\ступень_сдвигателя_64х_правого_логического_23_r1 ),
    .R0(\ступень_сдвигателя_64х_правого_логического_25_r0 ),
    .R1(\ступень_сдвигателя_64х_правого_логического_25_r1 ));
  \ступень_сдвигателя_64х_правого_логического  \u_ступень_сдвигателя_64х_правого_логического_26  (
    .\А0 (\ступень_сдвигателя_64х_правого_логического_27_r0 ),
    .\А1 (\ступень_сдвигателя_64х_правого_логического_27_r1 ),
    .R0(\ступень_сдвигателя_64х_правого_логического_26_r0 ),
    .R1(\ступень_сдвигателя_64х_правого_логического_26_r1 ));
  \ступень_сдвигателя_64х_правого_логического  \u_ступень_сдвигателя_64х_правого_логического_27  (
    .\А0 (\ступень_сдвигателя_64х_правого_логического_25_r0 ),
    .\А1 (\ступень_сдвигателя_64х_правого_логического_25_r1 ),
    .R0(\ступень_сдвигателя_64х_правого_логического_27_r0 ),
    .R1(\ступень_сдвигателя_64х_правого_логического_27_r1 ));
  \ступень_сдвигателя_64х_правого_логического  \u_ступень_сдвигателя_64х_правого_логического_28  (
    .\А0 (\ступень_сдвигателя_64х_правого_логического_26_r0 ),
    .\А1 (\ступень_сдвигателя_64х_правого_логического_26_r1 ),
    .R0(\ступень_сдвигателя_64х_правого_логического_28_r0 ),
    .R1(\ступень_сдвигателя_64х_правого_логического_28_r1 ));
  \ступень_сдвигателя_64х_правого_логического  \u_ступень_сдвигателя_64х_правого_логического_29  (
    .\А0 (\ступень_сдвигателя_64х_правого_логического_28_r0 ),
    .\А1 (\ступень_сдвигателя_64х_правого_логического_28_r1 ),
    .R0(\ступень_сдвигателя_64х_правого_логического_29_r0 ),
    .R1(\ступень_сдвигателя_64х_правого_логического_29_r1 ));
  \ступень_сдвигателя_64х_правого_логического  \u_ступень_сдвигателя_64х_правого_логического_30  (
    .\А0 (\ступень_сдвигателя_64х_правого_логического_29_r0 ),
    .\А1 (\ступень_сдвигателя_64х_правого_логического_29_r1 ),
    .R0(\ступень_сдвигателя_64х_правого_логического_30_r0 ),
    .R1(\ступень_сдвигателя_64х_правого_логического_30_r1 ));
  \ступень_сдвигателя_64х_правого_логического  \u_ступень_сдвигателя_64х_правого_логического_31  (
    .\А0 (\ступень_сдвигателя_64х_правого_логического_32_r0 ),
    .\А1 (\ступень_сдвигателя_64х_правого_логического_32_r1 ),
    .R0(\ступень_сдвигателя_64х_правого_логического_31_r0 ),
    .R1(\ступень_сдвигателя_64х_правого_логического_31_r1 ));
  \ступень_сдвигателя_64х_правого_логического  \u_ступень_сдвигателя_64х_правого_логического_32  (
    .\А0 (\ступень_сдвигателя_64х_правого_логического_30_r0 ),
    .\А1 (\ступень_сдвигателя_64х_правого_логического_30_r1 ),
    .R0(\ступень_сдвигателя_64х_правого_логического_32_r0 ),
    .R1(\ступень_сдвигателя_64х_правого_логического_32_r1 ));
  \ступень_сдвигателя_64х_правого_логического  \u_ступень_сдвигателя_64х_правого_логического_33  (
    .\А0 (\ступень_сдвигателя_64х_правого_логического_31_r0 ),
    .\А1 (\ступень_сдвигателя_64х_правого_логического_31_r1 ),
    .R0(\ступень_сдвигателя_64х_правого_логического_33_r0 ),
    .R1(\ступень_сдвигателя_64х_правого_логического_33_r1 ));
  \ступень_сдвигателя_64х_правого_логического  \u_ступень_сдвигателя_64х_правого_логического_34  (
    .\А0 (\ступень_сдвигателя_64х_правого_логического_33_r0 ),
    .\А1 (\ступень_сдвигателя_64х_правого_логического_33_r1 ),
    .R0(\ступень_сдвигателя_64х_правого_логического_34_r0 ),
    .R1(\ступень_сдвигателя_64х_правого_логического_34_r1 ));
  \ступень_сдвигателя_64х_правого_логического  \u_ступень_сдвигателя_64х_правого_логического_35  (
    .\А0 (\ступень_сдвигателя_64х_правого_логического_34_r0 ),
    .\А1 (\ступень_сдвигателя_64х_правого_логического_34_r1 ),
    .R0(\ступень_сдвигателя_64х_правого_логического_35_r0 ),
    .R1(\ступень_сдвигателя_64х_правого_логического_35_r1 ));
  Multiplexer #(.select(5), .width(32), .disabled(0), .enable("false")) multiplexer_5 (
    .in0(\ступень_сдвигателя_64х_правого_логического_31_r0 ),
    .in1(\ступень_сдвигателя_64х_правого_логического_33_r0 ),
    .in2(\ступень_сдвигателя_64х_правого_логического_34_r0 ),
    .in3(\ступень_сдвигателя_64х_правого_логического_35_r0 ),
    .in4(\ступень_сдвигателя_64х_правого_логического_36_r0 ),
    .in5(\ступень_сдвигателя_64х_правого_логического_38_r0 ),
    .in6(\ступень_сдвигателя_64х_правого_логического_37_r0 ),
    .in7(\ступень_сдвигателя_64х_правого_логического_40_r0 ),
    .in8(\ступень_сдвигателя_64х_правого_логического_39_r0 ),
    .in9(\ступень_сдвигателя_64х_правого_логического_41_r0 ),
    .in10(\ступень_сдвигателя_64х_правого_логического_42_r0 ),
    .in11(\ступень_сдвигателя_64х_правого_логического_43_r0 ),
    .in12(\ступень_сдвигателя_64х_правого_логического_44_r0 ),
    .in13(\ступень_сдвигателя_64х_правого_логического_45_r0 ),
    .in14(\ступень_сдвигателя_64х_правого_логического_46_r0 ),
    .in15(\ступень_сдвигателя_64х_правого_логического_47_r0 ),
    .in16(\ступень_сдвигателя_64х_правого_логического_48_r0 ),
    .in17(\ступень_сдвигателя_64х_правого_логического_49_r0 ),
    .in18(\ступень_сдвигателя_64х_правого_логического_50_r0 ),
    .in19(\ступень_сдвигателя_64х_правого_логического_51_r0 ),
    .in20(\ступень_сдвигателя_64х_правого_логического_52_r0 ),
    .in21(\ступень_сдвигателя_64х_правого_логического_54_r0 ),
    .in22(\ступень_сдвигателя_64х_правого_логического_53_r0 ),
    .in23(\ступень_сдвигателя_64х_правого_логического_55_r0 ),
    .in24(\ступень_сдвигателя_64х_правого_логического_56_r0 ),
    .in25(\ступень_сдвигателя_64х_правого_логического_57_r0 ),
    .in26(\ступень_сдвигателя_64х_правого_логического_58_r0 ),
    .in27(\ступень_сдвигателя_64х_правого_логического_59_r0 ),
    .in28(\ступень_сдвигателя_64х_правого_логического_60_r0 ),
    .in29(\ступень_сдвигателя_64х_правого_логического_61_r0 ),
    .in30(\ступень_сдвигателя_64х_правого_логического_62_r0 ),
    .in31(\ступень_сдвигателя_64х_правого_логического_63_r0 ), .out(multiplexer_5_out), .sel(in_3[4:0]));
  \ступень_сдвигателя_64х_правого_логического  \u_ступень_сдвигателя_64х_правого_логического_36  (
    .\А0 (\ступень_сдвигателя_64х_правого_логического_35_r0 ),
    .\А1 (\ступень_сдвигателя_64х_правого_логического_35_r1 ),
    .R0(\ступень_сдвигателя_64х_правого_логического_36_r0 ),
    .R1(\ступень_сдвигателя_64х_правого_логического_36_r1 ));
  Multiplexer #(.select(5), .width(32), .disabled(0), .enable("false")) multiplexer_6 (
    .in0(\ступень_сдвигателя_64х_правого_логического_31_r1 ),
    .in1(\ступень_сдвигателя_64х_правого_логического_33_r1 ),
    .in2(\ступень_сдвигателя_64х_правого_логического_34_r1 ),
    .in3(\ступень_сдвигателя_64х_правого_логического_35_r1 ),
    .in4(\ступень_сдвигателя_64х_правого_логического_36_r1 ),
    .in5(\ступень_сдвигателя_64х_правого_логического_38_r1 ),
    .in6(\ступень_сдвигателя_64х_правого_логического_37_r1 ),
    .in7(\ступень_сдвигателя_64х_правого_логического_40_r1 ),
    .in8(\ступень_сдвигателя_64х_правого_логического_39_r1 ),
    .in9(\ступень_сдвигателя_64х_правого_логического_41_r1 ),
    .in10(\ступень_сдвигателя_64х_правого_логического_42_r1 ),
    .in11(\ступень_сдвигателя_64х_правого_логического_43_r1 ),
    .in12(\ступень_сдвигателя_64х_правого_логического_44_r1 ),
    .in13(\ступень_сдвигателя_64х_правого_логического_45_r1 ),
    .in14(\ступень_сдвигателя_64х_правого_логического_46_r1 ),
    .in15(\ступень_сдвигателя_64х_правого_логического_47_r1 ),
    .in16(\ступень_сдвигателя_64х_правого_логического_48_r1 ),
    .in17(\ступень_сдвигателя_64х_правого_логического_49_r1 ),
    .in18(\ступень_сдвигателя_64х_правого_логического_50_r1 ),
    .in19(\ступень_сдвигателя_64х_правого_логического_51_r1 ),
    .in20(\ступень_сдвигателя_64х_правого_логического_52_r1 ),
    .in21(\ступень_сдвигателя_64х_правого_логического_54_r1 ),
    .in22(\ступень_сдвигателя_64х_правого_логического_53_r1 ),
    .in23(\ступень_сдвигателя_64х_правого_логического_55_r1 ),
    .in24(\ступень_сдвигателя_64х_правого_логического_56_r1 ),
    .in25(\ступень_сдвигателя_64х_правого_логического_57_r1 ),
    .in26(\ступень_сдвигателя_64х_правого_логического_58_r1 ),
    .in27(\ступень_сдвигателя_64х_правого_логического_59_r1 ),
    .in28(\ступень_сдвигателя_64х_правого_логического_60_r1 ),
    .in29(\ступень_сдвигателя_64х_правого_логического_61_r1 ),
    .in30(\ступень_сдвигателя_64х_правого_логического_62_r1 ),
    .in31(\ступень_сдвигателя_64х_правого_логического_63_r1 ), .out(multiplexer_6_out), .sel(in_3[4:0]));
  \ступень_сдвигателя_64х_правого_логического  \u_ступень_сдвигателя_64х_правого_логического_37  (
    .\А0 (\ступень_сдвигателя_64х_правого_логического_38_r0 ),
    .\А1 (\ступень_сдвигателя_64х_правого_логического_38_r1 ),
    .R0(\ступень_сдвигателя_64х_правого_логического_37_r0 ),
    .R1(\ступень_сдвигателя_64х_правого_логического_37_r1 ));
  \ступень_сдвигателя_64х_правого_логического  \u_ступень_сдвигателя_64х_правого_логического_38  (
    .\А0 (\ступень_сдвигателя_64х_правого_логического_36_r0 ),
    .\А1 (\ступень_сдвигателя_64х_правого_логического_36_r1 ),
    .R0(\ступень_сдвигателя_64х_правого_логического_38_r0 ),
    .R1(\ступень_сдвигателя_64х_правого_логического_38_r1 ));
  \ступень_сдвигателя_64х_правого_логического  \u_ступень_сдвигателя_64х_правого_логического_39  (
    .\А0 (\ступень_сдвигателя_64х_правого_логического_40_r0 ),
    .\А1 (\ступень_сдвигателя_64х_правого_логического_40_r1 ),
    .R0(\ступень_сдвигателя_64х_правого_логического_39_r0 ),
    .R1(\ступень_сдвигателя_64х_правого_логического_39_r1 ));
  \ступень_сдвигателя_64х_правого_логического  \u_ступень_сдвигателя_64х_правого_логического_40  (
    .\А0 (\ступень_сдвигателя_64х_правого_логического_37_r0 ),
    .\А1 (\ступень_сдвигателя_64х_правого_логического_37_r1 ),
    .R0(\ступень_сдвигателя_64х_правого_логического_40_r0 ),
    .R1(\ступень_сдвигателя_64х_правого_логического_40_r1 ));
  \ступень_сдвигателя_64х_правого_логического  \u_ступень_сдвигателя_64х_правого_логического_41  (
    .\А0 (\ступень_сдвигателя_64х_правого_логического_39_r0 ),
    .\А1 (\ступень_сдвигателя_64х_правого_логического_39_r1 ),
    .R0(\ступень_сдвигателя_64х_правого_логического_41_r0 ),
    .R1(\ступень_сдвигателя_64х_правого_логического_41_r1 ));
  \ступень_сдвигателя_64х_правого_логического  \u_ступень_сдвигателя_64х_правого_логического_42  (
    .\А0 (\ступень_сдвигателя_64х_правого_логического_41_r0 ),
    .\А1 (\ступень_сдвигателя_64х_правого_логического_41_r1 ),
    .R0(\ступень_сдвигателя_64х_правого_логического_42_r0 ),
    .R1(\ступень_сдвигателя_64х_правого_логического_42_r1 ));
  \ступень_сдвигателя_64х_правого_логического  \u_ступень_сдвигателя_64х_правого_логического_43  (
    .\А0 (\ступень_сдвигателя_64х_правого_логического_42_r0 ),
    .\А1 (\ступень_сдвигателя_64х_правого_логического_42_r1 ),
    .R0(\ступень_сдвигателя_64х_правого_логического_43_r0 ),
    .R1(\ступень_сдвигателя_64х_правого_логического_43_r1 ));
  \ступень_сдвигателя_64х_правого_логического  \u_ступень_сдвигателя_64х_правого_логического_44  (
    .\А0 (\ступень_сдвигателя_64х_правого_логического_43_r0 ),
    .\А1 (\ступень_сдвигателя_64х_правого_логического_43_r1 ),
    .R0(\ступень_сдвигателя_64х_правого_логического_44_r0 ),
    .R1(\ступень_сдвигателя_64х_правого_логического_44_r1 ));
  \ступень_сдвигателя_64х_правого_логического  \u_ступень_сдвигателя_64х_правого_логического_45  (
    .\А0 (\ступень_сдвигателя_64х_правого_логического_44_r0 ),
    .\А1 (\ступень_сдвигателя_64х_правого_логического_44_r1 ),
    .R0(\ступень_сдвигателя_64х_правого_логического_45_r0 ),
    .R1(\ступень_сдвигателя_64х_правого_логического_45_r1 ));
  \ступень_сдвигателя_64х_правого_логического  \u_ступень_сдвигателя_64х_правого_логического_46  (
    .\А0 (\ступень_сдвигателя_64х_правого_логического_45_r0 ),
    .\А1 (\ступень_сдвигателя_64х_правого_логического_45_r1 ),
    .R0(\ступень_сдвигателя_64х_правого_логического_46_r0 ),
    .R1(\ступень_сдвигателя_64х_правого_логического_46_r1 ));
  \ступень_сдвигателя_64х_правого_логического  \u_ступень_сдвигателя_64х_правого_логического_47  (
    .\А0 (\ступень_сдвигателя_64х_правого_логического_46_r0 ),
    .\А1 (\ступень_сдвигателя_64х_правого_логического_46_r1 ),
    .R0(\ступень_сдвигателя_64х_правого_логического_47_r0 ),
    .R1(\ступень_сдвигателя_64х_правого_логического_47_r1 ));
  \ступень_сдвигателя_64х_правого_логического  \u_ступень_сдвигателя_64х_правого_логического_48  (
    .\А0 (\ступень_сдвигателя_64х_правого_логического_47_r0 ),
    .\А1 (\ступень_сдвигателя_64х_правого_логического_47_r1 ),
    .R0(\ступень_сдвигателя_64х_правого_логического_48_r0 ),
    .R1(\ступень_сдвигателя_64х_правого_логического_48_r1 ));
  \ступень_сдвигателя_64х_правого_логического  \u_ступень_сдвигателя_64х_правого_логического_49  (
    .\А0 (\ступень_сдвигателя_64х_правого_логического_48_r0 ),
    .\А1 (\ступень_сдвигателя_64х_правого_логического_48_r1 ),
    .R0(\ступень_сдвигателя_64х_правого_логического_49_r0 ),
    .R1(\ступень_сдвигателя_64х_правого_логического_49_r1 ));
  \ступень_сдвигателя_64х_правого_логического  \u_ступень_сдвигателя_64х_правого_логического_50  (
    .\А0 (\ступень_сдвигателя_64х_правого_логического_49_r0 ),
    .\А1 (\ступень_сдвигателя_64х_правого_логического_49_r1 ),
    .R0(\ступень_сдвигателя_64х_правого_логического_50_r0 ),
    .R1(\ступень_сдвигателя_64х_правого_логического_50_r1 ));
  \ступень_сдвигателя_64х_правого_логического  \u_ступень_сдвигателя_64х_правого_логического_51  (
    .\А0 (\ступень_сдвигателя_64х_правого_логического_50_r0 ),
    .\А1 (\ступень_сдвигателя_64х_правого_логического_50_r1 ),
    .R0(\ступень_сдвигателя_64х_правого_логического_51_r0 ),
    .R1(\ступень_сдвигателя_64х_правого_логического_51_r1 ));
  \ступень_сдвигателя_64х_правого_логического  \u_ступень_сдвигателя_64х_правого_логического_52  (
    .\А0 (\ступень_сдвигателя_64х_правого_логического_51_r0 ),
    .\А1 (\ступень_сдвигателя_64х_правого_логического_51_r1 ),
    .R0(\ступень_сдвигателя_64х_правого_логического_52_r0 ),
    .R1(\ступень_сдвигателя_64х_правого_логического_52_r1 ));
  \ступень_сдвигателя_64х_правого_логического  \u_ступень_сдвигателя_64х_правого_логического_53  (
    .\А0 (\ступень_сдвигателя_64х_правого_логического_54_r0 ),
    .\А1 (\ступень_сдвигателя_64х_правого_логического_54_r1 ),
    .R0(\ступень_сдвигателя_64х_правого_логического_53_r0 ),
    .R1(\ступень_сдвигателя_64х_правого_логического_53_r1 ));
  \ступень_сдвигателя_64х_правого_логического  \u_ступень_сдвигателя_64х_правого_логического_54  (
    .\А0 (\ступень_сдвигателя_64х_правого_логического_52_r0 ),
    .\А1 (\ступень_сдвигателя_64х_правого_логического_52_r1 ),
    .R0(\ступень_сдвигателя_64х_правого_логического_54_r0 ),
    .R1(\ступень_сдвигателя_64х_правого_логического_54_r1 ));
  \ступень_сдвигателя_64х_правого_логического  \u_ступень_сдвигателя_64х_правого_логического_55  (
    .\А0 (\ступень_сдвигателя_64х_правого_логического_53_r0 ),
    .\А1 (\ступень_сдвигателя_64х_правого_логического_53_r1 ),
    .R0(\ступень_сдвигателя_64х_правого_логического_55_r0 ),
    .R1(\ступень_сдвигателя_64х_правого_логического_55_r1 ));
  \ступень_сдвигателя_64х_правого_логического  \u_ступень_сдвигателя_64х_правого_логического_56  (
    .\А0 (\ступень_сдвигателя_64х_правого_логического_55_r0 ),
    .\А1 (\ступень_сдвигателя_64х_правого_логического_55_r1 ),
    .R0(\ступень_сдвигателя_64х_правого_логического_56_r0 ),
    .R1(\ступень_сдвигателя_64х_правого_логического_56_r1 ));
  \ступень_сдвигателя_64х_правого_логического  \u_ступень_сдвигателя_64х_правого_логического_57  (
    .\А0 (\ступень_сдвигателя_64х_правого_логического_56_r0 ),
    .\А1 (\ступень_сдвигателя_64х_правого_логического_56_r1 ),
    .R0(\ступень_сдвигателя_64х_правого_логического_57_r0 ),
    .R1(\ступень_сдвигателя_64х_правого_логического_57_r1 ));
  \ступень_сдвигателя_64х_правого_логического  \u_ступень_сдвигателя_64х_правого_логического_58  (
    .\А0 (\ступень_сдвигателя_64х_правого_логического_57_r0 ),
    .\А1 (\ступень_сдвигателя_64х_правого_логического_57_r1 ),
    .R0(\ступень_сдвигателя_64х_правого_логического_58_r0 ),
    .R1(\ступень_сдвигателя_64х_правого_логического_58_r1 ));
  \ступень_сдвигателя_64х_правого_логического  \u_ступень_сдвигателя_64х_правого_логического_59  (
    .\А0 (\ступень_сдвигателя_64х_правого_логического_58_r0 ),
    .\А1 (\ступень_сдвигателя_64х_правого_логического_58_r1 ),
    .R0(\ступень_сдвигателя_64х_правого_логического_59_r0 ),
    .R1(\ступень_сдвигателя_64х_правого_логического_59_r1 ));
  \ступень_сдвигателя_64х_правого_логического  \u_ступень_сдвигателя_64х_правого_логического_60  (
    .\А0 (\ступень_сдвигателя_64х_правого_логического_59_r0 ),
    .\А1 (\ступень_сдвигателя_64х_правого_логического_59_r1 ),
    .R0(\ступень_сдвигателя_64х_правого_логического_60_r0 ),
    .R1(\ступень_сдвигателя_64х_правого_логического_60_r1 ));
  \ступень_сдвигателя_64х_правого_логического  \u_ступень_сдвигателя_64х_правого_логического_61  (
    .\А0 (\ступень_сдвигателя_64х_правого_логического_60_r0 ),
    .\А1 (\ступень_сдвигателя_64х_правого_логического_60_r1 ),
    .R0(\ступень_сдвигателя_64х_правого_логического_61_r0 ),
    .R1(\ступень_сдвигателя_64х_правого_логического_61_r1 ));
  \ступень_сдвигателя_64х_правого_логического  \u_ступень_сдвигателя_64х_правого_логического_62  (
    .\А0 (\ступень_сдвигателя_64х_правого_логического_61_r0 ),
    .\А1 (\ступень_сдвигателя_64х_правого_логического_61_r1 ),
    .R0(\ступень_сдвигателя_64х_правого_логического_62_r0 ),
    .R1(\ступень_сдвигателя_64х_правого_логического_62_r1 ));
  \ступень_сдвигателя_64х_правого_логического  \u_ступень_сдвигателя_64х_правого_логического_63  (
    .\А0 (\ступень_сдвигателя_64х_правого_логического_62_r0 ),
    .\А1 (\ступень_сдвигателя_64х_правого_логического_62_r1 ),
    .R0(\ступень_сдвигателя_64х_правого_логического_63_r0 ),
    .R1(\ступень_сдвигателя_64х_правого_логического_63_r1 ));
endmodule

module \сдвигатель_64х_левый_циклический  (
  input  [31:0] A0,
  input  [31:0] A1,
  input  [5:0] in_3,
  output [31:0] R0,
  output [31:0] R1
);

  wire [31:0] multiplexer_3_out, multiplexer_4_out, multiplexer_5_out, multiplexer_6_out,
       \ступень_сдвигателя_64х_левого_циклического_1_r0 , \ступень_сдвигателя_64х_левого_циклического_1_r1 ,
       \ступень_сдвигателя_64х_левого_циклического_2_r0 , \ступень_сдвигателя_64х_левого_циклического_2_r1 ,
       \ступень_сдвигателя_64х_левого_циклического_3_r0 , \ступень_сдвигателя_64х_левого_циклического_3_r1 ,
       \ступень_сдвигателя_64х_левого_циклического_4_r0 , \ступень_сдвигателя_64х_левого_циклического_4_r1 ,
       \ступень_сдвигателя_64х_левого_циклического_5_r0 , \ступень_сдвигателя_64х_левого_циклического_5_r1 ,
       \ступень_сдвигателя_64х_левого_циклического_6_r0 , \ступень_сдвигателя_64х_левого_циклического_6_r1 ,
       \ступень_сдвигателя_64х_левого_циклического_7_r0 , \ступень_сдвигателя_64х_левого_циклического_7_r1 ,
       \ступень_сдвигателя_64х_левого_циклического_8_r0 , \ступень_сдвигателя_64х_левого_циклического_8_r1 ,
       \ступень_сдвигателя_64х_левого_циклического_9_r0 , \ступень_сдвигателя_64х_левого_циклического_9_r1 ,
       \ступень_сдвигателя_64х_левого_циклического_10_r0 ,
       \ступень_сдвигателя_64х_левого_циклического_10_r1 ,
       \ступень_сдвигателя_64х_левого_циклического_11_r0 ,
       \ступень_сдвигателя_64х_левого_циклического_11_r1 ,
       \ступень_сдвигателя_64х_левого_циклического_12_r0 ,
       \ступень_сдвигателя_64х_левого_циклического_12_r1 ,
       \ступень_сдвигателя_64х_левого_циклического_13_r0 ,
       \ступень_сдвигателя_64х_левого_циклического_13_r1 ,
       \ступень_сдвигателя_64х_левого_циклического_14_r0 ,
       \ступень_сдвигателя_64х_левого_циклического_14_r1 ,
       \ступень_сдвигателя_64х_левого_циклического_15_r0 ,
       \ступень_сдвигателя_64х_левого_циклического_15_r1 ,
       \ступень_сдвигателя_64х_левого_циклического_16_r0 ,
       \ступень_сдвигателя_64х_левого_циклического_16_r1 ,
       \ступень_сдвигателя_64х_левого_циклического_17_r0 ,
       \ступень_сдвигателя_64х_левого_циклического_17_r1 ,
       \ступень_сдвигателя_64х_левого_циклического_18_r0 ,
       \ступень_сдвигателя_64х_левого_циклического_18_r1 ,
       \ступень_сдвигателя_64х_левого_циклического_19_r0 ,
       \ступень_сдвигателя_64х_левого_циклического_19_r1 ,
       \ступень_сдвигателя_64х_левого_циклического_20_r0 ,
       \ступень_сдвигателя_64х_левого_циклического_20_r1 ,
       \ступень_сдвигателя_64х_левого_циклического_21_r0 ,
       \ступень_сдвигателя_64х_левого_циклического_21_r1 ,
       \ступень_сдвигателя_64х_левого_циклического_22_r0 ,
       \ступень_сдвигателя_64х_левого_циклического_22_r1 ,
       \ступень_сдвигателя_64х_левого_циклического_23_r0 ,
       \ступень_сдвигателя_64х_левого_циклического_23_r1 ,
       \ступень_сдвигателя_64х_левого_циклического_24_r0 ,
       \ступень_сдвигателя_64х_левого_циклического_24_r1 ,
       \ступень_сдвигателя_64х_левого_циклического_25_r0 ,
       \ступень_сдвигателя_64х_левого_циклического_25_r1 ,
       \ступень_сдвигателя_64х_левого_циклического_26_r0 ,
       \ступень_сдвигателя_64х_левого_циклического_26_r1 ,
       \ступень_сдвигателя_64х_левого_циклического_27_r0 ,
       \ступень_сдвигателя_64х_левого_циклического_27_r1 ,
       \ступень_сдвигателя_64х_левого_циклического_28_r0 ,
       \ступень_сдвигателя_64х_левого_циклического_28_r1 ,
       \ступень_сдвигателя_64х_левого_циклического_29_r0 ,
       \ступень_сдвигателя_64х_левого_циклического_29_r1 ,
       \ступень_сдвигателя_64х_левого_циклического_30_r0 ,
       \ступень_сдвигателя_64х_левого_циклического_30_r1 ,
       \ступень_сдвигателя_64х_левого_циклического_31_r0 ,
       \ступень_сдвигателя_64х_левого_циклического_31_r1 ,
       \ступень_сдвигателя_64х_левого_циклического_32_r0 ,
       \ступень_сдвигателя_64х_левого_циклического_32_r1 ,
       \ступень_сдвигателя_64х_левого_циклического_33_r0 ,
       \ступень_сдвигателя_64х_левого_циклического_33_r1 ,
       \ступень_сдвигателя_64х_левого_циклического_34_r0 ,
       \ступень_сдвигателя_64х_левого_циклического_34_r1 ,
       \ступень_сдвигателя_64х_левого_циклического_35_r0 ,
       \ступень_сдвигателя_64х_левого_циклического_35_r1 ,
       \ступень_сдвигателя_64х_левого_циклического_36_r0 ,
       \ступень_сдвигателя_64х_левого_циклического_36_r1 ,
       \ступень_сдвигателя_64х_левого_циклического_37_r0 ,
       \ступень_сдвигателя_64х_левого_циклического_37_r1 ,
       \ступень_сдвигателя_64х_левого_циклического_38_r0 ,
       \ступень_сдвигателя_64х_левого_циклического_38_r1 ,
       \ступень_сдвигателя_64х_левого_циклического_39_r0 ,
       \ступень_сдвигателя_64х_левого_циклического_39_r1 ,
       \ступень_сдвигателя_64х_левого_циклического_40_r0 ,
       \ступень_сдвигателя_64х_левого_циклического_40_r1 ,
       \ступень_сдвигателя_64х_левого_циклического_41_r0 ,
       \ступень_сдвигателя_64х_левого_циклического_41_r1 ,
       \ступень_сдвигателя_64х_левого_циклического_42_r0 ,
       \ступень_сдвигателя_64х_левого_циклического_42_r1 ,
       \ступень_сдвигателя_64х_левого_циклического_43_r0 ,
       \ступень_сдвигателя_64х_левого_циклического_43_r1 ,
       \ступень_сдвигателя_64х_левого_циклического_44_r0 ,
       \ступень_сдвигателя_64х_левого_циклического_44_r1 ,
       \ступень_сдвигателя_64х_левого_циклического_45_r0 ,
       \ступень_сдвигателя_64х_левого_циклического_45_r1 ,
       \ступень_сдвигателя_64х_левого_циклического_46_r0 ,
       \ступень_сдвигателя_64х_левого_циклического_46_r1 ,
       \ступень_сдвигателя_64х_левого_циклического_47_r0 ,
       \ступень_сдвигателя_64х_левого_циклического_47_r1 ,
       \ступень_сдвигателя_64х_левого_циклического_48_r0 ,
       \ступень_сдвигателя_64х_левого_циклического_48_r1 ,
       \ступень_сдвигателя_64х_левого_циклического_49_r0 ,
       \ступень_сдвигателя_64х_левого_циклического_49_r1 ,
       \ступень_сдвигателя_64х_левого_циклического_50_r0 ,
       \ступень_сдвигателя_64х_левого_циклического_50_r1 ,
       \ступень_сдвигателя_64х_левого_циклического_51_r0 ,
       \ступень_сдвигателя_64х_левого_циклического_51_r1 ,
       \ступень_сдвигателя_64х_левого_циклического_52_r0 ,
       \ступень_сдвигателя_64х_левого_циклического_52_r1 ,
       \ступень_сдвигателя_64х_левого_циклического_53_r0 ,
       \ступень_сдвигателя_64х_левого_циклического_53_r1 ,
       \ступень_сдвигателя_64х_левого_циклического_54_r0 ,
       \ступень_сдвигателя_64х_левого_циклического_54_r1 ,
       \ступень_сдвигателя_64х_левого_циклического_55_r0 ,
       \ступень_сдвигателя_64х_левого_циклического_55_r1 ,
       \ступень_сдвигателя_64х_левого_циклического_56_r0 ,
       \ступень_сдвигателя_64х_левого_циклического_56_r1 ,
       \ступень_сдвигателя_64х_левого_циклического_57_r0 ,
       \ступень_сдвигателя_64х_левого_циклического_57_r1 ,
       \ступень_сдвигателя_64х_левого_циклического_58_r0 ,
       \ступень_сдвигателя_64х_левого_циклического_58_r1 ,
       \ступень_сдвигателя_64х_левого_циклического_59_r0 ,
       \ступень_сдвигателя_64х_левого_циклического_59_r1 ,
       \ступень_сдвигателя_64х_левого_циклического_60_r0 ,
       \ступень_сдвигателя_64х_левого_циклического_60_r1 ,
       \ступень_сдвигателя_64х_левого_циклического_61_r0 ,
       \ступень_сдвигателя_64х_левого_циклического_61_r1 ,
       \ступень_сдвигателя_64х_левого_циклического_62_r0 ,
       \ступень_сдвигателя_64х_левого_циклического_62_r1 ,
       \ступень_сдвигателя_64х_левого_циклического_63_r0 , \ступень_сдвигателя_64х_левого_циклического_63_r1 ;

  Multiplexer #(.width(32), .disabled(0), .enable("false")) multiplexer_1 (
    .in0(multiplexer_3_out), .in1(multiplexer_5_out), .out(R0), .sel(in_3[5]));
  Multiplexer #(.width(32), .disabled(0), .enable("false")) multiplexer_2 (
    .in0(multiplexer_4_out), .in1(multiplexer_6_out), .out(R1), .sel(in_3[5]));
  \ступень_сдвигателя_64х_левого_циклического  \u_ступень_сдвигателя_64х_левого_циклического_1  (
    .\А0 (A0), .\А1 (A1), .R0(\ступень_сдвигателя_64х_левого_циклического_1_r0 ),
    .R1(\ступень_сдвигателя_64х_левого_циклического_1_r1 ));
  \ступень_сдвигателя_64х_левого_циклического  \u_ступень_сдвигателя_64х_левого_циклического_2  (
    .\А0 (\ступень_сдвигателя_64х_левого_циклического_3_r0 ),
    .\А1 (\ступень_сдвигателя_64х_левого_циклического_3_r1 ),
    .R0(\ступень_сдвигателя_64х_левого_циклического_2_r0 ),
    .R1(\ступень_сдвигателя_64х_левого_циклического_2_r1 ));
  \ступень_сдвигателя_64х_левого_циклического  \u_ступень_сдвигателя_64х_левого_циклического_3  (
    .\А0 (\ступень_сдвигателя_64х_левого_циклического_1_r0 ),
    .\А1 (\ступень_сдвигателя_64х_левого_циклического_1_r1 ),
    .R0(\ступень_сдвигателя_64х_левого_циклического_3_r0 ),
    .R1(\ступень_сдвигателя_64х_левого_циклического_3_r1 ));
  Multiplexer #(.select(5), .width(32), .disabled(0), .enable("false")) multiplexer_3 (
    .in0(A0), .in1(\ступень_сдвигателя_64х_левого_циклического_1_r0 ),
    .in2(\ступень_сдвигателя_64х_левого_циклического_3_r0 ),
    .in3(\ступень_сдвигателя_64х_левого_циклического_2_r0 ),
    .in4(\ступень_сдвигателя_64х_левого_циклического_4_r0 ),
    .in5(\ступень_сдвигателя_64х_левого_циклического_5_r0 ),
    .in6(\ступень_сдвигателя_64х_левого_циклического_6_r0 ),
    .in7(\ступень_сдвигателя_64х_левого_циклического_7_r0 ),
    .in8(\ступень_сдвигателя_64х_левого_циклического_8_r0 ),
    .in9(\ступень_сдвигателя_64х_левого_циклического_9_r0 ),
    .in10(\ступень_сдвигателя_64х_левого_циклического_11_r0 ),
    .in11(\ступень_сдвигателя_64х_левого_циклического_10_r0 ),
    .in12(\ступень_сдвигателя_64х_левого_циклического_12_r0 ),
    .in13(\ступень_сдвигателя_64х_левого_циклического_14_r0 ),
    .in14(\ступень_сдвигателя_64х_левого_циклического_13_r0 ),
    .in15(\ступень_сдвигателя_64х_левого_циклического_16_r0 ),
    .in16(\ступень_сдвигателя_64х_левого_циклического_15_r0 ),
    .in17(\ступень_сдвигателя_64х_левого_циклического_17_r0 ),
    .in18(\ступень_сдвигателя_64х_левого_циклического_18_r0 ),
    .in19(\ступень_сдвигателя_64х_левого_циклического_19_r0 ),
    .in20(\ступень_сдвигателя_64х_левого_циклического_20_r0 ),
    .in21(\ступень_сдвигателя_64х_левого_циклического_21_r0 ),
    .in22(\ступень_сдвигателя_64х_левого_циклического_22_r0 ),
    .in23(\ступень_сдвигателя_64х_левого_циклического_23_r0 ),
    .in24(\ступень_сдвигателя_64х_левого_циклического_24_r0 ),
    .in25(\ступень_сдвигателя_64х_левого_циклического_25_r0 ),
    .in26(\ступень_сдвигателя_64х_левого_циклического_26_r0 ),
    .in27(\ступень_сдвигателя_64х_левого_циклического_27_r0 ),
    .in28(\ступень_сдвигателя_64х_левого_циклического_28_r0 ),
    .in29(\ступень_сдвигателя_64х_левого_циклического_29_r0 ),
    .in30(\ступень_сдвигателя_64х_левого_циклического_30_r0 ),
    .in31(\ступень_сдвигателя_64х_левого_циклического_32_r0 ), .out(multiplexer_3_out), .sel(in_3[4:0]));
  \ступень_сдвигателя_64х_левого_циклического  \u_ступень_сдвигателя_64х_левого_циклического_4  (
    .\А0 (\ступень_сдвигателя_64х_левого_циклического_2_r0 ),
    .\А1 (\ступень_сдвигателя_64х_левого_циклического_2_r1 ),
    .R0(\ступень_сдвигателя_64х_левого_циклического_4_r0 ),
    .R1(\ступень_сдвигателя_64х_левого_циклического_4_r1 ));
  Multiplexer #(.select(5), .width(32), .disabled(0), .enable("false")) multiplexer_4 (
    .in0(A1), .in1(\ступень_сдвигателя_64х_левого_циклического_1_r1 ),
    .in2(\ступень_сдвигателя_64х_левого_циклического_3_r1 ),
    .in3(\ступень_сдвигателя_64х_левого_циклического_2_r1 ),
    .in4(\ступень_сдвигателя_64х_левого_циклического_4_r1 ),
    .in5(\ступень_сдвигателя_64х_левого_циклического_5_r1 ),
    .in6(\ступень_сдвигателя_64х_левого_циклического_6_r1 ),
    .in7(\ступень_сдвигателя_64х_левого_циклического_7_r1 ),
    .in8(\ступень_сдвигателя_64х_левого_циклического_8_r1 ),
    .in9(\ступень_сдвигателя_64х_левого_циклического_9_r1 ),
    .in10(\ступень_сдвигателя_64х_левого_циклического_11_r1 ),
    .in11(\ступень_сдвигателя_64х_левого_циклического_10_r1 ),
    .in12(\ступень_сдвигателя_64х_левого_циклического_12_r1 ),
    .in13(\ступень_сдвигателя_64х_левого_циклического_14_r1 ),
    .in14(\ступень_сдвигателя_64х_левого_циклического_13_r1 ),
    .in15(\ступень_сдвигателя_64х_левого_циклического_16_r1 ),
    .in16(\ступень_сдвигателя_64х_левого_циклического_15_r1 ),
    .in17(\ступень_сдвигателя_64х_левого_циклического_17_r1 ),
    .in18(\ступень_сдвигателя_64х_левого_циклического_18_r1 ),
    .in19(\ступень_сдвигателя_64х_левого_циклического_19_r1 ),
    .in20(\ступень_сдвигателя_64х_левого_циклического_20_r1 ),
    .in21(\ступень_сдвигателя_64х_левого_циклического_21_r1 ),
    .in22(\ступень_сдвигателя_64х_левого_циклического_22_r1 ),
    .in23(\ступень_сдвигателя_64х_левого_циклического_23_r1 ),
    .in24(\ступень_сдвигателя_64х_левого_циклического_24_r1 ),
    .in25(\ступень_сдвигателя_64х_левого_циклического_25_r1 ),
    .in26(\ступень_сдвигателя_64х_левого_циклического_26_r1 ),
    .in27(\ступень_сдвигателя_64х_левого_циклического_27_r1 ),
    .in28(\ступень_сдвигателя_64х_левого_циклического_28_r1 ),
    .in29(\ступень_сдвигателя_64х_левого_циклического_29_r1 ),
    .in30(\ступень_сдвигателя_64х_левого_циклического_30_r1 ),
    .in31(\ступень_сдвигателя_64х_левого_циклического_32_r1 ), .out(multiplexer_4_out), .sel(in_3[4:0]));
  \ступень_сдвигателя_64х_левого_циклического  \u_ступень_сдвигателя_64х_левого_циклического_5  (
    .\А0 (\ступень_сдвигателя_64х_левого_циклического_4_r0 ),
    .\А1 (\ступень_сдвигателя_64х_левого_циклического_4_r1 ),
    .R0(\ступень_сдвигателя_64х_левого_циклического_5_r0 ),
    .R1(\ступень_сдвигателя_64х_левого_циклического_5_r1 ));
  \ступень_сдвигателя_64х_левого_циклического  \u_ступень_сдвигателя_64х_левого_циклического_6  (
    .\А0 (\ступень_сдвигателя_64х_левого_циклического_5_r0 ),
    .\А1 (\ступень_сдвигателя_64х_левого_циклического_5_r1 ),
    .R0(\ступень_сдвигателя_64х_левого_циклического_6_r0 ),
    .R1(\ступень_сдвигателя_64х_левого_циклического_6_r1 ));
  \ступень_сдвигателя_64х_левого_циклического  \u_ступень_сдвигателя_64х_левого_циклического_7  (
    .\А0 (\ступень_сдвигателя_64х_левого_циклического_6_r0 ),
    .\А1 (\ступень_сдвигателя_64х_левого_циклического_6_r1 ),
    .R0(\ступень_сдвигателя_64х_левого_циклического_7_r0 ),
    .R1(\ступень_сдвигателя_64х_левого_циклического_7_r1 ));
  \ступень_сдвигателя_64х_левого_циклического  \u_ступень_сдвигателя_64х_левого_циклического_8  (
    .\А0 (\ступень_сдвигателя_64х_левого_циклического_7_r0 ),
    .\А1 (\ступень_сдвигателя_64х_левого_циклического_7_r1 ),
    .R0(\ступень_сдвигателя_64х_левого_циклического_8_r0 ),
    .R1(\ступень_сдвигателя_64х_левого_циклического_8_r1 ));
  \ступень_сдвигателя_64х_левого_циклического  \u_ступень_сдвигателя_64х_левого_циклического_9  (
    .\А0 (\ступень_сдвигателя_64х_левого_циклического_8_r0 ),
    .\А1 (\ступень_сдвигателя_64х_левого_циклического_8_r1 ),
    .R0(\ступень_сдвигателя_64х_левого_циклического_9_r0 ),
    .R1(\ступень_сдвигателя_64х_левого_циклического_9_r1 ));
  \ступень_сдвигателя_64х_левого_циклического  \u_ступень_сдвигателя_64х_левого_циклического_10  (
    .\А0 (\ступень_сдвигателя_64х_левого_циклического_11_r0 ),
    .\А1 (\ступень_сдвигателя_64х_левого_циклического_11_r1 ),
    .R0(\ступень_сдвигателя_64х_левого_циклического_10_r0 ),
    .R1(\ступень_сдвигателя_64х_левого_циклического_10_r1 ));
  \ступень_сдвигателя_64х_левого_циклического  \u_ступень_сдвигателя_64х_левого_циклического_11  (
    .\А0 (\ступень_сдвигателя_64х_левого_циклического_9_r0 ),
    .\А1 (\ступень_сдвигателя_64х_левого_циклического_9_r1 ),
    .R0(\ступень_сдвигателя_64х_левого_циклического_11_r0 ),
    .R1(\ступень_сдвигателя_64х_левого_циклического_11_r1 ));
  \ступень_сдвигателя_64х_левого_циклического  \u_ступень_сдвигателя_64х_левого_циклического_12  (
    .\А0 (\ступень_сдвигателя_64х_левого_циклического_10_r0 ),
    .\А1 (\ступень_сдвигателя_64х_левого_циклического_10_r1 ),
    .R0(\ступень_сдвигателя_64х_левого_циклического_12_r0 ),
    .R1(\ступень_сдвигателя_64х_левого_циклического_12_r1 ));
  \ступень_сдвигателя_64х_левого_циклического  \u_ступень_сдвигателя_64х_левого_циклического_13  (
    .\А0 (\ступень_сдвигателя_64х_левого_циклического_14_r0 ),
    .\А1 (\ступень_сдвигателя_64х_левого_циклического_14_r1 ),
    .R0(\ступень_сдвигателя_64х_левого_циклического_13_r0 ),
    .R1(\ступень_сдвигателя_64х_левого_циклического_13_r1 ));
  \ступень_сдвигателя_64х_левого_циклического  \u_ступень_сдвигателя_64х_левого_циклического_14  (
    .\А0 (\ступень_сдвигателя_64х_левого_циклического_12_r0 ),
    .\А1 (\ступень_сдвигателя_64х_левого_циклического_12_r1 ),
    .R0(\ступень_сдвигателя_64х_левого_циклического_14_r0 ),
    .R1(\ступень_сдвигателя_64х_левого_циклического_14_r1 ));
  \ступень_сдвигателя_64х_левого_циклического  \u_ступень_сдвигателя_64х_левого_циклического_15  (
    .\А0 (\ступень_сдвигателя_64х_левого_циклического_16_r0 ),
    .\А1 (\ступень_сдвигателя_64х_левого_циклического_16_r1 ),
    .R0(\ступень_сдвигателя_64х_левого_циклического_15_r0 ),
    .R1(\ступень_сдвигателя_64х_левого_циклического_15_r1 ));
  \ступень_сдвигателя_64х_левого_циклического  \u_ступень_сдвигателя_64х_левого_циклического_16  (
    .\А0 (\ступень_сдвигателя_64х_левого_циклического_13_r0 ),
    .\А1 (\ступень_сдвигателя_64х_левого_циклического_13_r1 ),
    .R0(\ступень_сдвигателя_64х_левого_циклического_16_r0 ),
    .R1(\ступень_сдвигателя_64х_левого_циклического_16_r1 ));
  \ступень_сдвигателя_64х_левого_циклического  \u_ступень_сдвигателя_64х_левого_циклического_17  (
    .\А0 (\ступень_сдвигателя_64х_левого_циклического_15_r0 ),
    .\А1 (\ступень_сдвигателя_64х_левого_циклического_15_r1 ),
    .R0(\ступень_сдвигателя_64х_левого_циклического_17_r0 ),
    .R1(\ступень_сдвигателя_64х_левого_циклического_17_r1 ));
  \ступень_сдвигателя_64х_левого_циклического  \u_ступень_сдвигателя_64х_левого_циклического_18  (
    .\А0 (\ступень_сдвигателя_64х_левого_циклического_17_r0 ),
    .\А1 (\ступень_сдвигателя_64х_левого_циклического_17_r1 ),
    .R0(\ступень_сдвигателя_64х_левого_циклического_18_r0 ),
    .R1(\ступень_сдвигателя_64х_левого_циклического_18_r1 ));
  \ступень_сдвигателя_64х_левого_циклического  \u_ступень_сдвигателя_64х_левого_циклического_19  (
    .\А0 (\ступень_сдвигателя_64х_левого_циклического_18_r0 ),
    .\А1 (\ступень_сдвигателя_64х_левого_циклического_18_r1 ),
    .R0(\ступень_сдвигателя_64х_левого_циклического_19_r0 ),
    .R1(\ступень_сдвигателя_64х_левого_циклического_19_r1 ));
  \ступень_сдвигателя_64х_левого_циклического  \u_ступень_сдвигателя_64х_левого_циклического_20  (
    .\А0 (\ступень_сдвигателя_64х_левого_циклического_19_r0 ),
    .\А1 (\ступень_сдвигателя_64х_левого_циклического_19_r1 ),
    .R0(\ступень_сдвигателя_64х_левого_циклического_20_r0 ),
    .R1(\ступень_сдвигателя_64х_левого_циклического_20_r1 ));
  \ступень_сдвигателя_64х_левого_циклического  \u_ступень_сдвигателя_64х_левого_циклического_21  (
    .\А0 (\ступень_сдвигателя_64х_левого_циклического_20_r0 ),
    .\А1 (\ступень_сдвигателя_64х_левого_циклического_20_r1 ),
    .R0(\ступень_сдвигателя_64х_левого_циклического_21_r0 ),
    .R1(\ступень_сдвигателя_64х_левого_циклического_21_r1 ));
  \ступень_сдвигателя_64х_левого_циклического  \u_ступень_сдвигателя_64х_левого_циклического_22  (
    .\А0 (\ступень_сдвигателя_64х_левого_циклического_21_r0 ),
    .\А1 (\ступень_сдвигателя_64х_левого_циклического_21_r1 ),
    .R0(\ступень_сдвигателя_64х_левого_циклического_22_r0 ),
    .R1(\ступень_сдвигателя_64х_левого_циклического_22_r1 ));
  \ступень_сдвигателя_64х_левого_циклического  \u_ступень_сдвигателя_64х_левого_циклического_23  (
    .\А0 (\ступень_сдвигателя_64х_левого_циклического_22_r0 ),
    .\А1 (\ступень_сдвигателя_64х_левого_циклического_22_r1 ),
    .R0(\ступень_сдвигателя_64х_левого_циклического_23_r0 ),
    .R1(\ступень_сдвигателя_64х_левого_циклического_23_r1 ));
  \ступень_сдвигателя_64х_левого_циклического  \u_ступень_сдвигателя_64х_левого_циклического_24  (
    .\А0 (\ступень_сдвигателя_64х_левого_циклического_23_r0 ),
    .\А1 (\ступень_сдвигателя_64х_левого_циклического_23_r1 ),
    .R0(\ступень_сдвигателя_64х_левого_циклического_24_r0 ),
    .R1(\ступень_сдвигателя_64х_левого_циклического_24_r1 ));
  \ступень_сдвигателя_64х_левого_циклического  \u_ступень_сдвигателя_64х_левого_циклического_25  (
    .\А0 (\ступень_сдвигателя_64х_левого_циклического_24_r0 ),
    .\А1 (\ступень_сдвигателя_64х_левого_циклического_24_r1 ),
    .R0(\ступень_сдвигателя_64х_левого_циклического_25_r0 ),
    .R1(\ступень_сдвигателя_64х_левого_циклического_25_r1 ));
  \ступень_сдвигателя_64х_левого_циклического  \u_ступень_сдвигателя_64х_левого_циклического_26  (
    .\А0 (\ступень_сдвигателя_64х_левого_циклического_25_r0 ),
    .\А1 (\ступень_сдвигателя_64х_левого_циклического_25_r1 ),
    .R0(\ступень_сдвигателя_64х_левого_циклического_26_r0 ),
    .R1(\ступень_сдвигателя_64х_левого_циклического_26_r1 ));
  \ступень_сдвигателя_64х_левого_циклического  \u_ступень_сдвигателя_64х_левого_циклического_27  (
    .\А0 (\ступень_сдвигателя_64х_левого_циклического_26_r0 ),
    .\А1 (\ступень_сдвигателя_64х_левого_циклического_26_r1 ),
    .R0(\ступень_сдвигателя_64х_левого_циклического_27_r0 ),
    .R1(\ступень_сдвигателя_64х_левого_циклического_27_r1 ));
  \ступень_сдвигателя_64х_левого_циклического  \u_ступень_сдвигателя_64х_левого_циклического_28  (
    .\А0 (\ступень_сдвигателя_64х_левого_циклического_27_r0 ),
    .\А1 (\ступень_сдвигателя_64х_левого_циклического_27_r1 ),
    .R0(\ступень_сдвигателя_64х_левого_циклического_28_r0 ),
    .R1(\ступень_сдвигателя_64х_левого_циклического_28_r1 ));
  \ступень_сдвигателя_64х_левого_циклического  \u_ступень_сдвигателя_64х_левого_циклического_29  (
    .\А0 (\ступень_сдвигателя_64х_левого_циклического_28_r0 ),
    .\А1 (\ступень_сдвигателя_64х_левого_циклического_28_r1 ),
    .R0(\ступень_сдвигателя_64х_левого_циклического_29_r0 ),
    .R1(\ступень_сдвигателя_64х_левого_циклического_29_r1 ));
  \ступень_сдвигателя_64х_левого_циклического  \u_ступень_сдвигателя_64х_левого_циклического_30  (
    .\А0 (\ступень_сдвигателя_64х_левого_циклического_29_r0 ),
    .\А1 (\ступень_сдвигателя_64х_левого_циклического_29_r1 ),
    .R0(\ступень_сдвигателя_64х_левого_циклического_30_r0 ),
    .R1(\ступень_сдвигателя_64х_левого_циклического_30_r1 ));
  \ступень_сдвигателя_64х_левого_циклического  \u_ступень_сдвигателя_64х_левого_циклического_31  (
    .\А0 (\ступень_сдвигателя_64х_левого_циклического_32_r0 ),
    .\А1 (\ступень_сдвигателя_64х_левого_циклического_32_r1 ),
    .R0(\ступень_сдвигателя_64х_левого_циклического_31_r0 ),
    .R1(\ступень_сдвигателя_64х_левого_циклического_31_r1 ));
  \ступень_сдвигателя_64х_левого_циклического  \u_ступень_сдвигателя_64х_левого_циклического_32  (
    .\А0 (\ступень_сдвигателя_64х_левого_циклического_30_r0 ),
    .\А1 (\ступень_сдвигателя_64х_левого_циклического_30_r1 ),
    .R0(\ступень_сдвигателя_64х_левого_циклического_32_r0 ),
    .R1(\ступень_сдвигателя_64х_левого_циклического_32_r1 ));
  \ступень_сдвигателя_64х_левого_циклического  \u_ступень_сдвигателя_64х_левого_циклического_33  (
    .\А0 (\ступень_сдвигателя_64х_левого_циклического_31_r0 ),
    .\А1 (\ступень_сдвигателя_64х_левого_циклического_31_r1 ),
    .R0(\ступень_сдвигателя_64х_левого_циклического_33_r0 ),
    .R1(\ступень_сдвигателя_64х_левого_циклического_33_r1 ));
  \ступень_сдвигателя_64х_левого_циклического  \u_ступень_сдвигателя_64х_левого_циклического_34  (
    .\А0 (\ступень_сдвигателя_64х_левого_циклического_35_r0 ),
    .\А1 (\ступень_сдвигателя_64х_левого_циклического_35_r1 ),
    .R0(\ступень_сдвигателя_64х_левого_циклического_34_r0 ),
    .R1(\ступень_сдвигателя_64х_левого_циклического_34_r1 ));
  \ступень_сдвигателя_64х_левого_циклического  \u_ступень_сдвигателя_64х_левого_циклического_35  (
    .\А0 (\ступень_сдвигателя_64х_левого_циклического_33_r0 ),
    .\А1 (\ступень_сдвигателя_64х_левого_циклического_33_r1 ),
    .R0(\ступень_сдвигателя_64х_левого_циклического_35_r0 ),
    .R1(\ступень_сдвигателя_64х_левого_циклического_35_r1 ));
  Multiplexer #(.select(5), .width(32), .disabled(0), .enable("false")) multiplexer_5 (
    .in0(\ступень_сдвигателя_64х_левого_циклического_31_r0 ),
    .in1(\ступень_сдвигателя_64х_левого_циклического_33_r0 ),
    .in2(\ступень_сдвигателя_64х_левого_циклического_35_r0 ),
    .in3(\ступень_сдвигателя_64х_левого_циклического_34_r0 ),
    .in4(\ступень_сдвигателя_64х_левого_циклического_36_r0 ),
    .in5(\ступень_сдвигателя_64х_левого_циклического_38_r0 ),
    .in6(\ступень_сдвигателя_64х_левого_циклического_37_r0 ),
    .in7(\ступень_сдвигателя_64х_левого_циклического_40_r0 ),
    .in8(\ступень_сдвигателя_64х_левого_циклического_39_r0 ),
    .in9(\ступень_сдвигателя_64х_левого_циклического_41_r0 ),
    .in10(\ступень_сдвигателя_64х_левого_циклического_43_r0 ),
    .in11(\ступень_сдвигателя_64х_левого_циклического_42_r0 ),
    .in12(\ступень_сдвигателя_64х_левого_циклического_44_r0 ),
    .in13(\ступень_сдвигателя_64х_левого_циклического_46_r0 ),
    .in14(\ступень_сдвигателя_64х_левого_циклического_45_r0 ),
    .in15(\ступень_сдвигателя_64х_левого_циклического_48_r0 ),
    .in16(\ступень_сдвигателя_64х_левого_циклического_47_r0 ),
    .in17(\ступень_сдвигателя_64х_левого_циклического_49_r0 ),
    .in18(\ступень_сдвигателя_64х_левого_циклического_51_r0 ),
    .in19(\ступень_сдвигателя_64х_левого_циклического_50_r0 ),
    .in20(\ступень_сдвигателя_64х_левого_циклического_52_r0 ),
    .in21(\ступень_сдвигателя_64х_левого_циклического_54_r0 ),
    .in22(\ступень_сдвигателя_64х_левого_циклического_53_r0 ),
    .in23(\ступень_сдвигателя_64х_левого_циклического_55_r0 ),
    .in24(\ступень_сдвигателя_64х_левого_циклического_56_r0 ),
    .in25(\ступень_сдвигателя_64х_левого_циклического_57_r0 ),
    .in26(\ступень_сдвигателя_64х_левого_циклического_59_r0 ),
    .in27(\ступень_сдвигателя_64х_левого_циклического_58_r0 ),
    .in28(\ступень_сдвигателя_64х_левого_циклического_60_r0 ),
    .in29(\ступень_сдвигателя_64х_левого_циклического_61_r0 ),
    .in30(\ступень_сдвигателя_64х_левого_циклического_62_r0 ),
    .in31(\ступень_сдвигателя_64х_левого_циклического_63_r0 ), .out(multiplexer_5_out), .sel(in_3[4:0]));
  \ступень_сдвигателя_64х_левого_циклического  \u_ступень_сдвигателя_64х_левого_циклического_36  (
    .\А0 (\ступень_сдвигателя_64х_левого_циклического_34_r0 ),
    .\А1 (\ступень_сдвигателя_64х_левого_циклического_34_r1 ),
    .R0(\ступень_сдвигателя_64х_левого_циклического_36_r0 ),
    .R1(\ступень_сдвигателя_64х_левого_циклического_36_r1 ));
  Multiplexer #(.select(5), .width(32), .disabled(0), .enable("false")) multiplexer_6 (
    .in0(\ступень_сдвигателя_64х_левого_циклического_31_r1 ),
    .in1(\ступень_сдвигателя_64х_левого_циклического_33_r1 ),
    .in2(\ступень_сдвигателя_64х_левого_циклического_35_r1 ),
    .in3(\ступень_сдвигателя_64х_левого_циклического_34_r1 ),
    .in4(\ступень_сдвигателя_64х_левого_циклического_36_r1 ),
    .in5(\ступень_сдвигателя_64х_левого_циклического_38_r1 ),
    .in6(\ступень_сдвигателя_64х_левого_циклического_37_r1 ),
    .in7(\ступень_сдвигателя_64х_левого_циклического_40_r1 ),
    .in8(\ступень_сдвигателя_64х_левого_циклического_39_r1 ),
    .in9(\ступень_сдвигателя_64х_левого_циклического_41_r1 ),
    .in10(\ступень_сдвигателя_64х_левого_циклического_43_r1 ),
    .in11(\ступень_сдвигателя_64х_левого_циклического_42_r1 ),
    .in12(\ступень_сдвигателя_64х_левого_циклического_44_r1 ),
    .in13(\ступень_сдвигателя_64х_левого_циклического_46_r1 ),
    .in14(\ступень_сдвигателя_64х_левого_циклического_45_r1 ),
    .in15(\ступень_сдвигателя_64х_левого_циклического_48_r1 ),
    .in16(\ступень_сдвигателя_64х_левого_циклического_47_r1 ),
    .in17(\ступень_сдвигателя_64х_левого_циклического_49_r1 ),
    .in18(\ступень_сдвигателя_64х_левого_циклического_51_r1 ),
    .in19(\ступень_сдвигателя_64х_левого_циклического_50_r1 ),
    .in20(\ступень_сдвигателя_64х_левого_циклического_52_r1 ),
    .in21(\ступень_сдвигателя_64х_левого_циклического_54_r1 ),
    .in22(\ступень_сдвигателя_64х_левого_циклического_53_r1 ),
    .in23(\ступень_сдвигателя_64х_левого_циклического_55_r1 ),
    .in24(\ступень_сдвигателя_64х_левого_циклического_56_r1 ),
    .in25(\ступень_сдвигателя_64х_левого_циклического_57_r1 ),
    .in26(\ступень_сдвигателя_64х_левого_циклического_59_r1 ),
    .in27(\ступень_сдвигателя_64х_левого_циклического_58_r1 ),
    .in28(\ступень_сдвигателя_64х_левого_циклического_60_r1 ),
    .in29(\ступень_сдвигателя_64х_левого_циклического_61_r1 ),
    .in30(\ступень_сдвигателя_64х_левого_циклического_62_r1 ),
    .in31(\ступень_сдвигателя_64х_левого_циклического_63_r1 ), .out(multiplexer_6_out), .sel(in_3[4:0]));
  \ступень_сдвигателя_64х_левого_циклического  \u_ступень_сдвигателя_64х_левого_циклического_37  (
    .\А0 (\ступень_сдвигателя_64х_левого_циклического_38_r0 ),
    .\А1 (\ступень_сдвигателя_64х_левого_циклического_38_r1 ),
    .R0(\ступень_сдвигателя_64х_левого_циклического_37_r0 ),
    .R1(\ступень_сдвигателя_64х_левого_циклического_37_r1 ));
  \ступень_сдвигателя_64х_левого_циклического  \u_ступень_сдвигателя_64х_левого_циклического_38  (
    .\А0 (\ступень_сдвигателя_64х_левого_циклического_36_r0 ),
    .\А1 (\ступень_сдвигателя_64х_левого_циклического_36_r1 ),
    .R0(\ступень_сдвигателя_64х_левого_циклического_38_r0 ),
    .R1(\ступень_сдвигателя_64х_левого_циклического_38_r1 ));
  \ступень_сдвигателя_64х_левого_циклического  \u_ступень_сдвигателя_64х_левого_циклического_39  (
    .\А0 (\ступень_сдвигателя_64х_левого_циклического_40_r0 ),
    .\А1 (\ступень_сдвигателя_64х_левого_циклического_40_r1 ),
    .R0(\ступень_сдвигателя_64х_левого_циклического_39_r0 ),
    .R1(\ступень_сдвигателя_64х_левого_циклического_39_r1 ));
  \ступень_сдвигателя_64х_левого_циклического  \u_ступень_сдвигателя_64х_левого_циклического_40  (
    .\А0 (\ступень_сдвигателя_64х_левого_циклического_37_r0 ),
    .\А1 (\ступень_сдвигателя_64х_левого_циклического_37_r1 ),
    .R0(\ступень_сдвигателя_64х_левого_циклического_40_r0 ),
    .R1(\ступень_сдвигателя_64х_левого_циклического_40_r1 ));
  \ступень_сдвигателя_64х_левого_циклического  \u_ступень_сдвигателя_64х_левого_циклического_41  (
    .\А0 (\ступень_сдвигателя_64х_левого_циклического_39_r0 ),
    .\А1 (\ступень_сдвигателя_64х_левого_циклического_39_r1 ),
    .R0(\ступень_сдвигателя_64х_левого_циклического_41_r0 ),
    .R1(\ступень_сдвигателя_64х_левого_циклического_41_r1 ));
  \ступень_сдвигателя_64х_левого_циклического  \u_ступень_сдвигателя_64х_левого_циклического_42  (
    .\А0 (\ступень_сдвигателя_64х_левого_циклического_43_r0 ),
    .\А1 (\ступень_сдвигателя_64х_левого_циклического_43_r1 ),
    .R0(\ступень_сдвигателя_64х_левого_циклического_42_r0 ),
    .R1(\ступень_сдвигателя_64х_левого_циклического_42_r1 ));
  \ступень_сдвигателя_64х_левого_циклического  \u_ступень_сдвигателя_64х_левого_циклического_43  (
    .\А0 (\ступень_сдвигателя_64х_левого_циклического_41_r0 ),
    .\А1 (\ступень_сдвигателя_64х_левого_циклического_41_r1 ),
    .R0(\ступень_сдвигателя_64х_левого_циклического_43_r0 ),
    .R1(\ступень_сдвигателя_64х_левого_циклического_43_r1 ));
  \ступень_сдвигателя_64х_левого_циклического  \u_ступень_сдвигателя_64х_левого_циклического_44  (
    .\А0 (\ступень_сдвигателя_64х_левого_циклического_42_r0 ),
    .\А1 (\ступень_сдвигателя_64х_левого_циклического_42_r1 ),
    .R0(\ступень_сдвигателя_64х_левого_циклического_44_r0 ),
    .R1(\ступень_сдвигателя_64х_левого_циклического_44_r1 ));
  \ступень_сдвигателя_64х_левого_циклического  \u_ступень_сдвигателя_64х_левого_циклического_45  (
    .\А0 (\ступень_сдвигателя_64х_левого_циклического_46_r0 ),
    .\А1 (\ступень_сдвигателя_64х_левого_циклического_46_r1 ),
    .R0(\ступень_сдвигателя_64х_левого_циклического_45_r0 ),
    .R1(\ступень_сдвигателя_64х_левого_циклического_45_r1 ));
  \ступень_сдвигателя_64х_левого_циклического  \u_ступень_сдвигателя_64х_левого_циклического_46  (
    .\А0 (\ступень_сдвигателя_64х_левого_циклического_44_r0 ),
    .\А1 (\ступень_сдвигателя_64х_левого_циклического_44_r1 ),
    .R0(\ступень_сдвигателя_64х_левого_циклического_46_r0 ),
    .R1(\ступень_сдвигателя_64х_левого_циклического_46_r1 ));
  \ступень_сдвигателя_64х_левого_циклического  \u_ступень_сдвигателя_64х_левого_циклического_47  (
    .\А0 (\ступень_сдвигателя_64х_левого_циклического_48_r0 ),
    .\А1 (\ступень_сдвигателя_64х_левого_циклического_48_r1 ),
    .R0(\ступень_сдвигателя_64х_левого_циклического_47_r0 ),
    .R1(\ступень_сдвигателя_64х_левого_циклического_47_r1 ));
  \ступень_сдвигателя_64х_левого_циклического  \u_ступень_сдвигателя_64х_левого_циклического_48  (
    .\А0 (\ступень_сдвигателя_64х_левого_циклического_45_r0 ),
    .\А1 (\ступень_сдвигателя_64х_левого_циклического_45_r1 ),
    .R0(\ступень_сдвигателя_64х_левого_циклического_48_r0 ),
    .R1(\ступень_сдвигателя_64х_левого_циклического_48_r1 ));
  \ступень_сдвигателя_64х_левого_циклического  \u_ступень_сдвигателя_64х_левого_циклического_49  (
    .\А0 (\ступень_сдвигателя_64х_левого_циклического_47_r0 ),
    .\А1 (\ступень_сдвигателя_64х_левого_циклического_47_r1 ),
    .R0(\ступень_сдвигателя_64х_левого_циклического_49_r0 ),
    .R1(\ступень_сдвигателя_64х_левого_циклического_49_r1 ));
  \ступень_сдвигателя_64х_левого_циклического  \u_ступень_сдвигателя_64х_левого_циклического_50  (
    .\А0 (\ступень_сдвигателя_64х_левого_циклического_51_r0 ),
    .\А1 (\ступень_сдвигателя_64х_левого_циклического_51_r1 ),
    .R0(\ступень_сдвигателя_64х_левого_циклического_50_r0 ),
    .R1(\ступень_сдвигателя_64х_левого_циклического_50_r1 ));
  \ступень_сдвигателя_64х_левого_циклического  \u_ступень_сдвигателя_64х_левого_циклического_51  (
    .\А0 (\ступень_сдвигателя_64х_левого_циклического_49_r0 ),
    .\А1 (\ступень_сдвигателя_64х_левого_циклического_49_r1 ),
    .R0(\ступень_сдвигателя_64х_левого_циклического_51_r0 ),
    .R1(\ступень_сдвигателя_64х_левого_циклического_51_r1 ));
  \ступень_сдвигателя_64х_левого_циклического  \u_ступень_сдвигателя_64х_левого_циклического_52  (
    .\А0 (\ступень_сдвигателя_64х_левого_циклического_50_r0 ),
    .\А1 (\ступень_сдвигателя_64х_левого_циклического_50_r1 ),
    .R0(\ступень_сдвигателя_64х_левого_циклического_52_r0 ),
    .R1(\ступень_сдвигателя_64х_левого_циклического_52_r1 ));
  \ступень_сдвигателя_64х_левого_циклического  \u_ступень_сдвигателя_64х_левого_циклического_53  (
    .\А0 (\ступень_сдвигателя_64х_левого_циклического_54_r0 ),
    .\А1 (\ступень_сдвигателя_64х_левого_циклического_54_r1 ),
    .R0(\ступень_сдвигателя_64х_левого_циклического_53_r0 ),
    .R1(\ступень_сдвигателя_64х_левого_циклического_53_r1 ));
  \ступень_сдвигателя_64х_левого_циклического  \u_ступень_сдвигателя_64х_левого_циклического_54  (
    .\А0 (\ступень_сдвигателя_64х_левого_циклического_52_r0 ),
    .\А1 (\ступень_сдвигателя_64х_левого_циклического_52_r1 ),
    .R0(\ступень_сдвигателя_64х_левого_циклического_54_r0 ),
    .R1(\ступень_сдвигателя_64х_левого_циклического_54_r1 ));
  \ступень_сдвигателя_64х_левого_циклического  \u_ступень_сдвигателя_64х_левого_циклического_55  (
    .\А0 (\ступень_сдвигателя_64х_левого_циклического_53_r0 ),
    .\А1 (\ступень_сдвигателя_64х_левого_циклического_53_r1 ),
    .R0(\ступень_сдвигателя_64х_левого_циклического_55_r0 ),
    .R1(\ступень_сдвигателя_64х_левого_циклического_55_r1 ));
  \ступень_сдвигателя_64х_левого_циклического  \u_ступень_сдвигателя_64х_левого_циклического_56  (
    .\А0 (\ступень_сдвигателя_64х_левого_циклического_55_r0 ),
    .\А1 (\ступень_сдвигателя_64х_левого_циклического_55_r1 ),
    .R0(\ступень_сдвигателя_64х_левого_циклического_56_r0 ),
    .R1(\ступень_сдвигателя_64х_левого_циклического_56_r1 ));
  \ступень_сдвигателя_64х_левого_циклического  \u_ступень_сдвигателя_64х_левого_циклического_57  (
    .\А0 (\ступень_сдвигателя_64х_левого_циклического_56_r0 ),
    .\А1 (\ступень_сдвигателя_64х_левого_циклического_56_r1 ),
    .R0(\ступень_сдвигателя_64х_левого_циклического_57_r0 ),
    .R1(\ступень_сдвигателя_64х_левого_циклического_57_r1 ));
  \ступень_сдвигателя_64х_левого_циклического  \u_ступень_сдвигателя_64х_левого_циклического_58  (
    .\А0 (\ступень_сдвигателя_64х_левого_циклического_59_r0 ),
    .\А1 (\ступень_сдвигателя_64х_левого_циклического_59_r1 ),
    .R0(\ступень_сдвигателя_64х_левого_циклического_58_r0 ),
    .R1(\ступень_сдвигателя_64х_левого_циклического_58_r1 ));
  \ступень_сдвигателя_64х_левого_циклического  \u_ступень_сдвигателя_64х_левого_циклического_59  (
    .\А0 (\ступень_сдвигателя_64х_левого_циклического_57_r0 ),
    .\А1 (\ступень_сдвигателя_64х_левого_циклического_57_r1 ),
    .R0(\ступень_сдвигателя_64х_левого_циклического_59_r0 ),
    .R1(\ступень_сдвигателя_64х_левого_циклического_59_r1 ));
  \ступень_сдвигателя_64х_левого_циклического  \u_ступень_сдвигателя_64х_левого_циклического_60  (
    .\А0 (\ступень_сдвигателя_64х_левого_циклического_58_r0 ),
    .\А1 (\ступень_сдвигателя_64х_левого_циклического_58_r1 ),
    .R0(\ступень_сдвигателя_64х_левого_циклического_60_r0 ),
    .R1(\ступень_сдвигателя_64х_левого_циклического_60_r1 ));
  \ступень_сдвигателя_64х_левого_циклического  \u_ступень_сдвигателя_64х_левого_циклического_61  (
    .\А0 (\ступень_сдвигателя_64х_левого_циклического_60_r0 ),
    .\А1 (\ступень_сдвигателя_64х_левого_циклического_60_r1 ),
    .R0(\ступень_сдвигателя_64х_левого_циклического_61_r0 ),
    .R1(\ступень_сдвигателя_64х_левого_циклического_61_r1 ));
  \ступень_сдвигателя_64х_левого_циклического  \u_ступень_сдвигателя_64х_левого_циклического_62  (
    .\А0 (\ступень_сдвигателя_64х_левого_циклического_61_r0 ),
    .\А1 (\ступень_сдвигателя_64х_левого_циклического_61_r1 ),
    .R0(\ступень_сдвигателя_64х_левого_циклического_62_r0 ),
    .R1(\ступень_сдвигателя_64х_левого_циклического_62_r1 ));
  \ступень_сдвигателя_64х_левого_циклического  \u_ступень_сдвигателя_64х_левого_циклического_63  (
    .\А0 (\ступень_сдвигателя_64х_левого_циклического_62_r0 ),
    .\А1 (\ступень_сдвигателя_64х_левого_циклического_62_r1 ),
    .R0(\ступень_сдвигателя_64х_левого_циклического_63_r0 ),
    .R1(\ступень_сдвигателя_64х_левого_циклического_63_r1 ));
endmodule
module \сдвигатель_64х_правый_циклический  (
  input  [31:0] A0,
  input  [31:0] A1,
  input  [5:0] in_3,
  output [31:0] R0,
  output [31:0] R1
);

  wire [31:0] multiplexer_3_out, multiplexer_4_out, multiplexer_5_out, multiplexer_6_out,
       \ступень_сдвигателя_64х_правого_циклического_1_r0 ,
       \ступень_сдвигателя_64х_правого_циклического_1_r1 ,
       \ступень_сдвигателя_64х_правого_циклического_2_r0 ,
       \ступень_сдвигателя_64х_правого_циклического_2_r1 ,
       \ступень_сдвигателя_64х_правого_циклического_3_r0 ,
       \ступень_сдвигателя_64х_правого_циклического_3_r1 ,
       \ступень_сдвигателя_64х_правого_циклического_4_r0 ,
       \ступень_сдвигателя_64х_правого_циклического_4_r1 ,
       \ступень_сдвигателя_64х_правого_циклического_5_r0 ,
       \ступень_сдвигателя_64х_правого_циклического_5_r1 ,
       \ступень_сдвигателя_64х_правого_циклического_6_r0 ,
       \ступень_сдвигателя_64х_правого_циклического_6_r1 ,
       \ступень_сдвигателя_64х_правого_циклического_7_r0 ,
       \ступень_сдвигателя_64х_правого_циклического_7_r1 ,
       \ступень_сдвигателя_64х_правого_циклического_8_r0 ,
       \ступень_сдвигателя_64х_правого_циклического_8_r1 ,
       \ступень_сдвигателя_64х_правого_циклического_9_r0 ,
       \ступень_сдвигателя_64х_правого_циклического_9_r1 ,
       \ступень_сдвигателя_64х_правого_циклического_10_r0 ,
       \ступень_сдвигателя_64х_правого_циклического_10_r1 ,
       \ступень_сдвигателя_64х_правого_циклического_11_r0 ,
       \ступень_сдвигателя_64х_правого_циклического_11_r1 ,
       \ступень_сдвигателя_64х_правого_циклического_12_r0 ,
       \ступень_сдвигателя_64х_правого_циклического_12_r1 ,
       \ступень_сдвигателя_64х_правого_циклического_13_r0 ,
       \ступень_сдвигателя_64х_правого_циклического_13_r1 ,
       \ступень_сдвигателя_64х_правого_циклического_14_r0 ,
       \ступень_сдвигателя_64х_правого_циклического_14_r1 ,
       \ступень_сдвигателя_64х_правого_циклического_15_r0 ,
       \ступень_сдвигателя_64х_правого_циклического_15_r1 ,
       \ступень_сдвигателя_64х_правого_циклического_16_r0 ,
       \ступень_сдвигателя_64х_правого_циклического_16_r1 ,
       \ступень_сдвигателя_64х_правого_циклического_17_r0 ,
       \ступень_сдвигателя_64х_правого_циклического_17_r1 ,
       \ступень_сдвигателя_64х_правого_циклического_18_r0 ,
       \ступень_сдвигателя_64х_правого_циклического_18_r1 ,
       \ступень_сдвигателя_64х_правого_циклического_19_r0 ,
       \ступень_сдвигателя_64х_правого_циклического_19_r1 ,
       \ступень_сдвигателя_64х_правого_циклического_20_r0 ,
       \ступень_сдвигателя_64х_правого_циклического_20_r1 ,
       \ступень_сдвигателя_64х_правого_циклического_21_r0 ,
       \ступень_сдвигателя_64х_правого_циклического_21_r1 ,
       \ступень_сдвигателя_64х_правого_циклического_22_r0 ,
       \ступень_сдвигателя_64х_правого_циклического_22_r1 ,
       \ступень_сдвигателя_64х_правого_циклического_23_r0 ,
       \ступень_сдвигателя_64х_правого_циклического_23_r1 ,
       \ступень_сдвигателя_64х_правого_циклического_24_r0 ,
       \ступень_сдвигателя_64х_правого_циклического_24_r1 ,
       \ступень_сдвигателя_64х_правого_циклического_25_r0 ,
       \ступень_сдвигателя_64х_правого_циклического_25_r1 ,
       \ступень_сдвигателя_64х_правого_циклического_26_r0 ,
       \ступень_сдвигателя_64х_правого_циклического_26_r1 ,
       \ступень_сдвигателя_64х_правого_циклического_27_r0 ,
       \ступень_сдвигателя_64х_правого_циклического_27_r1 ,
       \ступень_сдвигателя_64х_правого_циклического_28_r0 ,
       \ступень_сдвигателя_64х_правого_циклического_28_r1 ,
       \ступень_сдвигателя_64х_правого_циклического_29_r0 ,
       \ступень_сдвигателя_64х_правого_циклического_29_r1 ,
       \ступень_сдвигателя_64х_правого_циклического_30_r0 ,
       \ступень_сдвигателя_64х_правого_циклического_30_r1 ,
       \ступень_сдвигателя_64х_правого_циклического_31_r0 ,
       \ступень_сдвигателя_64х_правого_циклического_31_r1 ,
       \ступень_сдвигателя_64х_правого_циклического_32_r0 ,
       \ступень_сдвигателя_64х_правого_циклического_32_r1 ,
       \ступень_сдвигателя_64х_правого_циклического_33_r0 ,
       \ступень_сдвигателя_64х_правого_циклического_33_r1 ,
       \ступень_сдвигателя_64х_правого_циклического_34_r0 ,
       \ступень_сдвигателя_64х_правого_циклического_34_r1 ,
       \ступень_сдвигателя_64х_правого_циклического_35_r0 ,
       \ступень_сдвигателя_64х_правого_циклического_35_r1 ,
       \ступень_сдвигателя_64х_правого_циклического_36_r0 ,
       \ступень_сдвигателя_64х_правого_циклического_36_r1 ,
       \ступень_сдвигателя_64х_правого_циклического_37_r0 ,
       \ступень_сдвигателя_64х_правого_циклического_37_r1 ,
       \ступень_сдвигателя_64х_правого_циклического_38_r0 ,
       \ступень_сдвигателя_64х_правого_циклического_38_r1 ,
       \ступень_сдвигателя_64х_правого_циклического_39_r0 ,
       \ступень_сдвигателя_64х_правого_циклического_39_r1 ,
       \ступень_сдвигателя_64х_правого_циклического_40_r0 ,
       \ступень_сдвигателя_64х_правого_циклического_40_r1 ,
       \ступень_сдвигателя_64х_правого_циклического_41_r0 ,
       \ступень_сдвигателя_64х_правого_циклического_41_r1 ,
       \ступень_сдвигателя_64х_правого_циклического_42_r0 ,
       \ступень_сдвигателя_64х_правого_циклического_42_r1 ,
       \ступень_сдвигателя_64х_правого_циклического_43_r0 ,
       \ступень_сдвигателя_64х_правого_циклического_43_r1 ,
       \ступень_сдвигателя_64х_правого_циклического_44_r0 ,
       \ступень_сдвигателя_64х_правого_циклического_44_r1 ,
       \ступень_сдвигателя_64х_правого_циклического_45_r0 ,
       \ступень_сдвигателя_64х_правого_циклического_45_r1 ,
       \ступень_сдвигателя_64х_правого_циклического_46_r0 ,
       \ступень_сдвигателя_64х_правого_циклического_46_r1 ,
       \ступень_сдвигателя_64х_правого_циклического_47_r0 ,
       \ступень_сдвигателя_64х_правого_циклического_47_r1 ,
       \ступень_сдвигателя_64х_правого_циклического_48_r0 ,
       \ступень_сдвигателя_64х_правого_циклического_48_r1 ,
       \ступень_сдвигателя_64х_правого_циклического_49_r0 ,
       \ступень_сдвигателя_64х_правого_циклического_49_r1 ,
       \ступень_сдвигателя_64х_правого_циклического_50_r0 ,
       \ступень_сдвигателя_64х_правого_циклического_50_r1 ,
       \ступень_сдвигателя_64х_правого_циклического_51_r0 ,
       \ступень_сдвигателя_64х_правого_циклического_51_r1 ,
       \ступень_сдвигателя_64х_правого_циклического_52_r0 ,
       \ступень_сдвигателя_64х_правого_циклического_52_r1 ,
       \ступень_сдвигателя_64х_правого_циклического_53_r0 ,
       \ступень_сдвигателя_64х_правого_циклического_53_r1 ,
       \ступень_сдвигателя_64х_правого_циклического_54_r0 ,
       \ступень_сдвигателя_64х_правого_циклического_54_r1 ,
       \ступень_сдвигателя_64х_правого_циклического_55_r0 ,
       \ступень_сдвигателя_64х_правого_циклического_55_r1 ,
       \ступень_сдвигателя_64х_правого_циклического_56_r0 ,
       \ступень_сдвигателя_64х_правого_циклического_56_r1 ,
       \ступень_сдвигателя_64х_правого_циклического_57_r0 ,
       \ступень_сдвигателя_64х_правого_циклического_57_r1 ,
       \ступень_сдвигателя_64х_правого_циклического_58_r0 ,
       \ступень_сдвигателя_64х_правого_циклического_58_r1 ,
       \ступень_сдвигателя_64х_правого_циклического_59_r0 ,
       \ступень_сдвигателя_64х_правого_циклического_59_r1 ,
       \ступень_сдвигателя_64х_правого_циклического_60_r0 ,
       \ступень_сдвигателя_64х_правого_циклического_60_r1 ,
       \ступень_сдвигателя_64х_правого_циклического_61_r0 ,
       \ступень_сдвигателя_64х_правого_циклического_61_r1 ,
       \ступень_сдвигателя_64х_правого_циклического_62_r0 ,
       \ступень_сдвигателя_64х_правого_циклического_62_r1 ,
       \ступень_сдвигателя_64х_правого_циклического_63_r0 ,
       \ступень_сдвигателя_64х_правого_циклического_63_r1 ;

  Multiplexer #(.width(32), .disabled(0), .enable("false")) multiplexer_1 (
    .in0(multiplexer_3_out), .in1(multiplexer_5_out), .out(R0), .sel(in_3[5]));
  Multiplexer #(.width(32), .disabled(0), .enable("false")) multiplexer_2 (
    .in0(multiplexer_4_out), .in1(multiplexer_6_out), .out(R1), .sel(in_3[5]));
  \ступень_сдвигателя_64х_правого_циклического  \u_ступень_сдвигателя_64х_правого_циклического_1  (
    .\А0 (A0), .\А1 (A1), .R0(\ступень_сдвигателя_64х_правого_циклического_1_r0 ),
    .R1(\ступень_сдвигателя_64х_правого_циклического_1_r1 ));
  \ступень_сдвигателя_64х_правого_циклического  \u_ступень_сдвигателя_64х_правого_циклического_2  (
    .\А0 (\ступень_сдвигателя_64х_правого_циклического_3_r0 ),
    .\А1 (\ступень_сдвигателя_64х_правого_циклического_3_r1 ),
    .R0(\ступень_сдвигателя_64х_правого_циклического_2_r0 ),
    .R1(\ступень_сдвигателя_64х_правого_циклического_2_r1 ));
  \ступень_сдвигателя_64х_правого_циклического  \u_ступень_сдвигателя_64х_правого_циклического_3  (
    .\А0 (\ступень_сдвигателя_64х_правого_циклического_1_r0 ),
    .\А1 (\ступень_сдвигателя_64х_правого_циклического_1_r1 ),
    .R0(\ступень_сдвигателя_64х_правого_циклического_3_r0 ),
    .R1(\ступень_сдвигателя_64х_правого_циклического_3_r1 ));
  Multiplexer #(.select(5), .width(32), .disabled(0), .enable("false")) multiplexer_3 (
    .in0(A0), .in1(\ступень_сдвигателя_64х_правого_циклического_1_r0 ),
    .in2(\ступень_сдвигателя_64х_правого_циклического_3_r0 ),
    .in3(\ступень_сдвигателя_64х_правого_циклического_2_r0 ),
    .in4(\ступень_сдвигателя_64х_правого_циклического_4_r0 ),
    .in5(\ступень_сдвигателя_64х_правого_циклического_5_r0 ),
    .in6(\ступень_сдвигателя_64х_правого_циклического_6_r0 ),
    .in7(\ступень_сдвигателя_64х_правого_циклического_8_r0 ),
    .in8(\ступень_сдвигателя_64х_правого_циклического_7_r0 ),
    .in9(\ступень_сдвигателя_64х_правого_циклического_9_r0 ),
    .in10(\ступень_сдвигателя_64х_правого_циклического_10_r0 ),
    .in11(\ступень_сдвигателя_64х_правого_циклического_11_r0 ),
    .in12(\ступень_сдвигателя_64х_правого_циклического_12_r0 ),
    .in13(\ступень_сдвигателя_64х_правого_циклического_14_r0 ),
    .in14(\ступень_сдвигателя_64х_правого_циклического_13_r0 ),
    .in15(\ступень_сдвигателя_64х_правого_циклического_16_r0 ),
    .in16(\ступень_сдвигателя_64х_правого_циклического_15_r0 ),
    .in17(\ступень_сдвигателя_64х_правого_циклического_17_r0 ),
    .in18(\ступень_сдвигателя_64х_правого_циклического_18_r0 ),
    .in19(\ступень_сдвигателя_64х_правого_циклического_19_r0 ),
    .in20(\ступень_сдвигателя_64х_правого_циклического_20_r0 ),
    .in21(\ступень_сдвигателя_64х_правого_циклического_22_r0 ),
    .in22(\ступень_сдвигателя_64х_правого_циклического_21_r0 ),
    .in23(\ступень_сдвигателя_64х_правого_циклического_23_r0 ),
    .in24(\ступень_сдвигателя_64х_правого_циклического_24_r0 ),
    .in25(\ступень_сдвигателя_64х_правого_циклического_25_r0 ),
    .in26(\ступень_сдвигателя_64х_правого_циклического_26_r0 ),
    .in27(\ступень_сдвигателя_64х_правого_циклического_27_r0 ),
    .in28(\ступень_сдвигателя_64х_правого_циклического_28_r0 ),
    .in29(\ступень_сдвигателя_64х_правого_циклического_29_r0 ),
    .in30(\ступень_сдвигателя_64х_правого_циклического_30_r0 ),
    .in31(\ступень_сдвигателя_64х_правого_циклического_32_r0 ), .out(multiplexer_3_out), .sel(in_3[4:0]));
  \ступень_сдвигателя_64х_правого_циклического  \u_ступень_сдвигателя_64х_правого_циклического_4  (
    .\А0 (\ступень_сдвигателя_64х_правого_циклического_2_r0 ),
    .\А1 (\ступень_сдвигателя_64х_правого_циклического_2_r1 ),
    .R0(\ступень_сдвигателя_64х_правого_циклического_4_r0 ),
    .R1(\ступень_сдвигателя_64х_правого_циклического_4_r1 ));
  Multiplexer #(.select(5), .width(32), .disabled(0), .enable("false")) multiplexer_4 (
    .in0(A1), .in1(\ступень_сдвигателя_64х_правого_циклического_1_r1 ),
    .in2(\ступень_сдвигателя_64х_правого_циклического_3_r1 ),
    .in3(\ступень_сдвигателя_64х_правого_циклического_2_r1 ),
    .in4(\ступень_сдвигателя_64х_правого_циклического_4_r1 ),
    .in5(\ступень_сдвигателя_64х_правого_циклического_5_r1 ),
    .in6(\ступень_сдвигателя_64х_правого_циклического_6_r1 ),
    .in7(\ступень_сдвигателя_64х_правого_циклического_8_r1 ),
    .in8(\ступень_сдвигателя_64х_правого_циклического_7_r1 ),
    .in9(\ступень_сдвигателя_64х_правого_циклического_9_r1 ),
    .in10(\ступень_сдвигателя_64х_правого_циклического_10_r1 ),
    .in11(\ступень_сдвигателя_64х_правого_циклического_11_r1 ),
    .in12(\ступень_сдвигателя_64х_правого_циклического_12_r1 ),
    .in13(\ступень_сдвигателя_64х_правого_циклического_14_r1 ),
    .in14(\ступень_сдвигателя_64х_правого_циклического_13_r1 ),
    .in15(\ступень_сдвигателя_64х_правого_циклического_16_r1 ),
    .in16(\ступень_сдвигателя_64х_правого_циклического_15_r1 ),
    .in17(\ступень_сдвигателя_64х_правого_циклического_17_r1 ),
    .in18(\ступень_сдвигателя_64х_правого_циклического_18_r1 ),
    .in19(\ступень_сдвигателя_64х_правого_циклического_19_r1 ),
    .in20(\ступень_сдвигателя_64х_правого_циклического_20_r1 ),
    .in21(\ступень_сдвигателя_64х_правого_циклического_22_r1 ),
    .in22(\ступень_сдвигателя_64х_правого_циклического_21_r1 ),
    .in23(\ступень_сдвигателя_64х_правого_циклического_23_r1 ),
    .in24(\ступень_сдвигателя_64х_правого_циклического_24_r1 ),
    .in25(\ступень_сдвигателя_64х_правого_циклического_25_r1 ),
    .in26(\ступень_сдвигателя_64х_правого_циклического_26_r1 ),
    .in27(\ступень_сдвигателя_64х_правого_циклического_27_r1 ),
    .in28(\ступень_сдвигателя_64х_правого_циклического_28_r1 ),
    .in29(\ступень_сдвигателя_64х_правого_циклического_29_r1 ),
    .in30(\ступень_сдвигателя_64х_правого_циклического_30_r1 ),
    .in31(\ступень_сдвигателя_64х_правого_циклического_32_r1 ), .out(multiplexer_4_out), .sel(in_3[4:0]));
  \ступень_сдвигателя_64х_правого_циклического  \u_ступень_сдвигателя_64х_правого_циклического_5  (
    .\А0 (\ступень_сдвигателя_64х_правого_циклического_4_r0 ),
    .\А1 (\ступень_сдвигателя_64х_правого_циклического_4_r1 ),
    .R0(\ступень_сдвигателя_64х_правого_циклического_5_r0 ),
    .R1(\ступень_сдвигателя_64х_правого_циклического_5_r1 ));
  \ступень_сдвигателя_64х_правого_циклического  \u_ступень_сдвигателя_64х_правого_циклического_6  (
    .\А0 (\ступень_сдвигателя_64х_правого_циклического_5_r0 ),
    .\А1 (\ступень_сдвигателя_64х_правого_циклического_5_r1 ),
    .R0(\ступень_сдвигателя_64х_правого_циклического_6_r0 ),
    .R1(\ступень_сдвигателя_64х_правого_циклического_6_r1 ));
  \ступень_сдвигателя_64х_правого_циклического  \u_ступень_сдвигателя_64х_правого_циклического_7  (
    .\А0 (\ступень_сдвигателя_64х_правого_циклического_8_r0 ),
    .\А1 (\ступень_сдвигателя_64х_правого_циклического_8_r1 ),
    .R0(\ступень_сдвигателя_64х_правого_циклического_7_r0 ),
    .R1(\ступень_сдвигателя_64х_правого_циклического_7_r1 ));
  \ступень_сдвигателя_64х_правого_циклического  \u_ступень_сдвигателя_64х_правого_циклического_8  (
    .\А0 (\ступень_сдвигателя_64х_правого_циклического_6_r0 ),
    .\А1 (\ступень_сдвигателя_64х_правого_циклического_6_r1 ),
    .R0(\ступень_сдвигателя_64х_правого_циклического_8_r0 ),
    .R1(\ступень_сдвигателя_64х_правого_циклического_8_r1 ));
  \ступень_сдвигателя_64х_правого_циклического  \u_ступень_сдвигателя_64х_правого_циклического_9  (
    .\А0 (\ступень_сдвигателя_64х_правого_циклического_7_r0 ),
    .\А1 (\ступень_сдвигателя_64х_правого_циклического_7_r1 ),
    .R0(\ступень_сдвигателя_64х_правого_циклического_9_r0 ),
    .R1(\ступень_сдвигателя_64х_правого_циклического_9_r1 ));
  \ступень_сдвигателя_64х_правого_циклического  \u_ступень_сдвигателя_64х_правого_циклического_10  (
    .\А0 (\ступень_сдвигателя_64х_правого_циклического_9_r0 ),
    .\А1 (\ступень_сдвигателя_64х_правого_циклического_9_r1 ),
    .R0(\ступень_сдвигателя_64х_правого_циклического_10_r0 ),
    .R1(\ступень_сдвигателя_64х_правого_циклического_10_r1 ));
  \ступень_сдвигателя_64х_правого_циклического  \u_ступень_сдвигателя_64х_правого_циклического_11  (
    .\А0 (\ступень_сдвигателя_64х_правого_циклического_10_r0 ),
    .\А1 (\ступень_сдвигателя_64х_правого_циклического_10_r1 ),
    .R0(\ступень_сдвигателя_64х_правого_циклического_11_r0 ),
    .R1(\ступень_сдвигателя_64х_правого_циклического_11_r1 ));
  \ступень_сдвигателя_64х_правого_циклического  \u_ступень_сдвигателя_64х_правого_циклического_12  (
    .\А0 (\ступень_сдвигателя_64х_правого_циклического_11_r0 ),
    .\А1 (\ступень_сдвигателя_64х_правого_циклического_11_r1 ),
    .R0(\ступень_сдвигателя_64х_правого_циклического_12_r0 ),
    .R1(\ступень_сдвигателя_64х_правого_циклического_12_r1 ));
  \ступень_сдвигателя_64х_правого_циклического  \u_ступень_сдвигателя_64х_правого_циклического_13  (
    .\А0 (\ступень_сдвигателя_64х_правого_циклического_14_r0 ),
    .\А1 (\ступень_сдвигателя_64х_правого_циклического_14_r1 ),
    .R0(\ступень_сдвигателя_64х_правого_циклического_13_r0 ),
    .R1(\ступень_сдвигателя_64х_правого_циклического_13_r1 ));
  \ступень_сдвигателя_64х_правого_циклического  \u_ступень_сдвигателя_64х_правого_циклического_14  (
    .\А0 (\ступень_сдвигателя_64х_правого_циклического_12_r0 ),
    .\А1 (\ступень_сдвигателя_64х_правого_циклического_12_r1 ),
    .R0(\ступень_сдвигателя_64х_правого_циклического_14_r0 ),
    .R1(\ступень_сдвигателя_64х_правого_циклического_14_r1 ));
  \ступень_сдвигателя_64х_правого_циклического  \u_ступень_сдвигателя_64х_правого_циклического_15  (
    .\А0 (\ступень_сдвигателя_64х_правого_циклического_16_r0 ),
    .\А1 (\ступень_сдвигателя_64х_правого_циклического_16_r1 ),
    .R0(\ступень_сдвигателя_64х_правого_циклического_15_r0 ),
    .R1(\ступень_сдвигателя_64х_правого_циклического_15_r1 ));
  \ступень_сдвигателя_64х_правого_циклического  \u_ступень_сдвигателя_64х_правого_циклического_16  (
    .\А0 (\ступень_сдвигателя_64х_правого_циклического_13_r0 ),
    .\А1 (\ступень_сдвигателя_64х_правого_циклического_13_r1 ),
    .R0(\ступень_сдвигателя_64х_правого_циклического_16_r0 ),
    .R1(\ступень_сдвигателя_64х_правого_циклического_16_r1 ));
  \ступень_сдвигателя_64х_правого_циклического  \u_ступень_сдвигателя_64х_правого_циклического_17  (
    .\А0 (\ступень_сдвигателя_64х_правого_циклического_15_r0 ),
    .\А1 (\ступень_сдвигателя_64х_правого_циклического_15_r1 ),
    .R0(\ступень_сдвигателя_64х_правого_циклического_17_r0 ),
    .R1(\ступень_сдвигателя_64х_правого_циклического_17_r1 ));
  \ступень_сдвигателя_64х_правого_циклического  \u_ступень_сдвигателя_64х_правого_циклического_18  (
    .\А0 (\ступень_сдвигателя_64х_правого_циклического_17_r0 ),
    .\А1 (\ступень_сдвигателя_64х_правого_циклического_17_r1 ),
    .R0(\ступень_сдвигателя_64х_правого_циклического_18_r0 ),
    .R1(\ступень_сдвигателя_64х_правого_циклического_18_r1 ));
  \ступень_сдвигателя_64х_правого_циклического  \u_ступень_сдвигателя_64х_правого_циклического_19  (
    .\А0 (\ступень_сдвигателя_64х_правого_циклического_18_r0 ),
    .\А1 (\ступень_сдвигателя_64х_правого_циклического_18_r1 ),
    .R0(\ступень_сдвигателя_64х_правого_циклического_19_r0 ),
    .R1(\ступень_сдвигателя_64х_правого_циклического_19_r1 ));
  \ступень_сдвигателя_64х_правого_циклического  \u_ступень_сдвигателя_64х_правого_циклического_20  (
    .\А0 (\ступень_сдвигателя_64х_правого_циклического_19_r0 ),
    .\А1 (\ступень_сдвигателя_64х_правого_циклического_19_r1 ),
    .R0(\ступень_сдвигателя_64х_правого_циклического_20_r0 ),
    .R1(\ступень_сдвигателя_64х_правого_циклического_20_r1 ));
  \ступень_сдвигателя_64х_правого_циклического  \u_ступень_сдвигателя_64х_правого_циклического_21  (
    .\А0 (\ступень_сдвигателя_64х_правого_циклического_22_r0 ),
    .\А1 (\ступень_сдвигателя_64х_правого_циклического_22_r1 ),
    .R0(\ступень_сдвигателя_64х_правого_циклического_21_r0 ),
    .R1(\ступень_сдвигателя_64х_правого_циклического_21_r1 ));
  \ступень_сдвигателя_64х_правого_циклического  \u_ступень_сдвигателя_64х_правого_циклического_22  (
    .\А0 (\ступень_сдвигателя_64х_правого_циклического_20_r0 ),
    .\А1 (\ступень_сдвигателя_64х_правого_циклического_20_r1 ),
    .R0(\ступень_сдвигателя_64х_правого_циклического_22_r0 ),
    .R1(\ступень_сдвигателя_64х_правого_циклического_22_r1 ));
  \ступень_сдвигателя_64х_правого_циклического  \u_ступень_сдвигателя_64х_правого_циклического_23  (
    .\А0 (\ступень_сдвигателя_64х_правого_циклического_21_r0 ),
    .\А1 (\ступень_сдвигателя_64х_правого_циклического_21_r1 ),
    .R0(\ступень_сдвигателя_64х_правого_циклического_23_r0 ),
    .R1(\ступень_сдвигателя_64х_правого_циклического_23_r1 ));
  \ступень_сдвигателя_64х_правого_циклического  \u_ступень_сдвигателя_64х_правого_циклического_24  (
    .\А0 (\ступень_сдвигателя_64х_правого_циклического_23_r0 ),
    .\А1 (\ступень_сдвигателя_64х_правого_циклического_23_r1 ),
    .R0(\ступень_сдвигателя_64х_правого_циклического_24_r0 ),
    .R1(\ступень_сдвигателя_64х_правого_циклического_24_r1 ));
  \ступень_сдвигателя_64х_правого_циклического  \u_ступень_сдвигателя_64х_правого_циклического_25  (
    .\А0 (\ступень_сдвигателя_64х_правого_циклического_24_r0 ),
    .\А1 (\ступень_сдвигателя_64х_правого_циклического_24_r1 ),
    .R0(\ступень_сдвигателя_64х_правого_циклического_25_r0 ),
    .R1(\ступень_сдвигателя_64х_правого_циклического_25_r1 ));
  \ступень_сдвигателя_64х_правого_циклического  \u_ступень_сдвигателя_64х_правого_циклического_26  (
    .\А0 (\ступень_сдвигателя_64х_правого_циклического_25_r0 ),
    .\А1 (\ступень_сдвигателя_64х_правого_циклического_25_r1 ),
    .R0(\ступень_сдвигателя_64х_правого_циклического_26_r0 ),
    .R1(\ступень_сдвигателя_64х_правого_циклического_26_r1 ));
  \ступень_сдвигателя_64х_правого_циклического  \u_ступень_сдвигателя_64х_правого_циклического_27  (
    .\А0 (\ступень_сдвигателя_64х_правого_циклического_26_r0 ),
    .\А1 (\ступень_сдвигателя_64х_правого_циклического_26_r1 ),
    .R0(\ступень_сдвигателя_64х_правого_циклического_27_r0 ),
    .R1(\ступень_сдвигателя_64х_правого_циклического_27_r1 ));
  \ступень_сдвигателя_64х_правого_циклического  \u_ступень_сдвигателя_64х_правого_циклического_28  (
    .\А0 (\ступень_сдвигателя_64х_правого_циклического_27_r0 ),
    .\А1 (\ступень_сдвигателя_64х_правого_циклического_27_r1 ),
    .R0(\ступень_сдвигателя_64х_правого_циклического_28_r0 ),
    .R1(\ступень_сдвигателя_64х_правого_циклического_28_r1 ));
  \ступень_сдвигателя_64х_правого_циклического  \u_ступень_сдвигателя_64х_правого_циклического_29  (
    .\А0 (\ступень_сдвигателя_64х_правого_циклического_28_r0 ),
    .\А1 (\ступень_сдвигателя_64х_правого_циклического_28_r1 ),
    .R0(\ступень_сдвигателя_64х_правого_циклического_29_r0 ),
    .R1(\ступень_сдвигателя_64х_правого_циклического_29_r1 ));
  \ступень_сдвигателя_64х_правого_циклического  \u_ступень_сдвигателя_64х_правого_циклического_30  (
    .\А0 (\ступень_сдвигателя_64х_правого_циклического_29_r0 ),
    .\А1 (\ступень_сдвигателя_64х_правого_циклического_29_r1 ),
    .R0(\ступень_сдвигателя_64х_правого_циклического_30_r0 ),
    .R1(\ступень_сдвигателя_64х_правого_циклического_30_r1 ));
  \ступень_сдвигателя_64х_правого_циклического  \u_ступень_сдвигателя_64х_правого_циклического_31  (
    .\А0 (\ступень_сдвигателя_64х_правого_циклического_32_r0 ),
    .\А1 (\ступень_сдвигателя_64х_правого_циклического_32_r1 ),
    .R0(\ступень_сдвигателя_64х_правого_циклического_31_r0 ),
    .R1(\ступень_сдвигателя_64х_правого_циклического_31_r1 ));
  \ступень_сдвигателя_64х_правого_циклического  \u_ступень_сдвигателя_64х_правого_циклического_32  (
    .\А0 (\ступень_сдвигателя_64х_правого_циклического_30_r0 ),
    .\А1 (\ступень_сдвигателя_64х_правого_циклического_30_r1 ),
    .R0(\ступень_сдвигателя_64х_правого_циклического_32_r0 ),
    .R1(\ступень_сдвигателя_64х_правого_циклического_32_r1 ));
  \ступень_сдвигателя_64х_правого_циклического  \u_ступень_сдвигателя_64х_правого_циклического_33  (
    .\А0 (\ступень_сдвигателя_64х_правого_циклического_31_r0 ),
    .\А1 (\ступень_сдвигателя_64х_правого_циклического_31_r1 ),
    .R0(\ступень_сдвигателя_64х_правого_циклического_33_r0 ),
    .R1(\ступень_сдвигателя_64х_правого_циклического_33_r1 ));
  \ступень_сдвигателя_64х_правого_циклического  \u_ступень_сдвигателя_64х_правого_циклического_34  (
    .\А0 (\ступень_сдвигателя_64х_правого_циклического_35_r0 ),
    .\А1 (\ступень_сдвигателя_64х_правого_циклического_35_r1 ),
    .R0(\ступень_сдвигателя_64х_правого_циклического_34_r0 ),
    .R1(\ступень_сдвигателя_64х_правого_циклического_34_r1 ));
  \ступень_сдвигателя_64х_правого_циклического  \u_ступень_сдвигателя_64х_правого_циклического_35  (
    .\А0 (\ступень_сдвигателя_64х_правого_циклического_33_r0 ),
    .\А1 (\ступень_сдвигателя_64х_правого_циклического_33_r1 ),
    .R0(\ступень_сдвигателя_64х_правого_циклического_35_r0 ),
    .R1(\ступень_сдвигателя_64х_правого_циклического_35_r1 ));
  Multiplexer #(.select(5), .width(32), .disabled(0), .enable("false")) multiplexer_5 (
    .in0(\ступень_сдвигателя_64х_правого_циклического_31_r0 ),
    .in1(\ступень_сдвигателя_64х_правого_циклического_33_r0 ),
    .in2(\ступень_сдвигателя_64х_правого_циклического_35_r0 ),
    .in3(\ступень_сдвигателя_64х_правого_циклического_34_r0 ),
    .in4(\ступень_сдвигателя_64х_правого_циклического_36_r0 ),
    .in5(\ступень_сдвигателя_64х_правого_циклического_37_r0 ),
    .in6(\ступень_сдвигателя_64х_правого_циклического_38_r0 ),
    .in7(\ступень_сдвигателя_64х_правого_циклического_40_r0 ),
    .in8(\ступень_сдвигателя_64х_правого_циклического_39_r0 ),
    .in9(\ступень_сдвигателя_64х_правого_циклического_41_r0 ),
    .in10(\ступень_сдвигателя_64х_правого_циклического_42_r0 ),
    .in11(\ступень_сдвигателя_64х_правого_циклического_43_r0 ),
    .in12(\ступень_сдвигателя_64х_правого_циклического_44_r0 ),
    .in13(\ступень_сдвигателя_64х_правого_циклического_45_r0 ),
    .in14(\ступень_сдвигателя_64х_правого_циклического_46_r0 ),
    .in15(\ступень_сдвигателя_64х_правого_циклического_48_r0 ),
    .in16(\ступень_сдвигателя_64х_правого_циклического_47_r0 ),
    .in17(\ступень_сдвигателя_64х_правого_циклического_49_r0 ),
    .in18(\ступень_сдвигателя_64х_правого_циклического_51_r0 ),
    .in19(\ступень_сдвигателя_64х_правого_циклического_50_r0 ),
    .in20(\ступень_сдвигателя_64х_правого_циклического_52_r0 ),
    .in21(\ступень_сдвигателя_64х_правого_циклического_54_r0 ),
    .in22(\ступень_сдвигателя_64х_правого_циклического_53_r0 ),
    .in23(\ступень_сдвигателя_64х_правого_циклического_55_r0 ),
    .in24(\ступень_сдвигателя_64х_правого_циклического_56_r0 ),
    .in25(\ступень_сдвигателя_64х_правого_циклического_57_r0 ),
    .in26(\ступень_сдвигателя_64х_правого_циклического_59_r0 ),
    .in27(\ступень_сдвигателя_64х_правого_циклического_58_r0 ),
    .in28(\ступень_сдвигателя_64х_правого_циклического_60_r0 ),
    .in29(\ступень_сдвигателя_64х_правого_циклического_61_r0 ),
    .in30(\ступень_сдвигателя_64х_правого_циклического_62_r0 ),
    .in31(\ступень_сдвигателя_64х_правого_циклического_63_r0 ), .out(multiplexer_5_out), .sel(in_3[4:0]));
  \ступень_сдвигателя_64х_правого_циклического  \u_ступень_сдвигателя_64х_правого_циклического_36  (
    .\А0 (\ступень_сдвигателя_64х_правого_циклического_34_r0 ),
    .\А1 (\ступень_сдвигателя_64х_правого_циклического_34_r1 ),
    .R0(\ступень_сдвигателя_64х_правого_циклического_36_r0 ),
    .R1(\ступень_сдвигателя_64х_правого_циклического_36_r1 ));
  Multiplexer #(.select(5), .width(32), .disabled(0), .enable("false")) multiplexer_6 (
    .in0(\ступень_сдвигателя_64х_правого_циклического_31_r1 ),
    .in1(\ступень_сдвигателя_64х_правого_циклического_33_r1 ),
    .in2(\ступень_сдвигателя_64х_правого_циклического_35_r1 ),
    .in3(\ступень_сдвигателя_64х_правого_циклического_34_r1 ),
    .in4(\ступень_сдвигателя_64х_правого_циклического_36_r1 ),
    .in5(\ступень_сдвигателя_64х_правого_циклического_37_r1 ),
    .in6(\ступень_сдвигателя_64х_правого_циклического_38_r1 ),
    .in7(\ступень_сдвигателя_64х_правого_циклического_40_r1 ),
    .in8(\ступень_сдвигателя_64х_правого_циклического_39_r1 ),
    .in9(\ступень_сдвигателя_64х_правого_циклического_41_r1 ),
    .in10(\ступень_сдвигателя_64х_правого_циклического_42_r1 ),
    .in11(\ступень_сдвигателя_64х_правого_циклического_43_r1 ),
    .in12(\ступень_сдвигателя_64х_правого_циклического_44_r1 ),
    .in13(\ступень_сдвигателя_64х_правого_циклического_45_r1 ),
    .in14(\ступень_сдвигателя_64х_правого_циклического_46_r1 ),
    .in15(\ступень_сдвигателя_64х_правого_циклического_48_r1 ),
    .in16(\ступень_сдвигателя_64х_правого_циклического_47_r1 ),
    .in17(\ступень_сдвигателя_64х_правого_циклического_49_r1 ),
    .in18(\ступень_сдвигателя_64х_правого_циклического_51_r1 ),
    .in19(\ступень_сдвигателя_64х_правого_циклического_50_r1 ),
    .in20(\ступень_сдвигателя_64х_правого_циклического_52_r1 ),
    .in21(\ступень_сдвигателя_64х_правого_циклического_54_r1 ),
    .in22(\ступень_сдвигателя_64х_правого_циклического_53_r1 ),
    .in23(\ступень_сдвигателя_64х_правого_циклического_55_r1 ),
    .in24(\ступень_сдвигателя_64х_правого_циклического_56_r1 ),
    .in25(\ступень_сдвигателя_64х_правого_циклического_57_r1 ),
    .in26(\ступень_сдвигателя_64х_правого_циклического_59_r1 ),
    .in27(\ступень_сдвигателя_64х_правого_циклического_58_r1 ),
    .in28(\ступень_сдвигателя_64х_правого_циклического_60_r1 ),
    .in29(\ступень_сдвигателя_64х_правого_циклического_61_r1 ),
    .in30(\ступень_сдвигателя_64х_правого_циклического_62_r1 ),
    .in31(\ступень_сдвигателя_64х_правого_циклического_63_r1 ), .out(multiplexer_6_out), .sel(in_3[4:0]));
  \ступень_сдвигателя_64х_правого_циклического  \u_ступень_сдвигателя_64х_правого_циклического_37  (
    .\А0 (\ступень_сдвигателя_64х_правого_циклического_36_r0 ),
    .\А1 (\ступень_сдвигателя_64х_правого_циклического_36_r1 ),
    .R0(\ступень_сдвигателя_64х_правого_циклического_37_r0 ),
    .R1(\ступень_сдвигателя_64х_правого_циклического_37_r1 ));
  \ступень_сдвигателя_64х_правого_циклического  \u_ступень_сдвигателя_64х_правого_циклического_38  (
    .\А0 (\ступень_сдвигателя_64х_правого_циклического_37_r0 ),
    .\А1 (\ступень_сдвигателя_64х_правого_циклического_37_r1 ),
    .R0(\ступень_сдвигателя_64х_правого_циклического_38_r0 ),
    .R1(\ступень_сдвигателя_64х_правого_циклического_38_r1 ));
  \ступень_сдвигателя_64х_правого_циклического  \u_ступень_сдвигателя_64х_правого_циклического_39  (
    .\А0 (\ступень_сдвигателя_64х_правого_циклического_40_r0 ),
    .\А1 (\ступень_сдвигателя_64х_правого_циклического_40_r1 ),
    .R0(\ступень_сдвигателя_64х_правого_циклического_39_r0 ),
    .R1(\ступень_сдвигателя_64х_правого_циклического_39_r1 ));
  \ступень_сдвигателя_64х_правого_циклического  \u_ступень_сдвигателя_64х_правого_циклического_40  (
    .\А0 (\ступень_сдвигателя_64х_правого_циклического_38_r0 ),
    .\А1 (\ступень_сдвигателя_64х_правого_циклического_38_r1 ),
    .R0(\ступень_сдвигателя_64х_правого_циклического_40_r0 ),
    .R1(\ступень_сдвигателя_64х_правого_циклического_40_r1 ));
  \ступень_сдвигателя_64х_правого_циклического  \u_ступень_сдвигателя_64х_правого_циклического_41  (
    .\А0 (\ступень_сдвигателя_64х_правого_циклического_39_r0 ),
    .\А1 (\ступень_сдвигателя_64х_правого_циклического_39_r1 ),
    .R0(\ступень_сдвигателя_64х_правого_циклического_41_r0 ),
    .R1(\ступень_сдвигателя_64х_правого_циклического_41_r1 ));
  \ступень_сдвигателя_64х_правого_циклического  \u_ступень_сдвигателя_64х_правого_циклического_42  (
    .\А0 (\ступень_сдвигателя_64х_правого_циклического_41_r0 ),
    .\А1 (\ступень_сдвигателя_64х_правого_циклического_41_r1 ),
    .R0(\ступень_сдвигателя_64х_правого_циклического_42_r0 ),
    .R1(\ступень_сдвигателя_64х_правого_циклического_42_r1 ));
  \ступень_сдвигателя_64х_правого_циклического  \u_ступень_сдвигателя_64х_правого_циклического_43  (
    .\А0 (\ступень_сдвигателя_64х_правого_циклического_42_r0 ),
    .\А1 (\ступень_сдвигателя_64х_правого_циклического_42_r1 ),
    .R0(\ступень_сдвигателя_64х_правого_циклического_43_r0 ),
    .R1(\ступень_сдвигателя_64х_правого_циклического_43_r1 ));
  \ступень_сдвигателя_64х_правого_циклического  \u_ступень_сдвигателя_64х_правого_циклического_44  (
    .\А0 (\ступень_сдвигателя_64х_правого_циклического_43_r0 ),
    .\А1 (\ступень_сдвигателя_64х_правого_циклического_43_r1 ),
    .R0(\ступень_сдвигателя_64х_правого_циклического_44_r0 ),
    .R1(\ступень_сдвигателя_64х_правого_циклического_44_r1 ));
  \ступень_сдвигателя_64х_правого_циклического  \u_ступень_сдвигателя_64х_правого_циклического_45  (
    .\А0 (\ступень_сдвигателя_64х_правого_циклического_44_r0 ),
    .\А1 (\ступень_сдвигателя_64х_правого_циклического_44_r1 ),
    .R0(\ступень_сдвигателя_64х_правого_циклического_45_r0 ),
    .R1(\ступень_сдвигателя_64х_правого_циклического_45_r1 ));
  \ступень_сдвигателя_64х_правого_циклического  \u_ступень_сдвигателя_64х_правого_циклического_46  (
    .\А0 (\ступень_сдвигателя_64х_правого_циклического_45_r0 ),
    .\А1 (\ступень_сдвигателя_64х_правого_циклического_45_r1 ),
    .R0(\ступень_сдвигателя_64х_правого_циклического_46_r0 ),
    .R1(\ступень_сдвигателя_64х_правого_циклического_46_r1 ));
  \ступень_сдвигателя_64х_правого_циклического  \u_ступень_сдвигателя_64х_правого_циклического_47  (
    .\А0 (\ступень_сдвигателя_64х_правого_циклического_48_r0 ),
    .\А1 (\ступень_сдвигателя_64х_правого_циклического_48_r1 ),
    .R0(\ступень_сдвигателя_64х_правого_циклического_47_r0 ),
    .R1(\ступень_сдвигателя_64х_правого_циклического_47_r1 ));
  \ступень_сдвигателя_64х_правого_циклического  \u_ступень_сдвигателя_64х_правого_циклического_48  (
    .\А0 (\ступень_сдвигателя_64х_правого_циклического_46_r0 ),
    .\А1 (\ступень_сдвигателя_64х_правого_циклического_46_r1 ),
    .R0(\ступень_сдвигателя_64х_правого_циклического_48_r0 ),
    .R1(\ступень_сдвигателя_64х_правого_циклического_48_r1 ));
  \ступень_сдвигателя_64х_правого_циклического  \u_ступень_сдвигателя_64х_правого_циклического_49  (
    .\А0 (\ступень_сдвигателя_64х_правого_циклического_47_r0 ),
    .\А1 (\ступень_сдвигателя_64х_правого_циклического_47_r1 ),
    .R0(\ступень_сдвигателя_64х_правого_циклического_49_r0 ),
    .R1(\ступень_сдвигателя_64х_правого_циклического_49_r1 ));
  \ступень_сдвигателя_64х_правого_циклического  \u_ступень_сдвигателя_64х_правого_циклического_50  (
    .\А0 (\ступень_сдвигателя_64х_правого_циклического_51_r0 ),
    .\А1 (\ступень_сдвигателя_64х_правого_циклического_51_r1 ),
    .R0(\ступень_сдвигателя_64х_правого_циклического_50_r0 ),
    .R1(\ступень_сдвигателя_64х_правого_циклического_50_r1 ));
  \ступень_сдвигателя_64х_правого_циклического  \u_ступень_сдвигателя_64х_правого_циклического_51  (
    .\А0 (\ступень_сдвигателя_64х_правого_циклического_49_r0 ),
    .\А1 (\ступень_сдвигателя_64х_правого_циклического_49_r1 ),
    .R0(\ступень_сдвигателя_64х_правого_циклического_51_r0 ),
    .R1(\ступень_сдвигателя_64х_правого_циклического_51_r1 ));
  \ступень_сдвигателя_64х_правого_циклического  \u_ступень_сдвигателя_64х_правого_циклического_52  (
    .\А0 (\ступень_сдвигателя_64х_правого_циклического_50_r0 ),
    .\А1 (\ступень_сдвигателя_64х_правого_циклического_50_r1 ),
    .R0(\ступень_сдвигателя_64х_правого_циклического_52_r0 ),
    .R1(\ступень_сдвигателя_64х_правого_циклического_52_r1 ));
  \ступень_сдвигателя_64х_правого_циклического  \u_ступень_сдвигателя_64х_правого_циклического_53  (
    .\А0 (\ступень_сдвигателя_64х_правого_циклического_54_r0 ),
    .\А1 (\ступень_сдвигателя_64х_правого_циклического_54_r1 ),
    .R0(\ступень_сдвигателя_64х_правого_циклического_53_r0 ),
    .R1(\ступень_сдвигателя_64х_правого_циклического_53_r1 ));
  \ступень_сдвигателя_64х_правого_циклического  \u_ступень_сдвигателя_64х_правого_циклического_54  (
    .\А0 (\ступень_сдвигателя_64х_правого_циклического_52_r0 ),
    .\А1 (\ступень_сдвигателя_64х_правого_циклического_52_r1 ),
    .R0(\ступень_сдвигателя_64х_правого_циклического_54_r0 ),
    .R1(\ступень_сдвигателя_64х_правого_циклического_54_r1 ));
  \ступень_сдвигателя_64х_правого_циклического  \u_ступень_сдвигателя_64х_правого_циклического_55  (
    .\А0 (\ступень_сдвигателя_64х_правого_циклического_53_r0 ),
    .\А1 (\ступень_сдвигателя_64х_правого_циклического_53_r1 ),
    .R0(\ступень_сдвигателя_64х_правого_циклического_55_r0 ),
    .R1(\ступень_сдвигателя_64х_правого_циклического_55_r1 ));
  \ступень_сдвигателя_64х_правого_циклического  \u_ступень_сдвигателя_64х_правого_циклического_56  (
    .\А0 (\ступень_сдвигателя_64х_правого_циклического_55_r0 ),
    .\А1 (\ступень_сдвигателя_64х_правого_циклического_55_r1 ),
    .R0(\ступень_сдвигателя_64х_правого_циклического_56_r0 ),
    .R1(\ступень_сдвигателя_64х_правого_циклического_56_r1 ));
  \ступень_сдвигателя_64х_правого_циклического  \u_ступень_сдвигателя_64х_правого_циклического_57  (
    .\А0 (\ступень_сдвигателя_64х_правого_циклического_56_r0 ),
    .\А1 (\ступень_сдвигателя_64х_правого_циклического_56_r1 ),
    .R0(\ступень_сдвигателя_64х_правого_циклического_57_r0 ),
    .R1(\ступень_сдвигателя_64х_правого_циклического_57_r1 ));
  \ступень_сдвигателя_64х_правого_циклического  \u_ступень_сдвигателя_64х_правого_циклического_58  (
    .\А0 (\ступень_сдвигателя_64х_правого_циклического_59_r0 ),
    .\А1 (\ступень_сдвигателя_64х_правого_циклического_59_r1 ),
    .R0(\ступень_сдвигателя_64х_правого_циклического_58_r0 ),
    .R1(\ступень_сдвигателя_64х_правого_циклического_58_r1 ));
  \ступень_сдвигателя_64х_правого_циклического  \u_ступень_сдвигателя_64х_правого_циклического_59  (
    .\А0 (\ступень_сдвигателя_64х_правого_циклического_57_r0 ),
    .\А1 (\ступень_сдвигателя_64х_правого_циклического_57_r1 ),
    .R0(\ступень_сдвигателя_64х_правого_циклического_59_r0 ),
    .R1(\ступень_сдвигателя_64х_правого_циклического_59_r1 ));
  \ступень_сдвигателя_64х_правого_циклического  \u_ступень_сдвигателя_64х_правого_циклического_60  (
    .\А0 (\ступень_сдвигателя_64х_правого_циклического_58_r0 ),
    .\А1 (\ступень_сдвигателя_64х_правого_циклического_58_r1 ),
    .R0(\ступень_сдвигателя_64х_правого_циклического_60_r0 ),
    .R1(\ступень_сдвигателя_64х_правого_циклического_60_r1 ));
  \ступень_сдвигателя_64х_правого_циклического  \u_ступень_сдвигателя_64х_правого_циклического_61  (
    .\А0 (\ступень_сдвигателя_64х_правого_циклического_60_r0 ),
    .\А1 (\ступень_сдвигателя_64х_правого_циклического_60_r1 ),
    .R0(\ступень_сдвигателя_64х_правого_циклического_61_r0 ),
    .R1(\ступень_сдвигателя_64х_правого_циклического_61_r1 ));
  \ступень_сдвигателя_64х_правого_циклического  \u_ступень_сдвигателя_64х_правого_циклического_62  (
    .\А0 (\ступень_сдвигателя_64х_правого_циклического_61_r0 ),
    .\А1 (\ступень_сдвигателя_64х_правого_циклического_61_r1 ),
    .R0(\ступень_сдвигателя_64х_правого_циклического_62_r0 ),
    .R1(\ступень_сдвигателя_64х_правого_циклического_62_r1 ));
  \ступень_сдвигателя_64х_правого_циклического  \u_ступень_сдвигателя_64х_правого_циклического_63  (
    .\А0 (\ступень_сдвигателя_64х_правого_циклического_62_r0 ),
    .\А1 (\ступень_сдвигателя_64х_правого_циклического_62_r1 ),
    .R0(\ступень_сдвигателя_64х_правого_циклического_63_r0 ),
    .R1(\ступень_сдвигателя_64х_правого_циклического_63_r1 ));
endmodule

module cash_L2 (
  input  [31:0] ADDRESS_CPUC_1,
  input  [31:0] ADDRESS_CPUC_0,
  input  force_sector_load,
  input  L2_clock,
  input  CPUC_write,
  input  RAM_clock,
  input  [31:0] Data_IN_1,
  input  [31:0] Data_IN_0,
  input  clr_cash,
  output [31:0] RAM_address_1,
  output [31:0] DOUT_1,
  output [31:0] RAM_address_0,
  output [31:0] DOUT_0,
  output allow_CPUC_clock,
  output write_RAM
);

  wire cash_l2_cu_1_cash_clock, cash_l2_cu_1_write_cash, or_1_out;

  Multiplexer #(.width(32), .disabled(0), .enable("false")) multiplexer_1 (
    .in0(ADDRESS_CPUC_1), .in1({32{1'b1}}), .out(RAM_address_1), .sel(force_sector_load));
  cash_L2_CU cash_l2_cu_1 (
    .cash_sector_from_CPUC_1(RAM_address_1), .cash_sector_from_CPUC_0(ADDRESS_CPUC_0[31:16]),
    .cash_word(DOUT_0), .clock(L2_clock), .\такты_с_ОЗУ (RAM_clock), .allow_CPUC_clock(allow_CPUC_clock),
    .cash_address(RAM_address_0[15:0]), .cash_clock(cash_l2_cu_1_cash_clock), .write_RAM(write_RAM),
    .write_cash(cash_l2_cu_1_write_cash), .cash_address_from_CPUC(ADDRESS_CPUC_0[15:0]),
    .force_sector_load(force_sector_load));
  or or_1 (or_1_out, cash_l2_cu_1_write_cash, CPUC_write);
  RAM #(.addrWidth(16), .dataWidth(32), .bus("separate")) ram_1 (
    .addr(RAM_address_0[15:0]), .din(Data_IN_1), .data(DOUT_1), .str(or_1_out), .sel(1'b1),
    .clk(cash_l2_cu_1_cash_clock), .ld(1'b1), .clr(clr_cash));
  RAM #(.addrWidth(16), .dataWidth(32), .bus("separate")) ram_2 (
    .addr(RAM_address_0[15:0]), .din(Data_IN_0), .data(DOUT_0), .str(or_1_out), .sel(1'b1),
    .clk(cash_l2_cu_1_cash_clock), .ld(1'b1), .clr(clr_cash));

  assign RAM_address_0[31:16] = ADDRESS_CPUC_0[31:16];
endmodule

module cash_L2_CU (
  input  [15:0] cash_address_from_CPUC,
  input  [31:0] cash_sector_from_CPUC_1,
  input  [15:0] cash_sector_from_CPUC_0,
  input  [31:0] cash_word,
  input  force_sector_load,
  input  \такты_с_ОЗУ ,
  input  clock,
  output allow_CPUC_clock,
  output [15:0] cash_address,
  output cash_clock,
  output write_RAM,
  output write_cash
);

  wire and_1_out, cash_counter_carry, comparator_1_eq, comparator_2_eq, not_1_out, not_2_out, or_1_out,
       or_2_out, or_3_out, xor_1_out;
  wire [7:0] counter_1_q, rom_1_data;
  wire [15:0] cash_counter_q, cash_sector_in_RAM_2_q;
  wire [31:0] cash_sector_in_RAM_q;

  not not_1 (not_1_out, rom_1_data[7]);
  Counter counter_1 (
    .load(rom_1_data[7]), .D({8{1'b0}}), .count(not_1_out), .Q(counter_1_q), .clk(and_1_out),
    .clr(allow_CPUC_clock));  // open: carry
  and and_1 (and_1_out, clock, ~xor_1_out, ~allow_CPUC_clock);  // AND_Gate
  xor xor_1 (xor_1_out, rom_1_data[6], cash_counter_carry);
  or or_1 (or_1_out, force_sector_load, rom_1_data[0]);
  ROM rom_1 (.addr(counter_1_q), .data({rom_1_data[7:6], write_cash, write_RAM, rom_1_data[3:0]}), .sel(1'b1));
  Register #(.width(32), .trigger("falling")) cash_sector_in_RAM (
    .D(cash_sector_from_CPUC_1), .en(or_1_out), .Q(cash_sector_in_RAM_q), .clk(clock), .clr(rom_1_data[3]));
  Register #(.width(16), .trigger("falling")) cash_sector_in_RAM_2 (
    .D(cash_sector_from_CPUC_0), .en(or_1_out), .Q(cash_sector_in_RAM_2_q), .clk(clock), .clr(rom_1_data[3]));
  Counter #(.width(16), .max('hffff), .trigger("falling")) cash_counter (
    .load(rom_1_data[1]), .D(cash_word[15:0]), .count(not_2_out), .Q(cash_counter_q),
    .carry(cash_counter_carry), .clk(cash_clock), .clr(or_2_out));
  not not_2 (not_2_out, rom_1_data[1]);
  Multiplexer #(.disabled(0), .enable("false")) multiplexer_1 (
    .in0(clock), .in1(\такты_с_ОЗУ ), .out(cash_clock), .sel(write_cash));
  or or_2 (or_2_out, rom_1_data[2], or_3_out);
  or or_3 (or_3_out, rom_1_data[3], allow_CPUC_clock);
  Comparator #(.width(32), .mode("unsigned")) comparator_1 (
    .a(cash_sector_from_CPUC_1), .b(cash_sector_in_RAM_q), .eq(comparator_1_eq));  // open: gt, lt
  Comparator #(.width(16), .mode("unsigned")) comparator_2 (
    .a(cash_sector_from_CPUC_0), .b(cash_sector_in_RAM_2_q), .eq(comparator_2_eq));  // open: gt, lt
  and and_2 (allow_CPUC_clock, comparator_1_eq, comparator_2_eq);
  Multiplexer #(.width(16), .disabled(0), .enable("false")) multiplexer_2 (
    .in0(cash_counter_q), .in1(cash_address_from_CPUC), .out(cash_address), .sel(allow_CPUC_clock));

  // Notes on the sheet:
  //   contents of rom_1 (hex, n*v repeats v):
  //   6*0 60
endmodule
